// Logisim project basicgates.circ as structural Verilog: 50 circuits, main circuit main
module main (
);

  wire [63:0] multiplier_1_cout, multiplier_1_out;

  // Probe on multiplier_1_out
  Multiplier #(.width(64)) multiplier_1 (
    .a(64'hfffffffff), .b(64'hffffffffffffffee), .out(multiplier_1_out), .cin(64'h1234),
    .cout(multiplier_1_cout));
  // Probe on multiplier_1_cout
  // Probe on nothing
  // Probe on nothing
endmodule

module adder1bit (
  input  inflow,
  input  input1,
  input  input2,
  output overflow,
  output output1
);

  wire and_1_out, and_2_out, xor_1_out;

  and and_1 (and_1_out, input1, input2);
  xor xor_1 (xor_1_out, input1, input2);
  and and_2 (and_2_out, inflow, xor_1_out);
  xor xor_2 (output1, inflow, xor_1_out);
  or or_1 (overflow, and_1_out, and_2_out);
endmodule

module adder2bit (
  input  inflow,
  input  [1:0] input1,
  input  [1:0] input2,
  output overflow,
  output [1:0] output1
);

  wire adder1bit_1_overflow;

  adder1bit adder1bit_1 (
    .inflow(inflow), .input1(input1[0]), .input2(input2[0]), .overflow(adder1bit_1_overflow),
    .output1(output1[0]));
  adder1bit adder1bit_2 (
    .inflow(adder1bit_1_overflow), .input1(input1[1]), .input2(input2[1]), .overflow(overflow),
    .output1(output1[1]));
endmodule

module adder4bit (
  input  inflow,
  input  [3:0] input1,
  input  [3:0] input2,
  output overflow,
  output [3:0] output1
);

  wire adder2bit_1_overflow;

  adder2bit adder2bit_1 (
    .inflow(inflow), .input1(input1[1:0]), .input2(input2[1:0]), .overflow(adder2bit_1_overflow),
    .output1(output1[1:0]));
  adder2bit adder2bit_2 (
    .inflow(adder2bit_1_overflow), .input1(input1[3:2]), .input2(input2[3:2]), .overflow(overflow),
    .output1(output1[3:2]));
endmodule

module adder8bit (
  input  inflow,
  input  [7:0] input1,
  input  [7:0] input2,
  output overflow,
  output [7:0] output1
);

  wire adder4bit_1_overflow;

  adder4bit adder4bit_1 (
    .inflow(inflow), .input1(input1[3:0]), .input2(input2[3:0]), .overflow(adder4bit_1_overflow),
    .output1(output1[3:0]));
  adder4bit adder4bit_2 (
    .inflow(adder4bit_1_overflow), .input1(input1[7:4]), .input2(input2[7:4]), .overflow(overflow),
    .output1(output1[7:4]));
endmodule

module adder16bit (
  input  inflow,
  input  [15:0] input1,
  input  [15:0] input2,
  output overflow,
  output [15:0] output1
);

  wire adder8bit_1_overflow;

  adder8bit adder8bit_1 (
    .inflow(inflow), .input1(input1[7:0]), .input2(input2[7:0]), .overflow(adder8bit_1_overflow),
    .output1(output1[7:0]));
  adder8bit adder8bit_2 (
    .inflow(adder8bit_1_overflow), .input1(input1[15:8]), .input2(input2[15:8]), .overflow(overflow),
    .output1(output1[15:8]));
endmodule

module adder32bit (
  input  inflow,
  input  [31:0] input1,
  input  [31:0] input2,
  output overflow,
  output [31:0] output1
);

  wire adder16bit_1_overflow;

  adder16bit adder16bit_1 (
    .inflow(inflow), .input1(input1[15:0]), .input2(input2[15:0]), .overflow(adder16bit_1_overflow),
    .output1(output1[15:0]));
  adder16bit adder16bit_2 (
    .inflow(adder16bit_1_overflow), .input1(input1[31:16]), .input2(input2[31:16]), .overflow(overflow),
    .output1(output1[31:16]));
endmodule

module adder64bit (
  input  inflow,
  input  [63:0] input1,
  input  [63:0] input2,
  output overflow,
  output [63:0] output1
);

  wire adder32bit_1_overflow;

  adder32bit adder32bit_1 (
    .inflow(inflow), .input1(input1[31:0]), .input2(input2[31:0]), .overflow(adder32bit_1_overflow),
    .output1(output1[31:0]));
  adder32bit adder32bit_2 (
    .inflow(adder32bit_1_overflow), .input1(input1[63:32]), .input2(input2[63:32]), .overflow(overflow),
    .output1(output1[63:32]));
endmodule

module negate1bit (
  input  input1,
  output output1
);


  assign output1 = input1;
endmodule

module negate2bit (
  input  [1:0] input1,
  output [1:0] output1
);

  wire [1:0] not_1_out;

  assign not_1_out = ~input1;  // NOT_Gate not_1, 2 bits wide
  adder2bit adder2bit_1 (.input1(2'b01), .input2(not_1_out), .output1(output1));  // open: inflow, overflow
endmodule

module negate4bit (
  input  [3:0] input1,
  output [3:0] output1
);

  wire [3:0] not_1_out;

  assign not_1_out = ~input1;  // NOT_Gate not_1, 4 bits wide
  adder4bit adder4bit_1 (.input1(4'b0001), .input2(not_1_out), .output1(output1));  // open: inflow, overflow
endmodule

module negate8bit (
  input  [7:0] input1,
  output [7:0] output1
);

  wire [7:0] not_1_out;

  assign not_1_out = ~input1;  // NOT_Gate not_1, 8 bits wide
  adder8bit adder8bit_1 (.input1(8'h1), .input2(not_1_out), .output1(output1));  // open: inflow, overflow
endmodule

module negate16bit (
  input  [15:0] input1,
  output [15:0] output1
);

  wire [15:0] not_1_out;

  assign not_1_out = ~input1;  // NOT_Gate not_1, 16 bits wide
  adder16bit adder16bit_1 (.input1(16'h1), .input2(not_1_out), .output1(output1));  // open: inflow, overflow
endmodule

module negate32bit (
  input  [31:0] input1,
  output [31:0] output1
);

  wire [31:0] not_1_out;

  assign not_1_out = ~input1;  // NOT_Gate not_1, 32 bits wide
  adder32bit adder32bit_1 (.input1(32'h1), .input2(not_1_out), .output1(output1));  // open: inflow, overflow
endmodule

module negate64bit (
  input  [63:0] input1,
  output [63:0] output1
);

  wire [63:0] not_1_out;

  assign not_1_out = ~input1;  // NOT_Gate not_1, 64 bits wide
  adder64bit adder64bit_1 (.input1(64'h1), .input2(not_1_out), .output1(output1));  // open: inflow, overflow
endmodule

module subtractor1bit (
  input  inborrow,
  input  input1,
  input  input2,
  output borrow,
  output output1
);

  wire and_1_out, and_2_out, not_1_out, not_2_out, xor_1_out;

  not not_1 (not_1_out, input1);
  xor xor_1 (xor_1_out, input1, input2);
  and and_1 (and_1_out, not_1_out, input2);
  and and_2 (and_2_out, inborrow, not_2_out);
  not not_2 (not_2_out, xor_1_out);
  xor xor_2 (output1, inborrow, xor_1_out);
  or or_1 (borrow, and_1_out, and_2_out);
endmodule

module subtractor2bit (
  input  inborrow,
  input  [1:0] input1,
  input  [1:0] input2,
  output borrow,
  output [1:0] output1
);

  wire subtractor1bit_1_borrow;

  subtractor1bit subtractor1bit_1 (
    .inborrow(inborrow), .input1(input1[0]), .input2(input2[0]), .borrow(subtractor1bit_1_borrow),
    .output1(output1[0]));
  subtractor1bit subtractor1bit_2 (
    .inborrow(subtractor1bit_1_borrow), .input1(input1[1]), .input2(input2[1]), .borrow(borrow),
    .output1(output1[1]));
endmodule

module subtractor4bit (
  input  inborrow,
  input  [3:0] input1,
  input  [3:0] input2,
  output borrow,
  output [3:0] output1
);

  wire subtractor2bit_1_borrow;

  subtractor2bit subtractor2bit_1 (
    .inborrow(inborrow), .input1(input1[1:0]), .input2(input2[1:0]), .borrow(subtractor2bit_1_borrow),
    .output1(output1[1:0]));
  subtractor2bit subtractor2bit_2 (
    .inborrow(subtractor2bit_1_borrow), .input1(input1[3:2]), .input2(input2[3:2]), .borrow(borrow),
    .output1(output1[3:2]));
endmodule

module subtractor8bit (
  input  inborrow,
  input  [7:0] input1,
  input  [7:0] input2,
  output borrow,
  output [7:0] output1
);

  wire subtractor4bit_1_borrow;

  subtractor4bit subtractor4bit_1 (
    .inborrow(inborrow), .input1(input1[3:0]), .input2(input2[3:0]), .borrow(subtractor4bit_1_borrow),
    .output1(output1[3:0]));
  subtractor4bit subtractor4bit_2 (
    .inborrow(subtractor4bit_1_borrow), .input1(input1[7:4]), .input2(input2[7:4]), .borrow(borrow),
    .output1(output1[7:4]));
endmodule

module subtractor16bit (
  input  inborrow,
  input  [15:0] input1,
  input  [15:0] input2,
  output borrow,
  output [15:0] output1
);

  wire subtractor8bit_1_borrow;

  subtractor8bit subtractor8bit_1 (
    .inborrow(inborrow), .input1(input1[7:0]), .input2(input2[7:0]), .borrow(subtractor8bit_1_borrow),
    .output1(output1[7:0]));
  subtractor8bit subtractor8bit_2 (
    .inborrow(subtractor8bit_1_borrow), .input1(input1[15:8]), .input2(input2[15:8]), .borrow(borrow),
    .output1(output1[15:8]));
endmodule

module subtractor32bit (
  input  inborrow,
  input  [31:0] input1,
  input  [31:0] input2,
  output borrow,
  output [31:0] output1
);

  wire subtractor16bit_1_borrow;

  subtractor16bit subtractor16bit_1 (
    .inborrow(inborrow), .input1(input1[15:0]), .input2(input2[15:0]), .borrow(subtractor16bit_1_borrow),
    .output1(output1[15:0]));
  subtractor16bit subtractor16bit_2 (
    .inborrow(subtractor16bit_1_borrow), .input1(input1[31:16]), .input2(input2[31:16]), .borrow(borrow),
    .output1(output1[31:16]));
endmodule

module subtractor64bit (
  input  inborrow,
  input  [63:0] input1,
  input  [63:0] input2,
  output borrow,
  output [63:0] output1
);

  wire subtractor32bit_1_borrow;

  subtractor32bit subtractor32bit_1 (
    .inborrow(inborrow), .input1(input1[31:0]), .input2(input2[31:0]), .borrow(subtractor32bit_1_borrow),
    .output1(output1[31:0]));
  subtractor32bit subtractor32bit_2 (
    .inborrow(subtractor32bit_1_borrow), .input1(input1[63:32]), .input2(input2[63:32]), .borrow(borrow),
    .output1(output1[63:32]));
endmodule

module adder128bit (
  input  inflow,
  input  [63:0] input1a,
  input  [63:0] input1b,
  input  [63:0] input2a,
  input  [63:0] input2b,
  output overflow,
  output [63:0] output1a,
  output [63:0] output1b
);

  wire adder64bit_1_overflow;

  adder64bit adder64bit_1 (
    .inflow(inflow), .input1(input1a), .input2(input2a), .overflow(adder64bit_1_overflow), .output1(output1a));
  adder64bit adder64bit_2 (
    .inflow(adder64bit_1_overflow), .input1(input1b), .input2(input2b), .overflow(overflow),
    .output1(output1b));
endmodule

module negate128bit (
  input  [63:0] input1a,
  input  [63:0] input1b,
  output [63:0] output1a,
  output [63:0] output1b
);

  wire [63:0] not_1_out, not_2_out;

  assign not_1_out = ~input1a;  // NOT_Gate not_1, 64 bits wide
  assign not_2_out = ~input1b;  // NOT_Gate not_2, 64 bits wide
  adder128bit adder128bit_1 (
    .input1a(64'h1), .input2a(not_1_out), .input2b(not_2_out), .output1a(output1a), .output1b(output1b));  // open: inflow, input1b, overflow
endmodule

module subtractor128bit (
  input  inborrow,
  input  [63:0] input1a,
  input  [63:0] input1b,
  input  [63:0] input2a,
  input  [63:0] input2b,
  output borrow,
  output [63:0] output1a,
  output [63:0] output1b
);

  wire subtractor64bit_1_borrow;

  subtractor64bit subtractor64bit_1 (
    .inborrow(inborrow), .input1(input1a), .input2(input2a), .borrow(subtractor64bit_1_borrow),
    .output1(output1a));
  subtractor64bit subtractor64bit_2 (
    .inborrow(subtractor64bit_1_borrow), .input1(input1b), .input2(input2b), .borrow(borrow),
    .output1(output1b));
endmodule

module cbuffer1bit (
  input  buffer1,
  input  input1,
  output output1
);

  and and_1 (output1, buffer1, input1);
endmodule

module cbuffer2bit (
  input  buffer1,
  input  [1:0] input1,
  output [1:0] output1
);

  assign output1 = {2{buffer1}} & input1;  // AND_Gate and_1, 2 bits wide
endmodule

module cbuffer4bit (
  input  buffer1,
  input  [3:0] input1,
  output [3:0] output1
);

  assign output1 = {4{buffer1}} & input1;  // AND_Gate and_1, 4 bits wide
endmodule

module cbuffer8bit (
  input  buffer1,
  input  [7:0] input1,
  output [7:0] output1
);

  assign output1 = {8{buffer1}} & input1;  // AND_Gate and_1, 8 bits wide
endmodule

module cbuffer16bit (
  input  buffer1,
  input  [15:0] input1,
  output [15:0] output1
);

  assign output1 = {16{buffer1}} & input1;  // AND_Gate and_1, 16 bits wide
endmodule

module cbuffer32bit (
  input  buffer1,
  input  [31:0] input1,
  output [31:0] output1
);

  assign output1 = {32{buffer1}} & input1;  // AND_Gate and_1, 32 bits wide
endmodule

module cbuffer64bit (
  input  buffer1,
  input  [63:0] input1,
  output [63:0] output1
);

  assign output1 = {64{buffer1}} & input1;  // AND_Gate and_1, 64 bits wide
endmodule

module cbuffer128bit (
  input  buffer1,
  input  [63:0] input1a,
  input  [63:0] input1b,
  output [63:0] output1a,
  output [63:0] output1b
);

  assign output1a = {64{buffer1}} & input1a;  // AND_Gate and_1, 64 bits wide
  assign output1b = {64{buffer1}} & input1b;  // AND_Gate and_2, 64 bits wide
endmodule

module multiplier1bit (
  input  inflow,
  input  input1,
  input  input2,
  output overflow,
  output output1
);

  wire and_1_out;

  and and_1 (and_1_out, input1, input2);
  xor xor_1 (output1, inflow, and_1_out);
  and and_2 (overflow, inflow, and_1_out);
endmodule

module multiplier2bit (
  input  [1:0] inflow,
  input  [1:0] input1,
  input  [1:0] input2,
  output [1:0] overflow,
  output [1:0] output1
);

  wire [3:0] adder4bit_2_output1, cbuffer4bit_1_output1, cbuffer4bit_2_output1;

  adder4bit adder4bit_1 (
    .input1({2'b00, inflow}), .input2(adder4bit_2_output1), .output1({overflow, output1}));  // open: inflow, overflow
  cbuffer4bit cbuffer4bit_1 (.buffer1(input1[0]), .input1({2'b00, input2}), .output1(cbuffer4bit_1_output1));
  adder4bit adder4bit_2 (
    .input1(cbuffer4bit_1_output1), .input2(cbuffer4bit_2_output1), .output1(adder4bit_2_output1));  // open: inflow, overflow
  cbuffer4bit cbuffer4bit_2 (.buffer1(input1[1]), .input1({1'b0, input2, 1'b0}), .output1(cbuffer4bit_2_output1));
endmodule

module multiplier4bit (
  input  [3:0] inflow,
  input  [3:0] input1,
  input  [3:0] input2,
  output [3:0] overflow,
  output [3:0] output1
);

  wire [1:0] multiplier2bit_1_output1, multiplier2bit_1_overflow;
  wire [5:2] multiplier2bit_2_output1, multiplier2bit_3_output1;
  wire [7:0] adder8bit_1_output1, adder8bit_3_output1, adder8bit_4_output1;
  wire [7:4] multiplier2bit_4_output1;

  adder8bit adder8bit_1 (
    .input1({4'b0000, multiplier2bit_1_overflow, multiplier2bit_1_output1}),
    .input2({2'b00, multiplier2bit_2_output1, 2'b00}), .output1(adder8bit_1_output1));  // open: inflow, overflow
  multiplier2bit multiplier2bit_1 (
    .input1(input1[1:0]), .input2(input2[1:0]), .overflow(multiplier2bit_1_overflow),
    .output1(multiplier2bit_1_output1));  // open: inflow
  adder8bit adder8bit_2 (
    .input1({4'b0000, inflow}), .input2(adder8bit_3_output1), .output1({overflow, output1}));  // open: inflow, overflow
  adder8bit adder8bit_3 (
    .input1(adder8bit_1_output1), .input2(adder8bit_4_output1), .output1(adder8bit_3_output1));  // open: inflow, overflow
  adder8bit adder8bit_4 (
    .input1({2'b00, multiplier2bit_3_output1, 2'b00}), .input2({multiplier2bit_4_output1, 4'b0000}),
    .output1(adder8bit_4_output1));  // open: inflow, overflow
  multiplier2bit multiplier2bit_2 (
    .input1(input1[1:0]), .input2(input2[3:2]), .overflow(multiplier2bit_2_output1[5:4]),
    .output1(multiplier2bit_2_output1[3:2]));  // open: inflow
  multiplier2bit multiplier2bit_3 (
    .input1(input1[3:2]), .input2(input2[1:0]), .overflow(multiplier2bit_3_output1[5:4]),
    .output1(multiplier2bit_3_output1[3:2]));  // open: inflow
  multiplier2bit multiplier2bit_4 (
    .input1(input1[3:2]), .input2(input2[3:2]), .overflow(multiplier2bit_4_output1[7:6]),
    .output1(multiplier2bit_4_output1[5:4]));  // open: inflow
endmodule

module multiplier8bit (
  input  [7:0] inflow,
  input  [7:0] input1,
  input  [7:0] input2,
  output [7:0] overflow,
  output [7:0] output1
);

  wire [3:0] multiplier4bit_1_output1, multiplier4bit_1_overflow;
  wire [11:4] multiplier4bit_2_output1, multiplier4bit_3_output1;
  wire [15:0] adder16bit_1_output1, adder16bit_3_output1, adder16bit_4_output1;
  wire [15:8] multiplier4bit_4_output1;

  adder16bit adder16bit_1 (
    .input1({{8{1'b0}}, multiplier4bit_1_overflow, multiplier4bit_1_output1}),
    .input2({4'b0000, multiplier4bit_2_output1, 4'b0000}), .output1(adder16bit_1_output1));  // open: inflow, overflow
  multiplier4bit multiplier4bit_1 (
    .input1(input1[3:0]), .input2(input2[3:0]), .overflow(multiplier4bit_1_overflow),
    .output1(multiplier4bit_1_output1));  // open: inflow
  adder16bit adder16bit_2 (
    .input1({{8{1'b0}}, inflow}), .input2(adder16bit_3_output1), .output1({overflow, output1}));  // open: inflow, overflow
  adder16bit adder16bit_3 (
    .input1(adder16bit_1_output1), .input2(adder16bit_4_output1), .output1(adder16bit_3_output1));  // open: inflow, overflow
  adder16bit adder16bit_4 (
    .input1({4'b0000, multiplier4bit_3_output1, 4'b0000}), .input2({multiplier4bit_4_output1, {8{1'b0}}}),
    .output1(adder16bit_4_output1));  // open: inflow, overflow
  multiplier4bit multiplier4bit_2 (
    .input1(input1[3:0]), .input2(input2[7:4]), .overflow(multiplier4bit_2_output1[11:8]),
    .output1(multiplier4bit_2_output1[7:4]));  // open: inflow
  multiplier4bit multiplier4bit_3 (
    .input1(input1[7:4]), .input2(input2[3:0]), .overflow(multiplier4bit_3_output1[11:8]),
    .output1(multiplier4bit_3_output1[7:4]));  // open: inflow
  multiplier4bit multiplier4bit_4 (
    .input1(input1[7:4]), .input2(input2[7:4]), .overflow(multiplier4bit_4_output1[15:12]),
    .output1(multiplier4bit_4_output1[11:8]));  // open: inflow
endmodule

module multiplier16bit (
  input  [15:0] inflow,
  input  [15:0] input1,
  input  [15:0] input2,
  output [15:0] overflow,
  output [15:0] output1
);

  wire [7:0] multiplier8bit_1_output1, multiplier8bit_1_overflow;
  wire [23:8] multiplier8bit_2_output1, multiplier8bit_3_output1;
  wire [31:0] adder32bit_1_output1, adder32bit_3_output1, adder32bit_4_output1;
  wire [31:16] multiplier8bit_4_output1;

  adder32bit adder32bit_1 (
    .input1({{16{1'b0}}, multiplier8bit_1_overflow, multiplier8bit_1_output1}),
    .input2({{8{1'b0}}, multiplier8bit_2_output1, {8{1'b0}}}), .output1(adder32bit_1_output1));  // open: inflow, overflow
  multiplier8bit multiplier8bit_1 (
    .input1(input1[7:0]), .input2(input2[7:0]), .overflow(multiplier8bit_1_overflow),
    .output1(multiplier8bit_1_output1));  // open: inflow
  adder32bit adder32bit_2 (
    .input1({{16{1'b0}}, inflow}), .input2(adder32bit_3_output1), .output1({overflow, output1}));  // open: inflow, overflow
  adder32bit adder32bit_3 (
    .input1(adder32bit_1_output1), .input2(adder32bit_4_output1), .output1(adder32bit_3_output1));  // open: inflow, overflow
  adder32bit adder32bit_4 (
    .input1({{8{1'b0}}, multiplier8bit_3_output1, {8{1'b0}}}),
    .input2({multiplier8bit_4_output1, {16{1'b0}}}), .output1(adder32bit_4_output1));  // open: inflow, overflow
  multiplier8bit multiplier8bit_2 (
    .input1(input1[7:0]), .input2(input2[15:8]), .overflow(multiplier8bit_2_output1[23:16]),
    .output1(multiplier8bit_2_output1[15:8]));  // open: inflow
  multiplier8bit multiplier8bit_3 (
    .input1(input1[15:8]), .input2(input2[7:0]), .overflow(multiplier8bit_3_output1[23:16]),
    .output1(multiplier8bit_3_output1[15:8]));  // open: inflow
  multiplier8bit multiplier8bit_4 (
    .input1(input1[15:8]), .input2(input2[15:8]), .overflow(multiplier8bit_4_output1[31:24]),
    .output1(multiplier8bit_4_output1[23:16]));  // open: inflow
endmodule

module multiplier32bit (
  input  [31:0] inflow,
  input  [31:0] input1,
  input  [31:0] input2,
  output [31:0] overflow,
  output [31:0] output1
);

  wire [15:0] multiplier16bit_1_output1, multiplier16bit_1_overflow;
  wire [47:16] multiplier16bit_2_output1, multiplier16bit_3_output1;
  wire [63:0] adder64bit_1_output1, adder64bit_3_output1, adder64bit_4_output1;
  wire [63:32] multiplier16bit_4_output1;

  adder64bit adder64bit_1 (
    .input1({{32{1'b0}}, multiplier16bit_1_overflow, multiplier16bit_1_output1}),
    .input2({{16{1'b0}}, multiplier16bit_2_output1, {16{1'b0}}}), .output1(adder64bit_1_output1));  // open: inflow, overflow
  multiplier16bit multiplier16bit_1 (
    .input1(input1[15:0]), .input2(input2[15:0]), .overflow(multiplier16bit_1_overflow),
    .output1(multiplier16bit_1_output1));  // open: inflow
  adder64bit adder64bit_2 (
    .input1({{32{1'b0}}, inflow}), .input2(adder64bit_3_output1), .output1({overflow, output1}));  // open: inflow, overflow
  adder64bit adder64bit_3 (
    .input1(adder64bit_1_output1), .input2(adder64bit_4_output1), .output1(adder64bit_3_output1));  // open: inflow, overflow
  adder64bit adder64bit_4 (
    .input1({{16{1'b0}}, multiplier16bit_3_output1, {16{1'b0}}}),
    .input2({multiplier16bit_4_output1, {32{1'b0}}}), .output1(adder64bit_4_output1));  // open: inflow, overflow
  multiplier16bit multiplier16bit_2 (
    .input1(input1[15:0]), .input2(input2[31:16]), .overflow(multiplier16bit_2_output1[47:32]),
    .output1(multiplier16bit_2_output1[31:16]));  // open: inflow
  multiplier16bit multiplier16bit_3 (
    .input1(input1[31:16]), .input2(input2[15:0]), .overflow(multiplier16bit_3_output1[47:32]),
    .output1(multiplier16bit_3_output1[31:16]));  // open: inflow
  multiplier16bit multiplier16bit_4 (
    .input1(input1[31:16]), .input2(input2[31:16]), .overflow(multiplier16bit_4_output1[63:48]),
    .output1(multiplier16bit_4_output1[47:32]));  // open: inflow
endmodule

module multiplier64bit (
  input  [63:0] inflow,
  input  [63:0] input1,
  input  [63:0] input2,
  output [63:0] overflow,
  output [63:0] output1
);

  wire [31:0] multiplier32bit_2_overflow, multiplier32bit_3_overflow;
  wire [63:0] adder128bit_1_output1a, adder128bit_1_output1b, adder128bit_3_output1a, adder128bit_3_output1b,
       adder128bit_4_output1a, adder128bit_4_output1b, multiplier32bit_1_output1, multiplier32bit_4_output1;
  wire [63:32] multiplier32bit_2_output1, multiplier32bit_3_output1;

  adder128bit adder128bit_1 (
    .input1a(multiplier32bit_1_output1), .input1b({64{1'b0}}),
    .input2a({multiplier32bit_2_output1, {32{1'b0}}}), .input2b({{32{1'b0}}, multiplier32bit_2_overflow}),
    .output1a(adder128bit_1_output1a), .output1b(adder128bit_1_output1b));  // open: inflow, overflow
  multiplier32bit multiplier32bit_1 (
    .input1(input1[31:0]), .input2(input2[31:0]), .overflow(multiplier32bit_1_output1[63:32]),
    .output1(multiplier32bit_1_output1[31:0]));  // open: inflow
  adder128bit adder128bit_2 (
    .input1a(inflow), .input2a(adder128bit_3_output1a), .input2b(adder128bit_3_output1b), .output1a(output1),
    .output1b(overflow));  // open: inflow, input1b, overflow
  adder128bit adder128bit_3 (
    .input1a(adder128bit_1_output1a), .input1b(adder128bit_1_output1b), .input2a(adder128bit_4_output1a),
    .input2b(adder128bit_4_output1b), .output1a(adder128bit_3_output1a), .output1b(adder128bit_3_output1b));  // open: inflow, overflow
  multiplier32bit multiplier32bit_2 (
    .input1(input1[31:0]), .input2(input2[63:32]), .overflow(multiplier32bit_2_overflow),
    .output1(multiplier32bit_2_output1));  // open: inflow
  adder128bit adder128bit_4 (
    .input1a({multiplier32bit_3_output1, {32{1'b0}}}), .input1b({{32{1'b0}}, multiplier32bit_3_overflow}),
    .input2a({64{1'b0}}), .input2b(multiplier32bit_4_output1), .output1a(adder128bit_4_output1a),
    .output1b(adder128bit_4_output1b));  // open: inflow, overflow
  multiplier32bit multiplier32bit_3 (
    .input1(input1[63:32]), .input2(input2[31:0]), .overflow(multiplier32bit_3_overflow),
    .output1(multiplier32bit_3_output1));  // open: inflow
  multiplier32bit multiplier32bit_4 (
    .input1(input1[63:32]), .input2(input2[63:32]), .overflow(multiplier32bit_4_output1[63:32]),
    .output1(multiplier32bit_4_output1[31:0]));  // open: inflow
endmodule

module divider1bit (
  input  inupper,
  input  input1,
  input  input2,
  output remainder,
  output output1
);


  assign output1 = input1;
  assign remainder = 1'b0;
endmodule

module divideru2bit (
  input  [1:0] inupper,
  input  [1:0] input1,
  input  [1:0] input2,
  output [1:0] remainder,
  output [1:0] output1
);

  wire comparator_1_eq, comparator_2_eq, comparator_2_gt, comparator_3_eq, comparator_3_gt, comparator_4_eq,
       comparator_4_gt, comparator_5_eq, comparator_5_gt, not_1_out, or_1_out, or_2_out, or_3_out, or_4_out;
  wire [3:2] and_2_out;
  wire [7:0] cbuffer8bit_1_output1, cbuffer8bit_2_output1, cbuffer8bit_3_output1, cbuffer8bit_4_output1,
       subtractor8bit_1_output1, subtractor8bit_2_output1, subtractor8bit_3_output1;
  wire [7:2] subtractor8bit_4_output1;

  // Probe on inupper
  // Probe on inupper
  // Probe on input1
  // Probe on input1
  Comparator #(.mode("unsigned"), .width(2)) comparator_1 (
    .a(input2), .b(2'b00), .eq(comparator_1_eq));  // open: gt, lt
  // Probe on input2
  // Probe on input2
  not not_1 (not_1_out, comparator_1_eq);
  or or_1 (or_1_out, comparator_2_gt, comparator_2_eq);
  Comparator #(.mode("unsigned")) comparator_2 (
    .a({4'b0000, inupper, input1}), .b({3'b000, input2, 3'b000}), .gt(comparator_2_gt), .eq(comparator_2_eq));  // open: lt
  cbuffer8bit cbuffer8bit_1 (
    .buffer1(and_2_out[3]), .input1({3'b000, input2, 3'b000}), .output1(cbuffer8bit_1_output1));
  and and_1 (and_2_out[3], or_1_out, not_1_out);
  subtractor8bit subtractor8bit_1 (
    .input1({4'b0000, inupper, input1}), .input2(cbuffer8bit_1_output1), .output1(subtractor8bit_1_output1));  // open: inborrow, borrow
  cbuffer8bit cbuffer8bit_2 (
    .buffer1(and_2_out[2]), .input1({4'b0000, input2, 2'b00}), .output1(cbuffer8bit_2_output1));
  and and_2 (and_2_out[2], or_2_out, not_1_out);
  or or_2 (or_2_out, comparator_3_gt, comparator_3_eq);
  Comparator #(.mode("unsigned")) comparator_3 (
    .a(subtractor8bit_1_output1), .b({4'b0000, input2, 2'b00}), .gt(comparator_3_gt), .eq(comparator_3_eq));  // open: lt
  // Probe on subtractor8bit_2_output1
  // Probe on subtractor8bit_2_output1
  subtractor8bit subtractor8bit_2 (
    .input1(subtractor8bit_1_output1), .input2(cbuffer8bit_2_output1), .output1(subtractor8bit_2_output1));  // open: inborrow, borrow
  cbuffer8bit cbuffer8bit_3 (.buffer1(output1[1]), .input1({{5{1'b0}}, input2, 1'b0}), .output1(cbuffer8bit_3_output1));
  and and_3 (output1[1], or_3_out, not_1_out);
  or or_3 (or_3_out, comparator_4_gt, comparator_4_eq);
  Comparator #(.mode("unsigned")) comparator_4 (
    .a(subtractor8bit_2_output1), .b({{5{1'b0}}, input2, 1'b0}), .gt(comparator_4_gt), .eq(comparator_4_eq));  // open: lt
  // Probe on subtractor8bit_3_output1
  // Probe on subtractor8bit_3_output1
  subtractor8bit subtractor8bit_3 (
    .input1(subtractor8bit_2_output1), .input2(cbuffer8bit_3_output1), .output1(subtractor8bit_3_output1));  // open: inborrow, borrow
  cbuffer8bit cbuffer8bit_4 (.buffer1(output1[0]), .input1({{6{1'b0}}, input2}), .output1(cbuffer8bit_4_output1));
  and and_4 (output1[0], or_4_out, not_1_out);
  or or_4 (or_4_out, comparator_5_gt, comparator_5_eq);
  Comparator #(.mode("unsigned")) comparator_5 (
    .a(subtractor8bit_3_output1), .b({{6{1'b0}}, input2}), .gt(comparator_5_gt), .eq(comparator_5_eq));  // open: lt
  // Probe on {subtractor8bit_4_output1, remainder}
  // Probe on {subtractor8bit_4_output1, remainder}
  subtractor8bit subtractor8bit_4 (
    .input1(subtractor8bit_3_output1), .input2(cbuffer8bit_4_output1),
    .output1({subtractor8bit_4_output1, remainder}));  // open: inborrow, borrow
  // Probe on {subtractor8bit_4_output1, remainder}
  // Probe on {subtractor8bit_4_output1, remainder}
  // Probe on {4'b0000, and_2_out, output1}
  // Probe on {4'b0000, and_2_out, output1}
  // Probe on remainder
  // Probe on remainder
  // Probe on output1
  // Probe on output1
endmodule

module divider2bit (
  input  [1:0] inupper,
  input  [1:0] input1,
  input  [1:0] input2,
  output [1:0] remainder,
  output [1:0] output1
);

  wire comparator_1_lt, comparator_2_lt, not_1_out, not_2_out, not_3_out, not_4_out, not_5_out, xor_1_out;
  wire [1:0] cbuffer2bit_1_output1, cbuffer2bit_2_output1, cbuffer2bit_3_output1, cbuffer2bit_4_output1,
       cbuffer2bit_5_output1, cbuffer2bit_6_output1, cbuffer2bit_7_output1, cbuffer2bit_8_output1,
       cbuffer2bit_9_output1, cbuffer2bit_10_output1, divideru2bit_1_output1, divideru2bit_1_remainder,
       negate2bit_1_output1, negate2bit_2_output1, negate2bit_3_output1, negate2bit_4_output1,
       negate2bit_5_output1, or_1_out, or_2_out, or_3_out;

  // Probe on inupper
  // Probe on inupper
  // Probe on input1
  // Probe on input1
  // Probe on input2
  // Probe on input2
  Comparator #(.width(2)) comparator_1 (.a(input1), .b(2'b00), .lt(comparator_1_lt));  // open: gt, eq
  Comparator #(.width(2)) comparator_2 (.a(input2), .b(2'b00), .lt(comparator_2_lt));  // open: gt, eq
  negate2bit negate2bit_1 (.input1(inupper), .output1(negate2bit_1_output1));
  negate2bit negate2bit_2 (.input1(input1), .output1(negate2bit_2_output1));
  negate2bit negate2bit_3 (.input1(input2), .output1(negate2bit_3_output1));
  not not_1 (not_1_out, comparator_1_lt);
  not not_2 (not_2_out, comparator_1_lt);
  not not_3 (not_3_out, comparator_2_lt);
  cbuffer2bit cbuffer2bit_1 (.buffer1(not_1_out), .input1(inupper), .output1(cbuffer2bit_1_output1));
  cbuffer2bit cbuffer2bit_2 (.buffer1(comparator_1_lt), .input1(negate2bit_1_output1), .output1(cbuffer2bit_2_output1));
  cbuffer2bit cbuffer2bit_3 (.buffer1(not_2_out), .input1(input1), .output1(cbuffer2bit_3_output1));
  cbuffer2bit cbuffer2bit_4 (.buffer1(comparator_1_lt), .input1(negate2bit_2_output1), .output1(cbuffer2bit_4_output1));
  cbuffer2bit cbuffer2bit_5 (.buffer1(not_3_out), .input1(input2), .output1(cbuffer2bit_5_output1));
  cbuffer2bit cbuffer2bit_6 (.buffer1(comparator_2_lt), .input1(negate2bit_3_output1), .output1(cbuffer2bit_6_output1));
  assign or_1_out = cbuffer2bit_1_output1 | cbuffer2bit_2_output1;  // OR_Gate or_1, 2 bits wide
  assign or_2_out = cbuffer2bit_3_output1 | cbuffer2bit_4_output1;  // OR_Gate or_2, 2 bits wide
  assign or_3_out = cbuffer2bit_5_output1 | cbuffer2bit_6_output1;  // OR_Gate or_3, 2 bits wide
  xor xor_1 (xor_1_out, comparator_1_lt, comparator_2_lt);
  divideru2bit divideru2bit_1 (
    .inupper(or_1_out), .input1(or_2_out), .input2(or_3_out), .remainder(divideru2bit_1_remainder),
    .output1(divideru2bit_1_output1));
  negate2bit negate2bit_4 (.input1(divideru2bit_1_remainder), .output1(negate2bit_4_output1));
  negate2bit negate2bit_5 (.input1(divideru2bit_1_output1), .output1(negate2bit_5_output1));
  not not_4 (not_4_out, comparator_1_lt);
  not not_5 (not_5_out, xor_1_out);
  cbuffer2bit cbuffer2bit_7 (.buffer1(not_4_out), .input1(divideru2bit_1_remainder), .output1(cbuffer2bit_7_output1));
  cbuffer2bit cbuffer2bit_8 (.buffer1(comparator_1_lt), .input1(negate2bit_4_output1), .output1(cbuffer2bit_8_output1));
  cbuffer2bit cbuffer2bit_9 (.buffer1(not_5_out), .input1(divideru2bit_1_output1), .output1(cbuffer2bit_9_output1));
  cbuffer2bit cbuffer2bit_10 (.buffer1(xor_1_out), .input1(negate2bit_5_output1), .output1(cbuffer2bit_10_output1));
  assign remainder = cbuffer2bit_7_output1 | cbuffer2bit_8_output1;  // OR_Gate or_4, 2 bits wide
  assign output1 = cbuffer2bit_9_output1 | cbuffer2bit_10_output1;  // OR_Gate or_5, 2 bits wide
  // Probe on remainder
  // Probe on remainder
  // Probe on output1
  // Probe on output1

  // Notes on the sheet:
  //   input2: initial=0x2
  //   inupper: initial=0x3
  //   input1: initial=0x2
endmodule

module divideru4bit (
  input  [3:0] inupper,
  input  [3:0] input1,
  input  [3:0] input2,
  output [3:0] remainder,
  output [3:0] output1
);

  wire comparator_1_eq, comparator_2_eq, comparator_2_gt, comparator_3_eq, comparator_3_gt, comparator_4_eq,
       comparator_4_gt, comparator_5_eq, comparator_5_gt, comparator_6_eq, comparator_6_gt, comparator_7_eq,
       comparator_7_gt, comparator_8_eq, comparator_8_gt, comparator_9_eq, comparator_9_gt, not_1_out,
       or_1_out, or_2_out, or_3_out, or_4_out, or_5_out, or_6_out, or_7_out, or_8_out;
  wire [7:4] and_4_out;
  wire [15:0] cbuffer16bit_1_output1, cbuffer16bit_2_output1, cbuffer16bit_3_output1, cbuffer16bit_4_output1,
       cbuffer16bit_5_output1, cbuffer16bit_6_output1, cbuffer16bit_7_output1, cbuffer16bit_8_output1,
       subtractor16bit_1_output1, subtractor16bit_2_output1, subtractor16bit_3_output1,
       subtractor16bit_4_output1, subtractor16bit_5_output1, subtractor16bit_6_output1,
       subtractor16bit_7_output1;
  wire [15:4] subtractor16bit_8_output1;

  // Probe on inupper
  // Probe on inupper
  // Probe on input1
  // Probe on input1
  // Probe on input2
  // Probe on input2
  Comparator #(.mode("unsigned"), .width(4)) comparator_1 (
    .a(input2), .b(4'b0000), .eq(comparator_1_eq));  // open: gt, lt
  not not_1 (not_1_out, comparator_1_eq);
  // Probe on {{8{1'b0}}, inupper, input1}
  // Probe on {{8{1'b0}}, inupper, input1}
  cbuffer16bit cbuffer16bit_1 (
    .buffer1(and_4_out[7]), .input1({{5{1'b0}}, input2, {7{1'b0}}}), .output1(cbuffer16bit_1_output1));
  and and_1 (and_4_out[7], or_1_out, not_1_out);
  or or_1 (or_1_out, comparator_2_gt, comparator_2_eq);
  Comparator #(.mode("unsigned"), .width(16)) comparator_2 (
    .a({{8{1'b0}}, inupper, input1}), .b({{5{1'b0}}, input2, {7{1'b0}}}), .gt(comparator_2_gt),
    .eq(comparator_2_eq));  // open: lt
  // Probe on subtractor16bit_1_output1
  // Probe on subtractor16bit_1_output1
  subtractor16bit subtractor16bit_1 (
    .input1({{8{1'b0}}, inupper, input1}), .input2(cbuffer16bit_1_output1),
    .output1(subtractor16bit_1_output1));  // open: inborrow, borrow
  cbuffer16bit cbuffer16bit_2 (
    .buffer1(and_4_out[6]), .input1({{6{1'b0}}, input2, {6{1'b0}}}), .output1(cbuffer16bit_2_output1));
  and and_2 (and_4_out[6], or_2_out, not_1_out);
  or or_2 (or_2_out, comparator_3_gt, comparator_3_eq);
  Comparator #(.mode("unsigned"), .width(16)) comparator_3 (
    .a(subtractor16bit_1_output1), .b({{6{1'b0}}, input2, {6{1'b0}}}), .gt(comparator_3_gt),
    .eq(comparator_3_eq));  // open: lt
  // Probe on subtractor16bit_2_output1
  // Probe on subtractor16bit_2_output1
  subtractor16bit subtractor16bit_2 (
    .input1(subtractor16bit_1_output1), .input2(cbuffer16bit_2_output1), .output1(subtractor16bit_2_output1));  // open: inborrow, borrow
  cbuffer16bit cbuffer16bit_3 (
    .buffer1(and_4_out[5]), .input1({{7{1'b0}}, input2, {5{1'b0}}}), .output1(cbuffer16bit_3_output1));
  and and_3 (and_4_out[5], or_3_out, not_1_out);
  or or_3 (or_3_out, comparator_4_gt, comparator_4_eq);
  Comparator #(.mode("unsigned"), .width(16)) comparator_4 (
    .a(subtractor16bit_2_output1), .b({{7{1'b0}}, input2, {5{1'b0}}}), .gt(comparator_4_gt),
    .eq(comparator_4_eq));  // open: lt
  // Probe on subtractor16bit_3_output1
  // Probe on subtractor16bit_3_output1
  subtractor16bit subtractor16bit_3 (
    .input1(subtractor16bit_2_output1), .input2(cbuffer16bit_3_output1), .output1(subtractor16bit_3_output1));  // open: inborrow, borrow
  Comparator #(.mode("unsigned"), .width(16)) comparator_5 (
    .a(subtractor16bit_3_output1), .b({{8{1'b0}}, input2, 4'b0000}), .gt(comparator_5_gt),
    .eq(comparator_5_eq));  // open: lt
  cbuffer16bit cbuffer16bit_4 (
    .buffer1(and_4_out[4]), .input1({{8{1'b0}}, input2, 4'b0000}), .output1(cbuffer16bit_4_output1));
  and and_4 (and_4_out[4], or_4_out, not_1_out);
  or or_4 (or_4_out, comparator_5_gt, comparator_5_eq);
  subtractor16bit subtractor16bit_4 (
    .input1(subtractor16bit_3_output1), .input2(cbuffer16bit_4_output1), .output1(subtractor16bit_4_output1));  // open: inborrow, borrow
  // Probe on subtractor16bit_4_output1
  // Probe on subtractor16bit_4_output1
  Comparator #(.mode("unsigned"), .width(16)) comparator_6 (
    .a(subtractor16bit_4_output1), .b({{9{1'b0}}, input2, 3'b000}), .gt(comparator_6_gt), .eq(comparator_6_eq));  // open: lt
  cbuffer16bit cbuffer16bit_5 (
    .buffer1(output1[3]), .input1({{9{1'b0}}, input2, 3'b000}), .output1(cbuffer16bit_5_output1));
  and and_5 (output1[3], or_5_out, not_1_out);
  or or_5 (or_5_out, comparator_6_gt, comparator_6_eq);
  subtractor16bit subtractor16bit_5 (
    .input1(subtractor16bit_4_output1), .input2(cbuffer16bit_5_output1), .output1(subtractor16bit_5_output1));  // open: inborrow, borrow
  // Probe on subtractor16bit_5_output1
  // Probe on subtractor16bit_5_output1
  or or_6 (or_6_out, comparator_7_gt, comparator_7_eq);
  Comparator #(.mode("unsigned"), .width(16)) comparator_7 (
    .a(subtractor16bit_5_output1), .b({{10{1'b0}}, input2, 2'b00}), .gt(comparator_7_gt), .eq(comparator_7_eq));  // open: lt
  cbuffer16bit cbuffer16bit_6 (
    .buffer1(output1[2]), .input1({{10{1'b0}}, input2, 2'b00}), .output1(cbuffer16bit_6_output1));
  and and_6 (output1[2], or_6_out, not_1_out);
  subtractor16bit subtractor16bit_6 (
    .input1(subtractor16bit_5_output1), .input2(cbuffer16bit_6_output1), .output1(subtractor16bit_6_output1));  // open: inborrow, borrow
  // Probe on subtractor16bit_6_output1
  // Probe on subtractor16bit_6_output1
  cbuffer16bit cbuffer16bit_7 (
    .buffer1(output1[1]), .input1({{11{1'b0}}, input2, 1'b0}), .output1(cbuffer16bit_7_output1));
  and and_7 (output1[1], or_7_out, not_1_out);
  or or_7 (or_7_out, comparator_8_gt, comparator_8_eq);
  Comparator #(.mode("unsigned"), .width(16)) comparator_8 (
    .a(subtractor16bit_6_output1), .b({{11{1'b0}}, input2, 1'b0}), .gt(comparator_8_gt), .eq(comparator_8_eq));  // open: lt
  subtractor16bit subtractor16bit_7 (
    .input1(subtractor16bit_6_output1), .input2(cbuffer16bit_7_output1), .output1(subtractor16bit_7_output1));  // open: inborrow, borrow
  // Probe on subtractor16bit_7_output1
  // Probe on subtractor16bit_7_output1
  cbuffer16bit cbuffer16bit_8 (.buffer1(output1[0]), .input1({{12{1'b0}}, input2}), .output1(cbuffer16bit_8_output1));
  and and_8 (output1[0], or_8_out, not_1_out);
  or or_8 (or_8_out, comparator_9_gt, comparator_9_eq);
  Comparator #(.mode("unsigned"), .width(16)) comparator_9 (
    .a(subtractor16bit_7_output1), .b({{12{1'b0}}, input2}), .gt(comparator_9_gt), .eq(comparator_9_eq));  // open: lt
  // Probe on {subtractor16bit_8_output1, remainder}
  // Probe on {subtractor16bit_8_output1, remainder}
  subtractor16bit subtractor16bit_8 (
    .input1(subtractor16bit_7_output1), .input2(cbuffer16bit_8_output1),
    .output1({subtractor16bit_8_output1, remainder}));  // open: inborrow, borrow
  // Probe on {{8{1'b0}}, and_4_out, output1}
  // Probe on {{8{1'b0}}, and_4_out, output1}
  // Probe on remainder
  // Probe on remainder
  // Probe on output1
  // Probe on output1
endmodule

module divideru8bit (
  input  [7:0] inupper,
  input  [7:0] input1,
  input  [7:0] input2,
  output [7:0] remainder,
  output [7:0] output1
);

  wire comparator_1_eq, comparator_2_eq, comparator_2_gt, comparator_3_eq, comparator_3_gt, comparator_4_eq,
       comparator_4_gt, comparator_5_eq, comparator_5_gt, comparator_6_eq, comparator_6_gt, comparator_7_eq,
       comparator_7_gt, comparator_8_eq, comparator_8_gt, comparator_9_eq, comparator_9_gt, comparator_10_eq,
       comparator_10_gt, comparator_11_eq, comparator_11_gt, comparator_12_eq, comparator_12_gt,
       comparator_13_eq, comparator_13_gt, comparator_14_eq, comparator_14_gt, comparator_15_eq,
       comparator_15_gt, comparator_16_eq, comparator_16_gt, comparator_17_eq, comparator_17_gt, not_1_out,
       or_1_out, or_2_out, or_3_out, or_4_out, or_5_out, or_6_out, or_7_out, or_8_out, or_9_out, or_10_out,
       or_11_out, or_12_out, or_13_out, or_14_out, or_15_out, or_16_out;
  wire [15:8] and_8_out;
  wire [31:0] cbuffer32bit_1_output1, cbuffer32bit_2_output1, cbuffer32bit_3_output1, cbuffer32bit_4_output1,
       cbuffer32bit_5_output1, cbuffer32bit_6_output1, cbuffer32bit_7_output1, cbuffer32bit_8_output1,
       cbuffer32bit_9_output1, cbuffer32bit_10_output1, cbuffer32bit_11_output1, cbuffer32bit_12_output1,
       cbuffer32bit_13_output1, cbuffer32bit_14_output1, cbuffer32bit_15_output1, cbuffer32bit_16_output1,
       subtractor32bit_1_output1, subtractor32bit_2_output1, subtractor32bit_3_output1,
       subtractor32bit_4_output1, subtractor32bit_5_output1, subtractor32bit_6_output1,
       subtractor32bit_7_output1, subtractor32bit_8_output1, subtractor32bit_9_output1,
       subtractor32bit_10_output1, subtractor32bit_11_output1, subtractor32bit_12_output1,
       subtractor32bit_13_output1, subtractor32bit_14_output1, subtractor32bit_15_output1;
  wire [31:8] subtractor32bit_16_output1;

  // Probe on inupper
  // Probe on inupper
  // Probe on input1
  // Probe on input1
  // Probe on input2
  // Probe on input2
  not not_1 (not_1_out, comparator_1_eq);
  Comparator #(.mode("unsigned")) comparator_1 (.a(input2), .b({8{1'b0}}), .eq(comparator_1_eq));  // open: gt, lt
  // Probe on {{16{1'b0}}, inupper, input1}
  // Probe on {{16{1'b0}}, inupper, input1}
  subtractor32bit subtractor32bit_1 (
    .input1({{16{1'b0}}, inupper, input1}), .input2(cbuffer32bit_1_output1),
    .output1(subtractor32bit_1_output1));  // open: inborrow, borrow
  cbuffer32bit cbuffer32bit_1 (
    .buffer1(and_8_out[15]), .input1({{9{1'b0}}, input2, {15{1'b0}}}), .output1(cbuffer32bit_1_output1));
  and and_1 (and_8_out[15], or_1_out, not_1_out);
  or or_1 (or_1_out, comparator_2_gt, comparator_2_eq);
  Comparator #(.mode("unsigned"), .width(32)) comparator_2 (
    .a({{16{1'b0}}, inupper, input1}), .b({{9{1'b0}}, input2, {15{1'b0}}}), .gt(comparator_2_gt),
    .eq(comparator_2_eq));  // open: lt
  // Probe on subtractor32bit_1_output1
  // Probe on subtractor32bit_1_output1
  subtractor32bit subtractor32bit_2 (
    .input1(subtractor32bit_1_output1), .input2(cbuffer32bit_2_output1), .output1(subtractor32bit_2_output1));  // open: inborrow, borrow
  cbuffer32bit cbuffer32bit_2 (
    .buffer1(and_8_out[14]), .input1({{10{1'b0}}, input2, {14{1'b0}}}), .output1(cbuffer32bit_2_output1));
  and and_2 (and_8_out[14], or_2_out, not_1_out);
  or or_2 (or_2_out, comparator_3_gt, comparator_3_eq);
  Comparator #(.mode("unsigned"), .width(32)) comparator_3 (
    .a(subtractor32bit_1_output1), .b({{10{1'b0}}, input2, {14{1'b0}}}), .gt(comparator_3_gt),
    .eq(comparator_3_eq));  // open: lt
  // Probe on subtractor32bit_2_output1
  // Probe on subtractor32bit_2_output1
  subtractor32bit subtractor32bit_3 (
    .input1(subtractor32bit_2_output1), .input2(cbuffer32bit_3_output1), .output1(subtractor32bit_3_output1));  // open: inborrow, borrow
  cbuffer32bit cbuffer32bit_3 (
    .buffer1(and_8_out[13]), .input1({{11{1'b0}}, input2, {13{1'b0}}}), .output1(cbuffer32bit_3_output1));
  and and_3 (and_8_out[13], or_3_out, not_1_out);
  or or_3 (or_3_out, comparator_4_gt, comparator_4_eq);
  // Probe on subtractor32bit_3_output1
  // Probe on subtractor32bit_3_output1
  subtractor32bit subtractor32bit_4 (
    .input1(subtractor32bit_3_output1), .input2(cbuffer32bit_4_output1), .output1(subtractor32bit_4_output1));  // open: inborrow, borrow
  or or_4 (or_4_out, comparator_5_gt, comparator_5_eq);
  Comparator #(.mode("unsigned"), .width(32)) comparator_4 (
    .a(subtractor32bit_2_output1), .b({{11{1'b0}}, input2, {13{1'b0}}}), .gt(comparator_4_gt),
    .eq(comparator_4_eq));  // open: lt
  cbuffer32bit cbuffer32bit_4 (
    .buffer1(and_8_out[12]), .input1({{12{1'b0}}, input2, {12{1'b0}}}), .output1(cbuffer32bit_4_output1));
  and and_4 (and_8_out[12], or_4_out, not_1_out);
  Comparator #(.mode("unsigned"), .width(32)) comparator_5 (
    .a(subtractor32bit_3_output1), .b({{12{1'b0}}, input2, {12{1'b0}}}), .gt(comparator_5_gt),
    .eq(comparator_5_eq));  // open: lt
  // Probe on subtractor32bit_4_output1
  // Probe on subtractor32bit_4_output1
  subtractor32bit subtractor32bit_5 (
    .input1(subtractor32bit_4_output1), .input2(cbuffer32bit_5_output1), .output1(subtractor32bit_5_output1));  // open: inborrow, borrow
  cbuffer32bit cbuffer32bit_5 (
    .buffer1(and_8_out[11]), .input1({{13{1'b0}}, input2, {11{1'b0}}}), .output1(cbuffer32bit_5_output1));
  and and_5 (and_8_out[11], or_5_out, not_1_out);
  or or_5 (or_5_out, comparator_6_gt, comparator_6_eq);
  Comparator #(.mode("unsigned"), .width(32)) comparator_6 (
    .a(subtractor32bit_4_output1), .b({{13{1'b0}}, input2, {11{1'b0}}}), .gt(comparator_6_gt),
    .eq(comparator_6_eq));  // open: lt
  // Probe on subtractor32bit_5_output1
  // Probe on subtractor32bit_5_output1
  subtractor32bit subtractor32bit_6 (
    .input1(subtractor32bit_5_output1), .input2(cbuffer32bit_6_output1), .output1(subtractor32bit_6_output1));  // open: inborrow, borrow
  cbuffer32bit cbuffer32bit_6 (
    .buffer1(and_8_out[10]), .input1({{14{1'b0}}, input2, {10{1'b0}}}), .output1(cbuffer32bit_6_output1));
  and and_6 (and_8_out[10], or_6_out, not_1_out);
  or or_6 (or_6_out, comparator_7_gt, comparator_7_eq);
  Comparator #(.mode("unsigned"), .width(32)) comparator_7 (
    .a(subtractor32bit_5_output1), .b({{14{1'b0}}, input2, {10{1'b0}}}), .gt(comparator_7_gt),
    .eq(comparator_7_eq));  // open: lt
  // Probe on subtractor32bit_6_output1
  // Probe on subtractor32bit_6_output1
  subtractor32bit subtractor32bit_7 (
    .input1(subtractor32bit_6_output1), .input2(cbuffer32bit_7_output1), .output1(subtractor32bit_7_output1));  // open: inborrow, borrow
  cbuffer32bit cbuffer32bit_7 (
    .buffer1(and_8_out[9]), .input1({{15{1'b0}}, input2, {9{1'b0}}}), .output1(cbuffer32bit_7_output1));
  and and_7 (and_8_out[9], or_7_out, not_1_out);
  or or_7 (or_7_out, comparator_8_gt, comparator_8_eq);
  // Probe on subtractor32bit_7_output1
  // Probe on subtractor32bit_7_output1
  subtractor32bit subtractor32bit_8 (
    .input1(subtractor32bit_7_output1), .input2(cbuffer32bit_8_output1), .output1(subtractor32bit_8_output1));  // open: inborrow, borrow
  or or_8 (or_8_out, comparator_9_gt, comparator_9_eq);
  Comparator #(.mode("unsigned"), .width(32)) comparator_8 (
    .a(subtractor32bit_6_output1), .b({{15{1'b0}}, input2, {9{1'b0}}}), .gt(comparator_8_gt),
    .eq(comparator_8_eq));  // open: lt
  cbuffer32bit cbuffer32bit_8 (
    .buffer1(and_8_out[8]), .input1({{16{1'b0}}, input2, {8{1'b0}}}), .output1(cbuffer32bit_8_output1));
  and and_8 (and_8_out[8], or_8_out, not_1_out);
  Comparator #(.mode("unsigned"), .width(32)) comparator_9 (
    .a(subtractor32bit_7_output1), .b({{16{1'b0}}, input2, {8{1'b0}}}), .gt(comparator_9_gt),
    .eq(comparator_9_eq));  // open: lt
  // Probe on subtractor32bit_8_output1
  // Probe on subtractor32bit_8_output1
  subtractor32bit subtractor32bit_9 (
    .input1(subtractor32bit_8_output1), .input2(cbuffer32bit_9_output1), .output1(subtractor32bit_9_output1));  // open: inborrow, borrow
  cbuffer32bit cbuffer32bit_9 (
    .buffer1(output1[7]), .input1({{17{1'b0}}, input2, {7{1'b0}}}), .output1(cbuffer32bit_9_output1));
  and and_9 (output1[7], or_9_out, not_1_out);
  or or_9 (or_9_out, comparator_10_gt, comparator_10_eq);
  Comparator #(.mode("unsigned"), .width(32)) comparator_10 (
    .a(subtractor32bit_8_output1), .b({{17{1'b0}}, input2, {7{1'b0}}}), .gt(comparator_10_gt),
    .eq(comparator_10_eq));  // open: lt
  // Probe on subtractor32bit_9_output1
  // Probe on subtractor32bit_9_output1
  subtractor32bit subtractor32bit_10 (
    .input1(subtractor32bit_9_output1), .input2(cbuffer32bit_10_output1), .output1(subtractor32bit_10_output1));  // open: inborrow, borrow
  cbuffer32bit cbuffer32bit_10 (
    .buffer1(output1[6]), .input1({{18{1'b0}}, input2, {6{1'b0}}}), .output1(cbuffer32bit_10_output1));
  and and_10 (output1[6], or_10_out, not_1_out);
  or or_10 (or_10_out, comparator_11_gt, comparator_11_eq);
  Comparator #(.mode("unsigned"), .width(32)) comparator_11 (
    .a(subtractor32bit_9_output1), .b({{18{1'b0}}, input2, {6{1'b0}}}), .gt(comparator_11_gt),
    .eq(comparator_11_eq));  // open: lt
  // Probe on subtractor32bit_10_output1
  // Probe on subtractor32bit_10_output1
  subtractor32bit subtractor32bit_11 (
    .input1(subtractor32bit_10_output1), .input2(cbuffer32bit_11_output1),
    .output1(subtractor32bit_11_output1));  // open: inborrow, borrow
  cbuffer32bit cbuffer32bit_11 (
    .buffer1(output1[5]), .input1({{19{1'b0}}, input2, {5{1'b0}}}), .output1(cbuffer32bit_11_output1));
  and and_11 (output1[5], or_11_out, not_1_out);
  or or_11 (or_11_out, comparator_12_gt, comparator_12_eq);
  // Probe on subtractor32bit_11_output1
  // Probe on subtractor32bit_11_output1
  subtractor32bit subtractor32bit_12 (
    .input1(subtractor32bit_11_output1), .input2(cbuffer32bit_12_output1),
    .output1(subtractor32bit_12_output1));  // open: inborrow, borrow
  or or_12 (or_12_out, comparator_13_gt, comparator_13_eq);
  Comparator #(.mode("unsigned"), .width(32)) comparator_12 (
    .a(subtractor32bit_10_output1), .b({{19{1'b0}}, input2, {5{1'b0}}}), .gt(comparator_12_gt),
    .eq(comparator_12_eq));  // open: lt
  cbuffer32bit cbuffer32bit_12 (
    .buffer1(output1[4]), .input1({{20{1'b0}}, input2, 4'b0000}), .output1(cbuffer32bit_12_output1));
  and and_12 (output1[4], or_12_out, not_1_out);
  Comparator #(.mode("unsigned"), .width(32)) comparator_13 (
    .a(subtractor32bit_11_output1), .b({{20{1'b0}}, input2, 4'b0000}), .gt(comparator_13_gt),
    .eq(comparator_13_eq));  // open: lt
  // Probe on subtractor32bit_12_output1
  // Probe on subtractor32bit_12_output1
  subtractor32bit subtractor32bit_13 (
    .input1(subtractor32bit_12_output1), .input2(cbuffer32bit_13_output1),
    .output1(subtractor32bit_13_output1));  // open: inborrow, borrow
  cbuffer32bit cbuffer32bit_13 (
    .buffer1(output1[3]), .input1({{21{1'b0}}, input2, 3'b000}), .output1(cbuffer32bit_13_output1));
  and and_13 (output1[3], or_13_out, not_1_out);
  or or_13 (or_13_out, comparator_14_gt, comparator_14_eq);
  Comparator #(.mode("unsigned"), .width(32)) comparator_14 (
    .a(subtractor32bit_12_output1), .b({{21{1'b0}}, input2, 3'b000}), .gt(comparator_14_gt),
    .eq(comparator_14_eq));  // open: lt
  // Probe on subtractor32bit_13_output1
  // Probe on subtractor32bit_13_output1
  subtractor32bit subtractor32bit_14 (
    .input1(subtractor32bit_13_output1), .input2(cbuffer32bit_14_output1),
    .output1(subtractor32bit_14_output1));  // open: inborrow, borrow
  cbuffer32bit cbuffer32bit_14 (
    .buffer1(output1[2]), .input1({{22{1'b0}}, input2, 2'b00}), .output1(cbuffer32bit_14_output1));
  and and_14 (output1[2], or_14_out, not_1_out);
  or or_14 (or_14_out, comparator_15_gt, comparator_15_eq);
  Comparator #(.mode("unsigned"), .width(32)) comparator_15 (
    .a(subtractor32bit_13_output1), .b({{22{1'b0}}, input2, 2'b00}), .gt(comparator_15_gt),
    .eq(comparator_15_eq));  // open: lt
  // Probe on subtractor32bit_14_output1
  // Probe on subtractor32bit_14_output1
  subtractor32bit subtractor32bit_15 (
    .input1(subtractor32bit_14_output1), .input2(cbuffer32bit_15_output1),
    .output1(subtractor32bit_15_output1));  // open: inborrow, borrow
  cbuffer32bit cbuffer32bit_15 (
    .buffer1(output1[1]), .input1({{23{1'b0}}, input2, 1'b0}), .output1(cbuffer32bit_15_output1));
  and and_15 (output1[1], or_15_out, not_1_out);
  or or_15 (or_15_out, comparator_16_gt, comparator_16_eq);
  // Probe on subtractor32bit_15_output1
  // Probe on subtractor32bit_15_output1
  subtractor32bit subtractor32bit_16 (
    .input1(subtractor32bit_15_output1), .input2(cbuffer32bit_16_output1),
    .output1({subtractor32bit_16_output1, remainder}));  // open: inborrow, borrow
  or or_16 (or_16_out, comparator_17_gt, comparator_17_eq);
  Comparator #(.mode("unsigned"), .width(32)) comparator_16 (
    .a(subtractor32bit_14_output1), .b({{23{1'b0}}, input2, 1'b0}), .gt(comparator_16_gt),
    .eq(comparator_16_eq));  // open: lt
  cbuffer32bit cbuffer32bit_16 (.buffer1(output1[0]), .input1({{24{1'b0}}, input2}), .output1(cbuffer32bit_16_output1));
  and and_16 (output1[0], or_16_out, not_1_out);
  Comparator #(.mode("unsigned"), .width(32)) comparator_17 (
    .a(subtractor32bit_15_output1), .b({{24{1'b0}}, input2}), .gt(comparator_17_gt), .eq(comparator_17_eq));  // open: lt
  // Probe on {subtractor32bit_16_output1, remainder}
  // Probe on {subtractor32bit_16_output1, remainder}
  // Probe on {{16{1'b0}}, and_8_out, output1}
  // Probe on {{16{1'b0}}, and_8_out, output1}
  // Probe on remainder
  // Probe on remainder
  // Probe on output1
  // Probe on output1

  // Notes on the sheet:
  //   input2: initial=0x13
  //   input1: initial=0x4e
endmodule

module divideru16bit (
  input  [15:0] inupper,
  input  [15:0] input1,
  input  [15:0] input2,
  output [15:0] remainder,
  output [15:0] output1
);

  wire comparator_1_eq, comparator_2_eq, comparator_2_gt, comparator_3_eq, comparator_3_gt, comparator_4_eq,
       comparator_4_gt, comparator_5_eq, comparator_5_gt, comparator_6_eq, comparator_6_gt, comparator_7_eq,
       comparator_7_gt, comparator_8_eq, comparator_8_gt, comparator_9_eq, comparator_9_gt, comparator_10_eq,
       comparator_10_gt, comparator_11_eq, comparator_11_gt, comparator_12_eq, comparator_12_gt,
       comparator_13_eq, comparator_13_gt, comparator_14_eq, comparator_14_gt, comparator_15_eq,
       comparator_15_gt, comparator_16_eq, comparator_16_gt, comparator_17_eq, comparator_17_gt,
       comparator_18_eq, comparator_18_gt, comparator_19_eq, comparator_19_gt, comparator_20_eq,
       comparator_20_gt, comparator_21_eq, comparator_21_gt, comparator_22_eq, comparator_22_gt,
       comparator_23_eq, comparator_23_gt, comparator_24_eq, comparator_24_gt, comparator_25_eq,
       comparator_25_gt, comparator_26_eq, comparator_26_gt, comparator_27_eq, comparator_27_gt,
       comparator_28_eq, comparator_28_gt, comparator_29_eq, comparator_29_gt, comparator_30_eq,
       comparator_30_gt, comparator_31_eq, comparator_31_gt, comparator_32_eq, comparator_32_gt,
       comparator_33_eq, comparator_33_gt, not_1_out, or_1_out, or_2_out, or_3_out, or_4_out, or_5_out,
       or_6_out, or_7_out, or_8_out, or_9_out, or_10_out, or_11_out, or_12_out, or_13_out, or_14_out,
       or_15_out, or_16_out, or_17_out, or_18_out, or_19_out, or_20_out, or_21_out, or_22_out, or_23_out,
       or_24_out, or_25_out, or_26_out, or_27_out, or_28_out, or_29_out, or_30_out, or_31_out, or_32_out;
  wire [15:0] divider_1_out, divider_1_rem;
  wire [31:16] and_16_out;
  wire [63:0] cbuffer64bit_1_output1, cbuffer64bit_2_output1, cbuffer64bit_3_output1, cbuffer64bit_4_output1,
       cbuffer64bit_5_output1, cbuffer64bit_6_output1, cbuffer64bit_7_output1, cbuffer64bit_8_output1,
       cbuffer64bit_9_output1, cbuffer64bit_10_output1, cbuffer64bit_11_output1, cbuffer64bit_12_output1,
       cbuffer64bit_13_output1, cbuffer64bit_14_output1, cbuffer64bit_15_output1, cbuffer64bit_16_output1,
       cbuffer64bit_17_output1, cbuffer64bit_18_output1, cbuffer64bit_19_output1, cbuffer64bit_20_output1,
       cbuffer64bit_21_output1, cbuffer64bit_22_output1, cbuffer64bit_23_output1, cbuffer64bit_24_output1,
       cbuffer64bit_25_output1, cbuffer64bit_26_output1, cbuffer64bit_27_output1, cbuffer64bit_28_output1,
       cbuffer64bit_29_output1, cbuffer64bit_30_output1, cbuffer64bit_31_output1, cbuffer64bit_32_output1,
       subtractor64bit_1_output1, subtractor64bit_2_output1, subtractor64bit_3_output1,
       subtractor64bit_4_output1, subtractor64bit_5_output1, subtractor64bit_6_output1,
       subtractor64bit_7_output1, subtractor64bit_8_output1, subtractor64bit_9_output1,
       subtractor64bit_10_output1, subtractor64bit_11_output1, subtractor64bit_12_output1,
       subtractor64bit_13_output1, subtractor64bit_14_output1, subtractor64bit_15_output1,
       subtractor64bit_16_output1, subtractor64bit_17_output1, subtractor64bit_18_output1,
       subtractor64bit_19_output1, subtractor64bit_20_output1, subtractor64bit_21_output1,
       subtractor64bit_22_output1, subtractor64bit_23_output1, subtractor64bit_24_output1,
       subtractor64bit_25_output1, subtractor64bit_26_output1, subtractor64bit_27_output1,
       subtractor64bit_28_output1, subtractor64bit_29_output1, subtractor64bit_30_output1,
       subtractor64bit_31_output1;
  wire [63:16] subtractor64bit_32_output1;

  // Probe on divider_1_out
  // Probe on divider_1_out
  Divider #(.width(16)) divider_1 (.a(input1), .b(input2), .out(divider_1_out), .upper(inupper), .rem(divider_1_rem));
  // Probe on divider_1_rem
  // Probe on divider_1_rem
  // Probe on inupper
  // Probe on inupper
  // Probe on input1
  // Probe on input1
  // Probe on input2
  // Probe on input2
  not not_1 (not_1_out, comparator_1_eq);
  Comparator #(.mode("unsigned"), .width(16)) comparator_1 (
    .a(input2), .b({16{1'b0}}), .eq(comparator_1_eq));  // open: gt, lt
  // Probe on {{32{1'b0}}, inupper, input1}
  // Probe on {{32{1'b0}}, inupper, input1}
  subtractor64bit subtractor64bit_1 (
    .input1({{32{1'b0}}, inupper, input1}), .input2(cbuffer64bit_1_output1),
    .output1(subtractor64bit_1_output1));  // open: inborrow, borrow
  cbuffer64bit cbuffer64bit_1 (
    .buffer1(and_16_out[31]), .input1({{17{1'b0}}, input2, {31{1'b0}}}), .output1(cbuffer64bit_1_output1));
  and and_1 (and_16_out[31], or_1_out, not_1_out);
  or or_1 (or_1_out, comparator_2_gt, comparator_2_eq);
  Comparator #(.mode("unsigned"), .width(64)) comparator_2 (
    .a({{32{1'b0}}, inupper, input1}), .b({{17{1'b0}}, input2, {31{1'b0}}}), .gt(comparator_2_gt),
    .eq(comparator_2_eq));  // open: lt
  // Probe on subtractor64bit_1_output1
  // Probe on subtractor64bit_1_output1
  subtractor64bit subtractor64bit_2 (
    .input1(subtractor64bit_1_output1), .input2(cbuffer64bit_2_output1), .output1(subtractor64bit_2_output1));  // open: inborrow, borrow
  cbuffer64bit cbuffer64bit_2 (
    .buffer1(and_16_out[30]), .input1({{18{1'b0}}, input2, {30{1'b0}}}), .output1(cbuffer64bit_2_output1));
  and and_2 (and_16_out[30], or_2_out, not_1_out);
  or or_2 (or_2_out, comparator_3_gt, comparator_3_eq);
  Comparator #(.mode("unsigned"), .width(64)) comparator_3 (
    .a(subtractor64bit_1_output1), .b({{18{1'b0}}, input2, {30{1'b0}}}), .gt(comparator_3_gt),
    .eq(comparator_3_eq));  // open: lt
  // Probe on subtractor64bit_2_output1
  // Probe on subtractor64bit_2_output1
  subtractor64bit subtractor64bit_3 (
    .input1(subtractor64bit_2_output1), .input2(cbuffer64bit_3_output1), .output1(subtractor64bit_3_output1));  // open: inborrow, borrow
  cbuffer64bit cbuffer64bit_3 (
    .buffer1(and_16_out[29]), .input1({{19{1'b0}}, input2, {29{1'b0}}}), .output1(cbuffer64bit_3_output1));
  and and_3 (and_16_out[29], or_3_out, not_1_out);
  or or_3 (or_3_out, comparator_4_gt, comparator_4_eq);
  // Probe on subtractor64bit_3_output1
  // Probe on subtractor64bit_3_output1
  subtractor64bit subtractor64bit_4 (
    .input1(subtractor64bit_3_output1), .input2(cbuffer64bit_4_output1), .output1(subtractor64bit_4_output1));  // open: inborrow, borrow
  or or_4 (or_4_out, comparator_5_gt, comparator_5_eq);
  Comparator #(.mode("unsigned"), .width(64)) comparator_4 (
    .a(subtractor64bit_2_output1), .b({{19{1'b0}}, input2, {29{1'b0}}}), .gt(comparator_4_gt),
    .eq(comparator_4_eq));  // open: lt
  cbuffer64bit cbuffer64bit_4 (
    .buffer1(and_16_out[28]), .input1({{20{1'b0}}, input2, {28{1'b0}}}), .output1(cbuffer64bit_4_output1));
  and and_4 (and_16_out[28], or_4_out, not_1_out);
  Comparator #(.mode("unsigned"), .width(64)) comparator_5 (
    .a(subtractor64bit_3_output1), .b({{20{1'b0}}, input2, {28{1'b0}}}), .gt(comparator_5_gt),
    .eq(comparator_5_eq));  // open: lt
  // Probe on subtractor64bit_4_output1
  // Probe on subtractor64bit_4_output1
  subtractor64bit subtractor64bit_5 (
    .input1(subtractor64bit_4_output1), .input2(cbuffer64bit_5_output1), .output1(subtractor64bit_5_output1));  // open: inborrow, borrow
  cbuffer64bit cbuffer64bit_5 (
    .buffer1(and_16_out[27]), .input1({{21{1'b0}}, input2, {27{1'b0}}}), .output1(cbuffer64bit_5_output1));
  and and_5 (and_16_out[27], or_5_out, not_1_out);
  or or_5 (or_5_out, comparator_6_gt, comparator_6_eq);
  Comparator #(.mode("unsigned"), .width(64)) comparator_6 (
    .a(subtractor64bit_4_output1), .b({{21{1'b0}}, input2, {27{1'b0}}}), .gt(comparator_6_gt),
    .eq(comparator_6_eq));  // open: lt
  // Probe on subtractor64bit_5_output1
  // Probe on subtractor64bit_5_output1
  subtractor64bit subtractor64bit_6 (
    .input1(subtractor64bit_5_output1), .input2(cbuffer64bit_6_output1), .output1(subtractor64bit_6_output1));  // open: inborrow, borrow
  cbuffer64bit cbuffer64bit_6 (
    .buffer1(and_16_out[26]), .input1({{22{1'b0}}, input2, {26{1'b0}}}), .output1(cbuffer64bit_6_output1));
  and and_6 (and_16_out[26], or_6_out, not_1_out);
  or or_6 (or_6_out, comparator_7_gt, comparator_7_eq);
  Comparator #(.mode("unsigned"), .width(64)) comparator_7 (
    .a(subtractor64bit_5_output1), .b({{22{1'b0}}, input2, {26{1'b0}}}), .gt(comparator_7_gt),
    .eq(comparator_7_eq));  // open: lt
  // Probe on subtractor64bit_6_output1
  // Probe on subtractor64bit_6_output1
  subtractor64bit subtractor64bit_7 (
    .input1(subtractor64bit_6_output1), .input2(cbuffer64bit_7_output1), .output1(subtractor64bit_7_output1));  // open: inborrow, borrow
  cbuffer64bit cbuffer64bit_7 (
    .buffer1(and_16_out[25]), .input1({{23{1'b0}}, input2, {25{1'b0}}}), .output1(cbuffer64bit_7_output1));
  and and_7 (and_16_out[25], or_7_out, not_1_out);
  or or_7 (or_7_out, comparator_8_gt, comparator_8_eq);
  // Probe on subtractor64bit_7_output1
  // Probe on subtractor64bit_7_output1
  subtractor64bit subtractor64bit_8 (
    .input1(subtractor64bit_7_output1), .input2(cbuffer64bit_8_output1), .output1(subtractor64bit_8_output1));  // open: inborrow, borrow
  or or_8 (or_8_out, comparator_9_gt, comparator_9_eq);
  Comparator #(.mode("unsigned"), .width(64)) comparator_8 (
    .a(subtractor64bit_6_output1), .b({{23{1'b0}}, input2, {25{1'b0}}}), .gt(comparator_8_gt),
    .eq(comparator_8_eq));  // open: lt
  cbuffer64bit cbuffer64bit_8 (
    .buffer1(and_16_out[24]), .input1({{24{1'b0}}, input2, {24{1'b0}}}), .output1(cbuffer64bit_8_output1));
  and and_8 (and_16_out[24], or_8_out, not_1_out);
  Comparator #(.mode("unsigned"), .width(64)) comparator_9 (
    .a(subtractor64bit_7_output1), .b({{24{1'b0}}, input2, {24{1'b0}}}), .gt(comparator_9_gt),
    .eq(comparator_9_eq));  // open: lt
  // Probe on subtractor64bit_8_output1
  // Probe on subtractor64bit_8_output1
  subtractor64bit subtractor64bit_9 (
    .input1(subtractor64bit_8_output1), .input2(cbuffer64bit_9_output1), .output1(subtractor64bit_9_output1));  // open: inborrow, borrow
  cbuffer64bit cbuffer64bit_9 (
    .buffer1(and_16_out[23]), .input1({{25{1'b0}}, input2, {23{1'b0}}}), .output1(cbuffer64bit_9_output1));
  and and_9 (and_16_out[23], or_9_out, not_1_out);
  or or_9 (or_9_out, comparator_10_gt, comparator_10_eq);
  Comparator #(.mode("unsigned"), .width(64)) comparator_10 (
    .a(subtractor64bit_8_output1), .b({{25{1'b0}}, input2, {23{1'b0}}}), .gt(comparator_10_gt),
    .eq(comparator_10_eq));  // open: lt
  // Probe on subtractor64bit_9_output1
  // Probe on subtractor64bit_9_output1
  subtractor64bit subtractor64bit_10 (
    .input1(subtractor64bit_9_output1), .input2(cbuffer64bit_10_output1), .output1(subtractor64bit_10_output1));  // open: inborrow, borrow
  cbuffer64bit cbuffer64bit_10 (
    .buffer1(and_16_out[22]), .input1({{26{1'b0}}, input2, {22{1'b0}}}), .output1(cbuffer64bit_10_output1));
  and and_10 (and_16_out[22], or_10_out, not_1_out);
  or or_10 (or_10_out, comparator_11_gt, comparator_11_eq);
  Comparator #(.mode("unsigned"), .width(64)) comparator_11 (
    .a(subtractor64bit_9_output1), .b({{26{1'b0}}, input2, {22{1'b0}}}), .gt(comparator_11_gt),
    .eq(comparator_11_eq));  // open: lt
  // Probe on subtractor64bit_10_output1
  // Probe on subtractor64bit_10_output1
  subtractor64bit subtractor64bit_11 (
    .input1(subtractor64bit_10_output1), .input2(cbuffer64bit_11_output1),
    .output1(subtractor64bit_11_output1));  // open: inborrow, borrow
  cbuffer64bit cbuffer64bit_11 (
    .buffer1(and_16_out[21]), .input1({{27{1'b0}}, input2, {21{1'b0}}}), .output1(cbuffer64bit_11_output1));
  and and_11 (and_16_out[21], or_11_out, not_1_out);
  or or_11 (or_11_out, comparator_12_gt, comparator_12_eq);
  // Probe on subtractor64bit_11_output1
  // Probe on subtractor64bit_11_output1
  subtractor64bit subtractor64bit_12 (
    .input1(subtractor64bit_11_output1), .input2(cbuffer64bit_12_output1),
    .output1(subtractor64bit_12_output1));  // open: inborrow, borrow
  or or_12 (or_12_out, comparator_13_gt, comparator_13_eq);
  Comparator #(.mode("unsigned"), .width(64)) comparator_12 (
    .a(subtractor64bit_10_output1), .b({{27{1'b0}}, input2, {21{1'b0}}}), .gt(comparator_12_gt),
    .eq(comparator_12_eq));  // open: lt
  cbuffer64bit cbuffer64bit_12 (
    .buffer1(and_16_out[20]), .input1({{28{1'b0}}, input2, {20{1'b0}}}), .output1(cbuffer64bit_12_output1));
  and and_12 (and_16_out[20], or_12_out, not_1_out);
  Comparator #(.mode("unsigned"), .width(64)) comparator_13 (
    .a(subtractor64bit_11_output1), .b({{28{1'b0}}, input2, {20{1'b0}}}), .gt(comparator_13_gt),
    .eq(comparator_13_eq));  // open: lt
  // Probe on subtractor64bit_12_output1
  // Probe on subtractor64bit_12_output1
  subtractor64bit subtractor64bit_13 (
    .input1(subtractor64bit_12_output1), .input2(cbuffer64bit_13_output1),
    .output1(subtractor64bit_13_output1));  // open: inborrow, borrow
  cbuffer64bit cbuffer64bit_13 (
    .buffer1(and_16_out[19]), .input1({{29{1'b0}}, input2, {19{1'b0}}}), .output1(cbuffer64bit_13_output1));
  and and_13 (and_16_out[19], or_13_out, not_1_out);
  or or_13 (or_13_out, comparator_14_gt, comparator_14_eq);
  Comparator #(.mode("unsigned"), .width(64)) comparator_14 (
    .a(subtractor64bit_12_output1), .b({{29{1'b0}}, input2, {19{1'b0}}}), .gt(comparator_14_gt),
    .eq(comparator_14_eq));  // open: lt
  // Probe on subtractor64bit_13_output1
  // Probe on subtractor64bit_13_output1
  subtractor64bit subtractor64bit_14 (
    .input1(subtractor64bit_13_output1), .input2(cbuffer64bit_14_output1),
    .output1(subtractor64bit_14_output1));  // open: inborrow, borrow
  cbuffer64bit cbuffer64bit_14 (
    .buffer1(and_16_out[18]), .input1({{30{1'b0}}, input2, {18{1'b0}}}), .output1(cbuffer64bit_14_output1));
  and and_14 (and_16_out[18], or_14_out, not_1_out);
  or or_14 (or_14_out, comparator_15_gt, comparator_15_eq);
  Comparator #(.mode("unsigned"), .width(64)) comparator_15 (
    .a(subtractor64bit_13_output1), .b({{30{1'b0}}, input2, {18{1'b0}}}), .gt(comparator_15_gt),
    .eq(comparator_15_eq));  // open: lt
  // Probe on subtractor64bit_14_output1
  // Probe on subtractor64bit_14_output1
  subtractor64bit subtractor64bit_15 (
    .input1(subtractor64bit_14_output1), .input2(cbuffer64bit_15_output1),
    .output1(subtractor64bit_15_output1));  // open: inborrow, borrow
  cbuffer64bit cbuffer64bit_15 (
    .buffer1(and_16_out[17]), .input1({{31{1'b0}}, input2, {17{1'b0}}}), .output1(cbuffer64bit_15_output1));
  and and_15 (and_16_out[17], or_15_out, not_1_out);
  or or_15 (or_15_out, comparator_16_gt, comparator_16_eq);
  // Probe on subtractor64bit_15_output1
  // Probe on subtractor64bit_15_output1
  subtractor64bit subtractor64bit_16 (
    .input1(subtractor64bit_15_output1), .input2(cbuffer64bit_16_output1),
    .output1(subtractor64bit_16_output1));  // open: inborrow, borrow
  or or_16 (or_16_out, comparator_17_gt, comparator_17_eq);
  Comparator #(.mode("unsigned"), .width(64)) comparator_16 (
    .a(subtractor64bit_14_output1), .b({{31{1'b0}}, input2, {17{1'b0}}}), .gt(comparator_16_gt),
    .eq(comparator_16_eq));  // open: lt
  cbuffer64bit cbuffer64bit_16 (
    .buffer1(and_16_out[16]), .input1({{32{1'b0}}, input2, {16{1'b0}}}), .output1(cbuffer64bit_16_output1));
  and and_16 (and_16_out[16], or_16_out, not_1_out);
  Comparator #(.mode("unsigned"), .width(64)) comparator_17 (
    .a(subtractor64bit_15_output1), .b({{32{1'b0}}, input2, {16{1'b0}}}), .gt(comparator_17_gt),
    .eq(comparator_17_eq));  // open: lt
  // Probe on subtractor64bit_16_output1
  // Probe on subtractor64bit_16_output1
  subtractor64bit subtractor64bit_17 (
    .input1(subtractor64bit_16_output1), .input2(cbuffer64bit_17_output1),
    .output1(subtractor64bit_17_output1));  // open: inborrow, borrow
  cbuffer64bit cbuffer64bit_17 (
    .buffer1(output1[15]), .input1({{33{1'b0}}, input2, {15{1'b0}}}), .output1(cbuffer64bit_17_output1));
  and and_17 (output1[15], or_17_out, not_1_out);
  or or_17 (or_17_out, comparator_18_gt, comparator_18_eq);
  Comparator #(.mode("unsigned"), .width(64)) comparator_18 (
    .a(subtractor64bit_16_output1), .b({{33{1'b0}}, input2, {15{1'b0}}}), .gt(comparator_18_gt),
    .eq(comparator_18_eq));  // open: lt
  // Probe on subtractor64bit_17_output1
  // Probe on subtractor64bit_17_output1
  subtractor64bit subtractor64bit_18 (
    .input1(subtractor64bit_17_output1), .input2(cbuffer64bit_18_output1),
    .output1(subtractor64bit_18_output1));  // open: inborrow, borrow
  cbuffer64bit cbuffer64bit_18 (
    .buffer1(output1[14]), .input1({{34{1'b0}}, input2, {14{1'b0}}}), .output1(cbuffer64bit_18_output1));
  and and_18 (output1[14], or_18_out, not_1_out);
  or or_18 (or_18_out, comparator_19_gt, comparator_19_eq);
  Comparator #(.mode("unsigned"), .width(64)) comparator_19 (
    .a(subtractor64bit_17_output1), .b({{34{1'b0}}, input2, {14{1'b0}}}), .gt(comparator_19_gt),
    .eq(comparator_19_eq));  // open: lt
  // Probe on subtractor64bit_18_output1
  // Probe on subtractor64bit_18_output1
  subtractor64bit subtractor64bit_19 (
    .input1(subtractor64bit_18_output1), .input2(cbuffer64bit_19_output1),
    .output1(subtractor64bit_19_output1));  // open: inborrow, borrow
  cbuffer64bit cbuffer64bit_19 (
    .buffer1(output1[13]), .input1({{35{1'b0}}, input2, {13{1'b0}}}), .output1(cbuffer64bit_19_output1));
  and and_19 (output1[13], or_19_out, not_1_out);
  or or_19 (or_19_out, comparator_20_gt, comparator_20_eq);
  // Probe on subtractor64bit_19_output1
  // Probe on subtractor64bit_19_output1
  subtractor64bit subtractor64bit_20 (
    .input1(subtractor64bit_19_output1), .input2(cbuffer64bit_20_output1),
    .output1(subtractor64bit_20_output1));  // open: inborrow, borrow
  or or_20 (or_20_out, comparator_21_gt, comparator_21_eq);
  Comparator #(.mode("unsigned"), .width(64)) comparator_20 (
    .a(subtractor64bit_18_output1), .b({{35{1'b0}}, input2, {13{1'b0}}}), .gt(comparator_20_gt),
    .eq(comparator_20_eq));  // open: lt
  cbuffer64bit cbuffer64bit_20 (
    .buffer1(output1[12]), .input1({{36{1'b0}}, input2, {12{1'b0}}}), .output1(cbuffer64bit_20_output1));
  and and_20 (output1[12], or_20_out, not_1_out);
  Comparator #(.mode("unsigned"), .width(64)) comparator_21 (
    .a(subtractor64bit_19_output1), .b({{36{1'b0}}, input2, {12{1'b0}}}), .gt(comparator_21_gt),
    .eq(comparator_21_eq));  // open: lt
  // Probe on subtractor64bit_20_output1
  // Probe on subtractor64bit_20_output1
  subtractor64bit subtractor64bit_21 (
    .input1(subtractor64bit_20_output1), .input2(cbuffer64bit_21_output1),
    .output1(subtractor64bit_21_output1));  // open: inborrow, borrow
  cbuffer64bit cbuffer64bit_21 (
    .buffer1(output1[11]), .input1({{37{1'b0}}, input2, {11{1'b0}}}), .output1(cbuffer64bit_21_output1));
  and and_21 (output1[11], or_21_out, not_1_out);
  or or_21 (or_21_out, comparator_22_gt, comparator_22_eq);
  Comparator #(.mode("unsigned"), .width(64)) comparator_22 (
    .a(subtractor64bit_20_output1), .b({{37{1'b0}}, input2, {11{1'b0}}}), .gt(comparator_22_gt),
    .eq(comparator_22_eq));  // open: lt
  // Probe on subtractor64bit_21_output1
  // Probe on subtractor64bit_21_output1
  subtractor64bit subtractor64bit_22 (
    .input1(subtractor64bit_21_output1), .input2(cbuffer64bit_22_output1),
    .output1(subtractor64bit_22_output1));  // open: inborrow, borrow
  cbuffer64bit cbuffer64bit_22 (
    .buffer1(output1[10]), .input1({{38{1'b0}}, input2, {10{1'b0}}}), .output1(cbuffer64bit_22_output1));
  and and_22 (output1[10], or_22_out, not_1_out);
  or or_22 (or_22_out, comparator_23_gt, comparator_23_eq);
  Comparator #(.mode("unsigned"), .width(64)) comparator_23 (
    .a(subtractor64bit_21_output1), .b({{38{1'b0}}, input2, {10{1'b0}}}), .gt(comparator_23_gt),
    .eq(comparator_23_eq));  // open: lt
  // Probe on subtractor64bit_22_output1
  // Probe on subtractor64bit_22_output1
  subtractor64bit subtractor64bit_23 (
    .input1(subtractor64bit_22_output1), .input2(cbuffer64bit_23_output1),
    .output1(subtractor64bit_23_output1));  // open: inborrow, borrow
  cbuffer64bit cbuffer64bit_23 (
    .buffer1(output1[9]), .input1({{39{1'b0}}, input2, {9{1'b0}}}), .output1(cbuffer64bit_23_output1));
  and and_23 (output1[9], or_23_out, not_1_out);
  or or_23 (or_23_out, comparator_24_gt, comparator_24_eq);
  // Probe on subtractor64bit_23_output1
  // Probe on subtractor64bit_23_output1
  subtractor64bit subtractor64bit_24 (
    .input1(subtractor64bit_23_output1), .input2(cbuffer64bit_24_output1),
    .output1(subtractor64bit_24_output1));  // open: inborrow, borrow
  or or_24 (or_24_out, comparator_25_gt, comparator_25_eq);
  Comparator #(.mode("unsigned"), .width(64)) comparator_24 (
    .a(subtractor64bit_22_output1), .b({{39{1'b0}}, input2, {9{1'b0}}}), .gt(comparator_24_gt),
    .eq(comparator_24_eq));  // open: lt
  cbuffer64bit cbuffer64bit_24 (
    .buffer1(output1[8]), .input1({{40{1'b0}}, input2, {8{1'b0}}}), .output1(cbuffer64bit_24_output1));
  and and_24 (output1[8], or_24_out, not_1_out);
  Comparator #(.mode("unsigned"), .width(64)) comparator_25 (
    .a(subtractor64bit_23_output1), .b({{40{1'b0}}, input2, {8{1'b0}}}), .gt(comparator_25_gt),
    .eq(comparator_25_eq));  // open: lt
  // Probe on subtractor64bit_24_output1
  // Probe on subtractor64bit_24_output1
  subtractor64bit subtractor64bit_25 (
    .input1(subtractor64bit_24_output1), .input2(cbuffer64bit_25_output1),
    .output1(subtractor64bit_25_output1));  // open: inborrow, borrow
  cbuffer64bit cbuffer64bit_25 (
    .buffer1(output1[7]), .input1({{41{1'b0}}, input2, {7{1'b0}}}), .output1(cbuffer64bit_25_output1));
  and and_25 (output1[7], or_25_out, not_1_out);
  or or_25 (or_25_out, comparator_26_gt, comparator_26_eq);
  Comparator #(.mode("unsigned"), .width(64)) comparator_26 (
    .a(subtractor64bit_24_output1), .b({{41{1'b0}}, input2, {7{1'b0}}}), .gt(comparator_26_gt),
    .eq(comparator_26_eq));  // open: lt
  // Probe on subtractor64bit_25_output1
  // Probe on subtractor64bit_25_output1
  subtractor64bit subtractor64bit_26 (
    .input1(subtractor64bit_25_output1), .input2(cbuffer64bit_26_output1),
    .output1(subtractor64bit_26_output1));  // open: inborrow, borrow
  cbuffer64bit cbuffer64bit_26 (
    .buffer1(output1[6]), .input1({{42{1'b0}}, input2, {6{1'b0}}}), .output1(cbuffer64bit_26_output1));
  and and_26 (output1[6], or_26_out, not_1_out);
  or or_26 (or_26_out, comparator_27_gt, comparator_27_eq);
  Comparator #(.mode("unsigned"), .width(64)) comparator_27 (
    .a(subtractor64bit_25_output1), .b({{42{1'b0}}, input2, {6{1'b0}}}), .gt(comparator_27_gt),
    .eq(comparator_27_eq));  // open: lt
  // Probe on subtractor64bit_26_output1
  // Probe on subtractor64bit_26_output1
  subtractor64bit subtractor64bit_27 (
    .input1(subtractor64bit_26_output1), .input2(cbuffer64bit_27_output1),
    .output1(subtractor64bit_27_output1));  // open: inborrow, borrow
  cbuffer64bit cbuffer64bit_27 (
    .buffer1(output1[5]), .input1({{43{1'b0}}, input2, {5{1'b0}}}), .output1(cbuffer64bit_27_output1));
  and and_27 (output1[5], or_27_out, not_1_out);
  or or_27 (or_27_out, comparator_28_gt, comparator_28_eq);
  // Probe on subtractor64bit_27_output1
  // Probe on subtractor64bit_27_output1
  subtractor64bit subtractor64bit_28 (
    .input1(subtractor64bit_27_output1), .input2(cbuffer64bit_28_output1),
    .output1(subtractor64bit_28_output1));  // open: inborrow, borrow
  or or_28 (or_28_out, comparator_29_gt, comparator_29_eq);
  Comparator #(.mode("unsigned"), .width(64)) comparator_28 (
    .a(subtractor64bit_26_output1), .b({{43{1'b0}}, input2, {5{1'b0}}}), .gt(comparator_28_gt),
    .eq(comparator_28_eq));  // open: lt
  cbuffer64bit cbuffer64bit_28 (
    .buffer1(output1[4]), .input1({{44{1'b0}}, input2, 4'b0000}), .output1(cbuffer64bit_28_output1));
  and and_28 (output1[4], or_28_out, not_1_out);
  Comparator #(.mode("unsigned"), .width(64)) comparator_29 (
    .a(subtractor64bit_27_output1), .b({{44{1'b0}}, input2, 4'b0000}), .gt(comparator_29_gt),
    .eq(comparator_29_eq));  // open: lt
  // Probe on subtractor64bit_28_output1
  // Probe on subtractor64bit_28_output1
  subtractor64bit subtractor64bit_29 (
    .input1(subtractor64bit_28_output1), .input2(cbuffer64bit_29_output1),
    .output1(subtractor64bit_29_output1));  // open: inborrow, borrow
  cbuffer64bit cbuffer64bit_29 (
    .buffer1(output1[3]), .input1({{45{1'b0}}, input2, 3'b000}), .output1(cbuffer64bit_29_output1));
  and and_29 (output1[3], or_29_out, not_1_out);
  or or_29 (or_29_out, comparator_30_gt, comparator_30_eq);
  Comparator #(.mode("unsigned"), .width(64)) comparator_30 (
    .a(subtractor64bit_28_output1), .b({{45{1'b0}}, input2, 3'b000}), .gt(comparator_30_gt),
    .eq(comparator_30_eq));  // open: lt
  // Probe on subtractor64bit_29_output1
  // Probe on subtractor64bit_29_output1
  subtractor64bit subtractor64bit_30 (
    .input1(subtractor64bit_29_output1), .input2(cbuffer64bit_30_output1),
    .output1(subtractor64bit_30_output1));  // open: inborrow, borrow
  cbuffer64bit cbuffer64bit_30 (
    .buffer1(output1[2]), .input1({{46{1'b0}}, input2, 2'b00}), .output1(cbuffer64bit_30_output1));
  and and_30 (output1[2], or_30_out, not_1_out);
  or or_30 (or_30_out, comparator_31_gt, comparator_31_eq);
  Comparator #(.mode("unsigned"), .width(64)) comparator_31 (
    .a(subtractor64bit_29_output1), .b({{46{1'b0}}, input2, 2'b00}), .gt(comparator_31_gt),
    .eq(comparator_31_eq));  // open: lt
  // Probe on subtractor64bit_30_output1
  // Probe on subtractor64bit_30_output1
  subtractor64bit subtractor64bit_31 (
    .input1(subtractor64bit_30_output1), .input2(cbuffer64bit_31_output1),
    .output1(subtractor64bit_31_output1));  // open: inborrow, borrow
  cbuffer64bit cbuffer64bit_31 (
    .buffer1(output1[1]), .input1({{47{1'b0}}, input2, 1'b0}), .output1(cbuffer64bit_31_output1));
  and and_31 (output1[1], or_31_out, not_1_out);
  or or_31 (or_31_out, comparator_32_gt, comparator_32_eq);
  // Probe on subtractor64bit_31_output1
  // Probe on subtractor64bit_31_output1
  subtractor64bit subtractor64bit_32 (
    .input1(subtractor64bit_31_output1), .input2(cbuffer64bit_32_output1),
    .output1({subtractor64bit_32_output1, remainder}));  // open: inborrow, borrow
  or or_32 (or_32_out, comparator_33_gt, comparator_33_eq);
  Comparator #(.mode("unsigned"), .width(64)) comparator_32 (
    .a(subtractor64bit_30_output1), .b({{47{1'b0}}, input2, 1'b0}), .gt(comparator_32_gt),
    .eq(comparator_32_eq));  // open: lt
  cbuffer64bit cbuffer64bit_32 (.buffer1(output1[0]), .input1({{48{1'b0}}, input2}), .output1(cbuffer64bit_32_output1));
  and and_32 (output1[0], or_32_out, not_1_out);
  Comparator #(.mode("unsigned"), .width(64)) comparator_33 (
    .a(subtractor64bit_31_output1), .b({{48{1'b0}}, input2}), .gt(comparator_33_gt), .eq(comparator_33_eq));  // open: lt
  // Probe on {subtractor64bit_32_output1, remainder}
  // Probe on {subtractor64bit_32_output1, remainder}
  // Probe on {{32{1'b0}}, and_16_out, output1}
  // Probe on {{32{1'b0}}, and_16_out, output1}
  // Probe on remainder
  // Probe on remainder
  // Probe on output1
  // Probe on output1

  // Notes on the sheet:
  //   inupper: initial=0xd3
  //   input2: initial=0xaf
  //   input1: initial=0xf74e
endmodule
module divideru32bit (
  input  [31:0] inupper,
  input  [31:0] input1,
  input  [31:0] input2,
  output [31:0] remainder,
  output [31:0] output1
);

  wire comparator_1_eq, comparator_2_eq, comparator_2_gt, comparator_3_eq, comparator_3_gt, comparator_4_eq,
       comparator_4_gt, comparator_5_eq, comparator_5_gt, comparator_6_eq, comparator_6_gt, comparator_7_eq,
       comparator_7_gt, comparator_8_eq, comparator_8_gt, comparator_9_eq, comparator_9_gt, comparator_10_eq,
       comparator_10_gt, comparator_11_eq, comparator_11_gt, comparator_12_eq, comparator_12_gt,
       comparator_13_eq, comparator_13_gt, comparator_14_eq, comparator_14_gt, comparator_15_eq,
       comparator_15_gt, comparator_16_eq, comparator_16_gt, comparator_17_eq, comparator_17_gt,
       comparator_18_eq, comparator_18_gt, comparator_19_eq, comparator_19_gt, comparator_20_eq,
       comparator_20_gt, comparator_21_eq, comparator_21_gt, comparator_22_eq, comparator_22_gt,
       comparator_23_eq, comparator_23_gt, comparator_24_eq, comparator_24_gt, comparator_25_eq,
       comparator_25_gt, comparator_26_eq, comparator_26_gt, comparator_27_eq, comparator_27_gt,
       comparator_28_eq, comparator_28_gt, comparator_29_eq, comparator_29_gt, comparator_30_eq,
       comparator_30_gt, comparator_31_eq, comparator_31_gt, comparator_32_eq, comparator_32_gt,
       comparator_33_eq, comparator_33_gt, not_1_out, or_1_out, or_2_out, or_3_out, or_4_out, or_5_out,
       or_6_out, or_7_out, or_8_out, or_9_out, or_10_out, or_11_out, or_12_out, or_13_out, or_14_out,
       or_15_out, or_16_out, or_17_out, or_18_out, or_19_out, or_20_out, or_21_out, or_22_out, or_23_out,
       or_24_out, or_25_out, or_26_out, or_27_out, or_28_out, or_29_out, or_30_out, or_31_out, or_32_out;
  wire [31:0] divider_1_out, divider_1_rem;
  wire [61:18] undriven_15;
  wire [61:29] undriven_3;
  wire [61:30] undriven_2;
  wire [61:36] undriven_16, undriven_17, undriven_18, undriven_19, undriven_20, undriven_21, undriven_22,
       undriven_23, undriven_24, undriven_25, undriven_26, undriven_27, undriven_28, undriven_29,
       undriven_30, undriven_31, undriven_32, undriven_33, undriven_34;
  wire [61:48] undriven_4, undriven_5, undriven_6, undriven_7, undriven_8, undriven_10, undriven_11,
       undriven_12, undriven_13, undriven_14;
  wire [63:0] cbuffer64bit_1_output1, cbuffer64bit_2_output1, cbuffer64bit_3_output1, cbuffer64bit_4_output1,
       cbuffer64bit_5_output1, cbuffer64bit_6_output1, cbuffer64bit_7_output1, cbuffer64bit_8_output1,
       cbuffer64bit_9_output1, cbuffer64bit_10_output1, cbuffer64bit_11_output1, cbuffer64bit_12_output1,
       cbuffer64bit_13_output1, cbuffer64bit_14_output1, cbuffer64bit_15_output1, cbuffer64bit_16_output1,
       cbuffer64bit_17_output1, cbuffer64bit_18_output1, cbuffer64bit_19_output1, cbuffer64bit_20_output1,
       cbuffer64bit_21_output1, cbuffer64bit_22_output1, cbuffer64bit_23_output1, cbuffer64bit_24_output1,
       cbuffer64bit_25_output1, cbuffer64bit_26_output1, cbuffer64bit_27_output1, cbuffer64bit_28_output1,
       cbuffer64bit_29_output1, cbuffer64bit_30_output1, cbuffer64bit_31_output1, cbuffer64bit_32_output1,
       subtractor64bit_1_output1, subtractor64bit_2_output1, subtractor64bit_3_output1,
       subtractor64bit_4_output1, subtractor64bit_5_output1, subtractor64bit_6_output1,
       subtractor64bit_7_output1, subtractor64bit_8_output1, subtractor64bit_9_output1,
       subtractor64bit_10_output1, subtractor64bit_11_output1, subtractor64bit_12_output1,
       subtractor64bit_13_output1, subtractor64bit_14_output1, subtractor64bit_15_output1,
       subtractor64bit_16_output1, subtractor64bit_17_output1, subtractor64bit_18_output1,
       subtractor64bit_19_output1, subtractor64bit_20_output1, subtractor64bit_21_output1,
       subtractor64bit_22_output1, subtractor64bit_23_output1, subtractor64bit_24_output1,
       subtractor64bit_25_output1, subtractor64bit_26_output1, subtractor64bit_27_output1,
       subtractor64bit_28_output1, subtractor64bit_29_output1, subtractor64bit_30_output1,
       subtractor64bit_31_output1;
  wire [63:16] undriven;
  wire [63:32] subtractor64bit_32_output1, undriven_9;

  // Probe on divider_1_out
  // Probe on divider_1_out
  Divider #(.width(32)) divider_1 (.a(input1), .b(input2), .out(divider_1_out), .upper(inupper), .rem(divider_1_rem));
  // Probe on divider_1_rem
  // Probe on divider_1_rem
  // Probe on inupper
  // Probe on inupper
  // Probe on input1
  // Probe on input1
  // Probe on {undriven_9, input2}
  // Probe on {undriven_9, input2}
  not not_1 (not_1_out, comparator_1_eq);
  Comparator #(.mode("unsigned"), .width(64)) comparator_1 (
    .a({undriven_9, input2}), .b({undriven, {16{1'b0}}}), .eq(comparator_1_eq));  // open: gt, lt
  // Probe on {{32{1'b0}}, inupper[15:0], input1[15:0]}
  // Probe on {{32{1'b0}}, inupper[15:0], input1[15:0]}
  subtractor64bit subtractor64bit_1 (
    .input1({{32{1'b0}}, inupper[15:0], input1[15:0]}), .input2(cbuffer64bit_1_output1),
    .output1(subtractor64bit_1_output1));  // open: inborrow, borrow
  cbuffer64bit cbuffer64bit_1 (
    .buffer1(output1[31]), .input1({2'b00, undriven_2[61:47], input2[15:0], {31{undriven_2[30]}}}),
    .output1(cbuffer64bit_1_output1));
  and and_1 (output1[31], or_1_out, not_1_out);
  or or_1 (or_1_out, comparator_2_gt, comparator_2_eq);
  Comparator #(.mode("unsigned"), .width(64)) comparator_2 (
    .a({{32{1'b0}}, inupper[15:0], input1[15:0]}),
    .b({2'b00, undriven_2[61:47], input2[15:0], {31{undriven_2[30]}}}), .gt(comparator_2_gt),
    .eq(comparator_2_eq));  // open: lt
  // Probe on subtractor64bit_1_output1
  // Probe on subtractor64bit_1_output1
  subtractor64bit subtractor64bit_2 (
    .input1(subtractor64bit_1_output1), .input2(cbuffer64bit_2_output1), .output1(subtractor64bit_2_output1));  // open: inborrow, borrow
  cbuffer64bit cbuffer64bit_2 (
    .buffer1(output1[30]), .input1({2'b00, undriven_3[61:46], input2[15:0], {30{undriven_3[29]}}}),
    .output1(cbuffer64bit_2_output1));
  and and_2 (output1[30], or_2_out, not_1_out);
  or or_2 (or_2_out, comparator_3_gt, comparator_3_eq);
  Comparator #(.mode("unsigned"), .width(64)) comparator_3 (
    .a(subtractor64bit_1_output1), .b({2'b00, undriven_3[61:46], input2[15:0], {30{undriven_3[29]}}}),
    .gt(comparator_3_gt), .eq(comparator_3_eq));  // open: lt
  // Probe on subtractor64bit_2_output1
  // Probe on subtractor64bit_2_output1
  subtractor64bit subtractor64bit_3 (
    .input1(subtractor64bit_2_output1), .input2(cbuffer64bit_3_output1), .output1(subtractor64bit_3_output1));  // open: inborrow, borrow
  cbuffer64bit cbuffer64bit_3 (
    .buffer1(output1[29]),
    .input1({2'b00, undriven_4, {3{undriven_4[48]}}, input2[15:0], {29{undriven_4[48]}}}),
    .output1(cbuffer64bit_3_output1));
  and and_3 (output1[29], or_3_out, not_1_out);
  or or_3 (or_3_out, comparator_4_gt, comparator_4_eq);
  // Probe on subtractor64bit_3_output1
  // Probe on subtractor64bit_3_output1
  subtractor64bit subtractor64bit_4 (
    .input1(subtractor64bit_3_output1), .input2(cbuffer64bit_4_output1), .output1(subtractor64bit_4_output1));  // open: inborrow, borrow
  or or_4 (or_4_out, comparator_5_gt, comparator_5_eq);
  Comparator #(.mode("unsigned"), .width(64)) comparator_4 (
    .a(subtractor64bit_2_output1),
    .b({2'b00, undriven_4, {3{undriven_4[48]}}, input2[15:0], {29{undriven_4[48]}}}), .gt(comparator_4_gt),
    .eq(comparator_4_eq));  // open: lt
  cbuffer64bit cbuffer64bit_4 (
    .buffer1(output1[28]),
    .input1({2'b00, undriven_5, {4{undriven_5[48]}}, input2[15:0], {28{undriven_5[48]}}}),
    .output1(cbuffer64bit_4_output1));
  and and_4 (output1[28], or_4_out, not_1_out);
  Comparator #(.mode("unsigned"), .width(64)) comparator_5 (
    .a(subtractor64bit_3_output1),
    .b({2'b00, undriven_5, {4{undriven_5[48]}}, input2[15:0], {28{undriven_5[48]}}}), .gt(comparator_5_gt),
    .eq(comparator_5_eq));  // open: lt
  // Probe on subtractor64bit_4_output1
  // Probe on subtractor64bit_4_output1
  subtractor64bit subtractor64bit_5 (
    .input1(subtractor64bit_4_output1), .input2(cbuffer64bit_5_output1), .output1(subtractor64bit_5_output1));  // open: inborrow, borrow
  cbuffer64bit cbuffer64bit_5 (
    .buffer1(output1[27]),
    .input1({2'b00, undriven_6, {5{undriven_6[48]}}, input2[15:0], {27{undriven_6[48]}}}),
    .output1(cbuffer64bit_5_output1));
  and and_5 (output1[27], or_5_out, not_1_out);
  or or_5 (or_5_out, comparator_6_gt, comparator_6_eq);
  Comparator #(.mode("unsigned"), .width(64)) comparator_6 (
    .a(subtractor64bit_4_output1),
    .b({2'b00, undriven_6, {5{undriven_6[48]}}, input2[15:0], {27{undriven_6[48]}}}), .gt(comparator_6_gt),
    .eq(comparator_6_eq));  // open: lt
  // Probe on subtractor64bit_5_output1
  // Probe on subtractor64bit_5_output1
  subtractor64bit subtractor64bit_6 (
    .input1(subtractor64bit_5_output1), .input2(cbuffer64bit_6_output1), .output1(subtractor64bit_6_output1));  // open: inborrow, borrow
  cbuffer64bit cbuffer64bit_6 (
    .buffer1(output1[26]),
    .input1({2'b00, undriven_7, {6{undriven_7[48]}}, input2[15:0], {26{undriven_7[48]}}}),
    .output1(cbuffer64bit_6_output1));
  and and_6 (output1[26], or_6_out, not_1_out);
  or or_6 (or_6_out, comparator_7_gt, comparator_7_eq);
  Comparator #(.mode("unsigned"), .width(64)) comparator_7 (
    .a(subtractor64bit_5_output1),
    .b({2'b00, undriven_7, {6{undriven_7[48]}}, input2[15:0], {26{undriven_7[48]}}}), .gt(comparator_7_gt),
    .eq(comparator_7_eq));  // open: lt
  // Probe on subtractor64bit_6_output1
  // Probe on subtractor64bit_6_output1
  subtractor64bit subtractor64bit_7 (
    .input1(subtractor64bit_6_output1), .input2(cbuffer64bit_7_output1), .output1(subtractor64bit_7_output1));  // open: inborrow, borrow
  cbuffer64bit cbuffer64bit_7 (
    .buffer1(output1[25]),
    .input1({2'b00, undriven_8, {7{undriven_8[48]}}, input2[15:0], {25{undriven_8[48]}}}),
    .output1(cbuffer64bit_7_output1));
  and and_7 (output1[25], or_7_out, not_1_out);
  or or_7 (or_7_out, comparator_8_gt, comparator_8_eq);
  // Probe on subtractor64bit_7_output1
  // Probe on subtractor64bit_7_output1
  subtractor64bit subtractor64bit_8 (
    .input1(subtractor64bit_7_output1), .input2(cbuffer64bit_8_output1), .output1(subtractor64bit_8_output1));  // open: inborrow, borrow
  or or_8 (or_8_out, comparator_9_gt, comparator_9_eq);
  Comparator #(.mode("unsigned"), .width(64)) comparator_8 (
    .a(subtractor64bit_6_output1),
    .b({2'b00, undriven_8, {7{undriven_8[48]}}, input2[15:0], {25{undriven_8[48]}}}), .gt(comparator_8_gt),
    .eq(comparator_8_eq));  // open: lt
  cbuffer64bit cbuffer64bit_8 (
    .buffer1(output1[24]),
    .input1({2'b00, undriven_10, {8{undriven_10[48]}}, input2[15:0], {24{undriven_10[48]}}}),
    .output1(cbuffer64bit_8_output1));
  and and_8 (output1[24], or_8_out, not_1_out);
  Comparator #(.mode("unsigned"), .width(64)) comparator_9 (
    .a(subtractor64bit_7_output1),
    .b({2'b00, undriven_10, {8{undriven_10[48]}}, input2[15:0], {24{undriven_10[48]}}}),
    .gt(comparator_9_gt), .eq(comparator_9_eq));  // open: lt
  // Probe on subtractor64bit_8_output1
  // Probe on subtractor64bit_8_output1
  subtractor64bit subtractor64bit_9 (
    .input1(subtractor64bit_8_output1), .input2(cbuffer64bit_9_output1), .output1(subtractor64bit_9_output1));  // open: inborrow, borrow
  cbuffer64bit cbuffer64bit_9 (
    .buffer1(output1[23]),
    .input1({2'b00, undriven_11, {9{undriven_11[48]}}, input2[15:0], {23{undriven_11[48]}}}),
    .output1(cbuffer64bit_9_output1));
  and and_9 (output1[23], or_9_out, not_1_out);
  or or_9 (or_9_out, comparator_10_gt, comparator_10_eq);
  Comparator #(.mode("unsigned"), .width(64)) comparator_10 (
    .a(subtractor64bit_8_output1),
    .b({2'b00, undriven_11, {9{undriven_11[48]}}, input2[15:0], {23{undriven_11[48]}}}),
    .gt(comparator_10_gt), .eq(comparator_10_eq));  // open: lt
  // Probe on subtractor64bit_9_output1
  // Probe on subtractor64bit_9_output1
  subtractor64bit subtractor64bit_10 (
    .input1(subtractor64bit_9_output1), .input2(cbuffer64bit_10_output1), .output1(subtractor64bit_10_output1));  // open: inborrow, borrow
  cbuffer64bit cbuffer64bit_10 (
    .buffer1(output1[22]),
    .input1({2'b00, undriven_12, {10{undriven_12[48]}}, input2[15:0], {22{undriven_12[48]}}}),
    .output1(cbuffer64bit_10_output1));
  and and_10 (output1[22], or_10_out, not_1_out);
  or or_10 (or_10_out, comparator_11_gt, comparator_11_eq);
  Comparator #(.mode("unsigned"), .width(64)) comparator_11 (
    .a(subtractor64bit_9_output1),
    .b({2'b00, undriven_12, {10{undriven_12[48]}}, input2[15:0], {22{undriven_12[48]}}}),
    .gt(comparator_11_gt), .eq(comparator_11_eq));  // open: lt
  // Probe on subtractor64bit_10_output1
  // Probe on subtractor64bit_10_output1
  subtractor64bit subtractor64bit_11 (
    .input1(subtractor64bit_10_output1), .input2(cbuffer64bit_11_output1),
    .output1(subtractor64bit_11_output1));  // open: inborrow, borrow
  cbuffer64bit cbuffer64bit_11 (
    .buffer1(output1[21]),
    .input1({2'b00, undriven_13, {11{undriven_13[48]}}, input2[15:0], {21{undriven_13[48]}}}),
    .output1(cbuffer64bit_11_output1));
  and and_11 (output1[21], or_11_out, not_1_out);
  or or_11 (or_11_out, comparator_12_gt, comparator_12_eq);
  // Probe on subtractor64bit_11_output1
  // Probe on subtractor64bit_11_output1
  subtractor64bit subtractor64bit_12 (
    .input1(subtractor64bit_11_output1), .input2(cbuffer64bit_12_output1),
    .output1(subtractor64bit_12_output1));  // open: inborrow, borrow
  or or_12 (or_12_out, comparator_13_gt, comparator_13_eq);
  Comparator #(.mode("unsigned"), .width(64)) comparator_12 (
    .a(subtractor64bit_10_output1),
    .b({2'b00, undriven_13, {11{undriven_13[48]}}, input2[15:0], {21{undriven_13[48]}}}),
    .gt(comparator_12_gt), .eq(comparator_12_eq));  // open: lt
  cbuffer64bit cbuffer64bit_12 (
    .buffer1(output1[20]),
    .input1({2'b00, undriven_14, {12{undriven_14[48]}}, input2[15:0], {20{undriven_14[48]}}}),
    .output1(cbuffer64bit_12_output1));
  and and_12 (output1[20], or_12_out, not_1_out);
  Comparator #(.mode("unsigned"), .width(64)) comparator_13 (
    .a(subtractor64bit_11_output1),
    .b({2'b00, undriven_14, {12{undriven_14[48]}}, input2[15:0], {20{undriven_14[48]}}}),
    .gt(comparator_13_gt), .eq(comparator_13_eq));  // open: lt
  // Probe on subtractor64bit_12_output1
  // Probe on subtractor64bit_12_output1
  subtractor64bit subtractor64bit_13 (
    .input1(subtractor64bit_12_output1), .input2(cbuffer64bit_13_output1),
    .output1(subtractor64bit_13_output1));  // open: inborrow, borrow
  cbuffer64bit cbuffer64bit_13 (
    .buffer1(output1[19]), .input1({2'b00, undriven_15[61:35], input2[15:0], {19{undriven_15[18]}}}),
    .output1(cbuffer64bit_13_output1));
  and and_13 (output1[19], or_13_out, not_1_out);
  or or_13 (or_13_out, comparator_14_gt, comparator_14_eq);
  Comparator #(.mode("unsigned"), .width(64)) comparator_14 (
    .a(subtractor64bit_12_output1), .b({2'b00, undriven_15[61:35], input2[15:0], {19{undriven_15[18]}}}),
    .gt(comparator_14_gt), .eq(comparator_14_eq));  // open: lt
  // Probe on subtractor64bit_13_output1
  // Probe on subtractor64bit_13_output1
  subtractor64bit subtractor64bit_14 (
    .input1(subtractor64bit_13_output1), .input2(cbuffer64bit_14_output1),
    .output1(subtractor64bit_14_output1));  // open: inborrow, borrow
  cbuffer64bit cbuffer64bit_14 (
    .buffer1(output1[18]),
    .input1({2'b00, undriven_16, {2{undriven_16[36]}}, input2[15:0], {18{undriven_16[36]}}}),
    .output1(cbuffer64bit_14_output1));
  and and_14 (output1[18], or_14_out, not_1_out);
  or or_14 (or_14_out, comparator_15_gt, comparator_15_eq);
  Comparator #(.mode("unsigned"), .width(64)) comparator_15 (
    .a(subtractor64bit_13_output1),
    .b({2'b00, undriven_16, {2{undriven_16[36]}}, input2[15:0], {18{undriven_16[36]}}}),
    .gt(comparator_15_gt), .eq(comparator_15_eq));  // open: lt
  // Probe on subtractor64bit_14_output1
  // Probe on subtractor64bit_14_output1
  subtractor64bit subtractor64bit_15 (
    .input1(subtractor64bit_14_output1), .input2(cbuffer64bit_15_output1),
    .output1(subtractor64bit_15_output1));  // open: inborrow, borrow
  cbuffer64bit cbuffer64bit_15 (
    .buffer1(output1[17]),
    .input1({2'b00, undriven_17, {3{undriven_17[36]}}, input2[15:0], {17{undriven_17[36]}}}),
    .output1(cbuffer64bit_15_output1));
  and and_15 (output1[17], or_15_out, not_1_out);
  or or_15 (or_15_out, comparator_16_gt, comparator_16_eq);
  // Probe on subtractor64bit_15_output1
  // Probe on subtractor64bit_15_output1
  subtractor64bit subtractor64bit_16 (
    .input1(subtractor64bit_15_output1), .input2(cbuffer64bit_16_output1),
    .output1(subtractor64bit_16_output1));  // open: inborrow, borrow
  or or_16 (or_16_out, comparator_17_gt, comparator_17_eq);
  Comparator #(.mode("unsigned"), .width(64)) comparator_16 (
    .a(subtractor64bit_14_output1),
    .b({2'b00, undriven_17, {3{undriven_17[36]}}, input2[15:0], {17{undriven_17[36]}}}),
    .gt(comparator_16_gt), .eq(comparator_16_eq));  // open: lt
  cbuffer64bit cbuffer64bit_16 (
    .buffer1(output1[16]),
    .input1({2'b00, undriven_18, {4{undriven_18[36]}}, input2[15:0], {16{undriven_18[36]}}}),
    .output1(cbuffer64bit_16_output1));
  and and_16 (output1[16], or_16_out, not_1_out);
  Comparator #(.mode("unsigned"), .width(64)) comparator_17 (
    .a(subtractor64bit_15_output1),
    .b({2'b00, undriven_18, {4{undriven_18[36]}}, input2[15:0], {16{undriven_18[36]}}}),
    .gt(comparator_17_gt), .eq(comparator_17_eq));  // open: lt
  // Probe on subtractor64bit_16_output1
  // Probe on subtractor64bit_16_output1
  subtractor64bit subtractor64bit_17 (
    .input1(subtractor64bit_16_output1), .input2(cbuffer64bit_17_output1),
    .output1(subtractor64bit_17_output1));  // open: inborrow, borrow
  cbuffer64bit cbuffer64bit_17 (
    .buffer1(output1[15]),
    .input1({2'b00, undriven_19, {5{undriven_19[36]}}, input2[15:0], {15{undriven_19[36]}}}),
    .output1(cbuffer64bit_17_output1));
  and and_17 (output1[15], or_17_out, not_1_out);
  or or_17 (or_17_out, comparator_18_gt, comparator_18_eq);
  Comparator #(.mode("unsigned"), .width(64)) comparator_18 (
    .a(subtractor64bit_16_output1),
    .b({2'b00, undriven_19, {5{undriven_19[36]}}, input2[15:0], {15{undriven_19[36]}}}),
    .gt(comparator_18_gt), .eq(comparator_18_eq));  // open: lt
  // Probe on subtractor64bit_17_output1
  // Probe on subtractor64bit_17_output1
  subtractor64bit subtractor64bit_18 (
    .input1(subtractor64bit_17_output1), .input2(cbuffer64bit_18_output1),
    .output1(subtractor64bit_18_output1));  // open: inborrow, borrow
  cbuffer64bit cbuffer64bit_18 (
    .buffer1(output1[14]),
    .input1({2'b00, undriven_20, {6{undriven_20[36]}}, input2[15:0], {14{undriven_20[36]}}}),
    .output1(cbuffer64bit_18_output1));
  and and_18 (output1[14], or_18_out, not_1_out);
  or or_18 (or_18_out, comparator_19_gt, comparator_19_eq);
  Comparator #(.mode("unsigned"), .width(64)) comparator_19 (
    .a(subtractor64bit_17_output1),
    .b({2'b00, undriven_20, {6{undriven_20[36]}}, input2[15:0], {14{undriven_20[36]}}}),
    .gt(comparator_19_gt), .eq(comparator_19_eq));  // open: lt
  // Probe on subtractor64bit_18_output1
  // Probe on subtractor64bit_18_output1
  subtractor64bit subtractor64bit_19 (
    .input1(subtractor64bit_18_output1), .input2(cbuffer64bit_19_output1),
    .output1(subtractor64bit_19_output1));  // open: inborrow, borrow
  cbuffer64bit cbuffer64bit_19 (
    .buffer1(output1[13]),
    .input1({2'b00, undriven_21, {7{undriven_21[36]}}, input2[15:0], {13{undriven_21[36]}}}),
    .output1(cbuffer64bit_19_output1));
  and and_19 (output1[13], or_19_out, not_1_out);
  or or_19 (or_19_out, comparator_20_gt, comparator_20_eq);
  // Probe on subtractor64bit_19_output1
  // Probe on subtractor64bit_19_output1
  subtractor64bit subtractor64bit_20 (
    .input1(subtractor64bit_19_output1), .input2(cbuffer64bit_20_output1),
    .output1(subtractor64bit_20_output1));  // open: inborrow, borrow
  or or_20 (or_20_out, comparator_21_gt, comparator_21_eq);
  Comparator #(.mode("unsigned"), .width(64)) comparator_20 (
    .a(subtractor64bit_18_output1),
    .b({2'b00, undriven_21, {7{undriven_21[36]}}, input2[15:0], {13{undriven_21[36]}}}),
    .gt(comparator_20_gt), .eq(comparator_20_eq));  // open: lt
  cbuffer64bit cbuffer64bit_20 (
    .buffer1(output1[12]),
    .input1({2'b00, undriven_22, {8{undriven_22[36]}}, input2[15:0], {12{undriven_22[36]}}}),
    .output1(cbuffer64bit_20_output1));
  and and_20 (output1[12], or_20_out, not_1_out);
  Comparator #(.mode("unsigned"), .width(64)) comparator_21 (
    .a(subtractor64bit_19_output1),
    .b({2'b00, undriven_22, {8{undriven_22[36]}}, input2[15:0], {12{undriven_22[36]}}}),
    .gt(comparator_21_gt), .eq(comparator_21_eq));  // open: lt
  // Probe on subtractor64bit_20_output1
  // Probe on subtractor64bit_20_output1
  subtractor64bit subtractor64bit_21 (
    .input1(subtractor64bit_20_output1), .input2(cbuffer64bit_21_output1),
    .output1(subtractor64bit_21_output1));  // open: inborrow, borrow
  cbuffer64bit cbuffer64bit_21 (
    .buffer1(output1[11]),
    .input1({2'b00, undriven_23, {9{undriven_23[36]}}, input2[15:0], {11{undriven_23[36]}}}),
    .output1(cbuffer64bit_21_output1));
  and and_21 (output1[11], or_21_out, not_1_out);
  or or_21 (or_21_out, comparator_22_gt, comparator_22_eq);
  Comparator #(.mode("unsigned"), .width(64)) comparator_22 (
    .a(subtractor64bit_20_output1),
    .b({2'b00, undriven_23, {9{undriven_23[36]}}, input2[15:0], {11{undriven_23[36]}}}),
    .gt(comparator_22_gt), .eq(comparator_22_eq));  // open: lt
  // Probe on subtractor64bit_21_output1
  // Probe on subtractor64bit_21_output1
  subtractor64bit subtractor64bit_22 (
    .input1(subtractor64bit_21_output1), .input2(cbuffer64bit_22_output1),
    .output1(subtractor64bit_22_output1));  // open: inborrow, borrow
  cbuffer64bit cbuffer64bit_22 (
    .buffer1(output1[10]),
    .input1({2'b00, undriven_24, {10{undriven_24[36]}}, input2[15:0], {10{undriven_24[36]}}}),
    .output1(cbuffer64bit_22_output1));
  and and_22 (output1[10], or_22_out, not_1_out);
  or or_22 (or_22_out, comparator_23_gt, comparator_23_eq);
  Comparator #(.mode("unsigned"), .width(64)) comparator_23 (
    .a(subtractor64bit_21_output1),
    .b({2'b00, undriven_24, {10{undriven_24[36]}}, input2[15:0], {10{undriven_24[36]}}}),
    .gt(comparator_23_gt), .eq(comparator_23_eq));  // open: lt
  // Probe on subtractor64bit_22_output1
  // Probe on subtractor64bit_22_output1
  subtractor64bit subtractor64bit_23 (
    .input1(subtractor64bit_22_output1), .input2(cbuffer64bit_23_output1),
    .output1(subtractor64bit_23_output1));  // open: inborrow, borrow
  cbuffer64bit cbuffer64bit_23 (
    .buffer1(output1[9]),
    .input1({2'b00, undriven_25, {11{undriven_25[36]}}, input2[15:0], {9{undriven_25[36]}}}),
    .output1(cbuffer64bit_23_output1));
  and and_23 (output1[9], or_23_out, not_1_out);
  or or_23 (or_23_out, comparator_24_gt, comparator_24_eq);
  // Probe on subtractor64bit_23_output1
  // Probe on subtractor64bit_23_output1
  subtractor64bit subtractor64bit_24 (
    .input1(subtractor64bit_23_output1), .input2(cbuffer64bit_24_output1),
    .output1(subtractor64bit_24_output1));  // open: inborrow, borrow
  or or_24 (or_24_out, comparator_25_gt, comparator_25_eq);
  Comparator #(.mode("unsigned"), .width(64)) comparator_24 (
    .a(subtractor64bit_22_output1),
    .b({2'b00, undriven_25, {11{undriven_25[36]}}, input2[15:0], {9{undriven_25[36]}}}),
    .gt(comparator_24_gt), .eq(comparator_24_eq));  // open: lt
  cbuffer64bit cbuffer64bit_24 (
    .buffer1(output1[8]),
    .input1({2'b00, undriven_26, {12{undriven_26[36]}}, input2[15:0], {8{undriven_26[36]}}}),
    .output1(cbuffer64bit_24_output1));
  and and_24 (output1[8], or_24_out, not_1_out);
  Comparator #(.mode("unsigned"), .width(64)) comparator_25 (
    .a(subtractor64bit_23_output1),
    .b({2'b00, undriven_26, {12{undriven_26[36]}}, input2[15:0], {8{undriven_26[36]}}}),
    .gt(comparator_25_gt), .eq(comparator_25_eq));  // open: lt
  // Probe on subtractor64bit_24_output1
  // Probe on subtractor64bit_24_output1
  subtractor64bit subtractor64bit_25 (
    .input1(subtractor64bit_24_output1), .input2(cbuffer64bit_25_output1),
    .output1(subtractor64bit_25_output1));  // open: inborrow, borrow
  cbuffer64bit cbuffer64bit_25 (
    .buffer1(output1[7]),
    .input1({2'b00, undriven_27, {13{undriven_27[36]}}, input2[15:0], {7{undriven_27[36]}}}),
    .output1(cbuffer64bit_25_output1));
  and and_25 (output1[7], or_25_out, not_1_out);
  or or_25 (or_25_out, comparator_26_gt, comparator_26_eq);
  Comparator #(.mode("unsigned"), .width(64)) comparator_26 (
    .a(subtractor64bit_24_output1),
    .b({2'b00, undriven_27, {13{undriven_27[36]}}, input2[15:0], {7{undriven_27[36]}}}),
    .gt(comparator_26_gt), .eq(comparator_26_eq));  // open: lt
  // Probe on subtractor64bit_25_output1
  // Probe on subtractor64bit_25_output1
  subtractor64bit subtractor64bit_26 (
    .input1(subtractor64bit_25_output1), .input2(cbuffer64bit_26_output1),
    .output1(subtractor64bit_26_output1));  // open: inborrow, borrow
  cbuffer64bit cbuffer64bit_26 (
    .buffer1(output1[6]),
    .input1({2'b00, undriven_28, {14{undriven_28[36]}}, input2[15:0], {6{undriven_28[36]}}}),
    .output1(cbuffer64bit_26_output1));
  and and_26 (output1[6], or_26_out, not_1_out);
  or or_26 (or_26_out, comparator_27_gt, comparator_27_eq);
  Comparator #(.mode("unsigned"), .width(64)) comparator_27 (
    .a(subtractor64bit_25_output1),
    .b({2'b00, undriven_28, {14{undriven_28[36]}}, input2[15:0], {6{undriven_28[36]}}}),
    .gt(comparator_27_gt), .eq(comparator_27_eq));  // open: lt
  // Probe on subtractor64bit_26_output1
  // Probe on subtractor64bit_26_output1
  subtractor64bit subtractor64bit_27 (
    .input1(subtractor64bit_26_output1), .input2(cbuffer64bit_27_output1),
    .output1(subtractor64bit_27_output1));  // open: inborrow, borrow
  cbuffer64bit cbuffer64bit_27 (
    .buffer1(output1[5]),
    .input1({2'b00, undriven_29, {15{undriven_29[36]}}, input2[15:0], {5{undriven_29[36]}}}),
    .output1(cbuffer64bit_27_output1));
  and and_27 (output1[5], or_27_out, not_1_out);
  or or_27 (or_27_out, comparator_28_gt, comparator_28_eq);
  // Probe on subtractor64bit_27_output1
  // Probe on subtractor64bit_27_output1
  subtractor64bit subtractor64bit_28 (
    .input1(subtractor64bit_27_output1), .input2(cbuffer64bit_28_output1),
    .output1(subtractor64bit_28_output1));  // open: inborrow, borrow
  or or_28 (or_28_out, comparator_29_gt, comparator_29_eq);
  Comparator #(.mode("unsigned"), .width(64)) comparator_28 (
    .a(subtractor64bit_26_output1),
    .b({2'b00, undriven_29, {15{undriven_29[36]}}, input2[15:0], {5{undriven_29[36]}}}),
    .gt(comparator_28_gt), .eq(comparator_28_eq));  // open: lt
  cbuffer64bit cbuffer64bit_28 (
    .buffer1(output1[4]),
    .input1({2'b00, undriven_30, {16{undriven_30[36]}}, input2[15:0], {4{undriven_30[36]}}}),
    .output1(cbuffer64bit_28_output1));
  and and_28 (output1[4], or_28_out, not_1_out);
  Comparator #(.mode("unsigned"), .width(64)) comparator_29 (
    .a(subtractor64bit_27_output1),
    .b({2'b00, undriven_30, {16{undriven_30[36]}}, input2[15:0], {4{undriven_30[36]}}}),
    .gt(comparator_29_gt), .eq(comparator_29_eq));  // open: lt
  // Probe on subtractor64bit_28_output1
  // Probe on subtractor64bit_28_output1
  subtractor64bit subtractor64bit_29 (
    .input1(subtractor64bit_28_output1), .input2(cbuffer64bit_29_output1),
    .output1(subtractor64bit_29_output1));  // open: inborrow, borrow
  cbuffer64bit cbuffer64bit_29 (
    .buffer1(output1[3]),
    .input1({2'b00, undriven_31, {17{undriven_31[36]}}, input2[15:0], {3{undriven_31[36]}}}),
    .output1(cbuffer64bit_29_output1));
  and and_29 (output1[3], or_29_out, not_1_out);
  or or_29 (or_29_out, comparator_30_gt, comparator_30_eq);
  Comparator #(.mode("unsigned"), .width(64)) comparator_30 (
    .a(subtractor64bit_28_output1),
    .b({2'b00, undriven_31, {17{undriven_31[36]}}, input2[15:0], {3{undriven_31[36]}}}),
    .gt(comparator_30_gt), .eq(comparator_30_eq));  // open: lt
  // Probe on subtractor64bit_29_output1
  // Probe on subtractor64bit_29_output1
  subtractor64bit subtractor64bit_30 (
    .input1(subtractor64bit_29_output1), .input2(cbuffer64bit_30_output1),
    .output1(subtractor64bit_30_output1));  // open: inborrow, borrow
  cbuffer64bit cbuffer64bit_30 (
    .buffer1(output1[2]),
    .input1({2'b00, undriven_32, {18{undriven_32[36]}}, input2[15:0], {2{undriven_32[36]}}}),
    .output1(cbuffer64bit_30_output1));
  and and_30 (output1[2], or_30_out, not_1_out);
  or or_30 (or_30_out, comparator_31_gt, comparator_31_eq);
  Comparator #(.mode("unsigned"), .width(64)) comparator_31 (
    .a(subtractor64bit_29_output1),
    .b({2'b00, undriven_32, {18{undriven_32[36]}}, input2[15:0], {2{undriven_32[36]}}}),
    .gt(comparator_31_gt), .eq(comparator_31_eq));  // open: lt
  // Probe on subtractor64bit_30_output1
  // Probe on subtractor64bit_30_output1
  subtractor64bit subtractor64bit_31 (
    .input1(subtractor64bit_30_output1), .input2(cbuffer64bit_31_output1),
    .output1(subtractor64bit_31_output1));  // open: inborrow, borrow
  cbuffer64bit cbuffer64bit_31 (
    .buffer1(output1[1]),
    .input1({2'b00, undriven_33, {19{undriven_33[36]}}, input2[15:0], undriven_33[36]}),
    .output1(cbuffer64bit_31_output1));
  and and_31 (output1[1], or_31_out, not_1_out);
  or or_31 (or_31_out, comparator_32_gt, comparator_32_eq);
  // Probe on subtractor64bit_31_output1
  // Probe on subtractor64bit_31_output1
  subtractor64bit subtractor64bit_32 (
    .input1(subtractor64bit_31_output1), .input2(cbuffer64bit_32_output1),
    .output1({subtractor64bit_32_output1, remainder}));  // open: inborrow, borrow
  or or_32 (or_32_out, comparator_33_gt, comparator_33_eq);
  Comparator #(.mode("unsigned"), .width(64)) comparator_32 (
    .a(subtractor64bit_30_output1),
    .b({2'b00, undriven_33, {19{undriven_33[36]}}, input2[15:0], undriven_33[36]}), .gt(comparator_32_gt),
    .eq(comparator_32_eq));  // open: lt
  cbuffer64bit cbuffer64bit_32 (
    .buffer1(output1[0]), .input1({2'b00, undriven_34, {20{undriven_34[36]}}, input2[15:0]}),
    .output1(cbuffer64bit_32_output1));
  and and_32 (output1[0], or_32_out, not_1_out);
  Comparator #(.mode("unsigned"), .width(64)) comparator_33 (
    .a(subtractor64bit_31_output1), .b({2'b00, undriven_34, {20{undriven_34[36]}}, input2[15:0]}),
    .gt(comparator_33_gt), .eq(comparator_33_eq));  // open: lt
  // Probe on {subtractor64bit_32_output1, remainder}
  // Probe on {subtractor64bit_32_output1, remainder}
  // Probe on {{32{1'b0}}, output1}
  // Probe on {{32{1'b0}}, output1}
  // Probe on remainder
  // Probe on remainder
  // Probe on output1
  // Probe on output1
  // Pins of 16 and 32 and 64 bits meet at {undriven_9, input2}
  // Pins of 16 and 32 bits meet at inupper
  // Pins of 16 and 32 bits meet at input1
  // Pins of 16 and 64 bits meet at {undriven, {16{1'b0}}}

  // Notes on the sheet:
  //   inupper: initial=0xd3
  //   input2: initial=0xaf
  //   input1: initial=0xf74e
endmodule

module comparatoru64bit (
  input  [63:0] input1,
  input  [63:0] input2,
  output greater1,
  output equal1,
  output less1
);

  wire and_1_out, and_2_out, and_3_out, and_4_out, and_5_out, and_6_out, and_7_out, and_8_out, and_9_out,
       and_10_out, and_11_out, and_12_out, and_13_out, and_14_out, and_15_out, and_16_out, and_17_out,
       and_18_out, and_19_out, and_20_out, and_21_out, and_22_out, and_23_out, and_24_out, and_25_out,
       and_26_out, and_27_out, and_28_out, and_29_out, and_30_out, and_31_out, and_32_out, and_33_out,
       and_34_out, and_35_out, and_36_out, and_37_out, and_38_out, and_39_out, and_40_out, and_41_out,
       and_42_out, and_43_out, and_44_out, and_45_out, and_46_out, and_47_out, and_48_out, and_49_out,
       and_50_out, and_51_out, and_52_out, and_53_out, and_54_out, and_55_out, and_56_out, and_57_out,
       and_58_out, and_59_out, and_60_out, and_61_out, and_62_out, and_63_out, and_64_out, and_66_out,
       and_67_out, and_68_out, and_69_out, and_70_out, and_71_out, and_72_out, and_73_out, and_74_out,
       and_75_out, and_76_out, and_77_out, and_78_out, and_79_out, and_80_out, and_81_out, and_82_out,
       and_83_out, and_84_out, and_85_out, and_86_out, and_87_out, and_88_out, and_89_out, and_90_out,
       and_91_out, and_92_out, and_93_out, and_94_out, and_95_out, and_96_out, and_97_out, and_98_out,
       and_99_out, and_100_out, and_101_out, and_102_out, and_103_out, and_104_out, and_105_out, and_106_out,
       and_107_out, and_108_out, and_109_out, and_110_out, and_111_out, and_112_out, and_113_out,
       and_114_out, and_115_out, and_116_out, and_117_out, and_118_out, and_119_out, and_120_out,
       and_121_out, and_122_out, and_123_out, and_124_out, and_125_out, and_126_out, and_127_out,
       and_128_out, and_129_out, and_130_out, and_131_out, and_132_out, and_133_out, and_134_out,
       and_135_out, and_136_out, and_137_out, and_138_out, and_139_out, and_140_out, and_141_out,
       and_142_out, and_143_out, and_144_out, and_145_out, and_146_out, and_147_out, and_148_out,
       and_149_out, and_150_out, and_151_out, and_152_out, and_153_out, and_154_out, and_155_out,
       and_156_out, and_157_out, and_158_out, and_159_out, and_160_out, and_161_out, and_162_out,
       and_163_out, and_164_out, and_165_out, and_166_out, and_167_out, and_168_out, and_169_out,
       and_170_out, and_171_out, and_172_out, and_173_out, and_174_out, and_175_out, and_176_out,
       and_177_out, and_178_out, and_179_out, and_180_out, and_181_out, and_182_out, and_183_out,
       and_184_out, and_185_out, and_186_out, and_187_out, and_188_out, and_189_out, and_190_out,
       and_191_out, not_1_out, not_2_out, not_3_out, not_4_out, not_5_out, not_6_out, not_7_out, not_8_out,
       not_9_out, not_10_out, not_11_out, not_12_out, not_13_out, not_14_out, not_15_out, not_16_out,
       not_17_out, not_18_out, not_19_out, not_20_out, not_21_out, not_22_out, not_23_out, not_24_out,
       not_25_out, not_26_out, not_27_out, not_28_out, not_29_out, not_30_out, not_31_out, not_32_out,
       not_33_out, not_34_out, not_35_out, not_36_out, not_37_out, not_38_out, not_39_out, not_40_out,
       not_41_out, not_42_out, not_43_out, not_44_out, not_45_out, not_46_out, not_47_out, not_48_out,
       not_49_out, not_50_out, not_51_out, not_52_out, not_53_out, not_54_out, not_55_out, not_56_out,
       not_57_out, not_58_out, not_59_out, not_60_out, not_61_out, not_62_out, not_63_out, not_64_out,
       not_65_out, not_66_out, not_67_out, not_68_out, not_69_out, not_70_out, not_71_out, not_72_out,
       not_73_out, not_74_out, not_75_out, not_76_out, not_77_out, not_78_out, not_79_out, not_80_out,
       not_81_out, not_82_out, not_83_out, not_84_out, not_85_out, not_86_out, not_87_out, not_88_out,
       not_89_out, not_90_out, not_91_out, not_92_out, not_93_out, not_94_out, not_95_out, not_96_out,
       not_97_out, not_98_out, not_99_out, not_100_out, not_101_out, not_102_out, not_103_out, not_104_out,
       not_105_out, not_106_out, not_107_out, not_108_out, not_109_out, not_110_out, not_111_out,
       not_112_out, not_113_out, not_114_out, not_115_out, not_116_out, not_117_out, not_118_out,
       not_119_out, not_120_out, not_121_out, not_122_out, not_123_out, not_124_out, not_125_out,
       not_126_out, not_127_out, not_128_out, or_2_out, or_3_out, or_4_out, or_5_out, or_6_out, or_7_out,
       or_8_out, or_9_out, or_10_out, or_11_out, or_12_out, or_13_out, or_14_out, or_15_out, or_16_out,
       or_17_out, or_18_out, or_19_out, or_20_out, or_21_out, or_22_out, or_23_out, or_24_out, or_25_out,
       or_26_out, or_27_out, or_28_out, or_29_out, or_30_out, or_31_out, or_32_out, or_33_out, or_34_out,
       or_35_out, or_36_out, or_37_out, or_38_out, or_39_out, or_40_out, or_41_out, or_42_out, or_43_out,
       or_44_out, or_45_out, or_46_out, or_47_out, or_48_out, or_49_out, or_50_out, or_51_out, or_52_out,
       or_53_out, or_54_out, or_55_out, or_56_out, or_57_out, or_58_out, or_59_out, or_60_out, or_61_out,
       or_62_out, or_63_out, or_65_out, or_66_out, or_67_out, or_68_out, or_69_out, or_70_out, or_71_out,
       or_72_out, or_73_out, or_74_out, or_75_out, or_76_out, or_77_out, or_78_out, or_79_out, or_80_out,
       or_81_out, or_82_out, or_83_out, or_84_out, or_85_out, or_86_out, or_87_out, or_88_out, or_89_out,
       or_90_out, or_91_out, or_92_out, or_93_out, or_94_out, or_95_out, or_96_out, or_97_out, or_98_out,
       or_99_out, or_100_out, or_101_out, or_102_out, or_103_out, or_104_out, or_105_out, or_106_out,
       or_107_out, or_108_out, or_109_out, or_110_out, or_111_out, or_112_out, or_113_out, or_114_out,
       or_115_out, or_116_out, or_117_out, or_118_out, or_119_out, or_120_out, or_121_out, or_122_out,
       or_123_out, or_124_out, or_125_out, or_126_out, xnor_1_out, xnor_2_out, xnor_3_out, xnor_4_out,
       xnor_5_out, xnor_6_out, xnor_7_out, xnor_8_out, xnor_9_out, xnor_10_out, xnor_11_out, xnor_12_out,
       xnor_13_out, xnor_14_out, xnor_15_out, xnor_16_out, xnor_17_out, xnor_18_out, xnor_19_out,
       xnor_20_out, xnor_21_out, xnor_22_out, xnor_23_out, xnor_24_out, xnor_25_out, xnor_26_out,
       xnor_27_out, xnor_28_out, xnor_29_out, xnor_30_out, xnor_31_out, xnor_32_out, xnor_33_out,
       xnor_34_out, xnor_35_out, xnor_36_out, xnor_37_out, xnor_38_out, xnor_39_out, xnor_40_out,
       xnor_41_out, xnor_42_out, xnor_43_out, xnor_44_out, xnor_45_out, xnor_46_out, xnor_47_out,
       xnor_48_out, xnor_49_out, xnor_50_out, xnor_51_out, xnor_52_out, xnor_53_out, xnor_54_out,
       xnor_55_out, xnor_56_out, xnor_57_out, xnor_58_out, xnor_59_out, xnor_60_out, xnor_61_out,
       xnor_62_out, xnor_63_out, xnor_64_out;

  or or_1 (greater1, or_2_out, and_1_out);
  or or_2 (or_2_out, or_3_out, and_2_out);
  or or_3 (or_3_out, or_4_out, and_3_out);
  or or_4 (or_4_out, or_5_out, and_4_out);
  or or_5 (or_5_out, or_6_out, and_5_out);
  or or_6 (or_6_out, or_7_out, and_6_out);
  or or_7 (or_7_out, or_8_out, and_7_out);
  or or_8 (or_8_out, or_9_out, and_8_out);
  or or_9 (or_9_out, or_10_out, and_9_out);
  or or_10 (or_10_out, or_11_out, and_10_out);
  or or_11 (or_11_out, or_12_out, and_11_out);
  or or_12 (or_12_out, or_13_out, and_12_out);
  or or_13 (or_13_out, or_14_out, and_13_out);
  or or_14 (or_14_out, or_15_out, and_14_out);
  or or_15 (or_15_out, or_16_out, and_15_out);
  or or_16 (or_16_out, or_17_out, and_16_out);
  or or_17 (or_17_out, or_18_out, and_17_out);
  or or_18 (or_18_out, or_19_out, and_18_out);
  or or_19 (or_19_out, or_20_out, and_19_out);
  or or_20 (or_20_out, or_21_out, and_20_out);
  or or_21 (or_21_out, or_22_out, and_21_out);
  or or_22 (or_22_out, or_23_out, and_22_out);
  or or_23 (or_23_out, or_24_out, and_23_out);
  or or_24 (or_24_out, or_25_out, and_24_out);
  or or_25 (or_25_out, or_26_out, and_25_out);
  or or_26 (or_26_out, or_27_out, and_26_out);
  or or_27 (or_27_out, or_28_out, and_27_out);
  or or_28 (or_28_out, or_29_out, and_28_out);
  or or_29 (or_29_out, or_30_out, and_29_out);
  or or_30 (or_30_out, or_31_out, and_30_out);
  or or_31 (or_31_out, or_32_out, and_31_out);
  or or_32 (or_32_out, or_33_out, and_32_out);
  or or_33 (or_33_out, or_34_out, and_33_out);
  or or_34 (or_34_out, or_35_out, and_34_out);
  or or_35 (or_35_out, or_36_out, and_35_out);
  or or_36 (or_36_out, or_37_out, and_36_out);
  or or_37 (or_37_out, or_38_out, and_37_out);
  or or_38 (or_38_out, or_39_out, and_38_out);
  or or_39 (or_39_out, or_40_out, and_39_out);
  or or_40 (or_40_out, or_41_out, and_40_out);
  or or_41 (or_41_out, or_42_out, and_41_out);
  or or_42 (or_42_out, or_43_out, and_42_out);
  or or_43 (or_43_out, or_44_out, and_43_out);
  or or_44 (or_44_out, or_45_out, and_44_out);
  or or_45 (or_45_out, or_46_out, and_45_out);
  or or_46 (or_46_out, or_47_out, and_46_out);
  or or_47 (or_47_out, or_48_out, and_47_out);
  or or_48 (or_48_out, or_49_out, and_48_out);
  or or_49 (or_49_out, or_50_out, and_49_out);
  or or_50 (or_50_out, or_51_out, and_50_out);
  or or_51 (or_51_out, or_52_out, and_51_out);
  or or_52 (or_52_out, or_53_out, and_52_out);
  or or_53 (or_53_out, or_54_out, and_53_out);
  or or_54 (or_54_out, or_55_out, and_54_out);
  or or_55 (or_55_out, or_56_out, and_55_out);
  or or_56 (or_56_out, or_57_out, and_56_out);
  or or_57 (or_57_out, or_58_out, and_57_out);
  or or_58 (or_58_out, or_59_out, and_58_out);
  or or_59 (or_59_out, or_60_out, and_59_out);
  or or_60 (or_60_out, or_61_out, and_60_out);
  or or_61 (or_61_out, or_62_out, and_61_out);
  or or_62 (or_62_out, or_63_out, and_62_out);
  or or_63 (or_63_out, and_64_out, and_63_out);
  and and_1 (and_1_out, input1[0], and_66_out, not_1_out);
  and and_2 (and_2_out, input1[1], and_67_out, not_2_out);
  and and_3 (and_3_out, input1[2], and_68_out, not_3_out);
  and and_4 (and_4_out, input1[3], and_69_out, not_4_out);
  and and_5 (and_5_out, input1[4], and_70_out, not_5_out);
  and and_6 (and_6_out, input1[5], and_71_out, not_6_out);
  and and_7 (and_7_out, input1[6], and_72_out, not_7_out);
  and and_8 (and_8_out, input1[7], and_73_out, not_8_out);
  and and_9 (and_9_out, input1[8], and_74_out, not_9_out);
  and and_10 (and_10_out, input1[9], and_75_out, not_10_out);
  and and_11 (and_11_out, input1[10], and_76_out, not_11_out);
  and and_12 (and_12_out, input1[11], and_77_out, not_12_out);
  and and_13 (and_13_out, input1[12], and_78_out, not_13_out);
  and and_14 (and_14_out, input1[13], and_79_out, not_14_out);
  and and_15 (and_15_out, input1[14], and_80_out, not_15_out);
  and and_16 (and_16_out, input1[15], and_81_out, not_16_out);
  and and_17 (and_17_out, input1[16], and_82_out, not_17_out);
  and and_18 (and_18_out, input1[17], and_83_out, not_18_out);
  and and_19 (and_19_out, input1[18], and_84_out, not_19_out);
  and and_20 (and_20_out, input1[19], and_85_out, not_20_out);
  and and_21 (and_21_out, input1[20], and_86_out, not_21_out);
  and and_22 (and_22_out, input1[21], and_87_out, not_22_out);
  and and_23 (and_23_out, input1[22], and_88_out, not_23_out);
  and and_24 (and_24_out, input1[23], and_89_out, not_24_out);
  and and_25 (and_25_out, input1[24], and_90_out, not_25_out);
  and and_26 (and_26_out, input1[25], and_91_out, not_26_out);
  and and_27 (and_27_out, input1[26], and_92_out, not_27_out);
  and and_28 (and_28_out, input1[27], and_93_out, not_28_out);
  and and_29 (and_29_out, input1[28], and_94_out, not_29_out);
  and and_30 (and_30_out, input1[29], and_95_out, not_30_out);
  and and_31 (and_31_out, input1[30], and_96_out, not_31_out);
  and and_32 (and_32_out, input1[31], and_97_out, not_32_out);
  and and_33 (and_33_out, input1[32], and_98_out, not_33_out);
  and and_34 (and_34_out, input1[33], and_99_out, not_34_out);
  and and_35 (and_35_out, input1[34], and_100_out, not_35_out);
  and and_36 (and_36_out, input1[35], and_101_out, not_36_out);
  and and_37 (and_37_out, input1[36], and_102_out, not_37_out);
  and and_38 (and_38_out, input1[37], and_103_out, not_38_out);
  and and_39 (and_39_out, input1[38], and_104_out, not_39_out);
  and and_40 (and_40_out, input1[39], and_105_out, not_40_out);
  and and_41 (and_41_out, input1[40], and_106_out, not_41_out);
  and and_42 (and_42_out, input1[41], and_107_out, not_42_out);
  and and_43 (and_43_out, input1[42], and_108_out, not_43_out);
  and and_44 (and_44_out, input1[43], and_109_out, not_44_out);
  and and_45 (and_45_out, input1[44], and_110_out, not_45_out);
  and and_46 (and_46_out, input1[45], and_111_out, not_46_out);
  and and_47 (and_47_out, input1[46], and_112_out, not_47_out);
  and and_48 (and_48_out, input1[47], and_113_out, not_48_out);
  and and_49 (and_49_out, input1[48], and_114_out, not_49_out);
  and and_50 (and_50_out, input1[49], and_115_out, not_50_out);
  and and_51 (and_51_out, input1[50], and_116_out, not_51_out);
  and and_52 (and_52_out, input1[51], and_117_out, not_52_out);
  and and_53 (and_53_out, input1[52], and_118_out, not_53_out);
  and and_54 (and_54_out, input1[53], and_119_out, not_54_out);
  and and_55 (and_55_out, input1[54], and_120_out, not_55_out);
  and and_56 (and_56_out, input1[55], and_121_out, not_56_out);
  and and_57 (and_57_out, input1[56], and_122_out, not_57_out);
  and and_58 (and_58_out, input1[57], and_123_out, not_58_out);
  and and_59 (and_59_out, input1[58], and_124_out, not_59_out);
  and and_60 (and_60_out, input1[59], and_125_out, not_60_out);
  and and_61 (and_61_out, input1[60], and_126_out, not_61_out);
  and and_62 (and_62_out, input1[61], and_127_out, not_62_out);
  and and_63 (and_63_out, input1[62], xnor_64_out, not_63_out);
  and and_64 (and_64_out, input1[63], not_64_out);
  not not_1 (not_1_out, input2[0]);
  not not_2 (not_2_out, input2[1]);
  not not_3 (not_3_out, input2[2]);
  not not_4 (not_4_out, input2[3]);
  not not_5 (not_5_out, input2[4]);
  not not_6 (not_6_out, input2[5]);
  not not_7 (not_7_out, input2[6]);
  not not_8 (not_8_out, input2[7]);
  not not_9 (not_9_out, input2[8]);
  not not_10 (not_10_out, input2[9]);
  not not_11 (not_11_out, input2[10]);
  not not_12 (not_12_out, input2[11]);
  not not_13 (not_13_out, input2[12]);
  not not_14 (not_14_out, input2[13]);
  not not_15 (not_15_out, input2[14]);
  not not_16 (not_16_out, input2[15]);
  not not_17 (not_17_out, input2[16]);
  not not_18 (not_18_out, input2[17]);
  not not_19 (not_19_out, input2[18]);
  not not_20 (not_20_out, input2[19]);
  not not_21 (not_21_out, input2[20]);
  not not_22 (not_22_out, input2[21]);
  not not_23 (not_23_out, input2[22]);
  not not_24 (not_24_out, input2[23]);
  not not_25 (not_25_out, input2[24]);
  not not_26 (not_26_out, input2[25]);
  not not_27 (not_27_out, input2[26]);
  not not_28 (not_28_out, input2[27]);
  not not_29 (not_29_out, input2[28]);
  not not_30 (not_30_out, input2[29]);
  not not_31 (not_31_out, input2[30]);
  not not_32 (not_32_out, input2[31]);
  not not_33 (not_33_out, input2[32]);
  not not_34 (not_34_out, input2[33]);
  not not_35 (not_35_out, input2[34]);
  not not_36 (not_36_out, input2[35]);
  not not_37 (not_37_out, input2[36]);
  not not_38 (not_38_out, input2[37]);
  not not_39 (not_39_out, input2[38]);
  not not_40 (not_40_out, input2[39]);
  not not_41 (not_41_out, input2[40]);
  not not_42 (not_42_out, input2[41]);
  not not_43 (not_43_out, input2[42]);
  not not_44 (not_44_out, input2[43]);
  not not_45 (not_45_out, input2[44]);
  not not_46 (not_46_out, input2[45]);
  not not_47 (not_47_out, input2[46]);
  not not_48 (not_48_out, input2[47]);
  not not_49 (not_49_out, input2[48]);
  not not_50 (not_50_out, input2[49]);
  not not_51 (not_51_out, input2[50]);
  not not_52 (not_52_out, input2[51]);
  not not_53 (not_53_out, input2[52]);
  not not_54 (not_54_out, input2[53]);
  not not_55 (not_55_out, input2[54]);
  not not_56 (not_56_out, input2[55]);
  not not_57 (not_57_out, input2[56]);
  not not_58 (not_58_out, input2[57]);
  not not_59 (not_59_out, input2[58]);
  not not_60 (not_60_out, input2[59]);
  not not_61 (not_61_out, input2[60]);
  not not_62 (not_62_out, input2[61]);
  not not_63 (not_63_out, input2[62]);
  not not_64 (not_64_out, input2[63]);
  and and_65 (equal1, xnor_1_out, and_66_out);
  xnor xnor_1 (xnor_1_out, input1[0], input2[0]);
  and and_66 (and_66_out, xnor_2_out, and_67_out);
  xnor xnor_2 (xnor_2_out, input1[1], input2[1]);
  and and_67 (and_67_out, xnor_3_out, and_68_out);
  xnor xnor_3 (xnor_3_out, input1[2], input2[2]);
  and and_68 (and_68_out, xnor_4_out, and_69_out);
  xnor xnor_4 (xnor_4_out, input1[3], input2[3]);
  and and_69 (and_69_out, xnor_5_out, and_70_out);
  xnor xnor_5 (xnor_5_out, input1[4], input2[4]);
  and and_70 (and_70_out, xnor_6_out, and_71_out);
  xnor xnor_6 (xnor_6_out, input1[5], input2[5]);
  and and_71 (and_71_out, xnor_7_out, and_72_out);
  xnor xnor_7 (xnor_7_out, input1[6], input2[6]);
  and and_72 (and_72_out, xnor_8_out, and_73_out);
  xnor xnor_8 (xnor_8_out, input1[7], input2[7]);
  and and_73 (and_73_out, xnor_9_out, and_74_out);
  xnor xnor_9 (xnor_9_out, input1[8], input2[8]);
  and and_74 (and_74_out, xnor_10_out, and_75_out);
  xnor xnor_10 (xnor_10_out, input1[9], input2[9]);
  and and_75 (and_75_out, xnor_11_out, and_76_out);
  xnor xnor_11 (xnor_11_out, input1[10], input2[10]);
  and and_76 (and_76_out, xnor_12_out, and_77_out);
  xnor xnor_12 (xnor_12_out, input1[11], input2[11]);
  and and_77 (and_77_out, xnor_13_out, and_78_out);
  xnor xnor_13 (xnor_13_out, input1[12], input2[12]);
  and and_78 (and_78_out, xnor_14_out, and_79_out);
  xnor xnor_14 (xnor_14_out, input1[13], input2[13]);
  and and_79 (and_79_out, xnor_15_out, and_80_out);
  xnor xnor_15 (xnor_15_out, input1[14], input2[14]);
  and and_80 (and_80_out, xnor_16_out, and_81_out);
  xnor xnor_16 (xnor_16_out, input1[15], input2[15]);
  and and_81 (and_81_out, xnor_17_out, and_82_out);
  xnor xnor_17 (xnor_17_out, input1[16], input2[16]);
  and and_82 (and_82_out, xnor_18_out, and_83_out);
  xnor xnor_18 (xnor_18_out, input1[17], input2[17]);
  and and_83 (and_83_out, xnor_19_out, and_84_out);
  xnor xnor_19 (xnor_19_out, input1[18], input2[18]);
  and and_84 (and_84_out, xnor_20_out, and_85_out);
  xnor xnor_20 (xnor_20_out, input1[19], input2[19]);
  and and_85 (and_85_out, xnor_21_out, and_86_out);
  xnor xnor_21 (xnor_21_out, input1[20], input2[20]);
  and and_86 (and_86_out, xnor_22_out, and_87_out);
  xnor xnor_22 (xnor_22_out, input1[21], input2[21]);
  and and_87 (and_87_out, xnor_23_out, and_88_out);
  xnor xnor_23 (xnor_23_out, input1[22], input2[22]);
  and and_88 (and_88_out, xnor_24_out, and_89_out);
  xnor xnor_24 (xnor_24_out, input1[23], input2[23]);
  and and_89 (and_89_out, xnor_25_out, and_90_out);
  xnor xnor_25 (xnor_25_out, input1[24], input2[24]);
  and and_90 (and_90_out, xnor_26_out, and_91_out);
  xnor xnor_26 (xnor_26_out, input1[25], input2[25]);
  and and_91 (and_91_out, xnor_27_out, and_92_out);
  xnor xnor_27 (xnor_27_out, input1[26], input2[26]);
  and and_92 (and_92_out, xnor_28_out, and_93_out);
  xnor xnor_28 (xnor_28_out, input1[27], input2[27]);
  and and_93 (and_93_out, xnor_29_out, and_94_out);
  xnor xnor_29 (xnor_29_out, input1[28], input2[28]);
  and and_94 (and_94_out, xnor_30_out, and_95_out);
  xnor xnor_30 (xnor_30_out, input1[29], input2[29]);
  and and_95 (and_95_out, xnor_31_out, and_96_out);
  xnor xnor_31 (xnor_31_out, input1[30], input2[30]);
  and and_96 (and_96_out, xnor_32_out, and_97_out);
  xnor xnor_32 (xnor_32_out, input1[31], input2[31]);
  and and_97 (and_97_out, xnor_33_out, and_98_out);
  xnor xnor_33 (xnor_33_out, input1[32], input2[32]);
  and and_98 (and_98_out, xnor_34_out, and_99_out);
  xnor xnor_34 (xnor_34_out, input1[33], input2[33]);
  and and_99 (and_99_out, xnor_35_out, and_100_out);
  xnor xnor_35 (xnor_35_out, input1[34], input2[34]);
  and and_100 (and_100_out, xnor_36_out, and_101_out);
  xnor xnor_36 (xnor_36_out, input1[35], input2[35]);
  and and_101 (and_101_out, xnor_37_out, and_102_out);
  xnor xnor_37 (xnor_37_out, input1[36], input2[36]);
  and and_102 (and_102_out, xnor_38_out, and_103_out);
  xnor xnor_38 (xnor_38_out, input1[37], input2[37]);
  and and_103 (and_103_out, xnor_39_out, and_104_out);
  xnor xnor_39 (xnor_39_out, input1[38], input2[38]);
  and and_104 (and_104_out, xnor_40_out, and_105_out);
  xnor xnor_40 (xnor_40_out, input1[39], input2[39]);
  and and_105 (and_105_out, xnor_41_out, and_106_out);
  xnor xnor_41 (xnor_41_out, input1[40], input2[40]);
  and and_106 (and_106_out, xnor_42_out, and_107_out);
  xnor xnor_42 (xnor_42_out, input1[41], input2[41]);
  and and_107 (and_107_out, xnor_43_out, and_108_out);
  xnor xnor_43 (xnor_43_out, input1[42], input2[42]);
  and and_108 (and_108_out, xnor_44_out, and_109_out);
  xnor xnor_44 (xnor_44_out, input1[43], input2[43]);
  and and_109 (and_109_out, xnor_45_out, and_110_out);
  xnor xnor_45 (xnor_45_out, input1[44], input2[44]);
  and and_110 (and_110_out, xnor_46_out, and_111_out);
  xnor xnor_46 (xnor_46_out, input1[45], input2[45]);
  and and_111 (and_111_out, xnor_47_out, and_112_out);
  xnor xnor_47 (xnor_47_out, input1[46], input2[46]);
  and and_112 (and_112_out, xnor_48_out, and_113_out);
  xnor xnor_48 (xnor_48_out, input1[47], input2[47]);
  and and_113 (and_113_out, xnor_49_out, and_114_out);
  xnor xnor_49 (xnor_49_out, input1[48], input2[48]);
  and and_114 (and_114_out, xnor_50_out, and_115_out);
  xnor xnor_50 (xnor_50_out, input1[49], input2[49]);
  and and_115 (and_115_out, xnor_51_out, and_116_out);
  xnor xnor_51 (xnor_51_out, input1[50], input2[50]);
  and and_116 (and_116_out, xnor_52_out, and_117_out);
  xnor xnor_52 (xnor_52_out, input1[51], input2[51]);
  and and_117 (and_117_out, xnor_53_out, and_118_out);
  xnor xnor_53 (xnor_53_out, input1[52], input2[52]);
  and and_118 (and_118_out, xnor_54_out, and_119_out);
  xnor xnor_54 (xnor_54_out, input1[53], input2[53]);
  and and_119 (and_119_out, xnor_55_out, and_120_out);
  xnor xnor_55 (xnor_55_out, input1[54], input2[54]);
  and and_120 (and_120_out, xnor_56_out, and_121_out);
  xnor xnor_56 (xnor_56_out, input1[55], input2[55]);
  and and_121 (and_121_out, xnor_57_out, and_122_out);
  xnor xnor_57 (xnor_57_out, input1[56], input2[56]);
  and and_122 (and_122_out, xnor_58_out, and_123_out);
  xnor xnor_58 (xnor_58_out, input1[57], input2[57]);
  and and_123 (and_123_out, xnor_59_out, and_124_out);
  xnor xnor_59 (xnor_59_out, input1[58], input2[58]);
  and and_124 (and_124_out, xnor_60_out, and_125_out);
  xnor xnor_60 (xnor_60_out, input1[59], input2[59]);
  and and_125 (and_125_out, xnor_61_out, and_126_out);
  xnor xnor_61 (xnor_61_out, input1[60], input2[60]);
  and and_126 (and_126_out, xnor_62_out, and_127_out);
  xnor xnor_62 (xnor_62_out, input1[61], input2[61]);
  and and_127 (and_127_out, xnor_63_out, xnor_64_out);
  xnor xnor_63 (xnor_63_out, input1[62], input2[62]);
  xnor xnor_64 (xnor_64_out, input1[63], input2[63]);
  not not_65 (not_65_out, input1[0]);
  not not_66 (not_66_out, input1[1]);
  not not_67 (not_67_out, input1[2]);
  not not_68 (not_68_out, input1[3]);
  not not_69 (not_69_out, input1[4]);
  not not_70 (not_70_out, input1[5]);
  not not_71 (not_71_out, input1[6]);
  not not_72 (not_72_out, input1[7]);
  not not_73 (not_73_out, input1[8]);
  not not_74 (not_74_out, input1[9]);
  not not_75 (not_75_out, input1[10]);
  not not_76 (not_76_out, input1[11]);
  not not_77 (not_77_out, input1[12]);
  not not_78 (not_78_out, input1[13]);
  not not_79 (not_79_out, input1[14]);
  not not_80 (not_80_out, input1[15]);
  not not_81 (not_81_out, input1[16]);
  not not_82 (not_82_out, input1[17]);
  not not_83 (not_83_out, input1[18]);
  not not_84 (not_84_out, input1[19]);
  not not_85 (not_85_out, input1[20]);
  not not_86 (not_86_out, input1[21]);
  not not_87 (not_87_out, input1[22]);
  not not_88 (not_88_out, input1[23]);
  not not_89 (not_89_out, input1[24]);
  not not_90 (not_90_out, input1[25]);
  not not_91 (not_91_out, input1[26]);
  not not_92 (not_92_out, input1[27]);
  not not_93 (not_93_out, input1[28]);
  not not_94 (not_94_out, input1[29]);
  not not_95 (not_95_out, input1[30]);
  not not_96 (not_96_out, input1[31]);
  not not_97 (not_97_out, input1[32]);
  not not_98 (not_98_out, input1[33]);
  not not_99 (not_99_out, input1[34]);
  not not_100 (not_100_out, input1[35]);
  not not_101 (not_101_out, input1[36]);
  not not_102 (not_102_out, input1[37]);
  not not_103 (not_103_out, input1[38]);
  not not_104 (not_104_out, input1[39]);
  not not_105 (not_105_out, input1[40]);
  not not_106 (not_106_out, input1[41]);
  not not_107 (not_107_out, input1[42]);
  not not_108 (not_108_out, input1[43]);
  not not_109 (not_109_out, input1[44]);
  not not_110 (not_110_out, input1[45]);
  not not_111 (not_111_out, input1[46]);
  not not_112 (not_112_out, input1[47]);
  not not_113 (not_113_out, input1[48]);
  not not_114 (not_114_out, input1[49]);
  not not_115 (not_115_out, input1[50]);
  not not_116 (not_116_out, input1[51]);
  not not_117 (not_117_out, input1[52]);
  not not_118 (not_118_out, input1[53]);
  not not_119 (not_119_out, input1[54]);
  not not_120 (not_120_out, input1[55]);
  not not_121 (not_121_out, input1[56]);
  not not_122 (not_122_out, input1[57]);
  not not_123 (not_123_out, input1[58]);
  not not_124 (not_124_out, input1[59]);
  not not_125 (not_125_out, input1[60]);
  not not_126 (not_126_out, input1[61]);
  not not_127 (not_127_out, input1[62]);
  not not_128 (not_128_out, input1[63]);
  and and_128 (and_128_out, not_65_out, input2[0]);
  and and_129 (and_129_out, not_66_out, input2[1]);
  and and_130 (and_130_out, not_67_out, input2[2]);
  and and_131 (and_131_out, not_68_out, input2[3]);
  and and_132 (and_132_out, not_69_out, input2[4]);
  and and_133 (and_133_out, not_70_out, input2[5]);
  and and_134 (and_134_out, not_71_out, input2[6]);
  and and_135 (and_135_out, not_72_out, input2[7]);
  and and_136 (and_136_out, not_73_out, input2[8]);
  and and_137 (and_137_out, not_74_out, input2[9]);
  and and_138 (and_138_out, not_75_out, input2[10]);
  and and_139 (and_139_out, not_76_out, input2[11]);
  and and_140 (and_140_out, not_77_out, input2[12]);
  and and_141 (and_141_out, not_78_out, input2[13]);
  and and_142 (and_142_out, not_79_out, input2[14]);
  and and_143 (and_143_out, not_80_out, input2[15]);
  and and_144 (and_144_out, not_81_out, input2[16]);
  and and_145 (and_145_out, not_82_out, input2[17]);
  and and_146 (and_146_out, not_83_out, input2[18]);
  and and_147 (and_147_out, not_84_out, input2[19]);
  and and_148 (and_148_out, not_85_out, input2[20]);
  and and_149 (and_149_out, not_86_out, input2[21]);
  and and_150 (and_150_out, not_87_out, input2[22]);
  and and_151 (and_151_out, not_88_out, input2[23]);
  and and_152 (and_152_out, not_89_out, input2[24]);
  and and_153 (and_153_out, not_90_out, input2[25]);
  and and_154 (and_154_out, not_91_out, input2[26]);
  and and_155 (and_155_out, not_92_out, input2[27]);
  and and_156 (and_156_out, not_93_out, input2[28]);
  and and_157 (and_157_out, not_94_out, input2[29]);
  and and_158 (and_158_out, not_95_out, input2[30]);
  and and_159 (and_159_out, not_96_out, input2[31]);
  and and_160 (and_160_out, not_97_out, input2[32]);
  and and_161 (and_161_out, not_98_out, input2[33]);
  and and_162 (and_162_out, not_99_out, input2[34]);
  and and_163 (and_163_out, not_100_out, input2[35]);
  and and_164 (and_164_out, not_101_out, input2[36]);
  and and_165 (and_165_out, not_102_out, input2[37]);
  and and_166 (and_166_out, not_103_out, input2[38]);
  and and_167 (and_167_out, not_104_out, input2[39]);
  and and_168 (and_168_out, not_105_out, input2[40]);
  and and_169 (and_169_out, not_106_out, input2[41]);
  and and_170 (and_170_out, not_107_out, and_108_out, input2[42]);
  and and_171 (and_171_out, not_108_out, and_109_out, input2[43]);
  and and_172 (and_172_out, not_109_out, and_110_out, input2[44]);
  and and_173 (and_173_out, not_110_out, and_111_out, input2[45]);
  and and_174 (and_174_out, not_111_out, and_112_out, input2[46]);
  and and_175 (and_175_out, not_112_out, and_113_out, input2[47]);
  and and_176 (and_176_out, not_113_out, and_114_out, input2[48]);
  and and_177 (and_177_out, not_114_out, and_115_out, input2[49]);
  and and_178 (and_178_out, not_115_out, and_116_out, input2[50]);
  and and_179 (and_179_out, not_116_out, and_117_out, input2[51]);
  and and_180 (and_180_out, not_117_out, and_118_out, input2[52]);
  and and_181 (and_181_out, not_118_out, and_119_out, input2[53]);
  and and_182 (and_182_out, not_119_out, and_120_out, input2[54]);
  and and_183 (and_183_out, not_120_out, and_121_out, input2[55]);
  and and_184 (and_184_out, not_121_out, and_122_out, input2[56]);
  and and_185 (and_185_out, not_122_out, and_123_out, input2[57]);
  and and_186 (and_186_out, not_123_out, and_124_out, input2[58]);
  and and_187 (and_187_out, not_124_out, and_125_out, input2[59]);
  and and_188 (and_188_out, not_125_out, and_126_out, input2[60]);
  and and_189 (and_189_out, not_126_out, and_127_out, input2[61]);
  and and_190 (and_190_out, not_127_out, xnor_64_out, input2[62]);
  and and_191 (and_191_out, not_128_out, input2[63]);
  or or_64 (less1, and_128_out, or_65_out);
  or or_65 (or_65_out, and_129_out, or_66_out);
  or or_66 (or_66_out, and_130_out, or_67_out);
  or or_67 (or_67_out, and_131_out, or_68_out);
  or or_68 (or_68_out, and_132_out, or_69_out);
  or or_69 (or_69_out, and_133_out, or_70_out);
  or or_70 (or_70_out, and_134_out, or_71_out);
  or or_71 (or_71_out, and_135_out, or_72_out);
  or or_72 (or_72_out, and_136_out, or_73_out);
  or or_73 (or_73_out, and_137_out, or_74_out);
  or or_74 (or_74_out, and_138_out, or_75_out);
  or or_75 (or_75_out, and_139_out, or_76_out);
  or or_76 (or_76_out, and_140_out, or_77_out);
  or or_77 (or_77_out, and_141_out, or_78_out);
  or or_78 (or_78_out, and_142_out, or_79_out);
  or or_79 (or_79_out, and_143_out, or_80_out);
  or or_80 (or_80_out, and_144_out, or_81_out);
  or or_81 (or_81_out, and_145_out, or_82_out);
  or or_82 (or_82_out, and_146_out, or_83_out);
  or or_83 (or_83_out, and_147_out, or_84_out);
  or or_84 (or_84_out, and_148_out, or_85_out);
  or or_85 (or_85_out, and_149_out, or_86_out);
  or or_86 (or_86_out, and_150_out, or_87_out);
  or or_87 (or_87_out, and_151_out, or_88_out);
  or or_88 (or_88_out, and_152_out, or_89_out);
  or or_89 (or_89_out, and_153_out, or_90_out);
  or or_90 (or_90_out, and_154_out, or_91_out);
  or or_91 (or_91_out, and_155_out, or_92_out);
  or or_92 (or_92_out, and_156_out, or_93_out);
  or or_93 (or_93_out, and_157_out, or_94_out);
  or or_94 (or_94_out, and_158_out, or_95_out);
  or or_95 (or_95_out, and_159_out, or_96_out);
  or or_96 (or_96_out, and_160_out, or_97_out);
  or or_97 (or_97_out, and_161_out, or_98_out);
  or or_98 (or_98_out, and_162_out, or_99_out);
  or or_99 (or_99_out, and_163_out, or_100_out);
  or or_100 (or_100_out, and_164_out, or_101_out);
  or or_101 (or_101_out, and_165_out, or_102_out);
  or or_102 (or_102_out, and_166_out, or_103_out);
  or or_103 (or_103_out, and_167_out, or_104_out);
  or or_104 (or_104_out, and_168_out, or_105_out);
  or or_105 (or_105_out, and_169_out, or_106_out);
  or or_106 (or_106_out, and_170_out, or_107_out);
  or or_107 (or_107_out, and_171_out, or_108_out);
  or or_108 (or_108_out, and_172_out, or_109_out);
  or or_109 (or_109_out, and_173_out, or_110_out);
  or or_110 (or_110_out, and_174_out, or_111_out);
  or or_111 (or_111_out, and_175_out, or_112_out);
  or or_112 (or_112_out, and_176_out, or_113_out);
  or or_113 (or_113_out, and_177_out, or_114_out);
  or or_114 (or_114_out, and_178_out, or_115_out);
  or or_115 (or_115_out, and_179_out, or_116_out);
  or or_116 (or_116_out, and_180_out, or_117_out);
  or or_117 (or_117_out, and_181_out, or_118_out);
  or or_118 (or_118_out, and_182_out, or_119_out);
  or or_119 (or_119_out, and_183_out, or_120_out);
  or or_120 (or_120_out, and_184_out, or_121_out);
  or or_121 (or_121_out, and_185_out, or_122_out);
  or or_122 (or_122_out, and_186_out, or_123_out);
  or or_123 (or_123_out, and_187_out, or_124_out);
  or or_124 (or_124_out, and_188_out, or_125_out);
  or or_125 (or_125_out, and_189_out, or_126_out);
  or or_126 (or_126_out, and_190_out, and_191_out);

  // Notes on the sheet:
  //   input1: initial=0xbdfffff2ffffff15
  //   input2: initial=0xbdfffff2ffffff16
endmodule

module comparatoru1bit (
  input  input1,
  input  input2,
  output greater1,
  output equal1,
  output less1
);

  wire not_1_out, not_2_out;

  and and_1 (greater1, input1, not_1_out);
  not not_1 (not_1_out, input2);
  xnor xnor_1 (equal1, input1, input2);
  not not_2 (not_2_out, input1);
  and and_2 (less1, not_2_out, input2);
endmodule

module comparatoru2bit (
  input  [1:0] input1,
  input  [1:0] input2,
  output greater1,
  output equal1,
  output less1
);

  wire and_2_out, and_3_out, comparatoru1bit_1_equal1, comparatoru1bit_1_greater1, comparatoru1bit_1_less1,
       comparatoru1bit_2_equal1, comparatoru1bit_2_greater1, comparatoru1bit_2_less1;

  comparatoru1bit comparatoru1bit_1 (
    .input1(input1[1]), .input2(input2[1]), .greater1(comparatoru1bit_1_greater1),
    .equal1(comparatoru1bit_1_equal1), .less1(comparatoru1bit_1_less1));
  and and_1 (equal1, comparatoru1bit_1_equal1, comparatoru1bit_2_equal1);
  or or_1 (greater1, comparatoru1bit_1_greater1, and_2_out);
  and and_2 (and_2_out, comparatoru1bit_1_equal1, comparatoru1bit_2_greater1);
  or or_2 (less1, comparatoru1bit_1_less1, and_3_out);
  and and_3 (and_3_out, comparatoru1bit_1_equal1, comparatoru1bit_2_less1);
  comparatoru1bit comparatoru1bit_2 (
    .input1(input1[0]), .input2(input2[0]), .greater1(comparatoru1bit_2_greater1),
    .equal1(comparatoru1bit_2_equal1), .less1(comparatoru1bit_2_less1));

  // Notes on the sheet:
  //   input1: initial=0x2
  //   input2: initial=0x3
endmodule
