// Logisim project fpcomp.circ as structural Verilog
module fneg64 (
  input  [63:0] inval1,
  output [63:0] outval1,
  output isnan1
);

  wire fpnegator_1_p2;

  // Probe on inval1
  // FPNegator #(.fpwidth(64)) fpnegator_1: pin names not known; wires that end beside it: inval1, fpnegator_1_p2
  not not_1 (outval1[63], inval1[63]);
  Comparator #(.width(11)) comparator_1 (.a(inval1[62:52]), .b({11{1'b1}}), .eq(isnan1));  // open: gt, lt
  // Probe on fpnegator_1_p2
  // Probe on {outval1[63], inval1[62:0]}

  assign outval1[62:0] = inval1[62:0];

  // Notes on the sheet:
  //   inval1: initial=0x4040152bd3c36113
endmodule

module fadd64 (
  input  [63:0] in_1,
  input  [63:0] in_2,
  input  [63:0] in_3,
  input  [63:0] inval1,
  input  [63:0] inval2,
  output [63:0] outval1,
  output isnan1
);

  wire comparator_1_eq, comparator_2_eq, comparator_3_gt, subtractor_1_bout;
  wire [5:0] hone64_1_outval1, multiplexer_3_out, subtractor_4_out, subtractor_5_out;
  wire [10:0] bit_extender_3_out, multiplexer_7_out;
  wire [15:0] bit_extender_1_out, bit_extender_2_out, negator_1_out, subtractor_1_out, subtractor_2_out,
       subtractor_3_out;
  wire [15:6] multiplexer_3_out_2;
  wire [63:0] adder_1_out, adder_2_out, fpadder_1_out, multiplexer_1_out, multiplexer_2_out,
       multiplexer_4_out, multiplexer_5_out, multiplexer_6_out, multiplexer_8_out, multiplexer_9_out,
       multiplexer_10_out, multiplexer_11_out, negator_2_out, negator_3_out, negator_4_out, shifter_1_out,
       shifter_2_out;

  // Probe on inval1
  // Probe on inval2
  Comparator #(.width(11)) comparator_1 (.a(inval1[62:52]), .b({11{1'b1}}), .eq(comparator_1_eq));  // open: gt, lt
  Comparator #(.width(11)) comparator_2 (.a(inval2[62:52]), .b({11{1'b1}}), .eq(comparator_2_eq));  // open: gt, lt
  Multiplexer #(.width(64)) multiplexer_1 (
    .in0({3'b001, inval1[51:0], {9{1'b0}}}), .in1({3'b001, inval2[51:0], {9{1'b0}}}),
    .out(multiplexer_1_out), .sel(subtractor_1_bout));
  Multiplexer #(.width(64)) multiplexer_2 (
    .in0({3'b001, inval2[51:0], {9{1'b0}}}), .in1({3'b001, inval1[51:0], {9{1'b0}}}),
    .out(multiplexer_2_out), .sel(subtractor_1_bout));
  Subtractor #(.width(16)) subtractor_1 (
    .a(subtractor_2_out), .b(subtractor_3_out), .out(subtractor_1_out), .bout(subtractor_1_bout));  // open: bin
  Subtractor #(.width(16)) subtractor_2 (
    .a(bit_extender_1_out), .b(16'h3ff), .out(subtractor_2_out));  // open: bin, bout
  assign bit_extender_1_out = {{5{1'b0}}, inval1[62:52]};  // Bit_Extender bit_extender_1
  or or_1 (isnan1, comparator_1_eq, comparator_2_eq);
  FPAdder #(.fpwidth(64)) fpadder_1 (.a(inval1), .b(inval2), .out(fpadder_1_out));
  Shifter #(.shift("lr"), .width(64)) shifter_1 (
    .in(multiplexer_2_out), .\dist (multiplexer_3_out), .out(shifter_1_out));
  Multiplexer #(.width(16)) multiplexer_3 (
    .in0(subtractor_1_out), .in1(negator_1_out), .out({multiplexer_3_out_2, multiplexer_3_out}),
    .sel(subtractor_1_bout));
  Negator #(.width(16)) negator_1 (.in(subtractor_1_out), .out(negator_1_out));
  Subtractor #(.width(16)) subtractor_3 (
    .a(bit_extender_2_out), .b(16'h3ff), .out(subtractor_3_out));  // open: bin, bout
  assign bit_extender_2_out = {{5{1'b0}}, inval2[62:52]};  // Bit_Extender bit_extender_2
  Comparator #(.width(16)) comparator_3 (
    .a({multiplexer_3_out_2, multiplexer_3_out}), .b(16'h3f), .gt(comparator_3_gt));  // open: eq, lt
  Multiplexer #(.width(64)) multiplexer_4 (
    .in0(shifter_1_out), .in1({64{1'b0}}), .out(multiplexer_4_out), .sel(comparator_3_gt));
  Multiplexer #(.width(64)) multiplexer_5 (
    .in0(multiplexer_1_out), .in1(multiplexer_4_out), .out(multiplexer_5_out), .sel(subtractor_1_bout));
  Multiplexer #(.width(64)) multiplexer_6 (
    .in0(multiplexer_4_out), .in1(multiplexer_1_out), .out(multiplexer_6_out), .sel(subtractor_1_bout));
  Multiplexer #(.width(11)) multiplexer_7 (
    .in0(inval1[62:52]), .in1(inval2[62:52]), .out(multiplexer_7_out), .sel(subtractor_1_bout));
  Negator #(.width(64)) negator_2 (.in(multiplexer_6_out), .out(negator_2_out));
  Negator #(.width(64)) negator_3 (.in(multiplexer_5_out), .out(negator_3_out));
  Multiplexer #(.width(64)) multiplexer_8 (
    .in0(multiplexer_6_out), .in1(negator_2_out), .out(multiplexer_8_out), .sel(inval2[63]));
  Multiplexer #(.width(64)) multiplexer_9 (
    .in0(multiplexer_5_out), .in1(negator_3_out), .out(multiplexer_9_out), .sel(inval1[63]));
  Adder #(.width(64)) adder_1 (.a(multiplexer_9_out), .b(multiplexer_8_out), .out(adder_1_out));  // open: cin, cout
  Negator #(.width(64)) negator_4 (.in(adder_1_out), .out(negator_4_out));
  Comparator #(.width(64)) comparator_4 (.a(adder_1_out), .b({64{1'b0}}), .lt(outval1[63]));  // open: gt, eq
  Multiplexer #(.width(64)) multiplexer_10 (
    .in0(adder_1_out), .in1(negator_4_out), .out(multiplexer_10_out), .sel(outval1[63]));
  Shifter #(.width(64)) shifter_2 (.in(multiplexer_10_out), .\dist (subtractor_4_out), .out(shifter_2_out));
  Subtractor #(.width(6)) subtractor_4 (
    .a({6{1'b1}}), .b(hone64_1_outval1), .out(subtractor_4_out));  // open: bin, bout
  Subtractor #(.width(6)) subtractor_5 (
    .a(subtractor_4_out), .b(6'b000010), .out(subtractor_5_out));  // open: bin, bout
  hone64 hone64_1 (.inval1(multiplexer_10_out), .outval1(hone64_1_outval1));  // open: contains1
  assign bit_extender_3_out = {{5{subtractor_5_out[5]}}, subtractor_5_out};  // Bit_Extender bit_extender_3
  Subtractor #(.width(11)) subtractor_6 (
    .a(multiplexer_7_out), .b(bit_extender_3_out), .out(outval1[62:52]));  // open: bin, bout
  Multiplexer #(.width(64)) multiplexer_11 (
    .in0(shifter_2_out), .in1(adder_2_out),
    .out({multiplexer_11_out[63], outval1[51:0], multiplexer_11_out[10:0]}), .sel(shifter_2_out[10]));
  Adder #(.width(64)) adder_2 (.a(64'h800), .b(shifter_2_out), .out(adder_2_out));  // open: cin, cout
  // Probe on fpadder_1_out
  // Probe on fpadder_1_out
  // Probe on outval1

  // Notes on the sheet:
  //   in_1: initial=0x4040152bd3c36113
  //   in_2: initial=0x4061d93f7ced9168
  //   in_3: initial=0xc056ef0d844d013b
  //   inval1: initial=0x4040152bd3c36113
  //   inval2: initial=0x4061d93f7ced9168
endmodule

module fsub64 (
  input  [63:0] inval1,
  input  [63:0] inval2,
  output [63:0] outval1
);
endmodule

module fmul64 (
  input  [63:0] inval1,
  input  [63:0] inval2,
  output [63:0] outval1
);
endmodule

module fdiv64 (
  input  [63:0] inval1,
  input  [63:0] inval2,
  output [63:0] outval1
);
endmodule

module hone64 (
  input  [63:0] inval1,
  output [5:0] outval1,
  output contains1
);

  wire bitfinder_1_found, not_1_out;
  wire [5:0] bitfinder_1_index, priority_encoder_1_out;

  // Probe on priority_encoder_1_out
  Priority_Encoder #(.select(6)) priority_encoder_1 (
    .in0(inval1[0]), .in1(inval1[1]), .in2(inval1[2]), .in3(inval1[3]), .in4(inval1[4]), .in5(inval1[5]),
    .in6(inval1[6]), .in7(inval1[7]), .in8(inval1[8]), .in9(inval1[9]), .in10(inval1[10]), .in11(inval1[11]),
    .in12(inval1[12]), .in13(inval1[13]), .in14(inval1[14]), .in15(inval1[15]), .in16(inval1[16]),
    .in17(inval1[17]), .in18(inval1[18]), .in19(inval1[19]), .in20(inval1[20]), .in21(inval1[21]),
    .in22(inval1[22]), .in23(inval1[23]), .in24(inval1[24]), .in25(inval1[25]), .in26(inval1[26]),
    .in27(inval1[27]), .in28(inval1[28]), .in29(inval1[29]), .in30(inval1[30]), .in31(inval1[31]),
    .in32(inval1[32]), .in33(inval1[33]), .in34(inval1[34]), .in35(inval1[35]), .in36(inval1[36]),
    .in37(inval1[37]), .in38(inval1[38]), .in39(inval1[39]), .in40(inval1[40]), .in41(inval1[41]),
    .in42(inval1[42]), .in43(inval1[43]), .in44(inval1[44]), .in45(inval1[45]), .in46(inval1[46]),
    .in47(inval1[47]), .in48(inval1[48]), .in49(inval1[49]), .in50(inval1[50]), .in51(inval1[51]),
    .in52(inval1[52]), .in53(inval1[53]), .in54(inval1[54]), .in55(inval1[55]), .in56(inval1[56]),
    .in57(inval1[57]), .in58(inval1[58]), .in59(inval1[59]), .in60(inval1[60]), .in61(inval1[61]),
    .in62(inval1[62]), .in63(inval1[63]), .out(priority_encoder_1_out), .gs(contains1));  // open: en_out, en_in
  BitFinder #(.\type ("high1"), .width(64)) bitfinder_1 (
    .in(inval1), .index(bitfinder_1_index), .found(bitfinder_1_found));
  Multiplexer #(.width(6)) multiplexer_1 (
    .in0(priority_encoder_1_out), .in1({6{1'b0}}), .out(outval1), .sel(not_1_out));
  not not_1 (not_1_out, contains1);
  // Probe on bitfinder_1_index
  // Probe on bitfinder_1_found
  // Probe on outval1

  // Notes on the sheet:
  //   inval1: initial=0xb000000003ff
endmodule

module add128 (
  input  [63:0] inval1a,
  input  [63:0] inval1b,
  input  [63:0] inval2a,
  input  [63:0] inval2b,
  input  carryin1,
  output [63:0] outval1a,
  output [63:0] outval1b,
  output carryout1
);

  wire adder_1_cout;

  Adder #(.width(64)) adder_1 (.a(inval1a), .b(inval2a), .out(outval1a), .cin(carryin1), .cout(adder_1_cout));
  Adder #(.width(64)) adder_2 (.a(inval1b), .b(inval2b), .out(outval1b), .cin(adder_1_cout), .cout(carryout1));

  // Notes on the sheet:
  //   inval1a: initial=0xf000b000000003ff
  //   inval1b: initial=0xfff0000bff
  //   inval2a: initial=0x8321000000001234
  //   inval2b: initial=0xb0000a4b2
endmodule

module neg128 (
  input  [63:0] inval1a,
  input  [63:0] inval1b,
  output [63:0] outval1a,
  output [63:0] outval1b
);

  wire adder_1_cout;
  wire [63:0] not_1_out, not_2_out;

  assign not_1_out = ~inval1a;  // NOT_Gate not_1, 64 bits wide
  assign not_2_out = ~inval1b;  // NOT_Gate not_2, 64 bits wide
  Adder #(.width(64)) adder_1 (.a(not_1_out), .b(64'h1), .out(outval1a), .cout(adder_1_cout));  // open: cin
  Adder #(.width(64)) adder_2 (.a(not_2_out), .b({64{1'b0}}), .out(outval1b), .cin(adder_1_cout));  // open: cout

  // Notes on the sheet:
  //   inval1a: initial=0x8000000000000000
  //   inval1b: initial=0xb000000003ff
endmodule

module shl128 (
  input  [63:0] inval1a,
  input  [63:0] inval1b,
  input  [6:0] shift1a,
  output [63:0] outval1a,
  output [63:0] outval1b
);

  wire [63:0] and_1_out, and_2_out, not_1_out, or_1_out, shifter_1_out, shifter_2_out, shifter_3_out,
       shifter_4_out;

  Shifter #(.width(64)) shifter_1 (.in({64{1'b1}}), .\dist (shift1a[5:0]), .out(shifter_1_out));
  Shifter #(.shift("rl"), .width(64)) shifter_2 (.in(inval1a), .\dist (shift1a[5:0]), .out(shifter_2_out));
  Shifter #(.width(64)) shifter_3 (.in(inval1b), .\dist (shift1a[5:0]), .out(shifter_3_out));
  Shifter #(.width(64)) shifter_4 (.in(inval1a), .\dist (shift1a[5:0]), .out(shifter_4_out));
  assign not_1_out = ~shifter_1_out;  // NOT_Gate not_1, 64 bits wide
  assign and_1_out = not_1_out & shifter_2_out;  // AND_Gate and_1, 64 bits wide
  assign and_2_out = shifter_1_out & shifter_2_out;  // AND_Gate and_2, 64 bits wide
  assign or_1_out = and_1_out | shifter_3_out;  // OR_Gate or_1, 64 bits wide
  Multiplexer #(.width(64)) multiplexer_1 (.in0(and_2_out), .in1({64{1'b0}}), .out(outval1a), .sel(shift1a[6]));
  Multiplexer #(.width(64)) multiplexer_2 (.in0(or_1_out), .in1(shifter_4_out), .out(outval1b), .sel(shift1a[6]));

  // Notes on the sheet:
  //   inval1a: initial=0xffff000000000000
  //   inval1b: initial=0xf00000000fff
  //   shift1a: initial=0x10
endmodule

module shr128 (
  input  [63:0] inval1a,
  input  [63:0] inval1b,
  input  [6:0] shift1a,
  output [63:0] outval1a,
  output [63:0] outval1b
);

  wire [63:0] and_1_out, and_2_out, not_1_out, or_1_out, shifter_1_out, shifter_2_out, shifter_3_out,
       shifter_4_out;

  Shifter #(.shift("lr"), .width(64)) shifter_1 (.in(inval1b), .\dist (shift1a[5:0]), .out(shifter_1_out));
  Shifter #(.shift("lr"), .width(64)) shifter_2 (.in(inval1a), .\dist (shift1a[5:0]), .out(shifter_2_out));
  Shifter #(.shift("lr"), .width(64)) shifter_3 (.in({64{1'b1}}), .\dist (shift1a[5:0]), .out(shifter_3_out));
  Shifter #(.shift("rr"), .width(64)) shifter_4 (.in(inval1b), .\dist (shift1a[5:0]), .out(shifter_4_out));
  assign not_1_out = ~shifter_3_out;  // NOT_Gate not_1, 64 bits wide
  assign and_1_out = not_1_out & shifter_4_out;  // AND_Gate and_1, 64 bits wide
  assign and_2_out = shifter_3_out & shifter_4_out;  // AND_Gate and_2, 64 bits wide
  assign or_1_out = shifter_2_out | and_1_out;  // OR_Gate or_1, 64 bits wide
  Multiplexer #(.width(64)) multiplexer_1 (.in0(or_1_out), .in1(shifter_1_out), .out(outval1a), .sel(shift1a[6]));
  Multiplexer #(.width(64)) multiplexer_2 (.in0(and_2_out), .in1({64{1'b0}}), .out(outval1b), .sel(shift1a[6]));

  // Notes on the sheet:
  //   inval1a: initial=0xffff000000000000
  //   inval1b: initial=0xf00000000fff
  //   shift1a: initial=0x10
endmodule

module lone64 (
  input  [63:0] inval1,
  output [5:0] outval1,
  output contains1
);

  wire bitfinder_1_found, not_1_out;
  wire [5:0] bitfinder_1_index, priority_encoder_1_p1, subtractor_1_out;

  BitFinder #(.width(64)) bitfinder_1 (.in(inval1), .index(bitfinder_1_index), .found(bitfinder_1_found));
  // Probe on priority_encoder_1_p1
  // Priority_Encoder #(.select(6)) priority_encoder_1: pin names not known; wires that end beside it: priority_encoder_1_p1, contains1
  Subtractor #(.width(6)) subtractor_1 (
    .a({6{1'b1}}), .b(priority_encoder_1_p1), .out(subtractor_1_out));  // open: bin, bout
  Multiplexer #(.width(6)) multiplexer_1 (.in0(subtractor_1_out), .in1({6{1'b0}}), .out(outval1), .sel(not_1_out));
  not not_1 (not_1_out, contains1);
  // Probe on bitfinder_1_index
  // Probe on bitfinder_1_found
  // Probe on outval1

  // Notes on the sheet:
  //   inval1: initial=0xb0000003ff80
endmodule

module hzero64 (
  input  [63:0] inval1,
  output [5:0] outval1,
  output contains1
);

  wire bitfinder_1_found, not_2_out;
  wire [5:0] bitfinder_1_index, priority_encoder_1_out;
  wire [63:0] not_1_out;

  assign not_1_out = ~inval1;  // NOT_Gate not_1, 64 bits wide
  // Probe on priority_encoder_1_out
  Priority_Encoder #(.select(6)) priority_encoder_1 (
    .in0(not_1_out[0]), .in1(not_1_out[1]), .in2(not_1_out[2]), .in3(not_1_out[3]), .in4(not_1_out[4]),
    .in5(not_1_out[5]), .in6(not_1_out[6]), .in7(not_1_out[7]), .in8(not_1_out[8]), .in9(not_1_out[9]),
    .in10(not_1_out[10]), .in11(not_1_out[11]), .in12(not_1_out[12]), .in13(not_1_out[13]),
    .in14(not_1_out[14]), .in15(not_1_out[15]), .in16(not_1_out[16]), .in17(not_1_out[17]),
    .in18(not_1_out[18]), .in19(not_1_out[19]), .in20(not_1_out[20]), .in21(not_1_out[21]),
    .in22(not_1_out[22]), .in23(not_1_out[23]), .in24(not_1_out[24]), .in25(not_1_out[25]),
    .in26(not_1_out[26]), .in27(not_1_out[27]), .in28(not_1_out[28]), .in29(not_1_out[29]),
    .in30(not_1_out[30]), .in31(not_1_out[31]), .in32(not_1_out[32]), .in33(not_1_out[33]),
    .in34(not_1_out[34]), .in35(not_1_out[35]), .in36(not_1_out[36]), .in37(not_1_out[37]),
    .in38(not_1_out[38]), .in39(not_1_out[39]), .in40(not_1_out[40]), .in41(not_1_out[41]),
    .in42(not_1_out[42]), .in43(not_1_out[43]), .in44(not_1_out[44]), .in45(not_1_out[45]),
    .in46(not_1_out[46]), .in47(not_1_out[47]), .in48(not_1_out[48]), .in49(not_1_out[49]),
    .in50(not_1_out[50]), .in51(not_1_out[51]), .in52(not_1_out[52]), .in53(not_1_out[53]),
    .in54(not_1_out[54]), .in55(not_1_out[55]), .in56(not_1_out[56]), .in57(not_1_out[57]),
    .in58(not_1_out[58]), .in59(not_1_out[59]), .in60(not_1_out[60]), .in61(not_1_out[61]),
    .in62(not_1_out[62]), .in63(not_1_out[63]), .out(priority_encoder_1_out), .gs(contains1));  // open: en_out, en_in
  BitFinder #(.\type ("high0"), .width(64)) bitfinder_1 (
    .in(inval1), .index(bitfinder_1_index), .found(bitfinder_1_found));
  Multiplexer #(.width(6)) multiplexer_1 (
    .in0(priority_encoder_1_out), .in1({6{1'b0}}), .out(outval1), .sel(not_2_out));
  not not_2 (not_2_out, contains1);
  // Probe on bitfinder_1_index
  // Probe on bitfinder_1_found
  // Probe on outval1

  // Notes on the sheet:
  //   inval1: initial=0xffffb000003fffff
endmodule

module lzero64 (
  input  [63:0] inval1,
  output [5:0] outval1,
  output contains1
);

  wire bitfinder_1_found, not_2_out;
  wire [5:0] bitfinder_1_index, priority_encoder_1_p1, subtractor_1_out;
  wire [63:0] not_1_out;

  assign not_1_out = ~inval1;  // NOT_Gate not_1, 64 bits wide
  BitFinder #(.\type ("low0"), .width(64)) bitfinder_1 (
    .in(inval1), .index(bitfinder_1_index), .found(bitfinder_1_found));
  // Probe on priority_encoder_1_p1
  // Priority_Encoder #(.select(6)) priority_encoder_1: pin names not known; wires that end beside it: priority_encoder_1_p1, contains1
  Subtractor #(.width(6)) subtractor_1 (
    .a({6{1'b1}}), .b(priority_encoder_1_p1), .out(subtractor_1_out));  // open: bin, bout
  Multiplexer #(.width(6)) multiplexer_1 (.in0(subtractor_1_out), .in1({6{1'b0}}), .out(outval1), .sel(not_2_out));
  not not_2 (not_2_out, contains1);
  // Probe on bitfinder_1_index
  // Probe on bitfinder_1_found
  // Probe on outval1

  // Notes on the sheet:
  //   inval1: initial=0xffffb0000003ffff
endmodule

module ones64 (
  input  [63:0] inval1,
  output [6:0] outval1
);

  wire [1:0] adder_1_out, adder_2_out, adder_3_out, adder_4_out, adder_5_out, adder_6_out, adder_7_out,
       adder_8_out, adder_9_out, adder_10_out, adder_11_out, adder_12_out, adder_13_out, adder_14_out,
       adder_15_out, adder_16_out, adder_17_out, adder_18_out, adder_19_out, adder_20_out, adder_21_out,
       adder_22_out, adder_23_out, adder_24_out, adder_25_out, adder_26_out, adder_27_out, adder_28_out,
       adder_29_out, adder_30_out, adder_31_out, adder_32_out, adder_33_out, adder_34_out, adder_35_out,
       adder_36_out, adder_37_out, adder_38_out, adder_39_out, adder_40_out, adder_41_out, adder_42_out,
       adder_43_out, adder_44_out, adder_45_out, adder_46_out, adder_47_out, adder_48_out;
  wire [2:0] adder_49_out, adder_50_out, adder_51_out, adder_52_out, adder_53_out, adder_54_out,
       adder_55_out, adder_56_out;
  wire [2:2] adder_33_cout, adder_34_cout, adder_35_cout, adder_36_cout, adder_37_cout, adder_38_cout,
       adder_39_cout, adder_40_cout, adder_41_cout, adder_42_cout, adder_43_cout, adder_44_cout,
       adder_45_cout, adder_46_cout, adder_47_cout, adder_48_cout;
  wire [3:0] adder_57_out, adder_58_out, adder_59_out, adder_60_out;
  wire [3:3] adder_49_cout, adder_50_cout, adder_51_cout, adder_52_cout, adder_53_cout, adder_54_cout,
       adder_55_cout, adder_56_cout;
  wire [4:0] adder_61_out, adder_62_out;
  wire [4:4] adder_57_cout, adder_58_cout, adder_59_cout, adder_60_cout;
  wire [5:5] adder_61_cout, adder_62_cout;
  wire [6:0] bitadder_1_out;

  BitAdder #(.width(64)) bitadder_1 (.in0(inval1), .out(bitadder_1_out));
  Adder #(.width(1)) adder_1 (.a(inval1[0]), .b(inval1[1]), .out(adder_1_out[0]), .cout(adder_1_out[1]));  // open: cin
  Adder #(.width(1)) adder_2 (.a(inval1[2]), .b(inval1[3]), .out(adder_2_out[0]), .cout(adder_2_out[1]));  // open: cin
  Adder #(.width(1)) adder_3 (.a(inval1[4]), .b(inval1[5]), .out(adder_3_out[0]), .cout(adder_3_out[1]));  // open: cin
  Adder #(.width(1)) adder_4 (.a(inval1[6]), .b(inval1[7]), .out(adder_4_out[0]), .cout(adder_4_out[1]));  // open: cin
  Adder #(.width(1)) adder_5 (.a(inval1[8]), .b(inval1[9]), .out(adder_5_out[0]), .cout(adder_5_out[1]));  // open: cin
  Adder #(.width(1)) adder_6 (
    .a(inval1[10]), .b(inval1[11]), .out(adder_6_out[0]), .cout(adder_6_out[1]));  // open: cin
  Adder #(.width(1)) adder_7 (
    .a(inval1[12]), .b(inval1[13]), .out(adder_7_out[0]), .cout(adder_7_out[1]));  // open: cin
  Adder #(.width(1)) adder_8 (
    .a(inval1[14]), .b(inval1[15]), .out(adder_8_out[0]), .cout(adder_8_out[1]));  // open: cin
  Adder #(.width(1)) adder_9 (
    .a(inval1[16]), .b(inval1[17]), .out(adder_9_out[0]), .cout(adder_9_out[1]));  // open: cin
  Adder #(.width(1)) adder_10 (
    .a(inval1[18]), .b(inval1[19]), .out(adder_10_out[0]), .cout(adder_10_out[1]));  // open: cin
  Adder #(.width(1)) adder_11 (
    .a(inval1[20]), .b(inval1[21]), .out(adder_11_out[0]), .cout(adder_11_out[1]));  // open: cin
  Adder #(.width(1)) adder_12 (
    .a(inval1[22]), .b(inval1[23]), .out(adder_12_out[0]), .cout(adder_12_out[1]));  // open: cin
  Adder #(.width(1)) adder_13 (
    .a(inval1[24]), .b(inval1[25]), .out(adder_13_out[0]), .cout(adder_13_out[1]));  // open: cin
  Adder #(.width(1)) adder_14 (
    .a(inval1[26]), .b(inval1[27]), .out(adder_14_out[0]), .cout(adder_14_out[1]));  // open: cin
  Adder #(.width(1)) adder_15 (
    .a(inval1[28]), .b(inval1[29]), .out(adder_15_out[0]), .cout(adder_15_out[1]));  // open: cin
  Adder #(.width(1)) adder_16 (
    .a(inval1[30]), .b(inval1[31]), .out(adder_16_out[0]), .cout(adder_16_out[1]));  // open: cin
  Adder #(.width(1)) adder_17 (
    .a(inval1[32]), .b(inval1[33]), .out(adder_17_out[0]), .cout(adder_17_out[1]));  // open: cin
  Adder #(.width(1)) adder_18 (
    .a(inval1[34]), .b(inval1[35]), .out(adder_18_out[0]), .cout(adder_18_out[1]));  // open: cin
  Adder #(.width(1)) adder_19 (
    .a(inval1[36]), .b(inval1[37]), .out(adder_19_out[0]), .cout(adder_19_out[1]));  // open: cin
  Adder #(.width(1)) adder_20 (
    .a(inval1[38]), .b(inval1[39]), .out(adder_20_out[0]), .cout(adder_20_out[1]));  // open: cin
  Adder #(.width(1)) adder_21 (
    .a(inval1[40]), .b(inval1[41]), .out(adder_21_out[0]), .cout(adder_21_out[1]));  // open: cin
  Adder #(.width(1)) adder_22 (
    .a(inval1[42]), .b(inval1[43]), .out(adder_22_out[0]), .cout(adder_22_out[1]));  // open: cin
  Adder #(.width(1)) adder_23 (
    .a(inval1[44]), .b(inval1[45]), .out(adder_23_out[0]), .cout(adder_23_out[1]));  // open: cin
  Adder #(.width(1)) adder_24 (
    .a(inval1[46]), .b(inval1[47]), .out(adder_24_out[0]), .cout(adder_24_out[1]));  // open: cin
  Adder #(.width(1)) adder_25 (
    .a(inval1[48]), .b(inval1[49]), .out(adder_25_out[0]), .cout(adder_25_out[1]));  // open: cin
  Adder #(.width(1)) adder_26 (
    .a(inval1[50]), .b(inval1[51]), .out(adder_26_out[0]), .cout(adder_26_out[1]));  // open: cin
  Adder #(.width(1)) adder_27 (
    .a(inval1[52]), .b(inval1[53]), .out(adder_27_out[0]), .cout(adder_27_out[1]));  // open: cin
  Adder #(.width(1)) adder_28 (
    .a(inval1[54]), .b(inval1[55]), .out(adder_28_out[0]), .cout(adder_28_out[1]));  // open: cin
  Adder #(.width(1)) adder_29 (
    .a(inval1[56]), .b(inval1[57]), .out(adder_29_out[0]), .cout(adder_29_out[1]));  // open: cin
  Adder #(.width(1)) adder_30 (
    .a(inval1[58]), .b(inval1[59]), .out(adder_30_out[0]), .cout(adder_30_out[1]));  // open: cin
  Adder #(.width(1)) adder_31 (
    .a(inval1[60]), .b(inval1[61]), .out(adder_31_out[0]), .cout(adder_31_out[1]));  // open: cin
  Adder #(.width(1)) adder_32 (
    .a(inval1[62]), .b(inval1[63]), .out(adder_32_out[0]), .cout(adder_32_out[1]));  // open: cin
  Adder #(.width(2)) adder_33 (
    .a(adder_1_out), .b(adder_2_out), .out(adder_33_out), .cout(adder_33_cout[2]));  // open: cin
  Adder #(.width(2)) adder_34 (
    .a(adder_3_out), .b(adder_4_out), .out(adder_34_out), .cout(adder_34_cout[2]));  // open: cin
  Adder #(.width(2)) adder_35 (
    .a(adder_5_out), .b(adder_6_out), .out(adder_35_out), .cout(adder_35_cout[2]));  // open: cin
  Adder #(.width(2)) adder_36 (
    .a(adder_7_out), .b(adder_8_out), .out(adder_36_out), .cout(adder_36_cout[2]));  // open: cin
  Adder #(.width(2)) adder_37 (
    .a(adder_9_out), .b(adder_10_out), .out(adder_37_out), .cout(adder_37_cout[2]));  // open: cin
  Adder #(.width(2)) adder_38 (
    .a(adder_11_out), .b(adder_12_out), .out(adder_38_out), .cout(adder_38_cout[2]));  // open: cin
  Adder #(.width(2)) adder_39 (
    .a(adder_13_out), .b(adder_14_out), .out(adder_39_out), .cout(adder_39_cout[2]));  // open: cin
  Adder #(.width(2)) adder_40 (
    .a(adder_15_out), .b(adder_16_out), .out(adder_40_out), .cout(adder_40_cout[2]));  // open: cin
  Adder #(.width(2)) adder_41 (
    .a(adder_17_out), .b(adder_18_out), .out(adder_41_out), .cout(adder_41_cout[2]));  // open: cin
  Adder #(.width(2)) adder_42 (
    .a(adder_19_out), .b(adder_20_out), .out(adder_42_out), .cout(adder_42_cout[2]));  // open: cin
  Adder #(.width(2)) adder_43 (
    .a(adder_21_out), .b(adder_22_out), .out(adder_43_out), .cout(adder_43_cout[2]));  // open: cin
  Adder #(.width(2)) adder_44 (
    .a(adder_23_out), .b(adder_24_out), .out(adder_44_out), .cout(adder_44_cout[2]));  // open: cin
  Adder #(.width(2)) adder_45 (
    .a(adder_25_out), .b(adder_26_out), .out(adder_45_out), .cout(adder_45_cout[2]));  // open: cin
  Adder #(.width(2)) adder_46 (
    .a(adder_27_out), .b(adder_28_out), .out(adder_46_out), .cout(adder_46_cout[2]));  // open: cin
  Adder #(.width(2)) adder_47 (
    .a(adder_29_out), .b(adder_30_out), .out(adder_47_out), .cout(adder_47_cout[2]));  // open: cin
  Adder #(.width(2)) adder_48 (
    .a(adder_31_out), .b(adder_32_out), .out(adder_48_out), .cout(adder_48_cout[2]));  // open: cin
  Adder #(.width(3)) adder_49 (
    .a({adder_33_cout[2], adder_33_out}), .b({adder_34_cout[2], adder_34_out}), .out(adder_49_out),
    .cout(adder_49_cout[3]));  // open: cin
  Adder #(.width(3)) adder_50 (
    .a({adder_35_cout[2], adder_35_out}), .b({adder_36_cout[2], adder_36_out}), .out(adder_50_out),
    .cout(adder_50_cout[3]));  // open: cin
  Adder #(.width(3)) adder_51 (
    .a({adder_37_cout[2], adder_37_out}), .b({adder_38_cout[2], adder_38_out}), .out(adder_51_out),
    .cout(adder_51_cout[3]));  // open: cin
  Adder #(.width(3)) adder_52 (
    .a({adder_39_cout[2], adder_39_out}), .b({adder_40_cout[2], adder_40_out}), .out(adder_52_out),
    .cout(adder_52_cout[3]));  // open: cin
  Adder #(.width(3)) adder_53 (
    .a({adder_41_cout[2], adder_41_out}), .b({adder_42_cout[2], adder_42_out}), .out(adder_53_out),
    .cout(adder_53_cout[3]));  // open: cin
  Adder #(.width(3)) adder_54 (
    .a({adder_43_cout[2], adder_43_out}), .b({adder_44_cout[2], adder_44_out}), .out(adder_54_out),
    .cout(adder_54_cout[3]));  // open: cin
  Adder #(.width(3)) adder_55 (
    .a({adder_45_cout[2], adder_45_out}), .b({adder_46_cout[2], adder_46_out}), .out(adder_55_out),
    .cout(adder_55_cout[3]));  // open: cin
  Adder #(.width(3)) adder_56 (
    .a({adder_47_cout[2], adder_47_out}), .b({adder_48_cout[2], adder_48_out}), .out(adder_56_out),
    .cout(adder_56_cout[3]));  // open: cin
  Adder #(.width(4)) adder_57 (
    .a({adder_49_cout[3], adder_49_out}), .b({adder_50_cout[3], adder_50_out}), .out(adder_57_out),
    .cout(adder_57_cout[4]));  // open: cin
  Adder #(.width(4)) adder_58 (
    .a({adder_51_cout[3], adder_51_out}), .b({adder_52_cout[3], adder_52_out}), .out(adder_58_out),
    .cout(adder_58_cout[4]));  // open: cin
  Adder #(.width(4)) adder_59 (
    .a({adder_53_cout[3], adder_53_out}), .b({adder_54_cout[3], adder_54_out}), .out(adder_59_out),
    .cout(adder_59_cout[4]));  // open: cin
  Adder #(.width(4)) adder_60 (
    .a({adder_55_cout[3], adder_55_out}), .b({adder_56_cout[3], adder_56_out}), .out(adder_60_out),
    .cout(adder_60_cout[4]));  // open: cin
  Adder #(.width(5)) adder_61 (
    .a({adder_57_cout[4], adder_57_out}), .b({adder_58_cout[4], adder_58_out}), .out(adder_61_out),
    .cout(adder_61_cout[5]));  // open: cin
  Adder #(.width(5)) adder_62 (
    .a({adder_59_cout[4], adder_59_out}), .b({adder_60_cout[4], adder_60_out}), .out(adder_62_out),
    .cout(adder_62_cout[5]));  // open: cin
  Adder #(.width(6)) adder_63 (
    .a({adder_61_cout[5], adder_61_out}), .b({adder_62_cout[5], adder_62_out}), .out(outval1[5:0]),
    .cout(outval1[6]));  // open: cin
  // Probe on bitadder_1_out
  // Probe on outval1

  // Notes on the sheet:
  //   inval1: initial=0xfa04c5873b93dd10
endmodule

module add64 (
  input  [63:0] in_1,
  input  [63:0] in_2,
  input  [63:0] inval1,
  input  [63:0] inval2,
  output [63:0] outval1
);

  wire [63:0] adder_1_out, and_1_out, and_2_out, and_3_out, and_4_out, and_5_out, and_6_out, and_7_out,
       and_8_out, and_9_out, and_10_out, and_11_out, and_12_out, and_13_out, and_14_out, and_15_out,
       and_16_out, and_17_out, shifter_1_out, shifter_2_out, shifter_3_out, shifter_4_out, shifter_5_out,
       shifter_6_out, shifter_7_out, shifter_8_out, shifter_9_out, shifter_10_out, shifter_11_out,
       shifter_12_out, shifter_13_out, shifter_14_out, shifter_15_out, shifter_16_out, xor_1_out, xor_2_out,
       xor_3_out, xor_4_out, xor_5_out, xor_6_out, xor_7_out, xor_8_out, xor_9_out, xor_10_out, xor_11_out,
       xor_12_out, xor_13_out, xor_14_out, xor_15_out, xor_16_out;

  // Probe on inval1
  // Probe on inval1
  // Probe on inval2
  // Probe on inval2
  assign xor_1_out = inval1 ^ inval2;  // XOR_Gate xor_1, 64 bits wide
  assign and_1_out = inval1 & inval2;  // AND_Gate and_1, 64 bits wide
  Shifter #(.width(64)) shifter_1 (.in(and_1_out), .\dist (6'b000001), .out(shifter_1_out));
  assign xor_2_out = xor_1_out ^ shifter_1_out;  // XOR_Gate xor_2, 64 bits wide
  assign and_2_out = xor_1_out & shifter_1_out;  // AND_Gate and_2, 64 bits wide
  Shifter #(.width(64)) shifter_2 (.in(and_2_out), .\dist (6'b000001), .out(shifter_2_out));
  assign xor_3_out = xor_2_out ^ shifter_2_out;  // XOR_Gate xor_3, 64 bits wide
  assign and_3_out = xor_2_out & shifter_2_out;  // AND_Gate and_3, 64 bits wide
  Shifter #(.width(64)) shifter_3 (.in(and_3_out), .\dist (6'b000001), .out(shifter_3_out));
  Adder #(.width(64)) adder_1 (.a(inval1), .b(inval2), .out(adder_1_out));  // open: cin, cout
  assign xor_4_out = xor_3_out ^ shifter_3_out;  // XOR_Gate xor_4, 64 bits wide
  assign and_4_out = xor_3_out & shifter_3_out;  // AND_Gate and_4, 64 bits wide
  Shifter #(.width(64)) shifter_4 (.in(and_4_out), .\dist (6'b000001), .out(shifter_4_out));
  assign xor_5_out = xor_4_out ^ shifter_4_out;  // XOR_Gate xor_5, 64 bits wide
  assign and_5_out = xor_4_out & shifter_4_out;  // AND_Gate and_5, 64 bits wide
  Shifter #(.width(64)) shifter_5 (.in(and_5_out), .\dist (6'b000001), .out(shifter_5_out));
  assign xor_6_out = xor_5_out ^ shifter_5_out;  // XOR_Gate xor_6, 64 bits wide
  assign and_6_out = xor_5_out & shifter_5_out;  // AND_Gate and_6, 64 bits wide
  Shifter #(.width(64)) shifter_6 (.in(and_6_out), .\dist (6'b000001), .out(shifter_6_out));
  assign xor_7_out = xor_6_out ^ shifter_6_out;  // XOR_Gate xor_7, 64 bits wide
  assign and_7_out = xor_6_out & shifter_6_out;  // AND_Gate and_7, 64 bits wide
  Shifter #(.width(64)) shifter_7 (.in(and_7_out), .\dist (6'b000001), .out(shifter_7_out));
  assign xor_8_out = xor_7_out ^ shifter_7_out;  // XOR_Gate xor_8, 64 bits wide
  assign and_8_out = xor_7_out & shifter_7_out;  // AND_Gate and_8, 64 bits wide
  Shifter #(.width(64)) shifter_8 (.in(and_8_out), .\dist (6'b000001), .out(shifter_8_out));
  assign xor_9_out = xor_8_out ^ shifter_8_out;  // XOR_Gate xor_9, 64 bits wide
  assign and_9_out = xor_8_out & shifter_8_out;  // AND_Gate and_9, 64 bits wide
  Shifter #(.width(64)) shifter_9 (.in(and_9_out), .\dist (6'b000001), .out(shifter_9_out));
  assign xor_10_out = xor_9_out ^ shifter_9_out;  // XOR_Gate xor_10, 64 bits wide
  assign and_10_out = xor_9_out & shifter_9_out;  // AND_Gate and_10, 64 bits wide
  Shifter #(.width(64)) shifter_10 (.in(and_10_out), .\dist (6'b000001), .out(shifter_10_out));
  assign xor_11_out = xor_10_out ^ shifter_10_out;  // XOR_Gate xor_11, 64 bits wide
  assign and_11_out = xor_10_out & shifter_10_out;  // AND_Gate and_11, 64 bits wide
  Shifter #(.width(64)) shifter_11 (.in(and_11_out), .\dist (6'b000001), .out(shifter_11_out));
  assign xor_12_out = xor_11_out ^ shifter_11_out;  // XOR_Gate xor_12, 64 bits wide
  assign and_12_out = xor_11_out & shifter_11_out;  // AND_Gate and_12, 64 bits wide
  Shifter #(.width(64)) shifter_12 (.in(and_12_out), .\dist (6'b000001), .out(shifter_12_out));
  assign xor_13_out = xor_12_out ^ shifter_12_out;  // XOR_Gate xor_13, 64 bits wide
  assign and_13_out = xor_12_out & shifter_12_out;  // AND_Gate and_13, 64 bits wide
  Shifter #(.width(64)) shifter_13 (.in(and_13_out), .\dist (6'b000001), .out(shifter_13_out));
  assign xor_14_out = xor_13_out ^ shifter_13_out;  // XOR_Gate xor_14, 64 bits wide
  assign and_14_out = xor_13_out & shifter_13_out;  // AND_Gate and_14, 64 bits wide
  Shifter #(.width(64)) shifter_14 (.in(and_14_out), .\dist (6'b000001), .out(shifter_14_out));
  assign xor_15_out = xor_14_out ^ shifter_14_out;  // XOR_Gate xor_15, 64 bits wide
  assign and_15_out = xor_14_out & shifter_14_out;  // AND_Gate and_15, 64 bits wide
  Shifter #(.width(64)) shifter_15 (.in(and_15_out), .\dist (6'b000001), .out(shifter_15_out));
  assign xor_16_out = xor_15_out ^ shifter_15_out;  // XOR_Gate xor_16, 64 bits wide
  assign and_16_out = xor_15_out & shifter_15_out;  // AND_Gate and_16, 64 bits wide
  Shifter #(.width(64)) shifter_16 (.in(and_16_out), .\dist (6'b000001), .out(shifter_16_out));
  assign outval1 = xor_16_out ^ shifter_16_out;  // XOR_Gate xor_17, 64 bits wide
  assign and_17_out = xor_16_out & shifter_16_out;  // AND_Gate and_17, 64 bits wide
  // Probe on adder_1_out
  // Probe on adder_1_out
  // Probe on adder_1_out
  // Probe on outval1
  // Probe on outval1
  // Probe on and_17_out

  // Notes on the sheet:
  //   inval1: initial=0xe0ff00ff000f12ff
  //   inval2: initial=0xe9ff0a20891512d7
  //   in_1: initial=0x4040152bd3c36113
  //   in_2: initial=0x4061d93f7ced9168
endmodule
