// Logisim project microfpgamux.circ as structural Verilog: 2 circuits, main circuit muxcore
module muxcore (
);

  wire [63:0] muxreg_1_o0, muxreg_1_o1, muxreg_1_o2, muxreg_1_o3, muxreg_1_o4, muxreg_1_o5, muxreg_1_o6,
       muxreg_1_o7, muxreg_1_o8, muxreg_1_o9, muxreg_1_o10, muxreg_1_o11, muxreg_1_o12, muxreg_1_o13,
       muxreg_1_o14, muxreg_1_o15, muxreg_1_r0, muxreg_1_r1, muxreg_1_r2, muxreg_1_r3, muxreg_1_r4,
       muxreg_1_r5, muxreg_1_r6, muxreg_1_r7, muxreg_1_r8, muxreg_1_r9, muxreg_1_r10, muxreg_1_r11,
       muxreg_1_r12, muxreg_1_r13, muxreg_1_r14, muxreg_1_r15, muxreg_2_o0, muxreg_2_o1, muxreg_2_o2,
       muxreg_2_o3, muxreg_2_o4, muxreg_2_o5, muxreg_2_o6, muxreg_2_o7, muxreg_2_o8, muxreg_2_o9,
       muxreg_2_o10, muxreg_2_o11, muxreg_2_o12, muxreg_2_o13, muxreg_2_o14, muxreg_2_o15, muxreg_2_r0,
       muxreg_2_r1, muxreg_2_r2, muxreg_2_r3, muxreg_2_r4, muxreg_2_r5, muxreg_2_r6, muxreg_2_r7,
       muxreg_2_r8, muxreg_2_r9, muxreg_2_r10, muxreg_2_r11, muxreg_2_r12, muxreg_2_r13, muxreg_2_r14,
       muxreg_2_r15, muxreg_3_o0, muxreg_3_o1, muxreg_3_o2, muxreg_3_o3, muxreg_3_o4, muxreg_3_o5,
       muxreg_3_o6, muxreg_3_o7, muxreg_3_o8, muxreg_3_o9, muxreg_3_o10, muxreg_3_o11, muxreg_3_o12,
       muxreg_3_o13, muxreg_3_o14, muxreg_3_o15, muxreg_3_r0, muxreg_3_r1, muxreg_3_r2, muxreg_3_r3,
       muxreg_3_r4, muxreg_3_r5, muxreg_3_r6, muxreg_3_r7, muxreg_3_r8, muxreg_3_r9, muxreg_3_r10,
       muxreg_3_r11, muxreg_3_r12, muxreg_3_r13, muxreg_3_r14, muxreg_3_r15;

  // Probe on muxreg_1_r0
  muxreg muxreg_1 (
    .A0(4'b0000), .A1(4'b0001), .A2(4'b0010), .A3(4'b0011), .A4(4'b0100), .A5(4'b0101), .A6(4'b0110),
    .A7(4'b0111), .A8(4'b1000), .A9(4'b1001), .A10(4'b1010), .A11(4'b1011), .A12(4'b1100), .A13(4'b1101),
    .A14(4'b1110), .A15(4'b1111), .D0({64{1'b0}}), .D1(64'h1111), .D2(64'h2222), .D3(64'h3333),
    .D4(64'h4444), .D5(64'h5555), .D6(64'h6666), .D7(64'h7777), .D8(64'h8888), .D9(64'h9999), .D10(64'haaaa),
    .D11(64'hbbbb), .D12(64'hcccc), .D13(64'hdddd), .D14(64'heeee), .D15(64'hffff), .LE0(1'b1), .LE1(1'b1),
    .LE2(1'b1), .LE3(1'b1), .LE4(1'b1), .LE5(1'b1), .LE6(1'b1), .LE7(1'b1), .LE8(1'b1), .LE9(1'b1),
    .LE10(1'b1), .LE11(1'b1), .LE12(1'b1), .LE13(1'b1), .LE14(1'b1), .LE15(1'b1), .R0(muxreg_1_r0),
    .R1(muxreg_1_r1), .R2(muxreg_1_r2), .R3(muxreg_1_r3), .R4(muxreg_1_r4), .R5(muxreg_1_r5),
    .R6(muxreg_1_r6), .R7(muxreg_1_r7), .R8(muxreg_1_r8), .R9(muxreg_1_r9), .R10(muxreg_1_r10),
    .R11(muxreg_1_r11), .R12(muxreg_1_r12), .R13(muxreg_1_r13), .R14(muxreg_1_r14), .R15(muxreg_1_r15),
    .O0(muxreg_1_o0), .O1(muxreg_1_o1), .O2(muxreg_1_o2), .O3(muxreg_1_o3), .O4(muxreg_1_o4),
    .O5(muxreg_1_o5), .O6(muxreg_1_o6), .O7(muxreg_1_o7), .O8(muxreg_1_o8), .O9(muxreg_1_o9),
    .O10(muxreg_1_o10), .O11(muxreg_1_o11), .O12(muxreg_1_o12), .O13(muxreg_1_o13), .O14(muxreg_1_o14),
    .O15(muxreg_1_o15));
  // Probe on muxreg_1_r1
  // Probe on muxreg_1_r2
  // Probe on muxreg_1_r3
  // Probe on muxreg_1_r4
  // Probe on muxreg_1_r5
  // Probe on muxreg_1_r6
  // Probe on muxreg_1_r7
  // Probe on muxreg_1_r8
  // Probe on muxreg_1_r9
  // Probe on muxreg_1_r10
  // Probe on muxreg_1_r11
  // Probe on muxreg_1_r12
  // Probe on muxreg_1_r13
  // Probe on muxreg_1_r14
  // Probe on muxreg_1_r15
  // Probe on muxreg_1_o0
  // Probe on muxreg_1_o1
  // Probe on muxreg_1_o2
  // Probe on muxreg_1_o3
  // Probe on muxreg_1_o4
  // Probe on muxreg_1_o5
  // Probe on muxreg_1_o6
  // Probe on muxreg_1_o7
  // Probe on muxreg_1_o8
  // Probe on muxreg_1_o9
  // Probe on muxreg_1_o10
  // Probe on muxreg_1_o11
  // Probe on muxreg_1_o12
  // Probe on muxreg_1_o13
  // Probe on muxreg_1_o14
  // Probe on muxreg_1_o15
  // Probe on muxreg_2_r0
  muxreg muxreg_2 (
    .A0(4'b0000), .A1(4'b0000), .A2(4'b1011), .A3(4'b0011), .A4(4'b0100), .A5(4'b1100), .A6(4'b0000),
    .A7(4'b0111), .A8(4'b0011), .A9(4'b1111), .A10(4'b1010), .A11(4'b0000), .A12(4'b1100), .A13(4'b1101),
    .A14(4'b0011), .A15(4'b0010), .D0({64{1'b0}}), .D1(64'h1111), .D2(64'h2222), .D3(64'h3333),
    .D4(64'h4444), .D5(64'h5555), .D6(64'h6666), .D7(64'h7777), .D8(64'h8888), .D9(64'h9999), .D10(64'haaaa),
    .D11(64'hbbbb), .D12(64'hcccc), .D13(64'hdddd), .D14(64'heeee), .D15(64'hffff), .LE0(1'b1), .LE1(1'b1),
    .LE2(1'b1), .LE3(1'b1), .LE4(1'b1), .LE5(1'b1), .LE6(1'b1), .LE7(1'b1), .LE8(1'b1), .LE9(1'b1),
    .LE10(1'b1), .LE11(1'b1), .LE12(1'b1), .LE13(1'b1), .LE14(1'b1), .LE15(1'b1), .R0(muxreg_2_r0),
    .R1(muxreg_2_r1), .R2(muxreg_2_r2), .R3(muxreg_2_r3), .R4(muxreg_2_r4), .R5(muxreg_2_r5),
    .R6(muxreg_2_r6), .R7(muxreg_2_r7), .R8(muxreg_2_r8), .R9(muxreg_2_r9), .R10(muxreg_2_r10),
    .R11(muxreg_2_r11), .R12(muxreg_2_r12), .R13(muxreg_2_r13), .R14(muxreg_2_r14), .R15(muxreg_2_r15),
    .O0(muxreg_2_o0), .O1(muxreg_2_o1), .O2(muxreg_2_o2), .O3(muxreg_2_o3), .O4(muxreg_2_o4),
    .O5(muxreg_2_o5), .O6(muxreg_2_o6), .O7(muxreg_2_o7), .O8(muxreg_2_o8), .O9(muxreg_2_o9),
    .O10(muxreg_2_o10), .O11(muxreg_2_o11), .O12(muxreg_2_o12), .O13(muxreg_2_o13), .O14(muxreg_2_o14),
    .O15(muxreg_2_o15));
  // Probe on muxreg_2_r1
  // Probe on muxreg_2_r2
  // Probe on muxreg_2_r3
  // Probe on muxreg_2_r4
  // Probe on muxreg_2_r5
  // Probe on muxreg_2_r6
  // Probe on muxreg_2_r7
  // Probe on muxreg_2_r8
  // Probe on muxreg_2_r9
  // Probe on muxreg_2_r10
  // Probe on muxreg_2_r11
  // Probe on muxreg_2_r12
  // Probe on muxreg_2_r13
  // Probe on muxreg_2_r14
  // Probe on muxreg_2_r15
  // Probe on muxreg_2_o0
  // Probe on muxreg_2_o1
  // Probe on muxreg_2_o2
  // Probe on muxreg_2_o3
  // Probe on muxreg_2_o4
  // Probe on muxreg_2_o5
  // Probe on muxreg_2_o6
  // Probe on muxreg_2_o7
  // Probe on muxreg_2_o8
  // Probe on muxreg_2_o9
  // Probe on muxreg_2_o10
  // Probe on muxreg_2_o11
  // Probe on muxreg_2_o12
  // Probe on muxreg_2_o13
  // Probe on muxreg_2_o14
  // Probe on muxreg_2_o15
  // Probe on muxreg_3_r0
  muxreg muxreg_3 (
    .A0(4'b0000), .A1(4'b0000), .A2(4'b1011), .A3(4'b0011), .A4(4'b0100), .A5(4'b1100), .A6(4'b0000),
    .A7(4'b0111), .A8(4'b0011), .A9(4'b1111), .A10(4'b1010), .A11(4'b0000), .A12(4'b1100), .A13(4'b1101),
    .A14(4'b0011), .A15(4'b0010), .D0({64{1'b0}}), .D1(64'h1111), .D2(64'h2222), .D3(64'h3333),
    .D4(64'h4444), .D5(64'h5555), .D6(64'h6666), .D7(64'h7777), .D8(64'h8888), .D9(64'h9999), .D10(64'haaaa),
    .D11(64'hbbbb), .D12(64'hcccc), .D13(64'hdddd), .D14(64'heeee), .D15(64'hffff), .LE0(1'b0), .LE1(1'b1),
    .LE2(1'b1), .LE3(1'b1), .LE4(1'b0), .LE5(1'b1), .LE6(1'b1), .LE7(1'b1), .LE8(1'b0), .LE9(1'b0),
    .LE10(1'b1), .LE11(1'b1), .LE12(1'b0), .LE13(1'b1), .LE14(1'b0), .LE15(1'b1), .R0(muxreg_3_r0),
    .R1(muxreg_3_r1), .R2(muxreg_3_r2), .R3(muxreg_3_r3), .R4(muxreg_3_r4), .R5(muxreg_3_r5),
    .R6(muxreg_3_r6), .R7(muxreg_3_r7), .R8(muxreg_3_r8), .R9(muxreg_3_r9), .R10(muxreg_3_r10),
    .R11(muxreg_3_r11), .R12(muxreg_3_r12), .R13(muxreg_3_r13), .R14(muxreg_3_r14), .R15(muxreg_3_r15),
    .O0(muxreg_3_o0), .O1(muxreg_3_o1), .O2(muxreg_3_o2), .O3(muxreg_3_o3), .O4(muxreg_3_o4),
    .O5(muxreg_3_o5), .O6(muxreg_3_o6), .O7(muxreg_3_o7), .O8(muxreg_3_o8), .O9(muxreg_3_o9),
    .O10(muxreg_3_o10), .O11(muxreg_3_o11), .O12(muxreg_3_o12), .O13(muxreg_3_o13), .O14(muxreg_3_o14),
    .O15(muxreg_3_o15));
  // Probe on muxreg_3_r1
  // Probe on muxreg_3_r2
  // Probe on muxreg_3_r3
  // Probe on muxreg_3_r4
  // Probe on muxreg_3_r5
  // Probe on muxreg_3_r6
  // Probe on muxreg_3_r7
  // Probe on muxreg_3_r8
  // Probe on muxreg_3_r9
  // Probe on muxreg_3_r10
  // Probe on muxreg_3_r11
  // Probe on muxreg_3_r12
  // Probe on muxreg_3_r13
  // Probe on muxreg_3_r14
  // Probe on muxreg_3_r15
  // Probe on muxreg_3_o0
  // Probe on muxreg_3_o1
  // Probe on muxreg_3_o2
  // Probe on muxreg_3_o3
  // Probe on muxreg_3_o4
  // Probe on muxreg_3_o5
  // Probe on muxreg_3_o6
  // Probe on muxreg_3_o7
  // Probe on muxreg_3_o8
  // Probe on muxreg_3_o9
  // Probe on muxreg_3_o10
  // Probe on muxreg_3_o11
  // Probe on muxreg_3_o12
  // Probe on muxreg_3_o13
  // Probe on muxreg_3_o14
  // Probe on muxreg_3_o15
endmodule

module muxreg (
  input  [3:0] A0,
  input  [3:0] A1,
  input  [3:0] A2,
  input  [3:0] A3,
  input  [3:0] A4,
  input  [3:0] A5,
  input  [3:0] A6,
  input  [3:0] A7,
  input  [3:0] A8,
  input  [3:0] A9,
  input  [3:0] A10,
  input  [3:0] A11,
  input  [3:0] A12,
  input  [3:0] A13,
  input  [3:0] A14,
  input  [3:0] A15,
  input  [63:0] D0,
  input  [63:0] D1,
  input  [63:0] D2,
  input  [63:0] D3,
  input  [63:0] D4,
  input  [63:0] D5,
  input  [63:0] D6,
  input  [63:0] D7,
  input  [63:0] D8,
  input  [63:0] D9,
  input  [63:0] D10,
  input  [63:0] D11,
  input  [63:0] D12,
  input  [63:0] D13,
  input  [63:0] D14,
  input  [63:0] D15,
  input  LE0,
  input  LE1,
  input  LE2,
  input  LE3,
  input  LE4,
  input  LE5,
  input  LE6,
  input  LE7,
  input  LE8,
  input  LE9,
  input  LE10,
  input  LE11,
  input  LE12,
  input  LE13,
  input  LE14,
  input  LE15,
  output [63:0] R0,
  output [63:0] R1,
  output [63:0] R2,
  output [63:0] R3,
  output [63:0] R4,
  output [63:0] R5,
  output [63:0] R6,
  output [63:0] R7,
  output [63:0] R8,
  output [63:0] R9,
  output [63:0] R10,
  output [63:0] R11,
  output [63:0] R12,
  output [63:0] R13,
  output [63:0] R14,
  output [63:0] R15,
  output [63:0] O0,
  output [63:0] O1,
  output [63:0] O2,
  output [63:0] O3,
  output [63:0] O4,
  output [63:0] O5,
  output [63:0] O6,
  output [63:0] O7,
  output [63:0] O8,
  output [63:0] O9,
  output [63:0] O10,
  output [63:0] O11,
  output [63:0] O12,
  output [63:0] O13,
  output [63:0] O14,
  output [63:0] O15
);

  wire clock_1_out, clock_2_out, clock_3_out, clock_4_out, clock_5_out, clock_6_out, clock_7_out,
       clock_8_out, clock_9_out, clock_10_out, clock_11_out, clock_12_out, clock_13_out, clock_14_out,
       clock_15_out, clock_16_out, comparator_1_eq, comparator_2_eq, comparator_3_eq, comparator_4_eq,
       comparator_5_eq, comparator_6_eq, comparator_7_eq, comparator_8_eq, comparator_9_eq, comparator_10_eq,
       comparator_11_eq, comparator_12_eq, comparator_13_eq, comparator_14_eq, comparator_15_eq,
       comparator_16_eq, comparator_17_eq, comparator_18_eq, comparator_19_eq, comparator_20_eq,
       comparator_21_eq, comparator_22_eq, comparator_23_eq, comparator_24_eq, comparator_25_eq,
       comparator_26_eq, comparator_27_eq, comparator_28_eq, comparator_29_eq, comparator_30_eq,
       comparator_31_eq, comparator_32_eq, comparator_33_eq, comparator_34_eq, comparator_35_eq,
       comparator_36_eq, comparator_37_eq, comparator_38_eq, comparator_39_eq, comparator_40_eq,
       comparator_41_eq, comparator_42_eq, comparator_43_eq, comparator_44_eq, comparator_45_eq,
       comparator_46_eq, comparator_47_eq, comparator_48_eq, comparator_49_eq, comparator_50_eq,
       comparator_51_eq, comparator_52_eq, comparator_53_eq, comparator_54_eq, comparator_55_eq,
       comparator_56_eq, comparator_57_eq, comparator_58_eq, comparator_59_eq, comparator_60_eq,
       comparator_61_eq, comparator_62_eq, comparator_63_eq, comparator_64_eq, comparator_65_eq,
       comparator_66_eq, comparator_67_eq, comparator_68_eq, comparator_69_eq, comparator_70_eq,
       comparator_71_eq, comparator_72_eq, comparator_73_eq, comparator_74_eq, comparator_75_eq,
       comparator_76_eq, comparator_77_eq, comparator_78_eq, comparator_79_eq, comparator_80_eq,
       comparator_81_eq, comparator_82_eq, comparator_83_eq, comparator_84_eq, comparator_85_eq,
       comparator_86_eq, comparator_87_eq, comparator_88_eq, comparator_89_eq, comparator_90_eq,
       comparator_91_eq, comparator_92_eq, comparator_93_eq, comparator_94_eq, comparator_95_eq,
       comparator_96_eq, comparator_97_eq, comparator_98_eq, comparator_99_eq, comparator_100_eq,
       comparator_101_eq, comparator_102_eq, comparator_103_eq, comparator_104_eq, comparator_105_eq,
       comparator_106_eq, comparator_107_eq, comparator_108_eq, comparator_109_eq, comparator_110_eq,
       comparator_111_eq, comparator_112_eq, comparator_113_eq, comparator_114_eq, comparator_115_eq,
       comparator_116_eq, comparator_117_eq, comparator_118_eq, comparator_119_eq, comparator_120_eq,
       comparator_121_eq, comparator_122_eq, comparator_123_eq, comparator_124_eq, comparator_125_eq,
       comparator_126_eq, comparator_127_eq, comparator_128_eq, comparator_129_eq, comparator_130_eq,
       comparator_131_eq, comparator_132_eq, comparator_133_eq, comparator_134_eq, comparator_135_eq,
       comparator_136_eq, comparator_137_eq, comparator_138_eq, comparator_139_eq, comparator_140_eq,
       comparator_141_eq, comparator_142_eq, comparator_143_eq, comparator_144_eq, comparator_145_eq,
       comparator_146_eq, comparator_147_eq, comparator_148_eq, comparator_149_eq, comparator_150_eq,
       comparator_151_eq, comparator_152_eq, comparator_153_eq, comparator_154_eq, comparator_155_eq,
       comparator_156_eq, comparator_157_eq, comparator_158_eq, comparator_159_eq, comparator_160_eq,
       comparator_161_eq, comparator_162_eq, comparator_163_eq, comparator_164_eq, comparator_165_eq,
       comparator_166_eq, comparator_167_eq, comparator_168_eq, comparator_169_eq, comparator_170_eq,
       comparator_171_eq, comparator_172_eq, comparator_173_eq, comparator_174_eq, comparator_175_eq,
       comparator_176_eq, comparator_177_eq, comparator_178_eq, comparator_179_eq, comparator_180_eq,
       comparator_181_eq, comparator_182_eq, comparator_183_eq, comparator_184_eq, comparator_185_eq,
       comparator_186_eq, comparator_187_eq, comparator_188_eq, comparator_189_eq, comparator_190_eq,
       comparator_191_eq, comparator_192_eq, comparator_193_eq, comparator_194_eq, comparator_195_eq,
       comparator_196_eq, comparator_197_eq, comparator_198_eq, comparator_199_eq, comparator_200_eq,
       comparator_201_eq, comparator_202_eq, comparator_203_eq, comparator_204_eq, comparator_205_eq,
       comparator_206_eq, comparator_207_eq, comparator_208_eq, comparator_209_eq, comparator_210_eq,
       comparator_211_eq, comparator_212_eq, comparator_213_eq, comparator_214_eq, comparator_215_eq,
       comparator_216_eq, comparator_217_eq, comparator_218_eq, comparator_219_eq, comparator_220_eq,
       comparator_221_eq, comparator_222_eq, comparator_223_eq, comparator_224_eq, comparator_225_eq,
       comparator_226_eq, comparator_227_eq, comparator_228_eq, comparator_229_eq, comparator_230_eq,
       comparator_231_eq, comparator_232_eq, comparator_233_eq, comparator_234_eq, comparator_235_eq,
       comparator_236_eq, comparator_237_eq, comparator_238_eq, comparator_239_eq, comparator_240_eq,
       comparator_241_eq, comparator_242_eq, comparator_243_eq, comparator_244_eq, comparator_245_eq,
       comparator_246_eq, comparator_247_eq, comparator_248_eq, comparator_249_eq, comparator_250_eq,
       comparator_251_eq, comparator_252_eq, comparator_253_eq, comparator_254_eq, comparator_255_eq,
       comparator_256_eq, WE0, WE1, WE2, WE3, WE4, WE5, WE6, WE7, WE8, WE9, WE10, WE11, WE12, WE13, WE14,
       WE15;
  wire [3:0] IS0, IS1, IS2, IS3, IS4, IS5, IS6, IS7, IS8, IS9, IS10, IS11, IS12, IS13, IS14, IS15;
  wire [15:0] and_1_out, and_2_out, and_3_out, and_4_out, and_5_out, and_6_out, and_7_out, and_8_out,
       and_129_out, and_130_out, and_131_out, and_132_out, and_133_out, and_134_out, and_135_out, and_136_out;
  wire [63:0] multiplexer_1_out, multiplexer_3_out, multiplexer_5_out, multiplexer_6_out, multiplexer_8_out,
       multiplexer_10_out, multiplexer_12_out, multiplexer_14_out, multiplexer_15_out, multiplexer_17_out,
       multiplexer_19_out, multiplexer_21_out, multiplexer_22_out, multiplexer_24_out, multiplexer_26_out,
       multiplexer_28_out;

  BitFinder #(.width(16)) bitfinder_1 (.in(and_1_out), .index(IS0), .found(WE0));
  BitFinder #(.width(16)) bitfinder_2 (.in(and_2_out), .index(IS1), .found(WE1));
  BitFinder #(.width(16)) bitfinder_3 (.in(and_3_out), .index(IS2), .found(WE2));
  BitFinder #(.width(16)) bitfinder_4 (.in(and_4_out), .index(IS3), .found(WE3));
  BitFinder #(.width(16)) bitfinder_5 (.in(and_5_out), .index(IS4), .found(WE4));
  BitFinder #(.width(16)) bitfinder_6 (.in(and_6_out), .index(IS5), .found(WE5));
  BitFinder #(.width(16)) bitfinder_7 (.in(and_7_out), .index(IS6), .found(WE6));
  BitFinder #(.width(16)) bitfinder_8 (.in(and_8_out), .index(IS7), .found(WE7));
  Multiplexer #(.select(4), .width(64)) multiplexer_1 (
    .in0(D0), .in1(D1), .in2(D2), .in3(D3), .in4(D4), .in5(D5), .in6(D6), .in7(D7), .in8(D8), .in9(D9),
    .in10(D10), .in11(D11), .in12(D12), .in13(D13), .in14(D14), .in15(D15), .out(multiplexer_1_out), .sel(IS0));
  Register #(.width(64)) reg0 (.D(multiplexer_1_out), .en(WE0), .clk(clock_1_out), .Q(R0));  // open: clr
  Clock clock_1 (.out(clock_1_out));
  Multiplexer #(.select(4), .width(64)) multiplexer_2 (
    .in0(R0), .in1(R1), .in2(R2), .in3(R3), .in4(R4), .in5(R5), .in6(R6), .in7(R7), .in8(R8), .in9(R9),
    .in10(R10), .in11(R11), .in12(R12), .in13(R13), .in14(R14), .in15(R15), .out(O0), .sel(A0));
  Comparator #(.width(4)) comparator_1 (.a(4'b0000), .b(A0), .eq(comparator_1_eq));  // open: gt, lt
  Comparator #(.width(4)) comparator_2 (.a(4'b0001), .b(A0), .eq(comparator_2_eq));  // open: gt, lt
  Comparator #(.width(4)) comparator_3 (.a(4'b0010), .b(A0), .eq(comparator_3_eq));  // open: gt, lt
  Comparator #(.width(4)) comparator_4 (.a(4'b0011), .b(A0), .eq(comparator_4_eq));  // open: gt, lt
  Comparator #(.width(4)) comparator_5 (.a(4'b0100), .b(A0), .eq(comparator_5_eq));  // open: gt, lt
  Comparator #(.width(4)) comparator_6 (.a(4'b0101), .b(A0), .eq(comparator_6_eq));  // open: gt, lt
  Comparator #(.width(4)) comparator_7 (.a(4'b0110), .b(A0), .eq(comparator_7_eq));  // open: gt, lt
  Comparator #(.width(4)) comparator_8 (.a(4'b0111), .b(A0), .eq(comparator_8_eq));  // open: gt, lt
  and and_1 (and_1_out[0], comparator_1_eq, LE0);
  and and_2 (and_2_out[0], comparator_2_eq, LE0);
  and and_3 (and_3_out[0], comparator_3_eq, LE0);
  and and_4 (and_4_out[0], comparator_4_eq, LE0);
  and and_5 (and_5_out[0], comparator_5_eq, LE0);
  and and_6 (and_6_out[0], comparator_6_eq, LE0);
  and and_7 (and_7_out[0], comparator_7_eq, LE0);
  and and_8 (and_8_out[0], comparator_8_eq, LE0);
  Multiplexer #(.select(4), .width(64)) multiplexer_3 (
    .in0(D0), .in1(D1), .in2(D2), .in3(D3), .in4(D4), .in5(D5), .in6(D6), .in7(D7), .in8(D8), .in9(D9),
    .in10(D10), .in11(D11), .in12(D12), .in13(D13), .in14(D14), .in15(D15), .out(multiplexer_3_out), .sel(IS1));
  Register #(.width(64)) reg1 (.D(multiplexer_3_out), .en(WE1), .clk(clock_2_out), .Q(R1));  // open: clr
  Clock clock_2 (.out(clock_2_out));
  Comparator #(.width(4)) comparator_9 (.a(4'b0000), .b(A1), .eq(comparator_9_eq));  // open: gt, lt
  Comparator #(.width(4)) comparator_10 (.a(4'b0001), .b(A1), .eq(comparator_10_eq));  // open: gt, lt
  Comparator #(.width(4)) comparator_11 (.a(4'b0010), .b(A1), .eq(comparator_11_eq));  // open: gt, lt
  Comparator #(.width(4)) comparator_12 (.a(4'b0011), .b(A1), .eq(comparator_12_eq));  // open: gt, lt
  Comparator #(.width(4)) comparator_13 (.a(4'b0100), .b(A1), .eq(comparator_13_eq));  // open: gt, lt
  Comparator #(.width(4)) comparator_14 (.a(4'b0101), .b(A1), .eq(comparator_14_eq));  // open: gt, lt
  Comparator #(.width(4)) comparator_15 (.a(4'b0110), .b(A1), .eq(comparator_15_eq));  // open: gt, lt
  Comparator #(.width(4)) comparator_16 (.a(4'b0111), .b(A1), .eq(comparator_16_eq));  // open: gt, lt
  and and_9 (and_1_out[1], comparator_9_eq, LE1);
  and and_10 (and_2_out[1], comparator_10_eq, LE1);
  and and_11 (and_3_out[1], comparator_11_eq, LE1);
  and and_12 (and_4_out[1], comparator_12_eq, LE1);
  and and_13 (and_5_out[1], comparator_13_eq, LE1);
  and and_14 (and_6_out[1], comparator_14_eq, LE1);
  and and_15 (and_7_out[1], comparator_15_eq, LE1);
  and and_16 (and_8_out[1], comparator_16_eq, LE1);
  Multiplexer #(.select(4), .width(64)) multiplexer_4 (
    .in0(R0), .in1(R1), .in2(R2), .in3(R3), .in4(R4), .in5(R5), .in6(R6), .in7(R7), .in8(R8), .in9(R9),
    .in10(R10), .in11(R11), .in12(R12), .in13(R13), .in14(R14), .in15(R15), .out(O1), .sel(A1));
  Comparator #(.width(4)) comparator_17 (.a(4'b0000), .b(A2), .eq(comparator_17_eq));  // open: gt, lt
  and and_17 (and_1_out[2], comparator_17_eq, LE2);
  Comparator #(.width(4)) comparator_18 (.a(4'b0001), .b(A2), .eq(comparator_18_eq));  // open: gt, lt
  and and_18 (and_2_out[2], comparator_18_eq, LE2);
  Comparator #(.width(4)) comparator_19 (.a(4'b0010), .b(A2), .eq(comparator_19_eq));  // open: gt, lt
  and and_19 (and_3_out[2], comparator_19_eq, LE2);
  Comparator #(.width(4)) comparator_20 (.a(4'b0011), .b(A2), .eq(comparator_20_eq));  // open: gt, lt
  and and_20 (and_4_out[2], comparator_20_eq, LE2);
  Comparator #(.width(4)) comparator_21 (.a(4'b0100), .b(A2), .eq(comparator_21_eq));  // open: gt, lt
  and and_21 (and_5_out[2], comparator_21_eq, LE2);
  Comparator #(.width(4)) comparator_22 (.a(4'b0101), .b(A2), .eq(comparator_22_eq));  // open: gt, lt
  and and_22 (and_6_out[2], comparator_22_eq, LE2);
  Comparator #(.width(4)) comparator_23 (.a(4'b0110), .b(A2), .eq(comparator_23_eq));  // open: gt, lt
  and and_23 (and_7_out[2], comparator_23_eq, LE2);
  Comparator #(.width(4)) comparator_24 (.a(4'b0111), .b(A2), .eq(comparator_24_eq));  // open: gt, lt
  and and_24 (and_8_out[2], comparator_24_eq, LE2);
  Multiplexer #(.select(4), .width(64)) multiplexer_5 (
    .in0(D0), .in1(D1), .in2(D2), .in3(D3), .in4(D4), .in5(D5), .in6(D6), .in7(D7), .in8(D8), .in9(D9),
    .in10(D10), .in11(D11), .in12(D12), .in13(D13), .in14(D14), .in15(D15), .out(multiplexer_5_out), .sel(IS2));
  Register #(.width(64)) reg2 (.D(multiplexer_5_out), .en(WE2), .clk(clock_3_out), .Q(R2));  // open: clr
  Clock clock_3 (.out(clock_3_out));
  Comparator #(.width(4)) comparator_25 (.a(4'b0000), .b(A3), .eq(comparator_25_eq));  // open: gt, lt
  and and_25 (and_1_out[3], comparator_25_eq, LE3);
  Comparator #(.width(4)) comparator_26 (.a(4'b0001), .b(A3), .eq(comparator_26_eq));  // open: gt, lt
  and and_26 (and_2_out[3], comparator_26_eq, LE3);
  Comparator #(.width(4)) comparator_27 (.a(4'b0010), .b(A3), .eq(comparator_27_eq));  // open: gt, lt
  and and_27 (and_3_out[3], comparator_27_eq, LE3);
  Comparator #(.width(4)) comparator_28 (.a(4'b0011), .b(A3), .eq(comparator_28_eq));  // open: gt, lt
  and and_28 (and_4_out[3], comparator_28_eq, LE3);
  Comparator #(.width(4)) comparator_29 (.a(4'b0100), .b(A3), .eq(comparator_29_eq));  // open: gt, lt
  and and_29 (and_5_out[3], comparator_29_eq, LE3);
  Comparator #(.width(4)) comparator_30 (.a(4'b0101), .b(A3), .eq(comparator_30_eq));  // open: gt, lt
  and and_30 (and_6_out[3], comparator_30_eq, LE3);
  Comparator #(.width(4)) comparator_31 (.a(4'b0110), .b(A3), .eq(comparator_31_eq));  // open: gt, lt
  and and_31 (and_7_out[3], comparator_31_eq, LE3);
  Comparator #(.width(4)) comparator_32 (.a(4'b0111), .b(A3), .eq(comparator_32_eq));  // open: gt, lt
  and and_32 (and_8_out[3], comparator_32_eq, LE3);
  Multiplexer #(.select(4), .width(64)) multiplexer_6 (
    .in0(D0), .in1(D1), .in2(D2), .in3(D3), .in4(D4), .in5(D5), .in6(D6), .in7(D7), .in8(D8), .in9(D9),
    .in10(D10), .in11(D11), .in12(D12), .in13(D13), .in14(D14), .in15(D15), .out(multiplexer_6_out), .sel(IS3));
  Register #(.width(64)) reg3 (.D(multiplexer_6_out), .en(WE3), .clk(clock_4_out), .Q(R3));  // open: clr
  Clock clock_4 (.out(clock_4_out));
  Multiplexer #(.select(4), .width(64)) multiplexer_7 (
    .in0(R0), .in1(R1), .in2(R2), .in3(R3), .in4(R4), .in5(R5), .in6(R6), .in7(R7), .in8(R8), .in9(R9),
    .in10(R10), .in11(R11), .in12(R12), .in13(R13), .in14(R14), .in15(R15), .out(O2), .sel(A2));
  Comparator #(.width(4)) comparator_33 (.a(4'b0000), .b(A4), .eq(comparator_33_eq));  // open: gt, lt
  and and_33 (and_1_out[4], comparator_33_eq, LE4);
  Comparator #(.width(4)) comparator_34 (.a(4'b0001), .b(A4), .eq(comparator_34_eq));  // open: gt, lt
  and and_34 (and_2_out[4], comparator_34_eq, LE4);
  Comparator #(.width(4)) comparator_35 (.a(4'b0010), .b(A4), .eq(comparator_35_eq));  // open: gt, lt
  and and_35 (and_3_out[4], comparator_35_eq, LE4);
  Comparator #(.width(4)) comparator_36 (.a(4'b0011), .b(A4), .eq(comparator_36_eq));  // open: gt, lt
  and and_36 (and_4_out[4], comparator_36_eq, LE4);
  Comparator #(.width(4)) comparator_37 (.a(4'b0100), .b(A4), .eq(comparator_37_eq));  // open: gt, lt
  and and_37 (and_5_out[4], comparator_37_eq, LE4);
  Comparator #(.width(4)) comparator_38 (.a(4'b0101), .b(A4), .eq(comparator_38_eq));  // open: gt, lt
  and and_38 (and_6_out[4], comparator_38_eq, LE4);
  Comparator #(.width(4)) comparator_39 (.a(4'b0110), .b(A4), .eq(comparator_39_eq));  // open: gt, lt
  and and_39 (and_7_out[4], comparator_39_eq, LE4);
  Comparator #(.width(4)) comparator_40 (.a(4'b0111), .b(A4), .eq(comparator_40_eq));  // open: gt, lt
  and and_40 (and_8_out[4], comparator_40_eq, LE4);
  Comparator #(.width(4)) comparator_41 (.a(4'b0000), .b(A5), .eq(comparator_41_eq));  // open: gt, lt
  Comparator #(.width(4)) comparator_42 (.a(4'b0001), .b(A5), .eq(comparator_42_eq));  // open: gt, lt
  Comparator #(.width(4)) comparator_43 (.a(4'b0010), .b(A5), .eq(comparator_43_eq));  // open: gt, lt
  Comparator #(.width(4)) comparator_44 (.a(4'b0011), .b(A5), .eq(comparator_44_eq));  // open: gt, lt
  Comparator #(.width(4)) comparator_45 (.a(4'b0100), .b(A5), .eq(comparator_45_eq));  // open: gt, lt
  Comparator #(.width(4)) comparator_46 (.a(4'b0101), .b(A5), .eq(comparator_46_eq));  // open: gt, lt
  Comparator #(.width(4)) comparator_47 (.a(4'b0110), .b(A5), .eq(comparator_47_eq));  // open: gt, lt
  Comparator #(.width(4)) comparator_48 (.a(4'b0111), .b(A5), .eq(comparator_48_eq));  // open: gt, lt
  Multiplexer #(.select(4), .width(64)) multiplexer_8 (
    .in0(D0), .in1(D1), .in2(D2), .in3(D3), .in4(D4), .in5(D5), .in6(D6), .in7(D7), .in8(D8), .in9(D9),
    .in10(D10), .in11(D11), .in12(D12), .in13(D13), .in14(D14), .in15(D15), .out(multiplexer_8_out), .sel(IS4));
  Register #(.width(64)) reg4 (.D(multiplexer_8_out), .en(WE4), .clk(clock_5_out), .Q(R4));  // open: clr
  Clock clock_5 (.out(clock_5_out));
  and and_41 (and_1_out[5], comparator_41_eq, LE5);
  and and_42 (and_2_out[5], comparator_42_eq, LE5);
  and and_43 (and_3_out[5], comparator_43_eq, LE5);
  and and_44 (and_4_out[5], comparator_44_eq, LE5);
  and and_45 (and_5_out[5], comparator_45_eq, LE5);
  and and_46 (and_6_out[5], comparator_46_eq, LE5);
  and and_47 (and_7_out[5], comparator_47_eq, LE5);
  and and_48 (and_8_out[5], comparator_48_eq, LE5);
  Multiplexer #(.select(4), .width(64)) multiplexer_9 (
    .in0(R0), .in1(R1), .in2(R2), .in3(R3), .in4(R4), .in5(R5), .in6(R6), .in7(R7), .in8(R8), .in9(R9),
    .in10(R10), .in11(R11), .in12(R12), .in13(R13), .in14(R14), .in15(R15), .out(O3), .sel(A3));
  Comparator #(.width(4)) comparator_49 (.a(4'b0000), .b(A6), .eq(comparator_49_eq));  // open: gt, lt
  Comparator #(.width(4)) comparator_50 (.a(4'b0001), .b(A6), .eq(comparator_50_eq));  // open: gt, lt
  Comparator #(.width(4)) comparator_51 (.a(4'b0010), .b(A6), .eq(comparator_51_eq));  // open: gt, lt
  Comparator #(.width(4)) comparator_52 (.a(4'b0011), .b(A6), .eq(comparator_52_eq));  // open: gt, lt
  Comparator #(.width(4)) comparator_53 (.a(4'b0100), .b(A6), .eq(comparator_53_eq));  // open: gt, lt
  Comparator #(.width(4)) comparator_54 (.a(4'b0101), .b(A6), .eq(comparator_54_eq));  // open: gt, lt
  Comparator #(.width(4)) comparator_55 (.a(4'b0110), .b(A6), .eq(comparator_55_eq));  // open: gt, lt
  Comparator #(.width(4)) comparator_56 (.a(4'b0111), .b(A6), .eq(comparator_56_eq));  // open: gt, lt
  and and_49 (and_1_out[6], comparator_49_eq, LE6);
  and and_50 (and_2_out[6], comparator_50_eq, LE6);
  and and_51 (and_3_out[6], comparator_51_eq, LE6);
  and and_52 (and_4_out[6], comparator_52_eq, LE6);
  and and_53 (and_5_out[6], comparator_53_eq, LE6);
  and and_54 (and_6_out[6], comparator_54_eq, LE6);
  and and_55 (and_7_out[6], comparator_55_eq, LE6);
  and and_56 (and_8_out[6], comparator_56_eq, LE6);
  Multiplexer #(.select(4), .width(64)) multiplexer_10 (
    .in0(D0), .in1(D1), .in2(D2), .in3(D3), .in4(D4), .in5(D5), .in6(D6), .in7(D7), .in8(D8), .in9(D9),
    .in10(D10), .in11(D11), .in12(D12), .in13(D13), .in14(D14), .in15(D15), .out(multiplexer_10_out),
    .sel(IS5));
  Register #(.width(64)) reg5 (.D(multiplexer_10_out), .en(WE5), .clk(clock_6_out), .Q(R5));  // open: clr
  Clock clock_6 (.out(clock_6_out));
  Comparator #(.width(4)) comparator_57 (.a(4'b0000), .b(A7), .eq(comparator_57_eq));  // open: gt, lt
  Comparator #(.width(4)) comparator_58 (.a(4'b0001), .b(A7), .eq(comparator_58_eq));  // open: gt, lt
  Comparator #(.width(4)) comparator_59 (.a(4'b0010), .b(A7), .eq(comparator_59_eq));  // open: gt, lt
  Comparator #(.width(4)) comparator_60 (.a(4'b0011), .b(A7), .eq(comparator_60_eq));  // open: gt, lt
  Comparator #(.width(4)) comparator_61 (.a(4'b0100), .b(A7), .eq(comparator_61_eq));  // open: gt, lt
  Comparator #(.width(4)) comparator_62 (.a(4'b0101), .b(A7), .eq(comparator_62_eq));  // open: gt, lt
  Comparator #(.width(4)) comparator_63 (.a(4'b0110), .b(A7), .eq(comparator_63_eq));  // open: gt, lt
  Comparator #(.width(4)) comparator_64 (.a(4'b0111), .b(A7), .eq(comparator_64_eq));  // open: gt, lt
  and and_57 (and_1_out[7], comparator_57_eq, LE7);
  and and_58 (and_2_out[7], comparator_58_eq, LE7);
  and and_59 (and_3_out[7], comparator_59_eq, LE7);
  and and_60 (and_4_out[7], comparator_60_eq, LE7);
  and and_61 (and_5_out[7], comparator_61_eq, LE7);
  and and_62 (and_6_out[7], comparator_62_eq, LE7);
  and and_63 (and_7_out[7], comparator_63_eq, LE7);
  and and_64 (and_8_out[7], comparator_64_eq, LE7);
  Multiplexer #(.select(4), .width(64)) multiplexer_11 (
    .in0(R0), .in1(R1), .in2(R2), .in3(R3), .in4(R4), .in5(R5), .in6(R6), .in7(R7), .in8(R8), .in9(R9),
    .in10(R10), .in11(R11), .in12(R12), .in13(R13), .in14(R14), .in15(R15), .out(O4), .sel(A4));
  Comparator #(.width(4)) comparator_65 (.a(4'b0000), .b(A8), .eq(comparator_65_eq));  // open: gt, lt
  Comparator #(.width(4)) comparator_66 (.a(4'b0001), .b(A8), .eq(comparator_66_eq));  // open: gt, lt
  Comparator #(.width(4)) comparator_67 (.a(4'b0010), .b(A8), .eq(comparator_67_eq));  // open: gt, lt
  Comparator #(.width(4)) comparator_68 (.a(4'b0011), .b(A8), .eq(comparator_68_eq));  // open: gt, lt
  Comparator #(.width(4)) comparator_69 (.a(4'b0100), .b(A8), .eq(comparator_69_eq));  // open: gt, lt
  Comparator #(.width(4)) comparator_70 (.a(4'b0101), .b(A8), .eq(comparator_70_eq));  // open: gt, lt
  Comparator #(.width(4)) comparator_71 (.a(4'b0110), .b(A8), .eq(comparator_71_eq));  // open: gt, lt
  Comparator #(.width(4)) comparator_72 (.a(4'b0111), .b(A8), .eq(comparator_72_eq));  // open: gt, lt
  Multiplexer #(.select(4), .width(64)) multiplexer_12 (
    .in0(D0), .in1(D1), .in2(D2), .in3(D3), .in4(D4), .in5(D5), .in6(D6), .in7(D7), .in8(D8), .in9(D9),
    .in10(D10), .in11(D11), .in12(D12), .in13(D13), .in14(D14), .in15(D15), .out(multiplexer_12_out),
    .sel(IS6));
  Register #(.width(64)) reg6 (.D(multiplexer_12_out), .en(WE6), .clk(clock_7_out), .Q(R6));  // open: clr
  Clock clock_7 (.out(clock_7_out));
  and and_65 (and_1_out[8], comparator_65_eq, LE8);
  and and_66 (and_2_out[8], comparator_66_eq, LE8);
  and and_67 (and_3_out[8], comparator_67_eq, LE8);
  and and_68 (and_4_out[8], comparator_68_eq, LE8);
  and and_69 (and_5_out[8], comparator_69_eq, LE8);
  and and_70 (and_6_out[8], comparator_70_eq, LE8);
  and and_71 (and_7_out[8], comparator_71_eq, LE8);
  and and_72 (and_8_out[8], comparator_72_eq, LE8);
  Comparator #(.width(4)) comparator_73 (.a(4'b0000), .b(A9), .eq(comparator_73_eq));  // open: gt, lt
  Comparator #(.width(4)) comparator_74 (.a(4'b0001), .b(A9), .eq(comparator_74_eq));  // open: gt, lt
  Comparator #(.width(4)) comparator_75 (.a(4'b0010), .b(A9), .eq(comparator_75_eq));  // open: gt, lt
  Comparator #(.width(4)) comparator_76 (.a(4'b0011), .b(A9), .eq(comparator_76_eq));  // open: gt, lt
  Comparator #(.width(4)) comparator_77 (.a(4'b0100), .b(A9), .eq(comparator_77_eq));  // open: gt, lt
  Comparator #(.width(4)) comparator_78 (.a(4'b0101), .b(A9), .eq(comparator_78_eq));  // open: gt, lt
  Comparator #(.width(4)) comparator_79 (.a(4'b0110), .b(A9), .eq(comparator_79_eq));  // open: gt, lt
  Comparator #(.width(4)) comparator_80 (.a(4'b0111), .b(A9), .eq(comparator_80_eq));  // open: gt, lt
  Multiplexer #(.select(4), .width(64)) multiplexer_13 (
    .in0(R0), .in1(R1), .in2(R2), .in3(R3), .in4(R4), .in5(R5), .in6(R6), .in7(R7), .in8(R8), .in9(R9),
    .in10(R10), .in11(R11), .in12(R12), .in13(R13), .in14(R14), .in15(R15), .out(O5), .sel(A5));
  and and_73 (and_1_out[9], comparator_73_eq, LE9);
  and and_74 (and_2_out[9], comparator_74_eq, LE9);
  and and_75 (and_3_out[9], comparator_75_eq, LE9);
  and and_76 (and_4_out[9], comparator_76_eq, LE9);
  and and_77 (and_5_out[9], comparator_77_eq, LE9);
  and and_78 (and_6_out[9], comparator_78_eq, LE9);
  and and_79 (and_7_out[9], comparator_79_eq, LE9);
  and and_80 (and_8_out[9], comparator_80_eq, LE9);
  Multiplexer #(.select(4), .width(64)) multiplexer_14 (
    .in0(D0), .in1(D1), .in2(D2), .in3(D3), .in4(D4), .in5(D5), .in6(D6), .in7(D7), .in8(D8), .in9(D9),
    .in10(D10), .in11(D11), .in12(D12), .in13(D13), .in14(D14), .in15(D15), .out(multiplexer_14_out),
    .sel(IS7));
  Register #(.width(64)) reg7 (.D(multiplexer_14_out), .en(WE7), .clk(clock_8_out), .Q(R7));  // open: clr
  Clock clock_8 (.out(clock_8_out));
  Comparator #(.width(4)) comparator_81 (.a(4'b0000), .b(A10), .eq(comparator_81_eq));  // open: gt, lt
  Comparator #(.width(4)) comparator_82 (.a(4'b0001), .b(A10), .eq(comparator_82_eq));  // open: gt, lt
  Comparator #(.width(4)) comparator_83 (.a(4'b0010), .b(A10), .eq(comparator_83_eq));  // open: gt, lt
  Comparator #(.width(4)) comparator_84 (.a(4'b0011), .b(A10), .eq(comparator_84_eq));  // open: gt, lt
  Comparator #(.width(4)) comparator_85 (.a(4'b0100), .b(A10), .eq(comparator_85_eq));  // open: gt, lt
  Comparator #(.width(4)) comparator_86 (.a(4'b0101), .b(A10), .eq(comparator_86_eq));  // open: gt, lt
  Comparator #(.width(4)) comparator_87 (.a(4'b0110), .b(A10), .eq(comparator_87_eq));  // open: gt, lt
  Comparator #(.width(4)) comparator_88 (.a(4'b0111), .b(A10), .eq(comparator_88_eq));  // open: gt, lt
  and and_81 (and_1_out[10], comparator_81_eq, LE10);
  and and_82 (and_2_out[10], comparator_82_eq, LE10);
  and and_83 (and_3_out[10], comparator_83_eq, LE10);
  and and_84 (and_4_out[10], comparator_84_eq, LE10);
  and and_85 (and_5_out[10], comparator_85_eq, LE10);
  and and_86 (and_6_out[10], comparator_86_eq, LE10);
  and and_87 (and_7_out[10], comparator_87_eq, LE10);
  and and_88 (and_8_out[10], comparator_88_eq, LE10);
  Multiplexer #(.select(4), .width(64)) multiplexer_15 (
    .in0(D0), .in1(D1), .in2(D2), .in3(D3), .in4(D4), .in5(D5), .in6(D6), .in7(D7), .in8(D8), .in9(D9),
    .in10(D10), .in11(D11), .in12(D12), .in13(D13), .in14(D14), .in15(D15), .out(multiplexer_15_out),
    .sel(IS8));
  Register #(.width(64)) reg8 (.D(multiplexer_15_out), .en(WE8), .clk(clock_9_out), .Q(R8));  // open: clr
  Clock clock_9 (.out(clock_9_out));
  Comparator #(.width(4)) comparator_89 (.a(4'b0000), .b(A11), .eq(comparator_89_eq));  // open: gt, lt
  Comparator #(.width(4)) comparator_90 (.a(4'b0001), .b(A11), .eq(comparator_90_eq));  // open: gt, lt
  Comparator #(.width(4)) comparator_91 (.a(4'b0010), .b(A11), .eq(comparator_91_eq));  // open: gt, lt
  Comparator #(.width(4)) comparator_92 (.a(4'b0011), .b(A11), .eq(comparator_92_eq));  // open: gt, lt
  Comparator #(.width(4)) comparator_93 (.a(4'b0100), .b(A11), .eq(comparator_93_eq));  // open: gt, lt
  Comparator #(.width(4)) comparator_94 (.a(4'b0101), .b(A11), .eq(comparator_94_eq));  // open: gt, lt
  Comparator #(.width(4)) comparator_95 (.a(4'b0110), .b(A11), .eq(comparator_95_eq));  // open: gt, lt
  Comparator #(.width(4)) comparator_96 (.a(4'b0111), .b(A11), .eq(comparator_96_eq));  // open: gt, lt
  Multiplexer #(.select(4), .width(64)) multiplexer_16 (
    .in0(R0), .in1(R1), .in2(R2), .in3(R3), .in4(R4), .in5(R5), .in6(R6), .in7(R7), .in8(R8), .in9(R9),
    .in10(R10), .in11(R11), .in12(R12), .in13(R13), .in14(R14), .in15(R15), .out(O6), .sel(A6));
  and and_89 (and_1_out[11], comparator_89_eq, LE11);
  and and_90 (and_2_out[11], comparator_90_eq, LE11);
  and and_91 (and_3_out[11], comparator_91_eq, LE11);
  and and_92 (and_4_out[11], comparator_92_eq, LE11);
  and and_93 (and_5_out[11], comparator_93_eq, LE11);
  and and_94 (and_6_out[11], comparator_94_eq, LE11);
  and and_95 (and_7_out[11], comparator_95_eq, LE11);
  and and_96 (and_8_out[11], comparator_96_eq, LE11);
  Comparator #(.width(4)) comparator_97 (.a(4'b0000), .b(A12), .eq(comparator_97_eq));  // open: gt, lt
  Comparator #(.width(4)) comparator_98 (.a(4'b0001), .b(A12), .eq(comparator_98_eq));  // open: gt, lt
  Comparator #(.width(4)) comparator_99 (.a(4'b0010), .b(A12), .eq(comparator_99_eq));  // open: gt, lt
  Comparator #(.width(4)) comparator_100 (.a(4'b0011), .b(A12), .eq(comparator_100_eq));  // open: gt, lt
  Comparator #(.width(4)) comparator_101 (.a(4'b0100), .b(A12), .eq(comparator_101_eq));  // open: gt, lt
  Comparator #(.width(4)) comparator_102 (.a(4'b0101), .b(A12), .eq(comparator_102_eq));  // open: gt, lt
  Comparator #(.width(4)) comparator_103 (.a(4'b0110), .b(A12), .eq(comparator_103_eq));  // open: gt, lt
  Comparator #(.width(4)) comparator_104 (.a(4'b0111), .b(A12), .eq(comparator_104_eq));  // open: gt, lt
  Multiplexer #(.select(4), .width(64)) multiplexer_17 (
    .in0(D0), .in1(D1), .in2(D2), .in3(D3), .in4(D4), .in5(D5), .in6(D6), .in7(D7), .in8(D8), .in9(D9),
    .in10(D10), .in11(D11), .in12(D12), .in13(D13), .in14(D14), .in15(D15), .out(multiplexer_17_out),
    .sel(IS9));
  Register #(.width(64)) reg9 (.D(multiplexer_17_out), .en(WE9), .clk(clock_10_out), .Q(R9));  // open: clr
  Clock clock_10 (.out(clock_10_out));
  and and_97 (and_1_out[12], comparator_97_eq, LE12);
  and and_98 (and_2_out[12], comparator_98_eq, LE12);
  and and_99 (and_3_out[12], comparator_99_eq, LE12);
  and and_100 (and_4_out[12], comparator_100_eq, LE12);
  and and_101 (and_5_out[12], comparator_101_eq, LE12);
  and and_102 (and_6_out[12], comparator_102_eq, LE12);
  and and_103 (and_7_out[12], comparator_103_eq, LE12);
  and and_104 (and_8_out[12], comparator_104_eq, LE12);
  Comparator #(.width(4)) comparator_105 (.a(4'b0000), .b(A13), .eq(comparator_105_eq));  // open: gt, lt
  Comparator #(.width(4)) comparator_106 (.a(4'b0001), .b(A13), .eq(comparator_106_eq));  // open: gt, lt
  Comparator #(.width(4)) comparator_107 (.a(4'b0010), .b(A13), .eq(comparator_107_eq));  // open: gt, lt
  Comparator #(.width(4)) comparator_108 (.a(4'b0011), .b(A13), .eq(comparator_108_eq));  // open: gt, lt
  Comparator #(.width(4)) comparator_109 (.a(4'b0100), .b(A13), .eq(comparator_109_eq));  // open: gt, lt
  Comparator #(.width(4)) comparator_110 (.a(4'b0101), .b(A13), .eq(comparator_110_eq));  // open: gt, lt
  Comparator #(.width(4)) comparator_111 (.a(4'b0110), .b(A13), .eq(comparator_111_eq));  // open: gt, lt
  Comparator #(.width(4)) comparator_112 (.a(4'b0111), .b(A13), .eq(comparator_112_eq));  // open: gt, lt
  Multiplexer #(.select(4), .width(64)) multiplexer_18 (
    .in0(R0), .in1(R1), .in2(R2), .in3(R3), .in4(R4), .in5(R5), .in6(R6), .in7(R7), .in8(R8), .in9(R9),
    .in10(R10), .in11(R11), .in12(R12), .in13(R13), .in14(R14), .in15(R15), .out(O7), .sel(A7));
  and and_105 (and_1_out[13], comparator_105_eq, LE13);
  and and_106 (and_2_out[13], comparator_106_eq, LE13);
  and and_107 (and_3_out[13], comparator_107_eq, LE13);
  and and_108 (and_4_out[13], comparator_108_eq, LE13);
  and and_109 (and_5_out[13], comparator_109_eq, LE13);
  and and_110 (and_6_out[13], comparator_110_eq, LE13);
  and and_111 (and_7_out[13], comparator_111_eq, LE13);
  and and_112 (and_8_out[13], comparator_112_eq, LE13);
  Multiplexer #(.select(4), .width(64)) multiplexer_19 (
    .in0(D0), .in1(D1), .in2(D2), .in3(D3), .in4(D4), .in5(D5), .in6(D6), .in7(D7), .in8(D8), .in9(D9),
    .in10(D10), .in11(D11), .in12(D12), .in13(D13), .in14(D14), .in15(D15), .out(multiplexer_19_out),
    .sel(IS10));
  Register #(.width(64)) reg10 (.D(multiplexer_19_out), .en(WE10), .clk(clock_11_out), .Q(R10));  // open: clr
  Clock clock_11 (.out(clock_11_out));
  Comparator #(.width(4)) comparator_113 (.a(4'b0000), .b(A14), .eq(comparator_113_eq));  // open: gt, lt
  Comparator #(.width(4)) comparator_114 (.a(4'b0001), .b(A14), .eq(comparator_114_eq));  // open: gt, lt
  Comparator #(.width(4)) comparator_115 (.a(4'b0010), .b(A14), .eq(comparator_115_eq));  // open: gt, lt
  Comparator #(.width(4)) comparator_116 (.a(4'b0011), .b(A14), .eq(comparator_116_eq));  // open: gt, lt
  Comparator #(.width(4)) comparator_117 (.a(4'b0100), .b(A14), .eq(comparator_117_eq));  // open: gt, lt
  Comparator #(.width(4)) comparator_118 (.a(4'b0101), .b(A14), .eq(comparator_118_eq));  // open: gt, lt
  Comparator #(.width(4)) comparator_119 (.a(4'b0110), .b(A14), .eq(comparator_119_eq));  // open: gt, lt
  Comparator #(.width(4)) comparator_120 (.a(4'b0111), .b(A14), .eq(comparator_120_eq));  // open: gt, lt
  and and_113 (and_1_out[14], comparator_113_eq, LE14);
  and and_114 (and_2_out[14], comparator_114_eq, LE14);
  and and_115 (and_3_out[14], comparator_115_eq, LE14);
  and and_116 (and_4_out[14], comparator_116_eq, LE14);
  and and_117 (and_5_out[14], comparator_117_eq, LE14);
  and and_118 (and_6_out[14], comparator_118_eq, LE14);
  and and_119 (and_7_out[14], comparator_119_eq, LE14);
  and and_120 (and_8_out[14], comparator_120_eq, LE14);
  Multiplexer #(.select(4), .width(64)) multiplexer_20 (
    .in0(R0), .in1(R1), .in2(R2), .in3(R3), .in4(R4), .in5(R5), .in6(R6), .in7(R7), .in8(R8), .in9(R9),
    .in10(R10), .in11(R11), .in12(R12), .in13(R13), .in14(R14), .in15(R15), .out(O8), .sel(A8));
  Comparator #(.width(4)) comparator_121 (.a(4'b0000), .b(A15), .eq(comparator_121_eq));  // open: gt, lt
  Comparator #(.width(4)) comparator_122 (.a(4'b0001), .b(A15), .eq(comparator_122_eq));  // open: gt, lt
  Comparator #(.width(4)) comparator_123 (.a(4'b0010), .b(A15), .eq(comparator_123_eq));  // open: gt, lt
  Comparator #(.width(4)) comparator_124 (.a(4'b0011), .b(A15), .eq(comparator_124_eq));  // open: gt, lt
  Comparator #(.width(4)) comparator_125 (.a(4'b0100), .b(A15), .eq(comparator_125_eq));  // open: gt, lt
  Comparator #(.width(4)) comparator_126 (.a(4'b0101), .b(A15), .eq(comparator_126_eq));  // open: gt, lt
  Comparator #(.width(4)) comparator_127 (.a(4'b0110), .b(A15), .eq(comparator_127_eq));  // open: gt, lt
  Comparator #(.width(4)) comparator_128 (.a(4'b0111), .b(A15), .eq(comparator_128_eq));  // open: gt, lt
  Multiplexer #(.select(4), .width(64)) multiplexer_21 (
    .in0(D0), .in1(D1), .in2(D2), .in3(D3), .in4(D4), .in5(D5), .in6(D6), .in7(D7), .in8(D8), .in9(D9),
    .in10(D10), .in11(D11), .in12(D12), .in13(D13), .in14(D14), .in15(D15), .out(multiplexer_21_out),
    .sel(IS11));
  Register #(.width(64)) reg11 (.D(multiplexer_21_out), .en(WE11), .clk(clock_12_out), .Q(R11));  // open: clr
  Clock clock_12 (.out(clock_12_out));
  and and_121 (and_1_out[15], comparator_121_eq, LE15);
  and and_122 (and_2_out[15], comparator_122_eq, LE15);
  and and_123 (and_3_out[15], comparator_123_eq, LE15);
  and and_124 (and_4_out[15], comparator_124_eq, LE15);
  and and_125 (and_5_out[15], comparator_125_eq, LE15);
  and and_126 (and_6_out[15], comparator_126_eq, LE15);
  and and_127 (and_7_out[15], comparator_127_eq, LE15);
  and and_128 (and_8_out[15], comparator_128_eq, LE15);
  BitFinder #(.width(16)) bitfinder_9 (.in(and_129_out), .index(IS8), .found(WE8));
  BitFinder #(.width(16)) bitfinder_10 (.in(and_130_out), .index(IS9), .found(WE9));
  BitFinder #(.width(16)) bitfinder_11 (.in(and_131_out), .index(IS10), .found(WE10));
  BitFinder #(.width(16)) bitfinder_12 (.in(and_132_out), .index(IS11), .found(WE11));
  BitFinder #(.width(16)) bitfinder_13 (.in(and_133_out), .index(IS12), .found(WE12));
  BitFinder #(.width(16)) bitfinder_14 (.in(and_134_out), .index(IS13), .found(WE13));
  BitFinder #(.width(16)) bitfinder_15 (.in(and_135_out), .index(IS14), .found(WE14));
  BitFinder #(.width(16)) bitfinder_16 (.in(and_136_out), .index(IS15), .found(WE15));
  Multiplexer #(.select(4), .width(64)) multiplexer_22 (
    .in0(D0), .in1(D1), .in2(D2), .in3(D3), .in4(D4), .in5(D5), .in6(D6), .in7(D7), .in8(D8), .in9(D9),
    .in10(D10), .in11(D11), .in12(D12), .in13(D13), .in14(D14), .in15(D15), .out(multiplexer_22_out),
    .sel(IS12));
  Register #(.width(64)) reg12 (.D(multiplexer_22_out), .en(WE12), .clk(clock_13_out), .Q(R12));  // open: clr
  Clock clock_13 (.out(clock_13_out));
  Multiplexer #(.select(4), .width(64)) multiplexer_23 (
    .in0(R0), .in1(R1), .in2(R2), .in3(R3), .in4(R4), .in5(R5), .in6(R6), .in7(R7), .in8(R8), .in9(R9),
    .in10(R10), .in11(R11), .in12(R12), .in13(R13), .in14(R14), .in15(R15), .out(O9), .sel(A9));
  Comparator #(.width(4)) comparator_129 (.a(4'b1000), .b(A0), .eq(comparator_129_eq));  // open: gt, lt
  and and_129 (and_129_out[0], comparator_129_eq, LE0);
  Comparator #(.width(4)) comparator_130 (.a(4'b1001), .b(A0), .eq(comparator_130_eq));  // open: gt, lt
  and and_130 (and_130_out[0], comparator_130_eq, LE0);
  Comparator #(.width(4)) comparator_131 (.a(4'b1010), .b(A0), .eq(comparator_131_eq));  // open: gt, lt
  and and_131 (and_131_out[0], comparator_131_eq, LE0);
  Comparator #(.width(4)) comparator_132 (.a(4'b1011), .b(A0), .eq(comparator_132_eq));  // open: gt, lt
  and and_132 (and_132_out[0], comparator_132_eq, LE0);
  Comparator #(.width(4)) comparator_133 (.a(4'b1100), .b(A0), .eq(comparator_133_eq));  // open: gt, lt
  and and_133 (and_133_out[0], comparator_133_eq, LE0);
  Comparator #(.width(4)) comparator_134 (.a(4'b1101), .b(A0), .eq(comparator_134_eq));  // open: gt, lt
  and and_134 (and_134_out[0], comparator_134_eq, LE0);
  Comparator #(.width(4)) comparator_135 (.a(4'b1110), .b(A0), .eq(comparator_135_eq));  // open: gt, lt
  and and_135 (and_135_out[0], comparator_135_eq, LE0);
  Comparator #(.width(4)) comparator_136 (.a(4'b1111), .b(A0), .eq(comparator_136_eq));  // open: gt, lt
  and and_136 (and_136_out[0], comparator_136_eq, LE0);
  Multiplexer #(.select(4), .width(64)) multiplexer_24 (
    .in0(D0), .in1(D1), .in2(D2), .in3(D3), .in4(D4), .in5(D5), .in6(D6), .in7(D7), .in8(D8), .in9(D9),
    .in10(D10), .in11(D11), .in12(D12), .in13(D13), .in14(D14), .in15(D15), .out(multiplexer_24_out),
    .sel(IS13));
  Register #(.width(64)) reg13 (.D(multiplexer_24_out), .en(WE13), .clk(clock_14_out), .Q(R13));  // open: clr
  Clock clock_14 (.out(clock_14_out));
  Comparator #(.width(4)) comparator_137 (.a(4'b1000), .b(A1), .eq(comparator_137_eq));  // open: gt, lt
  and and_137 (and_129_out[1], comparator_137_eq, LE1);
  Comparator #(.width(4)) comparator_138 (.a(4'b1001), .b(A1), .eq(comparator_138_eq));  // open: gt, lt
  and and_138 (and_130_out[1], comparator_138_eq, LE1);
  Comparator #(.width(4)) comparator_139 (.a(4'b1010), .b(A1), .eq(comparator_139_eq));  // open: gt, lt
  and and_139 (and_131_out[1], comparator_139_eq, LE1);
  Comparator #(.width(4)) comparator_140 (.a(4'b1011), .b(A1), .eq(comparator_140_eq));  // open: gt, lt
  and and_140 (and_132_out[1], comparator_140_eq, LE1);
  Comparator #(.width(4)) comparator_141 (.a(4'b1100), .b(A1), .eq(comparator_141_eq));  // open: gt, lt
  and and_141 (and_133_out[1], comparator_141_eq, LE1);
  Comparator #(.width(4)) comparator_142 (.a(4'b1101), .b(A1), .eq(comparator_142_eq));  // open: gt, lt
  and and_142 (and_134_out[1], comparator_142_eq, LE1);
  Comparator #(.width(4)) comparator_143 (.a(4'b1110), .b(A1), .eq(comparator_143_eq));  // open: gt, lt
  and and_143 (and_135_out[1], comparator_143_eq, LE1);
  Comparator #(.width(4)) comparator_144 (.a(4'b1111), .b(A1), .eq(comparator_144_eq));  // open: gt, lt
  and and_144 (and_136_out[1], comparator_144_eq, LE1);
  Multiplexer #(.select(4), .width(64)) multiplexer_25 (
    .in0(R0), .in1(R1), .in2(R2), .in3(R3), .in4(R4), .in5(R5), .in6(R6), .in7(R7), .in8(R8), .in9(R9),
    .in10(R10), .in11(R11), .in12(R12), .in13(R13), .in14(R14), .in15(R15), .out(O10), .sel(A10));
  Comparator #(.width(4)) comparator_145 (.a(4'b1000), .b(A2), .eq(comparator_145_eq));  // open: gt, lt
  Comparator #(.width(4)) comparator_146 (.a(4'b1001), .b(A2), .eq(comparator_146_eq));  // open: gt, lt
  Comparator #(.width(4)) comparator_147 (.a(4'b1010), .b(A2), .eq(comparator_147_eq));  // open: gt, lt
  Comparator #(.width(4)) comparator_148 (.a(4'b1011), .b(A2), .eq(comparator_148_eq));  // open: gt, lt
  Comparator #(.width(4)) comparator_149 (.a(4'b1100), .b(A2), .eq(comparator_149_eq));  // open: gt, lt
  Comparator #(.width(4)) comparator_150 (.a(4'b1101), .b(A2), .eq(comparator_150_eq));  // open: gt, lt
  Comparator #(.width(4)) comparator_151 (.a(4'b1110), .b(A2), .eq(comparator_151_eq));  // open: gt, lt
  Comparator #(.width(4)) comparator_152 (.a(4'b1111), .b(A2), .eq(comparator_152_eq));  // open: gt, lt
  Multiplexer #(.select(4), .width(64)) multiplexer_26 (
    .in0(D0), .in1(D1), .in2(D2), .in3(D3), .in4(D4), .in5(D5), .in6(D6), .in7(D7), .in8(D8), .in9(D9),
    .in10(D10), .in11(D11), .in12(D12), .in13(D13), .in14(D14), .in15(D15), .out(multiplexer_26_out),
    .sel(IS14));
  Register #(.width(64)) reg14 (.D(multiplexer_26_out), .en(WE14), .clk(clock_15_out), .Q(R14));  // open: clr
  Clock clock_15 (.out(clock_15_out));
  and and_145 (and_129_out[2], comparator_145_eq, LE2);
  and and_146 (and_130_out[2], comparator_146_eq, LE2);
  and and_147 (and_131_out[2], comparator_147_eq, LE2);
  and and_148 (and_132_out[2], comparator_148_eq, LE2);
  and and_149 (and_133_out[2], comparator_149_eq, LE2);
  and and_150 (and_134_out[2], comparator_150_eq, LE2);
  and and_151 (and_135_out[2], comparator_151_eq, LE2);
  and and_152 (and_136_out[2], comparator_152_eq, LE2);
  Comparator #(.width(4)) comparator_153 (.a(4'b1000), .b(A3), .eq(comparator_153_eq));  // open: gt, lt
  Comparator #(.width(4)) comparator_154 (.a(4'b1001), .b(A3), .eq(comparator_154_eq));  // open: gt, lt
  Comparator #(.width(4)) comparator_155 (.a(4'b1010), .b(A3), .eq(comparator_155_eq));  // open: gt, lt
  Comparator #(.width(4)) comparator_156 (.a(4'b1011), .b(A3), .eq(comparator_156_eq));  // open: gt, lt
  Comparator #(.width(4)) comparator_157 (.a(4'b1100), .b(A3), .eq(comparator_157_eq));  // open: gt, lt
  Comparator #(.width(4)) comparator_158 (.a(4'b1101), .b(A3), .eq(comparator_158_eq));  // open: gt, lt
  Comparator #(.width(4)) comparator_159 (.a(4'b1110), .b(A3), .eq(comparator_159_eq));  // open: gt, lt
  Comparator #(.width(4)) comparator_160 (.a(4'b1111), .b(A3), .eq(comparator_160_eq));  // open: gt, lt
  Multiplexer #(.select(4), .width(64)) multiplexer_27 (
    .in0(R0), .in1(R1), .in2(R2), .in3(R3), .in4(R4), .in5(R5), .in6(R6), .in7(R7), .in8(R8), .in9(R9),
    .in10(R10), .in11(R11), .in12(R12), .in13(R13), .in14(R14), .in15(R15), .out(O11), .sel(A11));
  and and_153 (and_129_out[3], comparator_153_eq, LE3);
  and and_154 (and_130_out[3], comparator_154_eq, LE3);
  and and_155 (and_131_out[3], comparator_155_eq, LE3);
  and and_156 (and_132_out[3], comparator_156_eq, LE3);
  and and_157 (and_133_out[3], comparator_157_eq, LE3);
  and and_158 (and_134_out[3], comparator_158_eq, LE3);
  and and_159 (and_135_out[3], comparator_159_eq, LE3);
  and and_160 (and_136_out[3], comparator_160_eq, LE3);
  Multiplexer #(.select(4), .width(64)) multiplexer_28 (
    .in0(D0), .in1(D1), .in2(D2), .in3(D3), .in4(D4), .in5(D5), .in6(D6), .in7(D7), .in8(D8), .in9(D9),
    .in10(D10), .in11(D11), .in12(D12), .in13(D13), .in14(D14), .in15(D15), .out(multiplexer_28_out),
    .sel(IS15));
  Register #(.width(64)) reg15 (.D(multiplexer_28_out), .en(WE15), .clk(clock_16_out), .Q(R15));  // open: clr
  Clock clock_16 (.out(clock_16_out));
  Comparator #(.width(4)) comparator_161 (.a(4'b1000), .b(A4), .eq(comparator_161_eq));  // open: gt, lt
  Comparator #(.width(4)) comparator_162 (.a(4'b1001), .b(A4), .eq(comparator_162_eq));  // open: gt, lt
  Comparator #(.width(4)) comparator_163 (.a(4'b1010), .b(A4), .eq(comparator_163_eq));  // open: gt, lt
  Comparator #(.width(4)) comparator_164 (.a(4'b1011), .b(A4), .eq(comparator_164_eq));  // open: gt, lt
  Comparator #(.width(4)) comparator_165 (.a(4'b1100), .b(A4), .eq(comparator_165_eq));  // open: gt, lt
  Comparator #(.width(4)) comparator_166 (.a(4'b1101), .b(A4), .eq(comparator_166_eq));  // open: gt, lt
  Comparator #(.width(4)) comparator_167 (.a(4'b1110), .b(A4), .eq(comparator_167_eq));  // open: gt, lt
  Comparator #(.width(4)) comparator_168 (.a(4'b1111), .b(A4), .eq(comparator_168_eq));  // open: gt, lt
  and and_161 (and_129_out[4], comparator_161_eq, LE4);
  and and_162 (and_130_out[4], comparator_162_eq, LE4);
  and and_163 (and_131_out[4], comparator_163_eq, LE4);
  and and_164 (and_132_out[4], comparator_164_eq, LE4);
  and and_165 (and_133_out[4], comparator_165_eq, LE4);
  and and_166 (and_134_out[4], comparator_166_eq, LE4);
  and and_167 (and_135_out[4], comparator_167_eq, LE4);
  and and_168 (and_136_out[4], comparator_168_eq, LE4);
  Comparator #(.width(4)) comparator_169 (.a(4'b1000), .b(A5), .eq(comparator_169_eq));  // open: gt, lt
  Comparator #(.width(4)) comparator_170 (.a(4'b1001), .b(A5), .eq(comparator_170_eq));  // open: gt, lt
  Comparator #(.width(4)) comparator_171 (.a(4'b1010), .b(A5), .eq(comparator_171_eq));  // open: gt, lt
  Comparator #(.width(4)) comparator_172 (.a(4'b1011), .b(A5), .eq(comparator_172_eq));  // open: gt, lt
  Comparator #(.width(4)) comparator_173 (.a(4'b1100), .b(A5), .eq(comparator_173_eq));  // open: gt, lt
  Comparator #(.width(4)) comparator_174 (.a(4'b1101), .b(A5), .eq(comparator_174_eq));  // open: gt, lt
  Comparator #(.width(4)) comparator_175 (.a(4'b1110), .b(A5), .eq(comparator_175_eq));  // open: gt, lt
  Comparator #(.width(4)) comparator_176 (.a(4'b1111), .b(A5), .eq(comparator_176_eq));  // open: gt, lt
  Multiplexer #(.select(4), .width(64)) multiplexer_29 (
    .in0(R0), .in1(R1), .in2(R2), .in3(R3), .in4(R4), .in5(R5), .in6(R6), .in7(R7), .in8(R8), .in9(R9),
    .in10(R10), .in11(R11), .in12(R12), .in13(R13), .in14(R14), .in15(R15), .out(O12), .sel(A12));
  and and_169 (and_129_out[5], comparator_169_eq, LE5);
  and and_170 (and_130_out[5], comparator_170_eq, LE5);
  and and_171 (and_131_out[5], comparator_171_eq, LE5);
  and and_172 (and_132_out[5], comparator_172_eq, LE5);
  and and_173 (and_133_out[5], comparator_173_eq, LE5);
  and and_174 (and_134_out[5], comparator_174_eq, LE5);
  and and_175 (and_135_out[5], comparator_175_eq, LE5);
  and and_176 (and_136_out[5], comparator_176_eq, LE5);
  Comparator #(.width(4)) comparator_177 (.a(4'b1000), .b(A6), .eq(comparator_177_eq));  // open: gt, lt
  Comparator #(.width(4)) comparator_178 (.a(4'b1001), .b(A6), .eq(comparator_178_eq));  // open: gt, lt
  Comparator #(.width(4)) comparator_179 (.a(4'b1010), .b(A6), .eq(comparator_179_eq));  // open: gt, lt
  Comparator #(.width(4)) comparator_180 (.a(4'b1011), .b(A6), .eq(comparator_180_eq));  // open: gt, lt
  Comparator #(.width(4)) comparator_181 (.a(4'b1100), .b(A6), .eq(comparator_181_eq));  // open: gt, lt
  Comparator #(.width(4)) comparator_182 (.a(4'b1101), .b(A6), .eq(comparator_182_eq));  // open: gt, lt
  Comparator #(.width(4)) comparator_183 (.a(4'b1110), .b(A6), .eq(comparator_183_eq));  // open: gt, lt
  Comparator #(.width(4)) comparator_184 (.a(4'b1111), .b(A6), .eq(comparator_184_eq));  // open: gt, lt
  and and_177 (and_129_out[6], comparator_177_eq, LE6);
  and and_178 (and_130_out[6], comparator_178_eq, LE6);
  and and_179 (and_131_out[6], comparator_179_eq, LE6);
  and and_180 (and_132_out[6], comparator_180_eq, LE6);
  and and_181 (and_133_out[6], comparator_181_eq, LE6);
  and and_182 (and_134_out[6], comparator_182_eq, LE6);
  and and_183 (and_135_out[6], comparator_183_eq, LE6);
  and and_184 (and_136_out[6], comparator_184_eq, LE6);
  Multiplexer #(.select(4), .width(64)) multiplexer_30 (
    .in0(R0), .in1(R1), .in2(R2), .in3(R3), .in4(R4), .in5(R5), .in6(R6), .in7(R7), .in8(R8), .in9(R9),
    .in10(R10), .in11(R11), .in12(R12), .in13(R13), .in14(R14), .in15(R15), .out(O13), .sel(A13));
  Comparator #(.width(4)) comparator_185 (.a(4'b1000), .b(A7), .eq(comparator_185_eq));  // open: gt, lt
  and and_185 (and_129_out[7], comparator_185_eq, LE7);
  Comparator #(.width(4)) comparator_186 (.a(4'b1001), .b(A7), .eq(comparator_186_eq));  // open: gt, lt
  and and_186 (and_130_out[7], comparator_186_eq, LE7);
  Comparator #(.width(4)) comparator_187 (.a(4'b1010), .b(A7), .eq(comparator_187_eq));  // open: gt, lt
  and and_187 (and_131_out[7], comparator_187_eq, LE7);
  Comparator #(.width(4)) comparator_188 (.a(4'b1011), .b(A7), .eq(comparator_188_eq));  // open: gt, lt
  and and_188 (and_132_out[7], comparator_188_eq, LE7);
  Comparator #(.width(4)) comparator_189 (.a(4'b1100), .b(A7), .eq(comparator_189_eq));  // open: gt, lt
  and and_189 (and_133_out[7], comparator_189_eq, LE7);
  Comparator #(.width(4)) comparator_190 (.a(4'b1101), .b(A7), .eq(comparator_190_eq));  // open: gt, lt
  and and_190 (and_134_out[7], comparator_190_eq, LE7);
  Comparator #(.width(4)) comparator_191 (.a(4'b1110), .b(A7), .eq(comparator_191_eq));  // open: gt, lt
  and and_191 (and_135_out[7], comparator_191_eq, LE7);
  Comparator #(.width(4)) comparator_192 (.a(4'b1111), .b(A7), .eq(comparator_192_eq));  // open: gt, lt
  and and_192 (and_136_out[7], comparator_192_eq, LE7);
  Comparator #(.width(4)) comparator_193 (.a(4'b1000), .b(A8), .eq(comparator_193_eq));  // open: gt, lt
  and and_193 (and_129_out[8], comparator_193_eq, LE8);
  Comparator #(.width(4)) comparator_194 (.a(4'b1001), .b(A8), .eq(comparator_194_eq));  // open: gt, lt
  and and_194 (and_130_out[8], comparator_194_eq, LE8);
  Comparator #(.width(4)) comparator_195 (.a(4'b1010), .b(A8), .eq(comparator_195_eq));  // open: gt, lt
  and and_195 (and_131_out[8], comparator_195_eq, LE8);
  Comparator #(.width(4)) comparator_196 (.a(4'b1011), .b(A8), .eq(comparator_196_eq));  // open: gt, lt
  and and_196 (and_132_out[8], comparator_196_eq, LE8);
  Comparator #(.width(4)) comparator_197 (.a(4'b1100), .b(A8), .eq(comparator_197_eq));  // open: gt, lt
  and and_197 (and_133_out[8], comparator_197_eq, LE8);
  Comparator #(.width(4)) comparator_198 (.a(4'b1101), .b(A8), .eq(comparator_198_eq));  // open: gt, lt
  and and_198 (and_134_out[8], comparator_198_eq, LE8);
  Comparator #(.width(4)) comparator_199 (.a(4'b1110), .b(A8), .eq(comparator_199_eq));  // open: gt, lt
  and and_199 (and_135_out[8], comparator_199_eq, LE8);
  Comparator #(.width(4)) comparator_200 (.a(4'b1111), .b(A8), .eq(comparator_200_eq));  // open: gt, lt
  and and_200 (and_136_out[8], comparator_200_eq, LE8);
  Multiplexer #(.select(4), .width(64)) multiplexer_31 (
    .in0(R0), .in1(R1), .in2(R2), .in3(R3), .in4(R4), .in5(R5), .in6(R6), .in7(R7), .in8(R8), .in9(R9),
    .in10(R10), .in11(R11), .in12(R12), .in13(R13), .in14(R14), .in15(R15), .out(O14), .sel(A14));
  Comparator #(.width(4)) comparator_201 (.a(4'b1000), .b(A9), .eq(comparator_201_eq));  // open: gt, lt
  and and_201 (and_129_out[9], comparator_201_eq, LE9);
  Comparator #(.width(4)) comparator_202 (.a(4'b1001), .b(A9), .eq(comparator_202_eq));  // open: gt, lt
  and and_202 (and_130_out[9], comparator_202_eq, LE9);
  Comparator #(.width(4)) comparator_203 (.a(4'b1010), .b(A9), .eq(comparator_203_eq));  // open: gt, lt
  and and_203 (and_131_out[9], comparator_203_eq, LE9);
  Comparator #(.width(4)) comparator_204 (.a(4'b1011), .b(A9), .eq(comparator_204_eq));  // open: gt, lt
  and and_204 (and_132_out[9], comparator_204_eq, LE9);
  Comparator #(.width(4)) comparator_205 (.a(4'b1100), .b(A9), .eq(comparator_205_eq));  // open: gt, lt
  and and_205 (and_133_out[9], comparator_205_eq, LE9);
  Comparator #(.width(4)) comparator_206 (.a(4'b1101), .b(A9), .eq(comparator_206_eq));  // open: gt, lt
  and and_206 (and_134_out[9], comparator_206_eq, LE9);
  Comparator #(.width(4)) comparator_207 (.a(4'b1110), .b(A9), .eq(comparator_207_eq));  // open: gt, lt
  and and_207 (and_135_out[9], comparator_207_eq, LE9);
  Comparator #(.width(4)) comparator_208 (.a(4'b1111), .b(A9), .eq(comparator_208_eq));  // open: gt, lt
  and and_208 (and_136_out[9], comparator_208_eq, LE9);
  Comparator #(.width(4)) comparator_209 (.a(4'b1000), .b(A10), .eq(comparator_209_eq));  // open: gt, lt
  and and_209 (and_129_out[10], comparator_209_eq, LE10);
  Comparator #(.width(4)) comparator_210 (.a(4'b1001), .b(A10), .eq(comparator_210_eq));  // open: gt, lt
  and and_210 (and_130_out[10], comparator_210_eq, LE10);
  Comparator #(.width(4)) comparator_211 (.a(4'b1010), .b(A10), .eq(comparator_211_eq));  // open: gt, lt
  and and_211 (and_131_out[10], comparator_211_eq, LE10);
  Comparator #(.width(4)) comparator_212 (.a(4'b1011), .b(A10), .eq(comparator_212_eq));  // open: gt, lt
  and and_212 (and_132_out[10], comparator_212_eq, LE10);
  Comparator #(.width(4)) comparator_213 (.a(4'b1100), .b(A10), .eq(comparator_213_eq));  // open: gt, lt
  and and_213 (and_133_out[10], comparator_213_eq, LE10);
  Comparator #(.width(4)) comparator_214 (.a(4'b1101), .b(A10), .eq(comparator_214_eq));  // open: gt, lt
  and and_214 (and_134_out[10], comparator_214_eq, LE10);
  Comparator #(.width(4)) comparator_215 (.a(4'b1110), .b(A10), .eq(comparator_215_eq));  // open: gt, lt
  and and_215 (and_135_out[10], comparator_215_eq, LE10);
  Comparator #(.width(4)) comparator_216 (.a(4'b1111), .b(A10), .eq(comparator_216_eq));  // open: gt, lt
  and and_216 (and_136_out[10], comparator_216_eq, LE10);
  Multiplexer #(.select(4), .width(64)) multiplexer_32 (
    .in0(R0), .in1(R1), .in2(R2), .in3(R3), .in4(R4), .in5(R5), .in6(R6), .in7(R7), .in8(R8), .in9(R9),
    .in10(R10), .in11(R11), .in12(R12), .in13(R13), .in14(R14), .in15(R15), .out(O15), .sel(A15));
  Comparator #(.width(4)) comparator_217 (.a(4'b1000), .b(A11), .eq(comparator_217_eq));  // open: gt, lt
  and and_217 (and_129_out[11], comparator_217_eq, LE11);
  Comparator #(.width(4)) comparator_218 (.a(4'b1001), .b(A11), .eq(comparator_218_eq));  // open: gt, lt
  and and_218 (and_130_out[11], comparator_218_eq, LE11);
  Comparator #(.width(4)) comparator_219 (.a(4'b1010), .b(A11), .eq(comparator_219_eq));  // open: gt, lt
  and and_219 (and_131_out[11], comparator_219_eq, LE11);
  Comparator #(.width(4)) comparator_220 (.a(4'b1011), .b(A11), .eq(comparator_220_eq));  // open: gt, lt
  and and_220 (and_132_out[11], comparator_220_eq, LE11);
  Comparator #(.width(4)) comparator_221 (.a(4'b1100), .b(A11), .eq(comparator_221_eq));  // open: gt, lt
  and and_221 (and_133_out[11], comparator_221_eq, LE11);
  Comparator #(.width(4)) comparator_222 (.a(4'b1101), .b(A11), .eq(comparator_222_eq));  // open: gt, lt
  and and_222 (and_134_out[11], comparator_222_eq, LE11);
  Comparator #(.width(4)) comparator_223 (.a(4'b1110), .b(A11), .eq(comparator_223_eq));  // open: gt, lt
  and and_223 (and_135_out[11], comparator_223_eq, LE11);
  Comparator #(.width(4)) comparator_224 (.a(4'b1111), .b(A11), .eq(comparator_224_eq));  // open: gt, lt
  and and_224 (and_136_out[11], comparator_224_eq, LE11);
  Comparator #(.width(4)) comparator_225 (.a(4'b1000), .b(A12), .eq(comparator_225_eq));  // open: gt, lt
  and and_225 (and_129_out[12], comparator_225_eq, LE12);
  Comparator #(.width(4)) comparator_226 (.a(4'b1001), .b(A12), .eq(comparator_226_eq));  // open: gt, lt
  and and_226 (and_130_out[12], comparator_226_eq, LE12);
  Comparator #(.width(4)) comparator_227 (.a(4'b1010), .b(A12), .eq(comparator_227_eq));  // open: gt, lt
  and and_227 (and_131_out[12], comparator_227_eq, LE12);
  Comparator #(.width(4)) comparator_228 (.a(4'b1011), .b(A12), .eq(comparator_228_eq));  // open: gt, lt
  and and_228 (and_132_out[12], comparator_228_eq, LE12);
  Comparator #(.width(4)) comparator_229 (.a(4'b1100), .b(A12), .eq(comparator_229_eq));  // open: gt, lt
  and and_229 (and_133_out[12], comparator_229_eq, LE12);
  Comparator #(.width(4)) comparator_230 (.a(4'b1101), .b(A12), .eq(comparator_230_eq));  // open: gt, lt
  and and_230 (and_134_out[12], comparator_230_eq, LE12);
  Comparator #(.width(4)) comparator_231 (.a(4'b1110), .b(A12), .eq(comparator_231_eq));  // open: gt, lt
  and and_231 (and_135_out[12], comparator_231_eq, LE12);
  Comparator #(.width(4)) comparator_232 (.a(4'b1111), .b(A12), .eq(comparator_232_eq));  // open: gt, lt
  and and_232 (and_136_out[12], comparator_232_eq, LE12);
  Comparator #(.width(4)) comparator_233 (.a(4'b1000), .b(A13), .eq(comparator_233_eq));  // open: gt, lt
  and and_233 (and_129_out[13], comparator_233_eq, LE13);
  Comparator #(.width(4)) comparator_234 (.a(4'b1001), .b(A13), .eq(comparator_234_eq));  // open: gt, lt
  and and_234 (and_130_out[13], comparator_234_eq, LE13);
  Comparator #(.width(4)) comparator_235 (.a(4'b1010), .b(A13), .eq(comparator_235_eq));  // open: gt, lt
  and and_235 (and_131_out[13], comparator_235_eq, LE13);
  Comparator #(.width(4)) comparator_236 (.a(4'b1011), .b(A13), .eq(comparator_236_eq));  // open: gt, lt
  and and_236 (and_132_out[13], comparator_236_eq, LE13);
  Comparator #(.width(4)) comparator_237 (.a(4'b1100), .b(A13), .eq(comparator_237_eq));  // open: gt, lt
  and and_237 (and_133_out[13], comparator_237_eq, LE13);
  Comparator #(.width(4)) comparator_238 (.a(4'b1101), .b(A13), .eq(comparator_238_eq));  // open: gt, lt
  and and_238 (and_134_out[13], comparator_238_eq, LE13);
  Comparator #(.width(4)) comparator_239 (.a(4'b1110), .b(A13), .eq(comparator_239_eq));  // open: gt, lt
  and and_239 (and_135_out[13], comparator_239_eq, LE13);
  Comparator #(.width(4)) comparator_240 (.a(4'b1111), .b(A13), .eq(comparator_240_eq));  // open: gt, lt
  and and_240 (and_136_out[13], comparator_240_eq, LE13);
  Comparator #(.width(4)) comparator_241 (.a(4'b1000), .b(A14), .eq(comparator_241_eq));  // open: gt, lt
  and and_241 (and_129_out[14], comparator_241_eq, LE14);
  Comparator #(.width(4)) comparator_242 (.a(4'b1001), .b(A14), .eq(comparator_242_eq));  // open: gt, lt
  and and_242 (and_130_out[14], comparator_242_eq, LE14);
  Comparator #(.width(4)) comparator_243 (.a(4'b1010), .b(A14), .eq(comparator_243_eq));  // open: gt, lt
  and and_243 (and_131_out[14], comparator_243_eq, LE14);
  Comparator #(.width(4)) comparator_244 (.a(4'b1011), .b(A14), .eq(comparator_244_eq));  // open: gt, lt
  and and_244 (and_132_out[14], comparator_244_eq, LE14);
  Comparator #(.width(4)) comparator_245 (.a(4'b1100), .b(A14), .eq(comparator_245_eq));  // open: gt, lt
  and and_245 (and_133_out[14], comparator_245_eq, LE14);
  Comparator #(.width(4)) comparator_246 (.a(4'b1101), .b(A14), .eq(comparator_246_eq));  // open: gt, lt
  and and_246 (and_134_out[14], comparator_246_eq, LE14);
  Comparator #(.width(4)) comparator_247 (.a(4'b1110), .b(A14), .eq(comparator_247_eq));  // open: gt, lt
  and and_247 (and_135_out[14], comparator_247_eq, LE14);
  Comparator #(.width(4)) comparator_248 (.a(4'b1111), .b(A14), .eq(comparator_248_eq));  // open: gt, lt
  and and_248 (and_136_out[14], comparator_248_eq, LE14);
  Comparator #(.width(4)) comparator_249 (.a(4'b1000), .b(A15), .eq(comparator_249_eq));  // open: gt, lt
  and and_249 (and_129_out[15], comparator_249_eq, LE15);
  Comparator #(.width(4)) comparator_250 (.a(4'b1001), .b(A15), .eq(comparator_250_eq));  // open: gt, lt
  and and_250 (and_130_out[15], comparator_250_eq, LE15);
  Comparator #(.width(4)) comparator_251 (.a(4'b1010), .b(A15), .eq(comparator_251_eq));  // open: gt, lt
  and and_251 (and_131_out[15], comparator_251_eq, LE15);
  Comparator #(.width(4)) comparator_252 (.a(4'b1011), .b(A15), .eq(comparator_252_eq));  // open: gt, lt
  and and_252 (and_132_out[15], comparator_252_eq, LE15);
  Comparator #(.width(4)) comparator_253 (.a(4'b1100), .b(A15), .eq(comparator_253_eq));  // open: gt, lt
  and and_253 (and_133_out[15], comparator_253_eq, LE15);
  Comparator #(.width(4)) comparator_254 (.a(4'b1101), .b(A15), .eq(comparator_254_eq));  // open: gt, lt
  and and_254 (and_134_out[15], comparator_254_eq, LE15);
  Comparator #(.width(4)) comparator_255 (.a(4'b1110), .b(A15), .eq(comparator_255_eq));  // open: gt, lt
  and and_255 (and_135_out[15], comparator_255_eq, LE15);
  Comparator #(.width(4)) comparator_256 (.a(4'b1111), .b(A15), .eq(comparator_256_eq));  // open: gt, lt
  and and_256 (and_136_out[15], comparator_256_eq, LE15);
endmodule
