// Logisim project muxfpga.circ as structural Verilog: 3 circuits, main circuit main
module main (
);

  wire clock_1_out;
  wire [63:0] fpgaram_1_dx;

  Clock clock_1 (.out(clock_1_out));
  // Probe on fpgaram_1_dx
  fpgaram fpgaram_1 (
    .A(4'b0001), .WE(1'b1), .D(64'hffff), .RY(64'h1), .RZ(64'h2), .OP(4'b1011), .OE(1'b1), .CLK(clock_1_out),
    .DX(fpgaram_1_dx));
endmodule

module logicelement (
  input  [63:0] DY,
  input  [63:0] DZ,
  input  [63:0] RY,
  input  [63:0] RZ,
  input  [3:0] OP,
  input  OE,
  input  [63:0] DX,
  input  WE,
  input  CLK,
  output [63:0] AY,
  output [63:0] AZ,
  output [63:0] D
);

  wire [3:0] register_1_q;
  wire [63:0] and_1_out, nand_1_out, nor_1_out, not_1_out, or_1_out, register_2_q, register_3_q, xnor_1_out,
       xor_1_out;

  Register #(.width(4)) register_1 (.D(OP), .en(OE), .clk(CLK), .Q(register_1_q));  // open: clr
  Register #(.width(64)) register_2 (.D(DX), .en(WE), .clk(CLK), .Q(register_2_q));  // open: clr
  assign xnor_1_out = ~(DZ ^ DY);  // XNOR_Gate xnor_1, 64 bits wide
  assign xor_1_out = DZ ^ DY;  // XOR_Gate xor_1, 64 bits wide
  assign nor_1_out = ~(DZ | DY);  // NOR_Gate nor_1, 64 bits wide
  Register #(.width(64)) register_3 (.D(DY), .en(1'b1), .clk(CLK), .Q(register_3_q));  // open: clr
  assign or_1_out = DZ | DY;  // OR_Gate or_1, 64 bits wide
  assign nand_1_out = ~(DZ & DY);  // NAND_Gate nand_1, 64 bits wide
  assign not_1_out = ~DY;  // NOT_Gate not_1, 64 bits wide
  assign and_1_out = DZ & DY;  // AND_Gate and_1, 64 bits wide
  Multiplexer #(.select(4), .width(64)) multiplexer_1 (
    .in0(register_2_q), .in1(not_1_out), .in2(and_1_out), .in3(or_1_out), .in4(nand_1_out), .in5(nor_1_out),
    .in6(xor_1_out), .in7(xnor_1_out), .in8({64{1'b0}}), .in9(64'h1), .in10(64'hf), .in11(64'hff),
    .in12(64'hffff), .in13(64'hffffffff), .in14({64{1'b1}}), .in15(register_3_q), .out(D), .sel(register_1_q));
  Register #(.width(64)) Y (.D(RY), .en(OE), .clk(CLK), .Q(AY));  // open: clr
  Register #(.width(64)) Z (.D(RZ), .en(OE), .clk(CLK), .Q(AZ));  // open: clr
endmodule

module fpgaram (
  input  [3:0] A,
  input  WE,
  input  [63:0] D,
  input  [63:0] RY,
  input  [63:0] RZ,
  input  [3:0] OP,
  input  OE,
  input  CLK,
  output [63:0] DX
);

  wire demultiplexer_1_out0, demultiplexer_1_out1, demultiplexer_1_out2, demultiplexer_1_out3,
       demultiplexer_2_out0, demultiplexer_2_out1, demultiplexer_2_out2, demultiplexer_2_out3;
  wire [3:0] bitselector_1_out, bitselector_2_out, bitselector_3_out, bitselector_4_out, bitselector_5_out,
       bitselector_6_out, bitselector_7_out, bitselector_8_out;
  wire [63:0] D00, D01, D02, D03, multiplexer_1_out, multiplexer_2_out, multiplexer_3_out, multiplexer_4_out,
       multiplexer_5_out, multiplexer_6_out, multiplexer_7_out, multiplexer_8_out, R0_ay, R0_az, R1_ay,
       R1_az, R2_ay, R2_az, R3_ay, R3_az;

  Demultiplexer #(.select(4)) demultiplexer_1 (
    .out0(demultiplexer_1_out0), .out1(demultiplexer_1_out1), .out2(demultiplexer_1_out2),
    .out3(demultiplexer_1_out3), .in(WE), .sel(A));  // open: out4, out5, out6, out7, out8, out9, out10, out11, out12, out13, out14, out15
  Demultiplexer #(.select(4)) demultiplexer_2 (
    .out0(demultiplexer_2_out0), .out1(demultiplexer_2_out1), .out2(demultiplexer_2_out2),
    .out3(demultiplexer_2_out3), .in(OE), .sel(A));  // open: out4, out5, out6, out7, out8, out9, out10, out11, out12, out13, out14, out15
  // Probe on D00
  logicelement R0 (
    .DY(multiplexer_1_out), .DZ(multiplexer_5_out), .RY(RY), .RZ(RZ), .OP(OP), .OE(demultiplexer_2_out0),
    .DX(D), .WE(demultiplexer_1_out0), .CLK(CLK), .AY(R0_ay), .AZ(R0_az), .D(D00));
  // Probe on D01
  logicelement R1 (
    .DY(multiplexer_2_out), .DZ(multiplexer_6_out), .RY(RY), .RZ(RZ), .OP(OP), .OE(demultiplexer_2_out1),
    .DX(D), .WE(demultiplexer_1_out1), .CLK(CLK), .AY(R1_ay), .AZ(R1_az), .D(D01));
  // Probe on D02
  logicelement R2 (
    .DY(multiplexer_3_out), .DZ(multiplexer_7_out), .RY(RY), .RZ(RZ), .OP(OP), .OE(demultiplexer_2_out2),
    .DX(D), .WE(demultiplexer_1_out2), .CLK(CLK), .AY(R2_ay), .AZ(R2_az), .D(D02));
  // Probe on D03
  logicelement R3 (
    .DY(multiplexer_4_out), .DZ(multiplexer_8_out), .RY(RY), .RZ(RZ), .OP(OP), .OE(demultiplexer_2_out3),
    .DX(D), .WE(demultiplexer_1_out3), .CLK(CLK), .AY(R3_ay), .AZ(R3_az), .D(D03));
  Multiplexer #(.select(4), .width(64)) multiplexer_1 (
    .in0(D00), .in1(D01), .in2(D02), .in3(D03), .out(multiplexer_1_out), .sel(bitselector_1_out));  // open: in4, in5, in6, in7, in8, in9, in10, in11, in12, in13, in14, in15
  BitSelector #(.group(4), .width(64)) bitselector_1 (.in(R0_ay), .out(bitselector_1_out), .sel(4'b0000));
  Multiplexer #(.select(4), .width(64)) multiplexer_2 (
    .in0(D00), .in1(D01), .in2(D02), .in3(D03), .out(multiplexer_2_out), .sel(bitselector_2_out));  // open: in4, in5, in6, in7, in8, in9, in10, in11, in12, in13, in14, in15
  BitSelector #(.group(4), .width(64)) bitselector_2 (.in(R1_ay), .out(bitselector_2_out), .sel(4'b0000));
  Multiplexer #(.select(4), .width(64)) multiplexer_3 (
    .in0(D00), .in1(D01), .in2(D02), .in3(D03), .out(multiplexer_3_out), .sel(bitselector_3_out));  // open: in4, in5, in6, in7, in8, in9, in10, in11, in12, in13, in14, in15
  BitSelector #(.group(4), .width(64)) bitselector_3 (.in(R2_ay), .out(bitselector_3_out), .sel(4'b0000));
  Multiplexer #(.select(4), .width(64)) multiplexer_4 (
    .in0(D00), .in1(D01), .in2(D02), .in3(D03), .out(multiplexer_4_out), .sel(bitselector_4_out));  // open: in4, in5, in6, in7, in8, in9, in10, in11, in12, in13, in14, in15
  BitSelector #(.group(4), .width(64)) bitselector_4 (.in(R3_ay), .out(bitselector_4_out), .sel(4'b0000));
  Multiplexer #(.select(4), .width(64)) multiplexer_5 (
    .in0(D00), .in1(D01), .in2(D02), .in3(D03), .out(multiplexer_5_out), .sel(bitselector_5_out));  // open: in4, in5, in6, in7, in8, in9, in10, in11, in12, in13, in14, in15
  BitSelector #(.group(4), .width(64)) bitselector_5 (.in(R0_az), .out(bitselector_5_out), .sel(4'b0000));
  Multiplexer #(.select(4), .width(64)) multiplexer_6 (
    .in0(D00), .in1(D01), .in2(D02), .in3(D03), .out(multiplexer_6_out), .sel(bitselector_6_out));  // open: in4, in5, in6, in7, in8, in9, in10, in11, in12, in13, in14, in15
  BitSelector #(.group(4), .width(64)) bitselector_6 (.in(R1_az), .out(bitselector_6_out), .sel(4'b0000));
  Multiplexer #(.select(4), .width(64)) multiplexer_7 (
    .in0(D00), .in1(D01), .in2(D02), .in3(D03), .out(multiplexer_7_out), .sel(bitselector_7_out));  // open: in4, in5, in6, in7, in8, in9, in10, in11, in12, in13, in14, in15
  BitSelector #(.group(4), .width(64)) bitselector_7 (.in(R2_az), .out(bitselector_7_out), .sel(4'b0000));
  Multiplexer #(.select(4), .width(64)) multiplexer_8 (
    .in0(D00), .in1(D01), .in2(D02), .in3(D03), .out(multiplexer_8_out), .sel(bitselector_8_out));  // open: in4, in5, in6, in7, in8, in9, in10, in11, in12, in13, in14, in15
  BitSelector #(.group(4), .width(64)) bitselector_8 (.in(R3_az), .out(bitselector_8_out), .sel(4'b0000));
  Multiplexer #(.select(4), .width(64)) multiplexer_9 (
    .in0(D00), .in1(D01), .in2(D02), .in3(D03), .out(DX), .sel(A));  // open: in4, in5, in6, in7, in8, in9, in10, in11, in12, in13, in14, in15
endmodule
