// Logisim project muxrisccore.circ as structural Verilog: 3 circuits, main circuit core
module core (
);

  wire alu_1_we, and_1_out, and_2_out, and_3_out, and_5_out, and_6_out, and_7_out, and_9_out, and_10_out,
       and_11_out, and_13_out, and_14_out, and_15_out, and_16_out, and_17_out, and_18_out, and_19_out,
       and_21_out, and_22_out, and_23_out, and_25_out, and_26_out, and_27_out, and_29_out, and_30_out,
       and_31_out, and_33_out, and_34_out, and_35_out, and_36_out, and_37_out, cart1_p29, clock_1_out,
       clock_3_out, clock_5_out, clock_6_out, clock_7_out, clock_9_out, clock_11_out, clock_12_out,
       clock_14_out, clock_15_out, clock_16_out, clock_18_out, clock_19_out, clock_20_out, clock_22_out,
       clock_23_out, clock_25_out, clock_27_out, clock_28_out, clock_29_out, clock_30_out, clock_32_out,
       clock_33_out, clock_35_out, clock_36_out, clock_37_out, clock_38_out, clock_40_out, clock_41_out,
       comparator_1_eq, comparator_2_gt, comparator_3_eq, comparator_4_eq, comparator_5_eq, comparator_6_eq,
       comparator_7_eq, comparator_8_eq, comparator_9_eq, comparator_10_eq, comparator_11_eq,
       comparator_12_eq, comparator_13_eq, comparator_14_eq, comparator_15_eq, comparator_16_eq,
       comparator_17_eq, comparator_18_eq, comparator_19_eq, comparator_19_gt, comparator_19_lt,
       comparator_20_eq, comparator_21_eq, comparator_22_eq, comparator_23_eq, comparator_24_eq,
       comparator_25_eq, comparator_26_eq, comparator_27_eq, comparator_28_eq, comparator_28_gt,
       comparator_28_lt, comparator_29_eq, not_1_out, not_2_out, not_3_out, not_4_out, not_5_out, not_6_out,
       not_7_out, not_8_out, not_9_out, not_10_out, not_11_out, not_12_out, or_1_out, or_2_out, or_4_out,
       random_1_p1, random_1_p2, random_2_p1, random_2_p2, random_3_p1, random_3_p2, random_4_p1,
       random_5_p1, random_5_p2, random_6_p1, random_6_p2, random_7_p1, random_7_p2, random_8_p1,
       random_8_p2, register_9_q, regX_p2, regX_p11, rgb_video_1_p1;
  wire [1:0] bitselector_26_out, bitselector_31_out;
  wire [2:0] bitselector_11_out, bitselector_12_out, bitselector_13_out, bitselector_14_out,
       bitselector_15_out, bitselector_16_out, bitselector_17_out, bitselector_18_out;
  wire [3:0] bitselector_7_out, bitselector_8_out, bitselector_9_out, bitselector_10_out;
  wire [7:0] bitselector_5_out, bitselector_6_out, bitselector_21_out, bitselector_23_out, bitselector_25_out;
  wire [8:0] bitselector_27_out, bitselector_29_out;
  wire [15:0] bitselector_1_out, bitselector_2_out, bitselector_3_out, bitselector_4_out, bitselector_19_out,
       bitselector_20_out, bitselector_22_out;
  wire [17:0] bitselector_28_out;
  wire [23:0] bitselector_30_out, bitselector_33_out, ram1_p2;
  wire [31:0] regY_p10, regY_p10_2;
  wire [63:0] alu_1_outx, alu_2_outx, alu_3_outx, alu_4_outx, alu_5_outx, alu_6_outx, alu_7_outx, alu_8_outx,
       cart1_p31, cart1_p32, cart1_p33, cart1_p34, cart1_p35, cart1_p36, cart1_p37, cart1_p38, cart1_p39,
       counter_1_q, counter_2_q, counter_3_q, counter_4_q, counter_5_q, counter_6_q, counter_7_q,
       counter_8_q, counter_9_q, counter_10_q, counter_11_q, counter_12_q, counter_13_q, counter_14_q,
       counter_15_q, counter_16_q, counter_17_q, counter_18_q, multiplexer_2_out, multiplexer_3_out,
       multiplexer_4_out, multiplexer_6_out, multiplexer_7_out, multiplexer_8_out, multiplexer_11_out,
       multiplexer_12_out, multiplexer_13_out, multiplexer_15_out, multiplexer_17_out, multiplexer_18_out,
       multiplexer_20_out, multiplexer_21_out, multiplexer_22_out, multiplexer_24_out, multiplexer_25_out,
       multiplexer_26_out, multiplexer_27_out, multiplexer_28_out, multiplexer_29_out, multiplexer_30_out,
       multiplexer_31_out, multiplexer_32_out, multiplexer_33_out, multiplexer_34_out, multiplexer_35_out,
       ram1_p3, register_1_q, register_2_q, register_3_q, register_4_q, register_5_q, register_6_q,
       register_7_q, register_8_q, regX_p12, regX_p13, regX_p14, regX_p15, regX_p16, regX_p17, regX_p18,
       regX_p19, regX_p20, regX_p21, regX_p22, regX_p23, regX_p24, regX_p25, regX_p26, regX_p27, regY_p11,
       regY_p12, regY_p13, regY_p14, regY_p15, regY_p16, regY_p17, regZ_p10, regZ_p11, regZ_p12, regZ_p13,
       regZ_p14, regZ_p15, regZ_p16, regZ_p17, rom1_p9, rom1_p10, rom1_p11, rom1_p12, rom1_p13, rom1_p14,
       rom1_p15, rom1_p16, undriven, undriven_2, undriven_3, undriven_4, undriven_5, undriven_6, undriven_7,
       undriven_8;

  BitSelector #(.group(16), .width(64)) bitselector_1 (.in(multiplexer_27_out), .out(bitselector_1_out), .sel(2'b11));
  BitSelector #(.group(16), .width(64)) bitselector_2 (.in(multiplexer_27_out), .out(bitselector_2_out), .sel(2'b10));
  BitSelector #(.group(16), .width(64)) bitselector_3 (.in(multiplexer_27_out), .out(bitselector_3_out), .sel(2'b01));
  BitSelector #(.group(16), .width(64)) bitselector_4 (.in(multiplexer_27_out), .out(bitselector_4_out), .sel(2'b00));
  BitSelector #(.group(8), .width(16)) bitselector_5 (.in(bitselector_4_out), .out(bitselector_5_out), .sel(1'b1));
  BitSelector #(.group(8), .width(16)) bitselector_6 (.in(bitselector_4_out), .out(bitselector_6_out), .sel(1'b0));
  BitSelector #(.group(4)) bitselector_7 (.in(bitselector_6_out), .out(bitselector_7_out), .sel(1'b0));
  BitSelector #(.group(4)) bitselector_8 (.in(bitselector_6_out), .out(bitselector_8_out), .sel(1'b1));
  Comparator #(.mode("unsigned")) comparator_1 (
    .a(bitselector_6_out), .b(8'he0), .eq(comparator_1_eq));  // open: gt, lt
  BitSelector #(.group(4)) bitselector_9 (.in(bitselector_6_out), .out(bitselector_9_out), .sel(1'b0));
  BitSelector #(.group(4)) bitselector_10 (.in(bitselector_6_out), .out(bitselector_10_out), .sel(1'b1));
  Comparator #(.mode("unsigned"), .width(4)) comparator_2 (
    .a(bitselector_7_out), .b(4'b0000), .gt(comparator_2_gt));  // open: eq, lt
  Comparator #(.mode("unsigned")) comparator_3 (
    .a(bitselector_6_out), .b({8{1'b0}}), .eq(comparator_3_eq));  // open: gt, lt
  Counter #(.max('hffffffffffffffff), .width(64)) counter_1 (
    .load(or_1_out), .D({64{1'b0}}), .count(comparator_3_eq), .Q(counter_1_q), .clk(clock_1_out));  // open: carry, up, clr
  Clock clock_1 (.out(clock_1_out));
  Comparator #(.mode("unsigned")) comparator_4 (
    .a(bitselector_6_out), .b(8'h10), .eq(comparator_4_eq));  // open: gt, lt
  Comparator #(.mode("unsigned")) comparator_5 (
    .a(bitselector_6_out), .b(8'h20), .eq(comparator_5_eq));  // open: gt, lt
  Comparator #(.mode("unsigned")) comparator_6 (
    .a(bitselector_6_out), .b(8'h30), .eq(comparator_6_eq));  // open: gt, lt
  Comparator #(.mode("unsigned"), .width(64)) comparator_7 (
    .a({64{1'b0}}), .b({regY_p10, regY_p10_2}), .eq(comparator_7_eq));  // open: gt, lt
  Comparator #(.mode("unsigned")) comparator_8 (
    .a(bitselector_6_out), .b(8'h40), .eq(comparator_8_eq));  // open: gt, lt
  Comparator #(.mode("unsigned")) comparator_9 (
    .a(bitselector_6_out), .b(8'h50), .eq(comparator_9_eq));  // open: gt, lt
  Comparator #(.mode("unsigned")) comparator_10 (
    .a(bitselector_6_out), .b(8'h60), .eq(comparator_10_eq));  // open: gt, lt
  Comparator #(.mode("unsigned")) comparator_11 (
    .a(bitselector_6_out), .b(8'h70), .eq(comparator_11_eq));  // open: gt, lt
  Comparator #(.mode("unsigned")) comparator_12 (
    .a(bitselector_6_out), .b(8'h80), .eq(comparator_12_eq));  // open: gt, lt
  Comparator #(.mode("unsigned")) comparator_13 (
    .a(bitselector_6_out), .b(8'h90), .eq(comparator_13_eq));  // open: gt, lt
  Comparator #(.mode("unsigned")) comparator_14 (
    .a(bitselector_6_out), .b(8'ha0), .eq(comparator_14_eq));  // open: gt, lt
  Comparator #(.mode("unsigned")) comparator_15 (
    .a(bitselector_6_out), .b(8'hb0), .eq(comparator_15_eq));  // open: gt, lt
  Comparator #(.mode("unsigned")) comparator_16 (
    .a(bitselector_6_out), .b(8'hc0), .eq(comparator_16_eq));  // open: gt, lt
  Comparator #(.mode("unsigned")) comparator_17 (
    .a(bitselector_6_out), .b(8'hd0), .eq(comparator_17_eq));  // open: gt, lt
  Comparator #(.mode("unsigned")) comparator_18 (
    .a(bitselector_6_out), .b(8'hf0), .eq(comparator_18_eq));  // open: gt, lt
  Comparator #(.mode("unsigned"), .width(64)) comparator_19 (
    .a(counter_1_q), .b({{8{1'b0}}, multiplexer_27_out[63:8]}), .gt(comparator_19_gt), .eq(comparator_19_eq),
    .lt(comparator_19_lt));
  and and_1 (and_1_out, comparator_6_eq, not_1_out);
  not not_1 (not_1_out, comparator_7_eq);
  // RAM #(.addrWidth(16), .dataWidth(64), .enables("line"), .line("octo"), .misaligned("true")) regX: pin names not known; wires that end beside it: bitselector_1_out, regX_p2, regX_p2, bitselector_5_out[1], bitselector_5_out[2], bitselector_5_out[3], bitselector_5_out[4], bitselector_5_out[5], bitselector_5_out[6], bitselector_5_out[7], regX_p11, regX_p12, regX_p13, regX_p14, regX_p15, regX_p16, regX_p17, regX_p18, regX_p19, regX_p20, regX_p21, regX_p22, regX_p23, regX_p24, regX_p25, regX_p26, regX_p27
  Clock clock_2 (.out(regX_p11));
  or or_1 (or_1_out, comparator_19_gt, comparator_19_eq);
  and and_2 (and_2_out, comparator_19_lt, comparator_3_eq);
  or or_2 (or_2_out, comparator_4_eq, comparator_5_eq, and_1_out);
  or or_3 (regX_p2, comparator_8_eq, comparator_9_eq, comparator_10_eq, comparator_11_eq, comparator_12_eq, comparator_13_eq, comparator_14_eq, comparator_15_eq, comparator_16_eq, comparator_17_eq, comparator_1_eq, alu_1_we);
  BitSelector #(.group(3), .width(64)) bitselector_11 (
    .in({regY_p10, regY_p10_2}), .out(bitselector_11_out), .sel({5{1'b0}}));
  Multiplexer #(.width(64)) multiplexer_1 (
    .in0(multiplexer_2_out), .in1(alu_1_outx), .out(regX_p12), .sel(comparator_2_gt));
  Multiplexer #(.select(4), .width(64)) multiplexer_2 (
    .in4({{32{1'b0}}, bitselector_2_out, bitselector_3_out}), .in5({regY_p10, regY_p10_2}),
    .in6({regY_p10_2, regY_p10_2}),
    .in7({regY_p10_2[15:0], regY_p10_2[15:0], regY_p10_2[15:0], regY_p10_2[15:0]}),
    .in8({regY_p10_2[7:0], regY_p10_2[7:0], regY_p10_2[7:0], regY_p10_2[7:0], regY_p10_2[7:0], regY_p10_2[7:0], regY_p10_2[7:0], regY_p10_2[7:0]}),
    .in9(counter_2_q), .in10(undriven), .in11(multiplexer_3_out), .in12(register_1_q), .in13(counter_3_q),
    .in14(multiplexer_28_out), .out(multiplexer_2_out), .sel(bitselector_8_out));  // open: in0, in1, in2, in3, in15
  not not_2 (not_2_out, comparator_20_eq);
  Comparator #(.width(64)) comparator_20 (.a({64{1'b0}}), .b(regZ_p10), .eq(comparator_20_eq));  // open: gt, lt
  and and_3 (and_3_out, not_2_out, comparator_13_eq);
  Counter #(.max('hffffffffffffffff), .width(64)) counter_2 (
    .load(and_3_out), .D({regY_p10, regY_p10_2}), .Q(counter_2_q), .clk(clock_3_out));  // open: count, carry, up, clr
  Clock clock_3 (.out(clock_3_out));
  // Random #(.seed(12345667), .width(64)) random_1: pin names not known; wires that end beside it: random_1_p1, random_1_p2
  Clock clock_4 (.out(random_1_p1));
  and and_4 (random_1_p2, not_2_out, comparator_14_eq);
  Multiplexer #(.select(3), .width(64)) multiplexer_3 (
    .in0({64{1'b0}}), .in1(64'h1), .in2(64'h65536), .in3(64'h1000000), .in4(64'h200), .in5(64'h200),
    .in6(64'h12a05f200), .in7({64{1'b0}}), .out(multiplexer_3_out), .sel(bitselector_11_out));
  Register #(.width(64)) register_1 (
    .D({regY_p10, regY_p10_2}), .en(and_5_out), .clk(clock_5_out), .Q(register_1_q));  // open: clr
  and and_5 (and_5_out, not_2_out, comparator_16_eq);
  Clock #(.lowDuration(9)) clock_5 (.out(clock_5_out));
  and and_6 (and_6_out, not_2_out, comparator_17_eq);
  Counter #(.max('hffffffffffffffff), .width(64)) counter_3 (
    .load(and_6_out), .D({regY_p10, regY_p10_2}), .Q(counter_3_q), .clk(clock_6_out));  // open: count, carry, up, clr
  Clock #(.lowDuration(9)) clock_6 (.out(clock_6_out));
  alu alu_1 (
    .argX(regX_p20), .argY({regY_p10, regY_p10_2}), .argZ(regZ_p10), .op(bitselector_9_out),
    .\var (bitselector_10_out), .outX(alu_1_outx), .we(alu_1_we));
  Comparator #(.width(64)) comparator_21 (.a({64{1'b0}}), .b(regZ_p11), .eq(comparator_21_eq));  // open: gt, lt
  and and_7 (and_7_out, not_3_out, comparator_13_eq);
  Clock clock_7 (.out(clock_7_out));
  // Random #(.seed(12345668), .width(64)) random_2: pin names not known; wires that end beside it: random_2_p1, random_2_p2
  Clock clock_8 (.out(random_2_p1));
  and and_8 (random_2_p2, not_3_out, comparator_14_eq);
  BitSelector #(.group(3), .width(64)) bitselector_12 (.in(regY_p11), .out(bitselector_12_out), .sel({5{1'b0}}));
  Multiplexer #(.select(3), .width(64)) multiplexer_4 (
    .in0({64{1'b0}}), .in1(64'h1), .in2(64'h65536), .in3(64'h1000000), .in4(64'h200), .in5(64'h200),
    .in6(64'h12a05f200), .in7({64{1'b0}}), .out(multiplexer_4_out), .sel(bitselector_12_out));
  Register #(.width(64)) register_2 (.D(regY_p11), .en(and_9_out), .clk(clock_9_out), .Q(register_2_q));  // open: clr
  and and_9 (and_9_out, not_3_out, comparator_16_eq);
  Clock #(.lowDuration(9)) clock_9 (.out(clock_9_out));
  and and_10 (and_10_out, not_3_out, comparator_17_eq);
  alu alu_2 (
    .argX(regX_p21), .argY(regY_p11), .argZ(regZ_p11), .op(bitselector_9_out), .\var (bitselector_10_out),
    .outX(alu_2_outx));  // open: we
  // DualRAM #(.addrWidth(16), .dataWidth(64), .enables("line"), .line("octo"), .misaligned("true"), .\type ("nonvolatile")) regY: pin names not known; wires that end beside it: bitselector_2_out, bitselector_1_out, regX_p2, regX_p2, bitselector_5_out[1], bitselector_5_out[2], bitselector_5_out[3], bitselector_5_out[4], bitselector_5_out[5], {regY_p10, regY_p10_2}, regY_p11, regY_p12, regY_p13, regY_p14, regY_p15, regY_p16, regY_p17
  Clock clock_10 ();  // open: out
  Multiplexer #(.width(64)) multiplexer_5 (
    .in0(multiplexer_6_out), .in1(alu_2_outx), .out(regX_p13), .sel(comparator_2_gt));
  Multiplexer #(.select(4), .width(64)) multiplexer_6 (
    .in4({{32{1'b0}}, bitselector_2_out, bitselector_3_out}), .in5({regY_p10, regY_p10_2}),
    .in6({regY_p10_2, regY_p10_2}),
    .in7({regY_p10_2[15:0], regY_p10_2[15:0], regY_p10_2[15:0], regY_p10_2[15:0]}),
    .in8({regY_p10_2[7:0], regY_p10_2[7:0], regY_p10_2[7:0], regY_p10_2[7:0], regY_p10_2[7:0], regY_p10_2[7:0], regY_p10_2[7:0], regY_p10_2[7:0]}),
    .in9(counter_4_q), .in10(undriven_2), .in11(multiplexer_4_out), .in12(register_2_q), .in13(counter_5_q),
    .in14(multiplexer_29_out), .out(multiplexer_6_out), .sel(bitselector_8_out));  // open: in0, in1, in2, in3, in15
  not not_3 (not_3_out, comparator_21_eq);
  Counter #(.max('hffffffffffffffff), .width(64)) counter_4 (
    .load(and_7_out), .D(regY_p11), .Q(counter_4_q), .clk(clock_7_out));  // open: count, carry, up, clr
  Counter #(.max('hffffffffffffffff), .width(64)) counter_5 (
    .load(and_10_out), .D(regY_p11), .Q(counter_5_q), .clk(clock_11_out));  // open: count, carry, up, clr
  Clock #(.lowDuration(9)) clock_11 (.out(clock_11_out));
  Multiplexer #(.select(4), .width(64)) multiplexer_7 (
    .in4({{32{1'b0}}, bitselector_2_out, bitselector_3_out}), .in5({regY_p10, regY_p10_2}),
    .in6({regY_p10_2, regY_p10_2}),
    .in7({regY_p10_2[15:0], regY_p10_2[15:0], regY_p10_2[15:0], regY_p10_2[15:0]}),
    .in8({regY_p10_2[7:0], regY_p10_2[7:0], regY_p10_2[7:0], regY_p10_2[7:0], regY_p10_2[7:0], regY_p10_2[7:0], regY_p10_2[7:0], regY_p10_2[7:0]}),
    .in9(counter_6_q), .in10(undriven_3), .in11(multiplexer_8_out), .in12(register_3_q), .in13(counter_7_q),
    .in14(multiplexer_30_out), .out(multiplexer_7_out), .sel(bitselector_8_out));  // open: in0, in1, in2, in3, in15
  not not_4 (not_4_out, comparator_22_eq);
  Comparator #(.width(64)) comparator_22 (.a({64{1'b0}}), .b(regZ_p12), .eq(comparator_22_eq));  // open: gt, lt
  and and_11 (and_11_out, not_4_out, comparator_13_eq);
  Counter #(.max('hffffffffffffffff), .width(64)) counter_6 (
    .load(and_11_out), .D(regY_p12), .Q(counter_6_q), .clk(clock_12_out));  // open: count, carry, up, clr
  Clock clock_12 (.out(clock_12_out));
  // Random #(.seed(12345669), .width(64)) random_3: pin names not known; wires that end beside it: random_3_p1, random_3_p2
  Clock clock_13 (.out(random_3_p1));
  and and_12 (random_3_p2, not_4_out, comparator_14_eq);
  BitSelector #(.group(3), .width(64)) bitselector_13 (.in(regY_p12), .out(bitselector_13_out), .sel({5{1'b0}}));
  Multiplexer #(.select(3), .width(64)) multiplexer_8 (
    .in0({64{1'b0}}), .in1(64'h1), .in2(64'h65536), .in3(64'h1000000), .in4(64'h200), .in5(64'h200),
    .in6(64'h12a05f200), .in7({64{1'b0}}), .out(multiplexer_8_out), .sel(bitselector_13_out));
  Register #(.width(64)) register_3 (.D(regY_p12), .en(and_13_out), .clk(clock_14_out), .Q(register_3_q));  // open: clr
  and and_13 (and_13_out, not_4_out, comparator_16_eq);
  Clock #(.lowDuration(9)) clock_14 (.out(clock_14_out));
  and and_14 (and_14_out, not_4_out, comparator_17_eq);
  Counter #(.max('hffffffffffffffff), .width(64)) counter_7 (
    .load(and_14_out), .D(regY_p12), .Q(counter_7_q), .clk(clock_15_out));  // open: count, carry, up, clr
  Clock #(.lowDuration(9)) clock_15 (.out(clock_15_out));
  alu alu_3 (
    .argX(regX_p22), .argY(regY_p12), .argZ(regZ_p12), .op(bitselector_9_out), .\var (bitselector_10_out),
    .outX(alu_3_outx));  // open: we
  Multiplexer #(.width(64)) multiplexer_9 (
    .in0(multiplexer_7_out), .in1(alu_3_outx), .out(regX_p14), .sel(comparator_2_gt));
  and and_15 (and_15_out, not_5_out, comparator_13_eq);
  and and_16 (and_16_out, not_5_out, comparator_14_eq);
  BitSelector #(.group(3), .width(64)) bitselector_14 (.in(regY_p13), .out(bitselector_14_out), .sel({5{1'b0}}));
  and and_17 (and_17_out, not_5_out, comparator_17_eq);
  alu alu_4 (
    .argX(regX_p23), .argY(regY_p13), .argZ(regZ_p13), .op(bitselector_9_out), .\var (bitselector_10_out),
    .outX(alu_4_outx));  // open: we
  Multiplexer #(.width(64)) multiplexer_10 (
    .in0(multiplexer_11_out), .in1(alu_4_outx), .out(regX_p15), .sel(comparator_2_gt));
  Multiplexer #(.select(4), .width(64)) multiplexer_11 (
    .in4({{32{1'b0}}, bitselector_2_out, bitselector_3_out}), .in5({regY_p10, regY_p10_2}),
    .in6({regY_p10_2, regY_p10_2}),
    .in7({regY_p10_2[15:0], regY_p10_2[15:0], regY_p10_2[15:0], regY_p10_2[15:0]}),
    .in8({regY_p10_2[7:0], regY_p10_2[7:0], regY_p10_2[7:0], regY_p10_2[7:0], regY_p10_2[7:0], regY_p10_2[7:0], regY_p10_2[7:0], regY_p10_2[7:0]}),
    .in9(counter_8_q), .in10(undriven_4), .in11(multiplexer_12_out), .in12(register_4_q), .in13(counter_9_q),
    .in14(multiplexer_31_out), .out(multiplexer_11_out), .sel(bitselector_8_out));  // open: in0, in1, in2, in3, in15
  not not_5 (not_5_out, comparator_23_eq);
  Comparator #(.width(64)) comparator_23 (.a({64{1'b0}}), .b(regZ_p13), .eq(comparator_23_eq));  // open: gt, lt
  Counter #(.max('hffffffffffffffff), .width(64)) counter_8 (
    .load(and_15_out), .D(regY_p13), .Q(counter_8_q), .clk(clock_16_out));  // open: count, carry, up, clr
  Clock clock_16 (.out(clock_16_out));
  // Random #(.seed(12345670), .width(64)) random_4: pin names not known; wires that end beside it: random_4_p1, and_16_out
  Clock clock_17 (.out(random_4_p1));
  Multiplexer #(.select(3), .width(64)) multiplexer_12 (
    .in0({64{1'b0}}), .in1(64'h1), .in2(64'h65536), .in3(64'h1000000), .in4(64'h200), .in5(64'h200),
    .in6(64'h12a05f200), .in7({64{1'b0}}), .out(multiplexer_12_out), .sel(bitselector_14_out));
  Register #(.width(64)) register_4 (.D(regY_p13), .en(and_18_out), .clk(clock_18_out), .Q(register_4_q));  // open: clr
  and and_18 (and_18_out, not_5_out, comparator_16_eq);
  Clock #(.lowDuration(9)) clock_18 (.out(clock_18_out));
  Counter #(.max('hffffffffffffffff), .width(64)) counter_9 (
    .load(and_17_out), .D(regY_p13), .Q(counter_9_q), .clk(clock_19_out));  // open: count, carry, up, clr
  Clock #(.lowDuration(9)) clock_19 (.out(clock_19_out));
  Comparator #(.width(64)) comparator_24 (.a({64{1'b0}}), .b(regZ_p14), .eq(comparator_24_eq));  // open: gt, lt
  and and_19 (and_19_out, not_6_out, comparator_13_eq);
  Clock clock_20 (.out(clock_20_out));
  // Random #(.seed(12345671), .width(64)) random_5: pin names not known; wires that end beside it: random_5_p1, random_5_p2
  Clock clock_21 (.out(random_5_p1));
  and and_20 (random_5_p2, not_6_out, comparator_14_eq);
  BitSelector #(.group(3), .width(64)) bitselector_15 (.in(regY_p14), .out(bitselector_15_out), .sel({5{1'b0}}));
  Multiplexer #(.select(3), .width(64)) multiplexer_13 (
    .in0({64{1'b0}}), .in1(64'h1), .in2(64'h65536), .in3(64'h1000000), .in4(64'h200), .in5(64'h200),
    .in6(64'h12a05f200), .in7({64{1'b0}}), .out(multiplexer_13_out), .sel(bitselector_15_out));
  Register #(.width(64)) register_5 (.D(regY_p14), .en(and_21_out), .clk(clock_22_out), .Q(register_5_q));  // open: clr
  and and_21 (and_21_out, not_6_out, comparator_16_eq);
  Clock #(.lowDuration(9)) clock_22 (.out(clock_22_out));
  and and_22 (and_22_out, not_6_out, comparator_17_eq);
  Clock #(.lowDuration(9)) clock_23 (.out(clock_23_out));
  alu alu_5 (
    .argX(regX_p24), .argY(regY_p14), .argZ(regZ_p14), .op(bitselector_9_out), .\var (bitselector_10_out),
    .outX(alu_5_outx));  // open: we
  // DualRAM #(.addrWidth(16), .dataWidth(64), .enables("line"), .line("octo"), .misaligned("true"), .\type ("nonvolatile")) regZ: pin names not known; wires that end beside it: bitselector_3_out, bitselector_1_out, regX_p2, regX_p2, bitselector_5_out[1], bitselector_5_out[2], bitselector_5_out[3], bitselector_5_out[4], bitselector_5_out[5], regZ_p10, regZ_p11, regZ_p12, regZ_p13, regZ_p14, regZ_p15, regZ_p16, regZ_p17
  Clock clock_24 ();  // open: out
  Multiplexer #(.width(64)) multiplexer_14 (
    .in0(multiplexer_15_out), .in1(alu_5_outx), .out(regX_p16), .sel(comparator_2_gt));
  Multiplexer #(.select(4), .width(64)) multiplexer_15 (
    .in4({{32{1'b0}}, bitselector_2_out, bitselector_3_out}), .in5({regY_p10, regY_p10_2}),
    .in6({regY_p10_2, regY_p10_2}),
    .in7({regY_p10_2[15:0], regY_p10_2[15:0], regY_p10_2[15:0], regY_p10_2[15:0]}),
    .in8({regY_p10_2[7:0], regY_p10_2[7:0], regY_p10_2[7:0], regY_p10_2[7:0], regY_p10_2[7:0], regY_p10_2[7:0], regY_p10_2[7:0], regY_p10_2[7:0]}),
    .in9(counter_10_q), .in10(undriven_5), .in11(multiplexer_13_out), .in12(register_5_q),
    .in13(counter_11_q), .in14(multiplexer_32_out), .out(multiplexer_15_out), .sel(bitselector_8_out));  // open: in0, in1, in2, in3, in15
  not not_6 (not_6_out, comparator_24_eq);
  Counter #(.max('hffffffffffffffff), .width(64)) counter_10 (
    .load(and_19_out), .D(regY_p14), .Q(counter_10_q), .clk(clock_20_out));  // open: count, carry, up, clr
  Counter #(.max('hffffffffffffffff), .width(64)) counter_11 (
    .load(and_22_out), .D(regY_p14), .Q(counter_11_q), .clk(clock_23_out));  // open: count, carry, up, clr
  BitSelector #(.group(3), .width(64)) bitselector_16 (.in(regY_p15), .out(bitselector_16_out), .sel({5{1'b0}}));
  Multiplexer #(.width(64)) multiplexer_16 (
    .in0(multiplexer_17_out), .in1(alu_6_outx), .out(regX_p17), .sel(comparator_2_gt));
  Multiplexer #(.select(4), .width(64)) multiplexer_17 (
    .in4({{32{1'b0}}, bitselector_2_out, bitselector_3_out}), .in5({regY_p10, regY_p10_2}),
    .in6({regY_p10_2, regY_p10_2}),
    .in7({regY_p10_2[15:0], regY_p10_2[15:0], regY_p10_2[15:0], regY_p10_2[15:0]}),
    .in8({regY_p10_2[7:0], regY_p10_2[7:0], regY_p10_2[7:0], regY_p10_2[7:0], regY_p10_2[7:0], regY_p10_2[7:0], regY_p10_2[7:0], regY_p10_2[7:0]}),
    .in9(counter_12_q), .in10(undriven_6), .in11(multiplexer_18_out), .in12(register_6_q),
    .in13(counter_13_q), .in14(multiplexer_33_out), .out(multiplexer_17_out), .sel(bitselector_8_out));  // open: in0, in1, in2, in3, in15
  not not_7 (not_7_out, comparator_25_eq);
  Comparator #(.width(64)) comparator_25 (.a({64{1'b0}}), .b(regZ_p15), .eq(comparator_25_eq));  // open: gt, lt
  and and_23 (and_23_out, not_7_out, comparator_13_eq);
  Counter #(.max('hffffffffffffffff), .width(64)) counter_12 (
    .load(and_23_out), .D(regY_p15), .Q(counter_12_q), .clk(clock_25_out));  // open: count, carry, up, clr
  Clock clock_25 (.out(clock_25_out));
  // Random #(.seed(12345672), .width(64)) random_6: pin names not known; wires that end beside it: random_6_p1, random_6_p2
  Clock clock_26 (.out(random_6_p1));
  and and_24 (random_6_p2, not_7_out, comparator_14_eq);
  Multiplexer #(.select(3), .width(64)) multiplexer_18 (
    .in0({64{1'b0}}), .in1(64'h1), .in2(64'h65536), .in3(64'h1000000), .in4(64'h200), .in5(64'h200),
    .in6(64'h12a05f200), .in7({64{1'b0}}), .out(multiplexer_18_out), .sel(bitselector_16_out));
  Register #(.width(64)) register_6 (.D(regY_p15), .en(and_25_out), .clk(clock_27_out), .Q(register_6_q));  // open: clr
  and and_25 (and_25_out, not_7_out, comparator_16_eq);
  Clock #(.lowDuration(9)) clock_27 (.out(clock_27_out));
  and and_26 (and_26_out, not_7_out, comparator_17_eq);
  Counter #(.max('hffffffffffffffff), .width(64)) counter_13 (
    .load(and_26_out), .D(regY_p15), .Q(counter_13_q), .clk(clock_28_out));  // open: count, carry, up, clr
  Clock #(.lowDuration(9)) clock_28 (.out(clock_28_out));
  alu alu_6 (
    .argX(regX_p25), .argY(regY_p15), .argZ(regZ_p15), .op(bitselector_9_out), .\var (bitselector_10_out),
    .outX(alu_6_outx));  // open: we
  Comparator #(.width(64)) comparator_26 (.a({64{1'b0}}), .b(regZ_p16), .eq(comparator_26_eq));  // open: gt, lt
  and and_27 (and_27_out, not_8_out, comparator_13_eq);
  // Random #(.seed(12345673), .width(64)) random_7: pin names not known; wires that end beside it: random_7_p1, random_7_p2
  and and_28 (random_7_p2, not_8_out, comparator_14_eq);
  BitSelector #(.group(3), .width(64)) bitselector_17 (.in(regY_p16), .out(bitselector_17_out), .sel({5{1'b0}}));
  Register #(.width(64)) register_7 (.D(regY_p16), .en(and_29_out), .clk(clock_29_out), .Q(register_7_q));  // open: clr
  and and_29 (and_29_out, not_8_out, comparator_16_eq);
  Clock #(.lowDuration(9)) clock_29 (.out(clock_29_out));
  and and_30 (and_30_out, not_8_out, comparator_17_eq);
  alu alu_7 (
    .argX(regX_p26), .argY(regY_p16), .argZ(regZ_p16), .op(bitselector_9_out), .\var (bitselector_10_out),
    .outX(alu_7_outx));  // open: we
  Multiplexer #(.width(64)) multiplexer_19 (
    .in0(multiplexer_20_out), .in1(alu_7_outx), .out(regX_p18), .sel(comparator_2_gt));
  Multiplexer #(.select(4), .width(64)) multiplexer_20 (
    .in4({{32{1'b0}}, bitselector_2_out, bitselector_3_out}), .in5({regY_p10, regY_p10_2}),
    .in6({regY_p10_2, regY_p10_2}),
    .in7({regY_p10_2[15:0], regY_p10_2[15:0], regY_p10_2[15:0], regY_p10_2[15:0]}),
    .in8({regY_p10_2[7:0], regY_p10_2[7:0], regY_p10_2[7:0], regY_p10_2[7:0], regY_p10_2[7:0], regY_p10_2[7:0], regY_p10_2[7:0], regY_p10_2[7:0]}),
    .in9(counter_14_q), .in10(undriven_7), .in11(multiplexer_21_out), .in12(register_7_q),
    .in13(counter_15_q), .in14(multiplexer_34_out), .out(multiplexer_20_out), .sel(bitselector_8_out));  // open: in0, in1, in2, in3, in15
  not not_8 (not_8_out, comparator_26_eq);
  Counter #(.max('hffffffffffffffff), .width(64)) counter_14 (
    .load(and_27_out), .D(regY_p16), .Q(counter_14_q), .clk(clock_30_out));  // open: count, carry, up, clr
  Clock clock_30 (.out(clock_30_out));
  Clock clock_31 (.out(random_7_p1));
  Multiplexer #(.select(3), .width(64)) multiplexer_21 (
    .in0({64{1'b0}}), .in1(64'h1), .in2(64'h65536), .in3(64'h1000000), .in4(64'h200), .in5(64'h200),
    .in6(64'h12a05f200), .in7({64{1'b0}}), .out(multiplexer_21_out), .sel(bitselector_17_out));
  Counter #(.max('hffffffffffffffff), .width(64)) counter_15 (
    .load(and_30_out), .D(regY_p16), .Q(counter_15_q), .clk(clock_32_out));  // open: count, carry, up, clr
  Clock #(.lowDuration(9)) clock_32 (.out(clock_32_out));
  not not_9 (not_9_out, comparator_27_eq);
  Comparator #(.width(64)) comparator_27 (.a({64{1'b0}}), .b(regZ_p17), .eq(comparator_27_eq));  // open: gt, lt
  and and_31 (and_31_out, not_9_out, comparator_13_eq);
  Counter #(.max('hffffffffffffffff), .width(64)) counter_16 (
    .load(and_31_out), .D(regY_p17), .Q(counter_16_q), .clk(clock_33_out));  // open: count, carry, up, clr
  Clock clock_33 (.out(clock_33_out));
  // Random #(.seed(12345674), .width(64)) random_8: pin names not known; wires that end beside it: random_8_p1, random_8_p2
  Clock clock_34 (.out(random_8_p1));
  and and_32 (random_8_p2, not_9_out, comparator_14_eq);
  BitSelector #(.group(3), .width(64)) bitselector_18 (.in(regY_p17), .out(bitselector_18_out), .sel({5{1'b0}}));
  Multiplexer #(.select(3), .width(64)) multiplexer_22 (
    .in0({64{1'b0}}), .in1(64'h1), .in2(64'h65536), .in3(64'h1000000), .in4(64'h200), .in5(64'h200),
    .in6(64'h12a05f200), .in7({64{1'b0}}), .out(multiplexer_22_out), .sel(bitselector_18_out));
  Register #(.width(64)) register_8 (.D(regY_p17), .en(and_33_out), .clk(clock_35_out), .Q(register_8_q));  // open: clr
  and and_33 (and_33_out, not_9_out, comparator_16_eq);
  Clock #(.lowDuration(9)) clock_35 (.out(clock_35_out));
  and and_34 (and_34_out, not_9_out, comparator_17_eq);
  Clock #(.lowDuration(9)) clock_36 (.out(clock_36_out));
  alu alu_8 (
    .argX(regX_p27), .argY(regY_p17), .argZ(regZ_p17), .op(bitselector_9_out), .\var (bitselector_10_out),
    .outX(alu_8_outx));  // open: we
  Multiplexer #(.width(64)) multiplexer_23 (
    .in0(multiplexer_24_out), .in1(alu_8_outx), .out(regX_p19), .sel(comparator_2_gt));
  Multiplexer #(.select(4), .width(64)) multiplexer_24 (
    .in4({{32{1'b0}}, bitselector_2_out, bitselector_3_out}), .in5({regY_p10, regY_p10_2}),
    .in6({regY_p10_2, regY_p10_2}),
    .in7({regY_p10_2[15:0], regY_p10_2[15:0], regY_p10_2[15:0], regY_p10_2[15:0]}),
    .in8({regY_p10_2[7:0], regY_p10_2[7:0], regY_p10_2[7:0], regY_p10_2[7:0], regY_p10_2[7:0], regY_p10_2[7:0], regY_p10_2[7:0], regY_p10_2[7:0]}),
    .in9(counter_16_q), .in10(undriven_8), .in11(multiplexer_22_out), .in12(register_8_q),
    .in13(counter_17_q), .in14(multiplexer_35_out), .out(multiplexer_24_out), .sel(bitselector_8_out));  // open: in0, in1, in2, in3, in15
  Counter #(.max('hffffffffffffffff), .width(64)) counter_17 (
    .load(and_34_out), .D(regY_p17), .Q(counter_17_q), .clk(clock_36_out));  // open: count, carry, up, clr
  BitSelector #(.group(16), .width(64)) bitselector_19 (.in(regX_p20), .out(bitselector_19_out), .sel(2'b00));
  BitSelector #(.group(16), .width(64)) bitselector_20 (.in(regX_p20), .out(bitselector_20_out), .sel(2'b01));
  BitSelector #(.group(8), .width(16)) bitselector_21 (.in(bitselector_19_out), .out(bitselector_21_out), .sel(1'b0));
  BitSelector #(.group(16), .width(64)) bitselector_22 (.in(regX_p20), .out(bitselector_22_out), .sel(2'b10));
  BitSelector #(.group(8), .width(16)) bitselector_23 (.in(bitselector_20_out), .out(bitselector_23_out), .sel(1'b0));
  Multiplexer #(.width(64)) multiplexer_25 (
    .in0(regX_p20), .in1({{8{1'b0}}, multiplexer_27_out[63:8]}), .out(multiplexer_25_out),
    .sel(comparator_4_eq));
  BitSelector #(.group(16), .width(64)) bitselector_24 (.in(regX_p20), .sel(2'b11));  // open: out
  BitSelector #(.group(8), .width(16)) bitselector_25 (.in(bitselector_22_out), .out(bitselector_25_out), .sel(1'b0));
  Register #(.trigger("falling"), .width(1)) register_9 (
    .D(1'b1), .en(not_10_out), .Q(register_9_q), .clk(clock_37_out));  // open: clr
  Clock clock_37 (.out(clock_37_out));
  BitSelector #(.group(2), .width(64)) bitselector_26 (
    .in({regY_p10, regY_p10_2}), .out(bitselector_26_out), .sel({5{1'b1}}));
  BitSelector #(.group(9), .width(64)) bitselector_27 (
    .in({regY_p10, regY_p10_2}), .out(bitselector_27_out), .sel(3'b001));
  BitSelector #(.group(18), .width(64)) bitselector_28 (
    .in({regY_p10, regY_p10_2}), .out(bitselector_28_out), .sel(2'b00));
  Multiplexer #(.width(64)) multiplexer_26 (
    .in0(64'hc000000000000000), .in1(multiplexer_25_out), .out(multiplexer_26_out), .sel(register_9_q));
  or or_4 (or_4_out, or_2_out, not_10_out);
  not not_10 (not_10_out, register_9_q);
  and and_35 (and_35_out, comparator_18_eq, comparator_28_gt);
  Comparator #(.mode("unsigned"), .width(2)) comparator_28 (
    .a(bitselector_26_out), .b(2'b01), .gt(comparator_28_gt), .eq(comparator_28_eq), .lt(comparator_28_lt));
  BitSelector #(.group(9), .width(64)) bitselector_29 (
    .in({regY_p10, regY_p10_2}), .out(bitselector_29_out), .sel(3'b000));
  not not_11 (not_11_out, and_2_out);
  Clock clock_38 (.out(clock_38_out));
  not not_12 (not_12_out, comparator_28_lt);
  // RGB_Video #(.cursor("No Cursor"), .height(512), .scale(1), .width(512)) rgb_video_1: pin names not known; wires that end beside it: rgb_video_1_p1, and_35_out, bitselector_27_out, bitselector_29_out, {bitselector_21_out, bitselector_23_out, bitselector_25_out}
  Clock clock_39 (.out(rgb_video_1_p1));
  BitSelector #(.group(24), .width(64)) bitselector_30 (.in(counter_18_q), .out(bitselector_30_out), .sel(2'b00));
  Counter #(.max('hffffffffffffffff), .trigger("falling"), .width(64)) counter_18 (
    .load(or_4_out), .D(multiplexer_26_out), .count(not_11_out), .Q(counter_18_q), .clk(clock_38_out));  // open: carry, up, clr
  and and_36 (and_36_out, comparator_28_lt, comparator_18_eq);
  and and_37 (and_37_out, comparator_28_eq, comparator_18_eq);
  RAM #(.addrWidth(18), .dataWidth(64), .enables("line")) disp1 (
    .addr(bitselector_28_out), .we(and_35_out), .clk(clock_40_out), .din(regX_p20));  // open: dout
  Clock clock_40 (.out(clock_40_out));
  BitSelector #(.group(2), .width(64)) bitselector_31 (.in(counter_18_q), .out(bitselector_31_out), .sel({5{1'b1}}));
  // DualRAM #(.addrWidth(24), .dataWidth(64), .enables("line"), .line("octo"), .misaligned("true"), .\type ("nonvolatile")) ram1: pin names not known; wires that end beside it: bitselector_30_out, ram1_p2, ram1_p3
  BitSelector #(.group(24), .width(64)) bitselector_32 (.in({regY_p10, regY_p10_2}), .out(ram1_p2), .sel(2'b00));
  Clock clock_41 (.out(clock_41_out));
  BitSelector #(.group(24), .width(64)) bitselector_33 (
    .in({regY_p10, regY_p10_2}), .out(bitselector_33_out), .sel(2'b00));
  // RAM #(.addrWidth(24), .dataWidth(64), .enables("line"), .line("octo"), .misaligned("true")) cart1: pin names not known; wires that end beside it: and_36_out, and_36_out, bitselector_5_out[1], bitselector_5_out[2], bitselector_5_out[3], bitselector_5_out[4], bitselector_5_out[5], bitselector_5_out[6], bitselector_5_out[7], clock_41_out, regX_p20, regX_p21, regX_p22, regX_p23, regX_p24, regX_p25, regX_p26, regX_p27, bitselector_33_out, and_37_out, and_37_out, bitselector_5_out[1], bitselector_5_out[2], bitselector_5_out[3], bitselector_5_out[4], bitselector_5_out[5], bitselector_5_out[6], bitselector_5_out[7], cart1_p29, regX_p20, cart1_p31, cart1_p32, cart1_p33, cart1_p34, cart1_p35, cart1_p36, cart1_p37, cart1_p38, cart1_p39
  Clock clock_42 (.out(cart1_p29));
  // ROM #(.addrWidth(24), .dataWidth(64), .line("octo"), .misaligned("true")) rom1: pin names not known; wires that end beside it: regX_p21, regX_p22, regX_p23, regX_p24, regX_p25, regX_p26, regX_p27, bitselector_30_out, rom1_p9, rom1_p10, rom1_p11, rom1_p12, rom1_p13, rom1_p14, rom1_p15, rom1_p16
  Comparator #(.mode("unsigned"), .width(2)) comparator_29 (
    .a(bitselector_31_out), .b(2'b11), .eq(comparator_29_eq));  // open: gt, lt
  Multiplexer #(.width(64)) multiplexer_27 (
    .in0(ram1_p3), .in1(rom1_p16), .out(multiplexer_27_out), .sel(comparator_29_eq));
  Multiplexer #(.width(64)) multiplexer_28 (
    .in0(cart1_p31), .in1(cart1_p39), .out(multiplexer_28_out), .sel(not_12_out));
  Multiplexer #(.width(64)) multiplexer_29 (.in0(cart1_p32), .in1(rom1_p9), .out(multiplexer_29_out), .sel(not_12_out));
  Multiplexer #(.width(64)) multiplexer_30 (
    .in0(cart1_p33), .in1(rom1_p10), .out(multiplexer_30_out), .sel(not_12_out));
  Multiplexer #(.width(64)) multiplexer_31 (
    .in0(cart1_p34), .in1(rom1_p11), .out(multiplexer_31_out), .sel(not_12_out));
  Multiplexer #(.width(64)) multiplexer_32 (
    .in0(cart1_p35), .in1(rom1_p12), .out(multiplexer_32_out), .sel(not_12_out));
  Multiplexer #(.width(64)) multiplexer_33 (
    .in0(cart1_p36), .in1(rom1_p13), .out(multiplexer_33_out), .sel(not_12_out));
  Multiplexer #(.width(64)) multiplexer_34 (
    .in0(cart1_p37), .in1(rom1_p14), .out(multiplexer_34_out), .sel(not_12_out));
  Multiplexer #(.width(64)) multiplexer_35 (
    .in0(cart1_p38), .in1(rom1_p15), .out(multiplexer_35_out), .sel(not_12_out));

  // Notes on the sheet:
  //   contents of rom1 (hex, n*v repeats v):
  //   a000000110040 b000000000040 d000000010040 400000000040 2000000200040 3000000080340 5000000080040
  //   6c00000000040 6000600020084 60006000a0024 20084 70000000000e0 70007000500c4 c000700000001
  //   b000c00000030 7000d00070084 1000000030007 1000100030007 4000400030007 1000010000ffe0 1000040000fff0
  //   8000400070047 9000800000041 6000900000030 b000000000020
endmodule
module alu (
  input  [63:0] argX,
  input  [63:0] argY,
  input  [63:0] argZ,
  input  [3:0] op,
  input  [3:0] \var ,
  output [63:0] outX,
  output we
);

  wire adder_1_cout, adder_2_cout, adder_3_cout, adder_4_cout, adder_5_cout, adder_6_cout, adder_7_cout,
       adder_8_cout, adder_9_cout, adder_10_cout, adder_11_cout, adder_12_cout, adder_13_cout, adder_14_cout,
       adder_15_cout, bitfinder_1_found, bitfinder_2_found, bitfinder_3_found, bitfinder_4_found,
       bitfinder_5_found, bitfinder_6_found, bitfinder_7_found, bitfinder_8_found, bitfinder_9_found,
       bitfinder_10_found, bitfinder_11_found, bitfinder_12_found, bitfinder_13_found, bitfinder_14_found,
       bitfinder_15_found, bitfinder_16_found, bitfinder_17_found, bitfinder_18_found, bitfinder_19_found,
       bitfinder_20_found, bitfinder_21_found, bitfinder_22_found, bitfinder_23_found, bitfinder_24_found,
       bitfinder_25_found, bitfinder_26_found, bitfinder_27_found, bitfinder_28_found, bitfinder_29_found,
       bitfinder_30_found, bitfinder_31_found, bitfinder_32_found, bitfinder_33_found, bitfinder_34_found,
       bitfinder_35_found, bitfinder_36_found, bitfinder_37_found, bitfinder_38_found, bitfinder_39_found,
       bitfinder_40_found, bitfinder_41_found, bitfinder_42_found, bitfinder_43_found, bitfinder_44_found,
       bitfinder_45_found, bitfinder_46_found, bitfinder_47_found, bitfinder_48_found, bitfinder_49_found,
       bitfinder_50_found, bitfinder_51_found, bitfinder_52_found, bitfinder_53_found, bitfinder_54_found,
       bitfinder_55_found, bitfinder_56_found, bitfinder_57_found, bitfinder_58_found, bitfinder_59_found,
       bitfinder_60_found, comparator_1_eq, comparator_2_eq, comparator_3_eq, comparator_4_eq,
       comparator_5_eq, comparator_6_eq, comparator_7_eq, comparator_8_eq, comparator_9_eq, comparator_9_lt,
       comparator_10_eq, comparator_10_lt, comparator_11_eq, comparator_12_eq, comparator_12_lt,
       comparator_13_eq, comparator_13_lt, comparator_14_eq, comparator_14_lt, comparator_15_eq,
       comparator_15_lt, comparator_16_eq, comparator_17_eq, comparator_18_eq, comparator_18_lt,
       comparator_19_eq, comparator_19_lt, comparator_20_eq, comparator_20_lt, comparator_21_eq,
       comparator_21_lt, comparator_22_eq, comparator_23_eq, comparator_24_eq, comparator_25_eq,
       comparator_26_eq, comparator_26_lt, comparator_27_eq, comparator_27_lt, comparator_28_eq,
       comparator_28_lt, comparator_29_eq, comparator_29_lt, comparator_30_eq, comparator_31_eq,
       comparator_32_eq, comparator_33_eq, comparator_34_eq, comparator_35_eq, comparator_36_eq,
       comparator_37_eq, comparator_38_eq, comparator_38_lt, comparator_39_eq, comparator_39_lt,
       comparator_40_eq, comparator_40_lt, comparator_41_eq, comparator_41_lt, comparator_42_eq,
       comparator_42_lt, comparator_43_eq, comparator_43_lt, comparator_44_eq, comparator_44_lt,
       comparator_45_eq, comparator_45_lt, comparator_46_eq, comparator_46_lt, comparator_47_eq,
       comparator_47_lt, comparator_48_eq, comparator_48_lt, comparator_49_eq, comparator_49_lt,
       comparator_50_eq, comparator_50_lt, comparator_51_eq, comparator_51_lt, comparator_52_eq,
       comparator_52_lt, comparator_53_eq, comparator_53_lt, comparator_54_eq, comparator_55_eq,
       comparator_56_eq, comparator_57_eq, comparator_58_eq, comparator_59_eq, comparator_60_eq,
       fpclassificator_1_p2, fpclassificator_1_p3, fpclassificator_2_p2, fpclassificator_2_p3,
       fpclassificator_3_p2, fpclassificator_3_p3, fpclassificator_4_p2, fpclassificator_4_p3,
       fpclassificator_5_p2, fpclassificator_5_p3, fpclassificator_6_p2, fpclassificator_6_p3,
       fpclassificator_7_p2, fpclassificator_7_p3, fpclassificator_8_p2, fpclassificator_8_p3,
       fpclassificator_9_p2, fpclassificator_9_p3, fpclassificator_10_p2, fpclassificator_10_p3,
       fpclassificator_11_p2, fpclassificator_11_p3, fpclassificator_12_p2, fpclassificator_12_p3,
       fpclassificator_13_p2, fpclassificator_13_p3, fpclassificator_14_p2, fpclassificator_14_p3,
       fpclassificator_15_p2, fpclassificator_15_p3, fpcomparator_1_p3, fpcomparator_1_p4, fpcomparator_2_p3,
       fpcomparator_2_p4, fpcomparator_3_p3, fpcomparator_3_p4, fpcomparator_4_p3, fpcomparator_4_p4,
       fpcomparator_5_p3, fpcomparator_5_p4, fpcomparator_6_p3, fpcomparator_6_p4, fpcomparator_7_p3,
       fpcomparator_7_p4, fpcomparator_8_p3, fpcomparator_8_p4, fpcomparator_9_p3, fpcomparator_9_p4,
       fpcomparator_10_p3, fpcomparator_10_p4, fpcomparator_11_p3, fpcomparator_11_p4, fpcomparator_12_p3,
       fpcomparator_12_p4, fpcomparator_13_p3, fpcomparator_13_p4, fpcomparator_14_p3, fpcomparator_14_p4,
       fpcomparator_15_p3, fpcomparator_15_p4, fpcomparator_16_p3, fpcomparator_16_p4, fpcomparator_17_p3,
       fpcomparator_17_p4, fpcomparator_18_p3, fpcomparator_18_p4, fpcomparator_19_p3, fpcomparator_19_p4,
       fpcomparator_20_p3, fpcomparator_20_p4, fpcomparator_21_p3, fpcomparator_21_p4, fpcomparator_22_p3,
       fpcomparator_22_p4, fpcomparator_23_p3, fpcomparator_23_p4, fpcomparator_24_p3, fpcomparator_24_p4,
       fpcomparator_25_p3, fpcomparator_25_p4, fpcomparator_26_p3, fpcomparator_26_p4, fpcomparator_27_p3,
       fpcomparator_27_p4, fpcomparator_28_p3, fpcomparator_28_p4, fpcomparator_29_p3, fpcomparator_29_p4,
       fpcomparator_30_p3, fpcomparator_30_p4, not_2_out, not_3_out, not_4_out, not_5_out, not_6_out,
       not_7_out, not_8_out, not_9_out, not_10_out, not_11_out, not_12_out, not_13_out, not_14_out,
       not_15_out, not_16_out, subtractor_1_bout, subtractor_2_bout, subtractor_3_bout, subtractor_4_bout,
       subtractor_5_bout, subtractor_6_bout, subtractor_7_bout, subtractor_8_bout, subtractor_9_bout,
       subtractor_10_bout, subtractor_11_bout, subtractor_12_bout, subtractor_13_bout, subtractor_14_bout,
       subtractor_15_bout;
  wire [2:0] bitfinder_29_index, bitfinder_30_index, bitfinder_31_index, bitfinder_32_index,
       bitfinder_33_index, bitfinder_34_index, bitfinder_35_index, bitfinder_36_index, bitfinder_37_index,
       bitfinder_38_index, bitfinder_39_index, bitfinder_40_index, bitfinder_41_index, bitfinder_42_index,
       bitfinder_43_index, bitfinder_44_index, bitfinder_45_index, bitfinder_46_index, bitfinder_47_index,
       bitfinder_48_index, bitfinder_49_index, bitfinder_50_index, bitfinder_51_index, bitfinder_52_index,
       bitfinder_53_index, bitfinder_54_index, bitfinder_55_index, bitfinder_56_index, bitfinder_57_index,
       bitfinder_58_index, bitfinder_59_index, bitfinder_60_index, bitselector_15_out, bitselector_16_out,
       bitselector_17_out, bitselector_18_out, bitselector_19_out, bitselector_20_out, bitselector_21_out,
       bitselector_22_out, bitselector_23_out, bitselector_24_out, bitselector_25_out, bitselector_26_out,
       bitselector_27_out, bitselector_28_out, bitselector_29_out, bitselector_30_out;
  wire [3:0] bitadder_8_out, bitadder_9_out, bitadder_10_out, bitadder_11_out, bitadder_12_out,
       bitadder_13_out, bitadder_14_out, bitadder_15_out, bitfinder_13_index, bitfinder_14_index,
       bitfinder_15_index, bitfinder_16_index, bitfinder_17_index, bitfinder_18_index, bitfinder_19_index,
       bitfinder_20_index, bitfinder_21_index, bitfinder_22_index, bitfinder_23_index, bitfinder_24_index,
       bitfinder_25_index, bitfinder_26_index, bitfinder_27_index, bitfinder_28_index, bitselector_7_out,
       bitselector_8_out, bitselector_9_out, bitselector_10_out, bitselector_11_out, bitselector_12_out,
       bitselector_13_out, bitselector_14_out;
  wire [4:0] bitadder_4_out, bitadder_5_out, bitadder_6_out, bitadder_7_out, bitfinder_5_index,
       bitfinder_6_index, bitfinder_7_index, bitfinder_8_index, bitfinder_9_index, bitfinder_10_index,
       bitfinder_11_index, bitfinder_12_index, bitselector_3_out, bitselector_4_out, bitselector_5_out,
       bitselector_6_out;
  wire [5:0] bitadder_2_out, bitadder_3_out, bitfinder_1_index, bitfinder_2_index, bitfinder_3_index,
       bitfinder_4_index, bitselector_1_out, bitselector_2_out;
  wire [6:0] bitadder_1_out;
  wire [7:0] bit_extender_104_out, bit_extender_105_out, bit_extender_106_out, bit_extender_107_out,
       bit_extender_108_out, bit_extender_109_out, bit_extender_110_out, bit_extender_111_out,
       bit_extender_112_out, bit_extender_113_out, bit_extender_114_out, bit_extender_115_out,
       bit_extender_116_out, bit_extender_117_out, bit_extender_118_out, bit_extender_119_out,
       bit_extender_120_out, bit_extender_121_out, bit_extender_122_out, bit_extender_123_out,
       bit_extender_124_out, bit_extender_125_out, bit_extender_126_out, bit_extender_127_out,
       bit_extender_128_out, bit_extender_129_out, bit_extender_130_out, bit_extender_131_out,
       bit_extender_132_out, bit_extender_133_out, bit_extender_134_out, bit_extender_135_out, buffer_9_out,
       buffer_10_out, buffer_11_out, buffer_12_out, buffer_13_out, buffer_14_out, buffer_15_out,
       buffer_16_out;
  wire [15:0] bit_extender_48_out, bit_extender_49_out, bit_extender_50_out, bit_extender_51_out,
       bit_extender_52_out, bit_extender_53_out, bit_extender_54_out, bit_extender_55_out,
       bit_extender_80_out, bit_extender_81_out, bit_extender_82_out, bit_extender_83_out,
       bit_extender_84_out, bit_extender_85_out, bit_extender_86_out, bit_extender_87_out, buffer_5_out,
       buffer_6_out, buffer_7_out, buffer_8_out;
  wire [31:0] bit_extender_18_out, bit_extender_19_out, bit_extender_22_out, bit_extender_23_out,
       bit_extender_32_out, bit_extender_33_out, bit_extender_38_out, bit_extender_39_out, buffer_3_out,
       buffer_4_out;
  wire [63:0] adder_1_out, adder_3_out, adder_7_out, adder_15_out, and_1_out, bit_extender_1_out,
       bit_extender_2_out, bit_extender_3_out, bit_extender_4_out, bit_extender_5_out, bit_extender_6_out,
       bit_extender_7_out, bit_extender_8_out, bit_extender_9_out, bit_extender_12_out, bit_extender_13_out,
       bit_extender_15_out, bit_extender_17_out, bit_extender_21_out, bit_extender_30_out,
       bit_extender_31_out, bit_extender_37_out, bit_extender_43_out, bit_extender_47_out,
       bit_extender_63_out, bit_extender_78_out, bit_extender_79_out, bit_extender_95_out,
       bit_extender_103_out, bit_extender_136_out, bit_extender_137_out, bit_extender_139_out, buffer_1_out,
       buffer_2_out, divider_1_out, divider_1_rem, divider_3_out, divider_3_rem, divider_7_out,
       divider_7_rem, divider_15_out, divider_15_rem, fgam_1_outval, fpabsolute_1_p1, fpabsolute_3_p2,
       fpabsolute_7_p2, fpabsolute_15_p2, fpadder_1_out, fpadder_3_out, fpadder_7_out, fpadder_15_out,
       fpdivider_1_out, fpdivider_3_out, fpdivider_7_out, fpdivider_15_out, fpexponentiator_1_p1,
       fpexponentiator_2_p1, fpexponentiator_4_p2, fpexponentiator_6_p3, fpexponentiator_10_p2,
       fpexponentiator_14_p3, fpexponentiator_22_p2, fpexponentiator_30_p3, fplogarithm_1_p2,
       fplogarithm_2_p1, fplogarithm_4_p2, fplogarithm_6_p3, fplogarithm_10_p2, fplogarithm_14_p3,
       fplogarithm_22_p2, fplogarithm_30_p3, fpminmax_1_p3, fpminmax_2_p3, fpminmax_4_p3, fpminmax_6_p3,
       fpminmax_10_p3, fpminmax_14_p3, fpminmax_22_p3, fpminmax_30_p3, fpmultiplier_1_out,
       fpmultiplier_3_out, fpmultiplier_7_out, fpmultiplier_15_out, fpnegator_1_p2, fpnegator_3_p2,
       fpnegator_7_p2, fpnegator_15_p2, fpsquareroot_1_p1, fpsquareroot_3_p2, fpsquareroot_7_p2,
       fpsquareroot_15_p2, fpsubtractor_1_out, fpsubtractor_3_out, fpsubtractor_7_out, fpsubtractor_15_out,
       fptofp_4_p1, fptofp_12_p1, fptofp_31_p1, fptofp_36_p2, fptofp_37_p2, fptofp_39_p2, fptoint_1_p2,
       fptoint_2_p1, fptoint_3_p1, fptoint_4_p1, fptoint_6_p2, fptoint_8_p2, fptoint_10_p2, fptoint_12_p2,
       fptoint_16_p2, fptoint_20_p2, fptoint_24_p2, fptoint_28_p2, fptoint_36_p2, fptoint_44_p2,
       fptoint_52_p2, fptoint_60_p2, fptrigonometry_1_p2, fptrigonometry_1_p3, fptrigonometry_1_p4,
       fptrigonometry_2_p2, fptrigonometry_2_p3, fptrigonometry_2_p4, fptrigonometry_4_p2,
       fptrigonometry_4_p3, fptrigonometry_4_p4, fptrigonometry_6_p2, fptrigonometry_6_p3,
       fptrigonometry_6_p4, fptrigonometry_10_p2, fptrigonometry_10_p3, fptrigonometry_10_p4,
       fptrigonometry_14_p2, fptrigonometry_14_p3, fptrigonometry_14_p4, fptrigonometry_22_p2,
       fptrigonometry_22_p3, fptrigonometry_22_p4, fptrigonometry_30_p2, fptrigonometry_30_p3,
       fptrigonometry_30_p4, inttofp_1_p2, inttofp_3_p2, inttofp_7_p2, inttofp_15_p2, multiplexer_2_out,
       multiplexer_3_out, multiplexer_4_out, multiplexer_5_out, multiplexer_6_out, multiplexer_7_out,
       multiplexer_8_out, multiplexer_9_out, multiplexer_10_out, multiplexer_11_out, multiplexer_12_out,
       multiplexer_13_out, multiplexer_14_out, multiplexer_15_out, multiplexer_16_out, multiplexer_17_out,
       multiplexer_18_out, multiplexer_19_out, multiplexer_20_out, multiplexer_22_out, multiplexer_26_out,
       multiplexer_27_out, multiplexer_28_out, multiplexer_29_out, multiplexer_31_out, multiplexer_32_out,
       multiplexer_34_out, multiplexer_37_out, multiplexer_39_out, multiplexer_40_out, multiplexer_45_out,
       multiplexer_51_out, multiplexer_53_out, multiplexer_54_out, multiplexer_58_out, multiplexer_63_out,
       multiplexer_64_out, multiplexer_67_out, multiplexer_69_out, multiplexer_72_out, multiplexer_78_out,
       multiplexer_80_out, multiplexer_87_out, multiplexer_94_out, multiplexer_99_out, multiplexer_105_out,
       multiplexer_112_out, multiplexer_117_out, multiplexer_123_out, multiplexer_128_out,
       multiplexer_135_out, multiplexer_142_out, multiplexer_153_out, multiplexer_158_out,
       multiplexer_172_out, multiplexer_176_out, multiplexer_189_out, multiplexer_190_out,
       multiplexer_196_out, multiplexer_204_out, multiplexer_205_out, multiplexer_206_out,
       multiplexer_207_out, multiplexer_208_out, multiplexer_209_out, multiplexer_210_out,
       multiplexer_211_out, multiplier_1_cout, multiplier_1_out, multiplier_3_cout, multiplier_3_out,
       multiplier_7_cout, multiplier_7_out, multiplier_15_cout, multiplier_15_out, nand_1_out, negator_1_out,
       negator_3_out, negator_7_out, negator_15_out, nor_1_out, not_1_out, or_2_out, shifter_1_out,
       shifter_2_out, shifter_3_out, shifter_4_out, shifter_5_out, shifter_7_out, shifter_9_out,
       shifter_11_out, shifter_13_out, shifter_15_out, shifter_19_out, shifter_23_out, shifter_27_out,
       shifter_31_out, shifter_35_out, shifter_43_out, shifter_51_out, shifter_59_out, shifter_67_out,
       shifter_75_out, subtractor_1_out, subtractor_3_out, subtractor_7_out, subtractor_15_out, xnor_1_out,
       xor_1_out;
  wire [63:8] fptofp_32_p2;
  wire [63:16] fptofp_22_p2;
  wire [63:32] fptofp_21_p2;

  or or_1 (we, comparator_1_eq, comparator_2_eq, comparator_3_eq, comparator_4_eq, comparator_5_eq, comparator_6_eq, comparator_7_eq, comparator_8_eq, comparator_54_eq, comparator_55_eq, comparator_56_eq, comparator_57_eq, comparator_58_eq, comparator_59_eq, comparator_60_eq);
  Multiplexer #(.select(4), .width(64)) multiplexer_1 (
    .in1(multiplexer_2_out), .in2(multiplexer_3_out), .in3(multiplexer_4_out), .in4(multiplexer_5_out),
    .in5(multiplexer_6_out), .in6(multiplexer_7_out), .in7(multiplexer_8_out), .in8(multiplexer_9_out),
    .in9(multiplexer_205_out), .in10(multiplexer_206_out), .in11(multiplexer_207_out),
    .in12(multiplexer_208_out), .in13(multiplexer_209_out), .in14(multiplexer_210_out),
    .in15(multiplexer_211_out), .out(outX), .sel(op));  // open: in0
  Comparator #(.mode("unsigned"), .width(4)) comparator_1 (.a(op), .b(4'b0001), .eq(comparator_1_eq));  // open: gt, lt
  Comparator #(.mode("unsigned"), .width(4)) comparator_2 (.a(op), .b(4'b0010), .eq(comparator_2_eq));  // open: gt, lt
  Comparator #(.mode("unsigned"), .width(4)) comparator_3 (.a(op), .b(4'b0011), .eq(comparator_3_eq));  // open: gt, lt
  Comparator #(.mode("unsigned"), .width(4)) comparator_4 (.a(op), .b(4'b0100), .eq(comparator_4_eq));  // open: gt, lt
  Comparator #(.mode("unsigned"), .width(4)) comparator_5 (.a(op), .b(4'b0101), .eq(comparator_5_eq));  // open: gt, lt
  Comparator #(.mode("unsigned"), .width(4)) comparator_6 (.a(op), .b(4'b0110), .eq(comparator_6_eq));  // open: gt, lt
  Comparator #(.mode("unsigned"), .width(4)) comparator_7 (.a(op), .b(4'b0111), .eq(comparator_7_eq));  // open: gt, lt
  Comparator #(.mode("unsigned"), .width(4)) comparator_8 (.a(op), .b(4'b1000), .eq(comparator_8_eq));  // open: gt, lt
  Multiplexer #(.select(4), .width(64)) multiplexer_2 (
    .in0(multiplexer_10_out), .in1(multiplexer_22_out), .in2(multiplexer_54_out), .in3(multiplexer_112_out),
    .in4(multiplexer_13_out), .in5(multiplexer_29_out), .in6(multiplexer_64_out), .in7(multiplexer_135_out),
    .in8(multiplexer_16_out), .in9(multiplexer_34_out), .in10(multiplexer_72_out),
    .in11(multiplexer_158_out), .in12(multiplexer_17_out), .in13(multiplexer_39_out),
    .in14(multiplexer_80_out), .in15(multiplexer_190_out), .out(multiplexer_2_out), .sel(\var ));
  Multiplexer #(.select(4), .width(64)) multiplexer_3 (
    .in0(multiplexer_11_out), .in1(multiplexer_26_out), .in2(multiplexer_58_out), .in3(multiplexer_123_out),
    .in4(multiplexer_14_out), .in5(multiplexer_31_out), .in6(multiplexer_67_out), .in7(multiplexer_142_out),
    .in8(multiplexer_18_out), .in9(multiplexer_37_out), .in10(multiplexer_78_out),
    .in11(multiplexer_176_out), .in12(multiplexer_19_out), .in13(multiplexer_40_out),
    .in14(multiplexer_87_out), .in15(multiplexer_196_out), .out(multiplexer_3_out), .sel(\var ));
  Multiplexer #(.select(4), .width(64)) multiplexer_4 (
    .in0(negator_1_out), .in1(negator_3_out), .in2(negator_7_out), .in3(negator_15_out),
    .in4(multiplexer_12_out), .in5(multiplexer_27_out), .in6(multiplexer_51_out), .in7(multiplexer_99_out),
    .in8(bit_extender_2_out), .in9(bit_extender_12_out), .in10(bit_extender_30_out),
    .in11(bit_extender_78_out), .in12(bit_extender_3_out), .in13(bit_extender_13_out),
    .in14(bit_extender_31_out), .in15(bit_extender_79_out), .out(multiplexer_4_out), .sel(\var ));
  Negator #(.width(64)) negator_1 (.in(argY), .out(negator_1_out));
  Multiplexer #(.select(4), .width(64)) multiplexer_5 (
    .in0(buffer_1_out), .in1(not_1_out), .in2(or_2_out), .in3(and_1_out), .in4(nand_1_out), .in5(nor_1_out),
    .in6(xor_1_out), .in7(xnor_1_out), .in8(shifter_4_out), .in9(shifter_7_out), .in10(shifter_19_out),
    .in11(shifter_43_out), .in12(shifter_5_out), .in13(shifter_11_out), .in14(shifter_23_out),
    .in15(shifter_51_out), .out(multiplexer_5_out), .sel(\var ));
  assign or_2_out = argY | argZ;  // OR_Gate or_2, 64 bits wide
  assign not_1_out = ~argY;  // NOT_Gate not_1, 64 bits wide
  assign buffer_1_out = argY;  // Buffer buffer_1, 64 bits wide
  Multiplexer #(.select(4), .width(64)) multiplexer_6 (
    .in0(shifter_1_out), .in1(shifter_9_out), .in2(shifter_27_out), .in3(shifter_59_out),
    .in4(shifter_2_out), .in5(shifter_13_out), .in6(shifter_31_out), .in7(shifter_67_out),
    .in8(shifter_3_out), .in9(shifter_15_out), .in10(shifter_35_out), .in11(shifter_75_out),
    .in12(bit_extender_7_out), .in13(bit_extender_21_out), .in14(bit_extender_47_out),
    .in15(bit_extender_103_out), .out(multiplexer_6_out), .sel(\var ));
  BitSelector #(.group(6), .width(64)) bitselector_1 (.in(argZ), .out(bitselector_1_out), .sel(4'b0000));
  Multiplexer #(.select(4), .width(64)) multiplexer_7 (
    .in0(multiplexer_15_out), .in1(multiplexer_45_out), .in2(multiplexer_94_out), .in3(multiplexer_153_out),
    .in4(multiplexer_20_out), .in5(multiplexer_53_out), .in6(multiplexer_105_out), .in7(multiplexer_172_out),
    .in8(multiplexer_28_out), .in9(multiplexer_63_out), .in10(multiplexer_117_out),
    .in11(multiplexer_189_out), .in12(multiplexer_32_out), .in13(multiplexer_69_out),
    .in14(multiplexer_128_out), .in15(multiplexer_204_out), .out(multiplexer_7_out), .sel(\var ));
  Multiplexer #(.select(4), .width(64)) multiplexer_8 (
    .in0(adder_1_out), .in1(adder_3_out), .in2(adder_7_out), .in3(adder_15_out), .in4(subtractor_1_out),
    .in5(subtractor_3_out), .in6(subtractor_7_out), .in7(subtractor_15_out), .in8(multiplier_1_out),
    .in9(multiplier_3_out), .in10(multiplier_7_out), .in11(multiplier_15_out), .in12(divider_1_out),
    .in13(divider_3_out), .in14(divider_7_out), .in15(divider_15_out), .out(multiplexer_8_out), .sel(\var ));
  Multiplexer #(.select(4), .width(64)) multiplexer_9 (
    .in0(bit_extender_5_out), .in1(bit_extender_15_out), .in2(bit_extender_37_out),
    .in3(bit_extender_63_out), .in4(bit_extender_6_out), .in5(bit_extender_17_out),
    .in6(bit_extender_43_out), .in7(bit_extender_95_out), .in8(multiplier_1_cout), .in9(multiplier_3_cout),
    .in10(multiplier_7_cout), .in11(multiplier_15_cout), .in12(divider_1_rem), .in13(divider_3_rem),
    .in14(divider_7_rem), .in15(divider_15_rem), .out(multiplexer_9_out), .sel(\var ));
  Multiplexer #(.width(64)) multiplexer_10 (
    .in0({64{1'b0}}), .in1(64'h1), .out(multiplexer_10_out), .sel(comparator_9_eq));
  Comparator #(.width(64)) comparator_9 (
    .a(argY), .b({64{1'b0}}), .eq(comparator_9_eq), .lt(comparator_9_lt));  // open: gt
  // FPComparator #(.fpwidth(64)) fpcomparator_1: pin names not known; wires that end beside it: argY, {64{1'b0}}, fpcomparator_1_p3, fpcomparator_1_p4
  Multiplexer #(.width(64)) multiplexer_11 (
    .in0({64{1'b0}}), .in1(64'h1), .out(multiplexer_11_out), .sel(comparator_10_eq));
  Comparator #(.width(64)) comparator_10 (
    .a(argZ), .b(argY), .eq(comparator_10_eq), .lt(comparator_10_lt));  // open: gt
  // FPComparator #(.fpwidth(64)) fpcomparator_2: pin names not known; wires that end beside it: argZ, argY, fpcomparator_2_p3, fpcomparator_2_p4
  Multiplexer #(.width(64)) multiplexer_12 (.in0(argX), .in1(buffer_2_out), .out(multiplexer_12_out), .sel(not_2_out));
  assign buffer_2_out = argY;  // Buffer buffer_2, 64 bits wide
  not not_2 (not_2_out, comparator_11_eq);
  Comparator #(.mode("unsigned"), .width(64)) comparator_11 (
    .a(argZ), .b({64{1'b0}}), .eq(comparator_11_eq));  // open: gt, lt
  assign nand_1_out = ~(argY & argZ);  // NAND_Gate nand_1, 64 bits wide
  assign nor_1_out = ~(argY | argZ);  // NOR_Gate nor_1, 64 bits wide
  assign and_1_out = argY & argZ;  // AND_Gate and_1, 64 bits wide
  Shifter #(.shift("ar"), .width(64)) shifter_1 (.in(argY), .\dist (bitselector_1_out), .out(shifter_1_out));
  assign bit_extender_1_out = {{58{1'b0}}, bitfinder_1_index};  // Bit_Extender bit_extender_1
  BitFinder #(.width(64)) bitfinder_1 (.in(argY), .index(bitfinder_1_index), .found(bitfinder_1_found));
  Multiplexer #(.width(64)) multiplexer_13 (
    .in0({64{1'b0}}), .in1(64'h1), .out(multiplexer_13_out), .sel(comparator_9_lt));
  Multiplexer #(.width(64)) multiplexer_14 (
    .in0({64{1'b0}}), .in1(64'h1), .out(multiplexer_14_out), .sel(comparator_10_lt));
  // FPClassificator #(.fpwidth(64)) fpclassificator_1: pin names not known; wires that end beside it: argY, fpclassificator_1_p2, fpclassificator_1_p3
  assign xnor_1_out = ~(argY ^ argZ);  // XNOR_Gate xnor_1, 64 bits wide
  assign xor_1_out = argY ^ argZ;  // XOR_Gate xor_1, 64 bits wide
  Shifter #(.shift("rl"), .width(64)) shifter_2 (.in(argY), .\dist (bitselector_1_out), .out(shifter_2_out));
  Multiplexer #(.width(64)) multiplexer_15 (
    .in0({64{1'b1}}), .in1(bit_extender_1_out), .out(multiplexer_15_out), .sel(bitfinder_1_found));
  Adder #(.width(64)) adder_1 (.a(argZ), .b(argY), .out(adder_1_out), .cout(adder_1_cout));  // open: cin
  Multiplexer #(.width(64)) multiplexer_16 (
    .in0({64{1'b0}}), .in1(64'h1), .out(multiplexer_16_out), .sel(fpcomparator_1_p3));
  Multiplexer #(.width(64)) multiplexer_17 (
    .in0({64{1'b0}}), .in1(64'h1), .out(multiplexer_17_out), .sel(fpcomparator_1_p4));
  Multiplexer #(.width(64)) multiplexer_18 (
    .in0({64{1'b0}}), .in1(64'h1), .out(multiplexer_18_out), .sel(fpcomparator_2_p3));
  Multiplexer #(.width(64)) multiplexer_19 (
    .in0({64{1'b0}}), .in1(64'h1), .out(multiplexer_19_out), .sel(fpcomparator_2_p4));
  assign bit_extender_2_out = {{63{1'b0}}, fpclassificator_1_p2};  // Bit_Extender bit_extender_2
  assign bit_extender_3_out = {{63{1'b0}}, fpclassificator_1_p3};  // Bit_Extender bit_extender_3
  Shifter #(.shift("rr"), .width(64)) shifter_3 (.in(argY), .\dist (bitselector_1_out), .out(shifter_3_out));
  assign bit_extender_4_out = {{58{1'b0}}, bitfinder_2_index};  // Bit_Extender bit_extender_4
  BitFinder #(.\type ("high1"), .width(64)) bitfinder_2 (
    .in(argY), .index(bitfinder_2_index), .found(bitfinder_2_found));
  assign bit_extender_5_out = {{63{1'b0}}, adder_1_cout};  // Bit_Extender bit_extender_5
  BitSelector #(.group(6), .width(64)) bitselector_2 (.in(argZ), .out(bitselector_2_out), .sel(4'b0000));
  BitAdder #(.width(64)) bitadder_1 (.in0(argY), .out(bitadder_1_out));
  Multiplexer #(.width(64)) multiplexer_20 (
    .in0({64{1'b1}}), .in1(bit_extender_4_out), .out(multiplexer_20_out), .sel(bitfinder_2_found));
  Subtractor #(.width(64)) subtractor_1 (
    .a(argY), .b(argZ), .out(subtractor_1_out), .bout(subtractor_1_bout));  // open: bin
  assign bit_extender_6_out = {{63{1'b0}}, subtractor_1_bout};  // Bit_Extender bit_extender_6
  Comparator #(.width(32)) comparator_12 (
    .a(argY[63:32]), .b({32{1'b0}}), .eq(comparator_12_eq), .lt(comparator_12_lt));  // open: gt
  Comparator #(.width(32)) comparator_13 (
    .a(argY[31:0]), .b({32{1'b0}}), .eq(comparator_13_eq), .lt(comparator_13_lt));  // open: gt
  Negator #(.width(32)) negator_2 (.in(argY[63:32]), .out(negator_3_out[63:32]));
  Negator #(.width(32)) negator_3 (.in(argY[31:0]), .out(negator_3_out[31:0]));
  Shifter #(.width(64)) shifter_4 (.in(argY), .\dist (bitselector_2_out), .out(shifter_4_out));
  assign bit_extender_7_out = {{57{1'b0}}, bitadder_1_out};  // Bit_Extender bit_extender_7
  BitFinder #(.\type ("low0"), .width(64)) bitfinder_3 (
    .in(argY), .index(bitfinder_3_index), .found(bitfinder_3_found));
  Multiplier #(.mode("twosComplement"), .width(64)) multiplier_1 (
    .a(argY), .b(argZ), .out(multiplier_1_out), .cout(multiplier_1_cout));  // open: cin
  Multiplexer #(.width(32)) multiplexer_21 (
    .in0({32{1'b0}}), .in1(32'h1), .out(multiplexer_22_out[63:32]), .sel(comparator_12_eq));
  Multiplexer #(.width(32)) multiplexer_22 (
    .in0({32{1'b0}}), .in1(32'h1), .out(multiplexer_22_out[31:0]), .sel(comparator_13_eq));
  Multiplexer #(.width(32)) multiplexer_23 (
    .in0({32{1'b0}}), .in1(32'h1), .out(multiplexer_26_out[63:32]), .sel(comparator_14_eq));
  Comparator #(.width(32)) comparator_14 (
    .a(argY[63:32]), .b(argZ[63:32]), .eq(comparator_14_eq), .lt(comparator_14_lt));  // open: gt
  Comparator #(.width(32)) comparator_15 (
    .a(argY[31:0]), .b(argZ[31:0]), .eq(comparator_15_eq), .lt(comparator_15_lt));  // open: gt
  Multiplexer #(.width(32)) multiplexer_24 (
    .in0(argX[63:32]), .in1(buffer_3_out), .out(multiplexer_27_out[63:32]), .sel(not_3_out));
  assign buffer_3_out = argY[63:32];  // Buffer buffer_3, 32 bits wide
  Shifter #(.shift("lr"), .width(64)) shifter_5 (.in(argY), .\dist (bitselector_2_out), .out(shifter_5_out));
  assign bit_extender_8_out = {{58{1'b0}}, bitfinder_3_index};  // Bit_Extender bit_extender_8
  Divider #(.mode("twosComplement"), .width(64)) divider_1 (
    .a(argY), .b(argZ), .out(divider_1_out), .rem(divider_1_rem));  // open: upper
  Multiplexer #(.width(32)) multiplexer_25 (
    .in0({32{1'b0}}), .in1(32'h1), .out(multiplexer_29_out[63:32]), .sel(comparator_12_lt));
  Multiplexer #(.width(32)) multiplexer_26 (
    .in0({32{1'b0}}), .in1(32'h1), .out(multiplexer_26_out[31:0]), .sel(comparator_15_eq));
  Multiplexer #(.width(32)) multiplexer_27 (
    .in0(argX[31:0]), .in1(buffer_4_out), .out(multiplexer_27_out[31:0]), .sel(not_4_out));
  assign buffer_4_out = argY[31:0];  // Buffer buffer_4, 32 bits wide
  not not_3 (not_3_out, comparator_16_eq);
  Comparator #(.mode("unsigned"), .width(32)) comparator_16 (
    .a(argZ[63:32]), .b({32{1'b0}}), .eq(comparator_16_eq));  // open: gt, lt
  not not_4 (not_4_out, comparator_17_eq);
  Comparator #(.mode("unsigned"), .width(32)) comparator_17 (
    .a(argZ[31:0]), .b({32{1'b0}}), .eq(comparator_17_eq));  // open: gt, lt
  Multiplexer #(.width(64)) multiplexer_28 (
    .in0({64{1'b1}}), .in1(bit_extender_8_out), .out(multiplexer_28_out), .sel(bitfinder_3_found));
  Multiplexer #(.width(32)) multiplexer_29 (
    .in0({32{1'b0}}), .in1(32'h1), .out(multiplexer_29_out[31:0]), .sel(comparator_13_lt));
  Multiplexer #(.width(32)) multiplexer_30 (
    .in0({32{1'b0}}), .in1(32'h1), .out(multiplexer_31_out[63:32]), .sel(comparator_14_lt));
  // FPClassificator fpclassificator_2: pin names not known; wires that end beside it: argY[63:32], fpclassificator_2_p2, fpclassificator_2_p3
  // FPClassificator fpclassificator_3: pin names not known; wires that end beside it: argY[31:0], fpclassificator_3_p2, fpclassificator_3_p3
  BitSelector #(.group(5), .width(32)) bitselector_3 (.in(argZ[31:0]), .out(bitselector_3_out), .sel(3'b000));
  BitSelector #(.group(5), .width(32)) bitselector_4 (.in(argZ[63:32]), .out(bitselector_4_out), .sel(3'b000));
  BitSelector #(.group(5), .width(32)) bitselector_5 (.in(argZ[31:0]), .out(bitselector_5_out), .sel(3'b000));
  BitSelector #(.group(5), .width(32)) bitselector_6 (.in(argZ[63:32]), .out(bitselector_6_out), .sel(3'b000));
  assign bit_extender_9_out = {{58{1'b0}}, bitfinder_4_index};  // Bit_Extender bit_extender_9
  BitFinder #(.\type ("high0"), .width(64)) bitfinder_4 (
    .in(argY), .index(bitfinder_4_index), .found(bitfinder_4_found));
  // FPComparator fpcomparator_3: pin names not known; wires that end beside it: argY[63:32], {32{1'b0}}, fpcomparator_3_p3, fpcomparator_3_p4
  // FPComparator fpcomparator_4: pin names not known; wires that end beside it: argY[31:0], {32{1'b0}}, fpcomparator_4_p3, fpcomparator_4_p4
  Multiplexer #(.width(32)) multiplexer_31 (
    .in0({32{1'b0}}), .in1(32'h1), .out(multiplexer_31_out[31:0]), .sel(comparator_15_lt));
  // FPComparator fpcomparator_5: pin names not known; wires that end beside it: argY[63:32], argZ[63:32], fpcomparator_5_p3, fpcomparator_5_p4
  // FPComparator fpcomparator_6: pin names not known; wires that end beside it: argY[31:0], argZ[31:0], fpcomparator_6_p3, fpcomparator_6_p4
  assign bit_extender_12_out[63:32] = {{31{1'b0}}, fpclassificator_2_p2};  // Bit_Extender bit_extender_10
  assign bit_extender_13_out[63:32] = {{31{1'b0}}, fpclassificator_2_p3};  // Bit_Extender bit_extender_11
  assign bit_extender_12_out[31:0] = {{31{1'b0}}, fpclassificator_3_p2};  // Bit_Extender bit_extender_12
  assign bit_extender_13_out[31:0] = {{31{1'b0}}, fpclassificator_3_p3};  // Bit_Extender bit_extender_13
  Shifter #(.width(32)) shifter_6 (.in(argY[63:32]), .\dist (bitselector_4_out), .out(shifter_7_out[63:32]));
  Shifter #(.width(32)) shifter_7 (.in(argY[31:0]), .\dist (bitselector_3_out), .out(shifter_7_out[31:0]));
  Shifter #(.shift("ar"), .width(32)) shifter_8 (
    .in(argY[63:32]), .\dist (bitselector_6_out), .out(shifter_9_out[63:32]));
  Shifter #(.shift("ar"), .width(32)) shifter_9 (
    .in(argY[31:0]), .\dist (bitselector_5_out), .out(shifter_9_out[31:0]));
  Multiplexer #(.width(64)) multiplexer_32 (
    .in0({64{1'b1}}), .in1(bit_extender_9_out), .out(multiplexer_32_out), .sel(bitfinder_4_found));
  Multiplexer #(.width(32)) multiplexer_33 (
    .in0({32{1'b0}}), .in1(32'h1), .out(multiplexer_34_out[63:32]), .sel(fpcomparator_3_p3));
  Multiplexer #(.width(32)) multiplexer_34 (
    .in0({32{1'b0}}), .in1(32'h1), .out(multiplexer_34_out[31:0]), .sel(fpcomparator_4_p3));
  Multiplexer #(.width(32)) multiplexer_35 (
    .in0({32{1'b0}}), .in1(32'h1), .out(multiplexer_37_out[63:32]), .sel(fpcomparator_5_p3));
  Adder #(.width(32)) adder_2 (
    .a(argY[63:32]), .b(argZ[63:32]), .out(adder_3_out[63:32]), .cout(adder_2_cout));  // open: cin
  assign bit_extender_15_out[63:32] = {{31{1'b0}}, adder_2_cout};  // Bit_Extender bit_extender_14
  Adder #(.width(32)) adder_3 (
    .a(argY[31:0]), .b(argZ[31:0]), .out(adder_3_out[31:0]), .cout(adder_3_cout));  // open: cin
  assign bit_extender_15_out[31:0] = {{31{1'b0}}, adder_3_cout};  // Bit_Extender bit_extender_15
  Multiplexer #(.width(32)) multiplexer_36 (
    .in0({32{1'b0}}), .in1(32'h1), .out(multiplexer_39_out[63:32]), .sel(fpcomparator_3_p4));
  Multiplexer #(.width(32)) multiplexer_37 (
    .in0({32{1'b0}}), .in1(32'h1), .out(multiplexer_37_out[31:0]), .sel(fpcomparator_6_p3));
  Multiplexer #(.width(32)) multiplexer_38 (
    .in0({32{1'b0}}), .in1(32'h1), .out(multiplexer_40_out[63:32]), .sel(fpcomparator_5_p4));
  Shifter #(.shift("lr"), .width(32)) shifter_10 (
    .in(argY[63:32]), .\dist (bitselector_4_out), .out(shifter_11_out[63:32]));
  Shifter #(.shift("lr"), .width(32)) shifter_11 (
    .in(argY[31:0]), .\dist (bitselector_3_out), .out(shifter_11_out[31:0]));
  Shifter #(.shift("rl"), .width(32)) shifter_12 (
    .in(argY[63:32]), .\dist (bitselector_6_out), .out(shifter_13_out[63:32]));
  Shifter #(.shift("rl"), .width(32)) shifter_13 (
    .in(argY[31:0]), .\dist (bitselector_5_out), .out(shifter_13_out[31:0]));
  Multiplexer #(.width(32)) multiplexer_39 (
    .in0({32{1'b0}}), .in1(32'h1), .out(multiplexer_39_out[31:0]), .sel(fpcomparator_4_p4));
  Multiplexer #(.width(32)) multiplexer_40 (
    .in0({32{1'b0}}), .in1(32'h1), .out(multiplexer_40_out[31:0]), .sel(fpcomparator_6_p4));
  Negator #(.width(16)) negator_4 (.in(argY[63:48]), .out(negator_7_out[63:48]));
  Negator #(.width(16)) negator_5 (.in(argY[47:32]), .out(negator_7_out[47:32]));
  Negator #(.width(16)) negator_6 (.in(argY[31:16]), .out(negator_7_out[31:16]));
  Negator #(.width(16)) negator_7 (.in(argY[15:0]), .out(negator_7_out[15:0]));
  Shifter #(.shift("rr"), .width(32)) shifter_14 (
    .in(argY[63:32]), .\dist (bitselector_6_out), .out(shifter_15_out[63:32]));
  Shifter #(.shift("rr"), .width(32)) shifter_15 (
    .in(argY[31:0]), .\dist (bitselector_5_out), .out(shifter_15_out[31:0]));
  BitFinder #(.width(32)) bitfinder_5 (.in(argY[63:32]), .index(bitfinder_5_index), .found(bitfinder_5_found));
  BitFinder #(.width(32)) bitfinder_6 (.in(argY[31:0]), .index(bitfinder_6_index), .found(bitfinder_6_found));
  Subtractor #(.width(32)) subtractor_2 (
    .a(argY[63:32]), .b(argZ[63:32]), .out(subtractor_3_out[63:32]), .bout(subtractor_2_bout));  // open: bin
  assign bit_extender_17_out[63:32] = {{31{1'b0}}, subtractor_2_bout};  // Bit_Extender bit_extender_16
  Subtractor #(.width(32)) subtractor_3 (
    .a(argY[31:0]), .b(argZ[31:0]), .out(subtractor_3_out[31:0]), .bout(subtractor_3_bout));  // open: bin
  assign bit_extender_17_out[31:0] = {{31{1'b0}}, subtractor_3_bout};  // Bit_Extender bit_extender_17
  BitSelector #(.group(4), .width(16)) bitselector_7 (.in(argZ[15:0]), .out(bitselector_7_out), .sel(2'b00));
  BitSelector #(.group(4), .width(16)) bitselector_8 (.in(argZ[31:16]), .out(bitselector_8_out), .sel(2'b00));
  BitSelector #(.group(4), .width(16)) bitselector_9 (.in(argZ[47:32]), .out(bitselector_9_out), .sel(2'b00));
  BitSelector #(.group(4), .width(16)) bitselector_10 (.in(argZ[63:48]), .out(bitselector_10_out), .sel(2'b00));
  BitAdder #(.width(32)) bitadder_2 (.in0(argY[63:32]), .out(bitadder_2_out));
  BitAdder #(.width(32)) bitadder_3 (.in0(argY[31:0]), .out(bitadder_3_out));
  assign bit_extender_18_out = {{27{1'b0}}, bitfinder_5_index};  // Bit_Extender bit_extender_18
  assign bit_extender_19_out = {{27{1'b0}}, bitfinder_6_index};  // Bit_Extender bit_extender_19
  Multiplexer #(.width(16)) multiplexer_41 (
    .in0({16{1'b0}}), .in1(16'h1), .out(multiplexer_54_out[63:48]), .sel(comparator_18_eq));
  Comparator #(.width(16)) comparator_18 (
    .a(argY[63:48]), .b({16{1'b0}}), .eq(comparator_18_eq), .lt(comparator_18_lt));  // open: gt
  Comparator #(.width(16)) comparator_19 (
    .a(argY[47:32]), .b({16{1'b0}}), .eq(comparator_19_eq), .lt(comparator_19_lt));  // open: gt
  Comparator #(.width(16)) comparator_20 (
    .a(argY[31:16]), .b({16{1'b0}}), .eq(comparator_20_eq), .lt(comparator_20_lt));  // open: gt
  Comparator #(.width(16)) comparator_21 (
    .a(argY[15:0]), .b({16{1'b0}}), .eq(comparator_21_eq), .lt(comparator_21_lt));  // open: gt
  Multiplexer #(.width(16)) multiplexer_42 (
    .in0(argX[63:48]), .in1(buffer_5_out), .out(multiplexer_51_out[63:48]), .sel(not_5_out));
  Multiplexer #(.width(16)) multiplexer_43 (
    .in0(argX[47:32]), .in1(buffer_6_out), .out(multiplexer_51_out[47:32]), .sel(not_6_out));
  assign buffer_5_out = argY[63:48];  // Buffer buffer_5, 16 bits wide
  assign buffer_6_out = argY[47:32];  // Buffer buffer_6, 16 bits wide
  not not_5 (not_5_out, comparator_22_eq);
  Comparator #(.mode("unsigned"), .width(16)) comparator_22 (
    .a(argZ[63:48]), .b({16{1'b0}}), .eq(comparator_22_eq));  // open: gt, lt
  not not_6 (not_6_out, comparator_23_eq);
  Comparator #(.mode("unsigned"), .width(16)) comparator_23 (
    .a(argZ[47:32]), .b({16{1'b0}}), .eq(comparator_23_eq));  // open: gt, lt
  not not_7 (not_7_out, comparator_24_eq);
  Comparator #(.mode("unsigned"), .width(16)) comparator_24 (
    .a(argZ[31:16]), .b({16{1'b0}}), .eq(comparator_24_eq));  // open: gt, lt
  not not_8 (not_8_out, comparator_25_eq);
  Comparator #(.mode("unsigned"), .width(16)) comparator_25 (
    .a(argZ[15:0]), .b({16{1'b0}}), .eq(comparator_25_eq));  // open: gt, lt
  assign bit_extender_21_out[63:32] = {{26{1'b0}}, bitadder_2_out};  // Bit_Extender bit_extender_20
  assign bit_extender_21_out[31:0] = {{26{1'b0}}, bitadder_3_out};  // Bit_Extender bit_extender_21
  Multiplexer #(.width(32)) multiplexer_44 (
    .in0({32{1'b1}}), .in1(bit_extender_18_out), .out(multiplexer_45_out[63:32]), .sel(bitfinder_5_found));
  Multiplexer #(.width(32)) multiplexer_45 (
    .in0({32{1'b1}}), .in1(bit_extender_19_out), .out(multiplexer_45_out[31:0]), .sel(bitfinder_6_found));
  Multiplier #(.mode("twosComplement"), .width(32)) multiplier_2 (
    .a(argY[63:32]), .b(argZ[63:32]), .out(multiplier_3_out[63:32]), .cout(multiplier_3_cout[63:32]));  // open: cin
  Multiplier #(.mode("twosComplement"), .width(32)) multiplier_3 (
    .a(argY[31:0]), .b(argZ[31:0]), .out(multiplier_3_out[31:0]), .cout(multiplier_3_cout[31:0]));  // open: cin
  Multiplexer #(.width(16)) multiplexer_46 (
    .in0({16{1'b0}}), .in1(16'h1), .out(multiplexer_54_out[47:32]), .sel(comparator_19_eq));
  Multiplexer #(.width(16)) multiplexer_47 (
    .in0({16{1'b0}}), .in1(16'h1), .out(multiplexer_58_out[63:48]), .sel(comparator_26_eq));
  Comparator #(.width(16)) comparator_26 (
    .a(argY[63:48]), .b(argZ[63:48]), .eq(comparator_26_eq), .lt(comparator_26_lt));  // open: gt
  Comparator #(.width(16)) comparator_27 (
    .a(argY[47:32]), .b(argZ[47:32]), .eq(comparator_27_eq), .lt(comparator_27_lt));  // open: gt
  Comparator #(.width(16)) comparator_28 (
    .a(argY[31:16]), .b(argZ[31:16]), .eq(comparator_28_eq), .lt(comparator_28_lt));  // open: gt
  Comparator #(.width(16)) comparator_29 (
    .a(argY[15:0]), .b(argZ[15:0]), .eq(comparator_29_eq), .lt(comparator_29_lt));  // open: gt
  Multiplexer #(.width(16)) multiplexer_48 (
    .in0(argX[31:16]), .in1(buffer_7_out), .out(multiplexer_51_out[31:16]), .sel(not_7_out));
  assign buffer_7_out = argY[31:16];  // Buffer buffer_7, 16 bits wide
  Shifter #(.width(16)) shifter_16 (.in(argY[63:48]), .\dist (bitselector_10_out), .out(shifter_19_out[63:48]));
  Shifter #(.width(16)) shifter_17 (.in(argY[47:32]), .\dist (bitselector_9_out), .out(shifter_19_out[47:32]));
  Shifter #(.width(16)) shifter_18 (.in(argY[31:16]), .\dist (bitselector_8_out), .out(shifter_19_out[31:16]));
  Shifter #(.width(16)) shifter_19 (.in(argY[15:0]), .\dist (bitselector_7_out), .out(shifter_19_out[15:0]));
  assign bit_extender_22_out = {{27{1'b0}}, bitfinder_7_index};  // Bit_Extender bit_extender_22
  BitFinder #(.\type ("high1"), .width(32)) bitfinder_7 (
    .in(argY[63:32]), .index(bitfinder_7_index), .found(bitfinder_7_found));
  assign bit_extender_23_out = {{27{1'b0}}, bitfinder_8_index};  // Bit_Extender bit_extender_23
  BitFinder #(.\type ("high1"), .width(32)) bitfinder_8 (
    .in(argY[31:0]), .index(bitfinder_8_index), .found(bitfinder_8_found));
  Divider #(.mode("twosComplement"), .width(32)) divider_2 (
    .a(argY[63:32]), .b(argZ[63:32]), .out(divider_3_out[63:32]), .rem(divider_3_rem[63:32]));  // open: upper
  Divider #(.mode("twosComplement"), .width(32)) divider_3 (
    .a(argY[31:0]), .b(argZ[31:0]), .out(divider_3_out[31:0]), .rem(divider_3_rem[31:0]));  // open: upper
  Multiplexer #(.width(16)) multiplexer_49 (
    .in0({16{1'b0}}), .in1(16'h1), .out(multiplexer_54_out[31:16]), .sel(comparator_20_eq));
  Multiplexer #(.width(16)) multiplexer_50 (
    .in0({16{1'b0}}), .in1(16'h1), .out(multiplexer_58_out[47:32]), .sel(comparator_27_eq));
  Multiplexer #(.width(16)) multiplexer_51 (
    .in0(argX[15:0]), .in1(buffer_8_out), .out(multiplexer_51_out[15:0]), .sel(not_8_out));
  assign buffer_8_out = argY[15:0];  // Buffer buffer_8, 16 bits wide
  Multiplexer #(.width(32)) multiplexer_52 (
    .in0({32{1'b1}}), .in1(bit_extender_22_out), .out(multiplexer_53_out[63:32]), .sel(bitfinder_7_found));
  Multiplexer #(.width(32)) multiplexer_53 (
    .in0({32{1'b1}}), .in1(bit_extender_23_out), .out(multiplexer_53_out[31:0]), .sel(bitfinder_8_found));
  Multiplexer #(.width(16)) multiplexer_54 (
    .in0({16{1'b0}}), .in1(16'h1), .out(multiplexer_54_out[15:0]), .sel(comparator_21_eq));
  Multiplexer #(.width(16)) multiplexer_55 (
    .in0({16{1'b0}}), .in1(16'h1), .out(multiplexer_64_out[63:48]), .sel(comparator_18_lt));
  Multiplexer #(.width(16)) multiplexer_56 (
    .in0({16{1'b0}}), .in1(16'h1), .out(multiplexer_58_out[31:16]), .sel(comparator_28_eq));
  // FPClassificator #(.fpwidth(16)) fpclassificator_4: pin names not known; wires that end beside it: argY[63:48], fpclassificator_4_p2, fpclassificator_4_p3
  // FPClassificator #(.fpwidth(16)) fpclassificator_5: pin names not known; wires that end beside it: argY[47:32], fpclassificator_5_p2, fpclassificator_5_p3
  // FPClassificator #(.fpwidth(16)) fpclassificator_6: pin names not known; wires that end beside it: argY[31:16], fpclassificator_6_p2, fpclassificator_6_p3
  // FPClassificator #(.fpwidth(16)) fpclassificator_7: pin names not known; wires that end beside it: argY[15:0], fpclassificator_7_p2, fpclassificator_7_p3
  Shifter #(.shift("lr"), .width(16)) shifter_20 (
    .in(argY[63:48]), .\dist (bitselector_10_out), .out(shifter_23_out[63:48]));
  Shifter #(.shift("lr"), .width(16)) shifter_21 (
    .in(argY[47:32]), .\dist (bitselector_9_out), .out(shifter_23_out[47:32]));
  Shifter #(.shift("lr"), .width(16)) shifter_22 (
    .in(argY[31:16]), .\dist (bitselector_8_out), .out(shifter_23_out[31:16]));
  Shifter #(.shift("lr"), .width(16)) shifter_23 (
    .in(argY[15:0]), .\dist (bitselector_7_out), .out(shifter_23_out[15:0]));
  BitSelector #(.group(4), .width(16)) bitselector_11 (.in(argZ[15:0]), .out(bitselector_11_out), .sel(2'b00));
  BitSelector #(.group(4), .width(16)) bitselector_12 (.in(argZ[31:16]), .out(bitselector_12_out), .sel(2'b00));
  BitSelector #(.group(4), .width(16)) bitselector_13 (.in(argZ[47:32]), .out(bitselector_13_out), .sel(2'b00));
  BitSelector #(.group(4), .width(16)) bitselector_14 (.in(argZ[63:48]), .out(bitselector_14_out), .sel(2'b00));
  BitFinder #(.\type ("low0"), .width(32)) bitfinder_9 (
    .in(argY[63:32]), .index(bitfinder_9_index), .found(bitfinder_9_found));
  BitFinder #(.\type ("low0"), .width(32)) bitfinder_10 (
    .in(argY[31:0]), .index(bitfinder_10_index), .found(bitfinder_10_found));
  Multiplexer #(.width(16)) multiplexer_57 (
    .in0({16{1'b0}}), .in1(16'h1), .out(multiplexer_64_out[47:32]), .sel(comparator_19_lt));
  Multiplexer #(.width(16)) multiplexer_58 (
    .in0({16{1'b0}}), .in1(16'h1), .out(multiplexer_58_out[15:0]), .sel(comparator_29_eq));
  Multiplexer #(.width(16)) multiplexer_59 (
    .in0({16{1'b0}}), .in1(16'h1), .out(multiplexer_67_out[63:48]), .sel(comparator_26_lt));
  assign bit_extender_30_out[63:48] = {{15{1'b0}}, fpclassificator_4_p2};  // Bit_Extender bit_extender_24
  assign bit_extender_31_out[63:48] = {{15{1'b0}}, fpclassificator_4_p3};  // Bit_Extender bit_extender_25
  assign bit_extender_30_out[47:32] = {{15{1'b0}}, fpclassificator_5_p2};  // Bit_Extender bit_extender_26
  assign bit_extender_31_out[47:32] = {{15{1'b0}}, fpclassificator_5_p3};  // Bit_Extender bit_extender_27
  assign bit_extender_30_out[31:16] = {{15{1'b0}}, fpclassificator_6_p2};  // Bit_Extender bit_extender_28
  assign bit_extender_31_out[31:16] = {{15{1'b0}}, fpclassificator_6_p3};  // Bit_Extender bit_extender_29
  assign bit_extender_30_out[15:0] = {{15{1'b0}}, fpclassificator_7_p2};  // Bit_Extender bit_extender_30
  assign bit_extender_31_out[15:0] = {{15{1'b0}}, fpclassificator_7_p3};  // Bit_Extender bit_extender_31
  assign bit_extender_32_out = {{27{1'b0}}, bitfinder_9_index};  // Bit_Extender bit_extender_32
  assign bit_extender_33_out = {{27{1'b0}}, bitfinder_10_index};  // Bit_Extender bit_extender_33
  Multiplexer #(.width(16)) multiplexer_60 (
    .in0({16{1'b0}}), .in1(16'h1), .out(multiplexer_64_out[31:16]), .sel(comparator_20_lt));
  Multiplexer #(.width(16)) multiplexer_61 (
    .in0({16{1'b0}}), .in1(16'h1), .out(multiplexer_67_out[47:32]), .sel(comparator_27_lt));
  Shifter #(.shift("ar"), .width(16)) shifter_24 (
    .in(argY[63:48]), .\dist (bitselector_14_out), .out(shifter_27_out[63:48]));
  Shifter #(.shift("ar"), .width(16)) shifter_25 (
    .in(argY[47:32]), .\dist (bitselector_13_out), .out(shifter_27_out[47:32]));
  Shifter #(.shift("ar"), .width(16)) shifter_26 (
    .in(argY[31:16]), .\dist (bitselector_12_out), .out(shifter_27_out[31:16]));
  Shifter #(.shift("ar"), .width(16)) shifter_27 (
    .in(argY[15:0]), .\dist (bitselector_11_out), .out(shifter_27_out[15:0]));
  Multiplexer #(.width(32)) multiplexer_62 (
    .in0({32{1'b1}}), .in1(bit_extender_32_out), .out(multiplexer_63_out[63:32]), .sel(bitfinder_9_found));
  Multiplexer #(.width(32)) multiplexer_63 (
    .in0({32{1'b1}}), .in1(bit_extender_33_out), .out(multiplexer_63_out[31:0]), .sel(bitfinder_10_found));
  Adder #(.width(16)) adder_4 (
    .a(argY[63:48]), .b(argZ[63:48]), .out(adder_7_out[63:48]), .cout(adder_4_cout));  // open: cin
  assign bit_extender_37_out[63:48] = {{15{1'b0}}, adder_4_cout};  // Bit_Extender bit_extender_34
  Adder #(.width(16)) adder_5 (
    .a(argY[47:32]), .b(argZ[47:32]), .out(adder_7_out[47:32]), .cout(adder_5_cout));  // open: cin
  assign bit_extender_37_out[47:32] = {{15{1'b0}}, adder_5_cout};  // Bit_Extender bit_extender_35
  Adder #(.width(16)) adder_6 (
    .a(argY[31:16]), .b(argZ[31:16]), .out(adder_7_out[31:16]), .cout(adder_6_cout));  // open: cin
  assign bit_extender_37_out[31:16] = {{15{1'b0}}, adder_6_cout};  // Bit_Extender bit_extender_36
  Adder #(.width(16)) adder_7 (
    .a(argY[15:0]), .b(argZ[15:0]), .out(adder_7_out[15:0]), .cout(adder_7_cout));  // open: cin
  assign bit_extender_37_out[15:0] = {{15{1'b0}}, adder_7_cout};  // Bit_Extender bit_extender_37
  Multiplexer #(.width(16)) multiplexer_64 (
    .in0({16{1'b0}}), .in1(16'h1), .out(multiplexer_64_out[15:0]), .sel(comparator_21_lt));
  Multiplexer #(.width(16)) multiplexer_65 (
    .in0({16{1'b0}}), .in1(16'h1), .out(multiplexer_67_out[31:16]), .sel(comparator_28_lt));
  assign bit_extender_38_out = {{27{1'b0}}, bitfinder_11_index};  // Bit_Extender bit_extender_38
  BitFinder #(.\type ("high0"), .width(32)) bitfinder_11 (
    .in(argY[63:32]), .index(bitfinder_11_index), .found(bitfinder_11_found));
  assign bit_extender_39_out = {{27{1'b0}}, bitfinder_12_index};  // Bit_Extender bit_extender_39
  BitFinder #(.\type ("high0"), .width(32)) bitfinder_12 (
    .in(argY[31:0]), .index(bitfinder_12_index), .found(bitfinder_12_found));
  Multiplexer #(.width(16)) multiplexer_66 (
    .in0({16{1'b0}}), .in1(16'h1), .out(multiplexer_72_out[63:48]), .sel(fpcomparator_7_p3));
  // FPComparator #(.fpwidth(16)) fpcomparator_7: pin names not known; wires that end beside it: argY[63:48], {16{1'b0}}, fpcomparator_7_p3, fpcomparator_7_p4
  // FPComparator #(.fpwidth(16)) fpcomparator_8: pin names not known; wires that end beside it: argY[47:32], {16{1'b0}}, fpcomparator_8_p3, fpcomparator_8_p4
  // FPComparator #(.fpwidth(16)) fpcomparator_9: pin names not known; wires that end beside it: argY[31:16], {16{1'b0}}, fpcomparator_9_p3, fpcomparator_9_p4
  // FPComparator #(.fpwidth(16)) fpcomparator_10: pin names not known; wires that end beside it: argY[15:0], {16{1'b0}}, fpcomparator_10_p3, fpcomparator_10_p4
  Multiplexer #(.width(16)) multiplexer_67 (
    .in0({16{1'b0}}), .in1(16'h1), .out(multiplexer_67_out[15:0]), .sel(comparator_29_lt));
  BitSelector #(.group(3)) bitselector_15 (.in(argZ[7:0]), .out(bitselector_15_out), .sel(2'b00));
  BitSelector #(.group(3)) bitselector_16 (.in(argZ[15:8]), .out(bitselector_16_out), .sel(2'b00));
  BitSelector #(.group(3)) bitselector_17 (.in(argZ[23:16]), .out(bitselector_17_out), .sel(2'b00));
  BitSelector #(.group(3)) bitselector_18 (.in(argZ[31:24]), .out(bitselector_18_out), .sel(2'b00));
  BitSelector #(.group(3)) bitselector_19 (.in(argZ[39:32]), .out(bitselector_19_out), .sel(2'b00));
  BitSelector #(.group(3)) bitselector_20 (.in(argZ[47:40]), .out(bitselector_20_out), .sel(2'b00));
  BitSelector #(.group(3)) bitselector_21 (.in(argZ[55:48]), .out(bitselector_21_out), .sel(2'b00));
  BitSelector #(.group(3)) bitselector_22 (.in(argZ[63:56]), .out(bitselector_22_out), .sel(2'b00));
  Shifter #(.shift("rl"), .width(16)) shifter_28 (
    .in(argY[63:48]), .\dist (bitselector_14_out), .out(shifter_31_out[63:48]));
  Shifter #(.shift("rl"), .width(16)) shifter_29 (
    .in(argY[47:32]), .\dist (bitselector_13_out), .out(shifter_31_out[47:32]));
  Shifter #(.shift("rl"), .width(16)) shifter_30 (
    .in(argY[31:16]), .\dist (bitselector_12_out), .out(shifter_31_out[31:16]));
  Shifter #(.shift("rl"), .width(16)) shifter_31 (
    .in(argY[15:0]), .\dist (bitselector_11_out), .out(shifter_31_out[15:0]));
  Multiplexer #(.width(32)) multiplexer_68 (
    .in0({32{1'b1}}), .in1(bit_extender_38_out), .out(multiplexer_69_out[63:32]), .sel(bitfinder_11_found));
  Multiplexer #(.width(32)) multiplexer_69 (
    .in0({32{1'b1}}), .in1(bit_extender_39_out), .out(multiplexer_69_out[31:0]), .sel(bitfinder_12_found));
  Multiplexer #(.width(16)) multiplexer_70 (
    .in0({16{1'b0}}), .in1(16'h1), .out(multiplexer_72_out[47:32]), .sel(fpcomparator_8_p3));
  // FPComparator #(.fpwidth(16)) fpcomparator_11: pin names not known; wires that end beside it: argY[63:48], argZ[63:48], fpcomparator_11_p3, fpcomparator_11_p4
  // FPComparator #(.fpwidth(16)) fpcomparator_12: pin names not known; wires that end beside it: argY[47:32], argZ[47:32], fpcomparator_12_p3, fpcomparator_12_p4
  // FPComparator #(.fpwidth(16)) fpcomparator_13: pin names not known; wires that end beside it: argY[31:16], argZ[31:16], fpcomparator_13_p3, fpcomparator_13_p4
  // FPComparator #(.fpwidth(16)) fpcomparator_14: pin names not known; wires that end beside it: argY[15:0], argZ[15:0], fpcomparator_14_p3, fpcomparator_14_p4
  Subtractor #(.width(16)) subtractor_4 (
    .a(argY[63:48]), .b(argZ[63:48]), .out(subtractor_7_out[63:48]), .bout(subtractor_4_bout));  // open: bin
  assign bit_extender_43_out[63:48] = {{15{1'b0}}, subtractor_4_bout};  // Bit_Extender bit_extender_40
  Subtractor #(.width(16)) subtractor_5 (
    .a(argY[47:32]), .b(argZ[47:32]), .out(subtractor_7_out[47:32]), .bout(subtractor_5_bout));  // open: bin
  assign bit_extender_43_out[47:32] = {{15{1'b0}}, subtractor_5_bout};  // Bit_Extender bit_extender_41
  Subtractor #(.width(16)) subtractor_6 (
    .a(argY[31:16]), .b(argZ[31:16]), .out(subtractor_7_out[31:16]), .bout(subtractor_6_bout));  // open: bin
  assign bit_extender_43_out[31:16] = {{15{1'b0}}, subtractor_6_bout};  // Bit_Extender bit_extender_42
  Subtractor #(.width(16)) subtractor_7 (
    .a(argY[15:0]), .b(argZ[15:0]), .out(subtractor_7_out[15:0]), .bout(subtractor_7_bout));  // open: bin
  assign bit_extender_43_out[15:0] = {{15{1'b0}}, subtractor_7_bout};  // Bit_Extender bit_extender_43
  Multiplexer #(.width(16)) multiplexer_71 (
    .in0({16{1'b0}}), .in1(16'h1), .out(multiplexer_72_out[31:16]), .sel(fpcomparator_9_p3));
  Multiplexer #(.width(16)) multiplexer_72 (
    .in0({16{1'b0}}), .in1(16'h1), .out(multiplexer_72_out[15:0]), .sel(fpcomparator_10_p3));
  Multiplexer #(.width(16)) multiplexer_73 (
    .in0({16{1'b0}}), .in1(16'h1), .out(multiplexer_78_out[63:48]), .sel(fpcomparator_11_p3));
  Multiplexer #(.width(16)) multiplexer_74 (
    .in0({16{1'b0}}), .in1(16'h1), .out(multiplexer_78_out[47:32]), .sel(fpcomparator_12_p3));
  Shifter #(.shift("rr"), .width(16)) shifter_32 (
    .in(argY[63:48]), .\dist (bitselector_14_out), .out(shifter_35_out[63:48]));
  Shifter #(.shift("rr"), .width(16)) shifter_33 (
    .in(argY[47:32]), .\dist (bitselector_13_out), .out(shifter_35_out[47:32]));
  Shifter #(.shift("rr"), .width(16)) shifter_34 (
    .in(argY[31:16]), .\dist (bitselector_12_out), .out(shifter_35_out[31:16]));
  Shifter #(.shift("rr"), .width(16)) shifter_35 (
    .in(argY[15:0]), .\dist (bitselector_11_out), .out(shifter_35_out[15:0]));
  Multiplexer #(.width(16)) multiplexer_75 (
    .in0({16{1'b0}}), .in1(16'h1), .out(multiplexer_80_out[63:48]), .sel(fpcomparator_7_p4));
  Multiplexer #(.width(16)) multiplexer_76 (
    .in0({16{1'b0}}), .in1(16'h1), .out(multiplexer_78_out[31:16]), .sel(fpcomparator_13_p3));
  Negator negator_8 (.in(argY[63:56]), .out(negator_15_out[63:56]));
  Negator negator_9 (.in(argY[55:48]), .out(negator_15_out[55:48]));
  Negator negator_10 (.in(argY[47:40]), .out(negator_15_out[47:40]));
  Negator negator_11 (.in(argY[39:32]), .out(negator_15_out[39:32]));
  Negator negator_12 (.in(argY[31:24]), .out(negator_15_out[31:24]));
  Negator negator_13 (.in(argY[23:16]), .out(negator_15_out[23:16]));
  Negator negator_14 (.in(argY[15:8]), .out(negator_15_out[15:8]));
  Negator negator_15 (.in(argY[7:0]), .out(negator_15_out[7:0]));
  Shifter shifter_36 (.in(argY[63:56]), .\dist (bitselector_22_out), .out(shifter_43_out[63:56]));
  Shifter shifter_37 (.in(argY[55:48]), .\dist (bitselector_21_out), .out(shifter_43_out[55:48]));
  Shifter shifter_38 (.in(argY[47:40]), .\dist (bitselector_20_out), .out(shifter_43_out[47:40]));
  Shifter shifter_39 (.in(argY[39:32]), .\dist (bitselector_19_out), .out(shifter_43_out[39:32]));
  Shifter shifter_40 (.in(argY[31:24]), .\dist (bitselector_18_out), .out(shifter_43_out[31:24]));
  Shifter shifter_41 (.in(argY[23:16]), .\dist (bitselector_17_out), .out(shifter_43_out[23:16]));
  Shifter shifter_42 (.in(argY[15:8]), .\dist (bitselector_16_out), .out(shifter_43_out[15:8]));
  Shifter shifter_43 (.in(argY[7:0]), .\dist (bitselector_15_out), .out(shifter_43_out[7:0]));
  BitAdder #(.width(16)) bitadder_4 (.in0(argY[63:48]), .out(bitadder_4_out));
  BitAdder #(.width(16)) bitadder_5 (.in0(argY[47:32]), .out(bitadder_5_out));
  BitAdder #(.width(16)) bitadder_6 (.in0(argY[31:16]), .out(bitadder_6_out));
  BitAdder #(.width(16)) bitadder_7 (.in0(argY[15:0]), .out(bitadder_7_out));
  Multiplier #(.mode("twosComplement"), .width(16)) multiplier_4 (
    .a(argY[63:48]), .b(argZ[63:48]), .out(multiplier_7_out[63:48]), .cout(multiplier_7_cout[63:48]));  // open: cin
  Multiplier #(.mode("twosComplement"), .width(16)) multiplier_5 (
    .a(argY[47:32]), .b(argZ[47:32]), .out(multiplier_7_out[47:32]), .cout(multiplier_7_cout[47:32]));  // open: cin
  Multiplier #(.mode("twosComplement"), .width(16)) multiplier_6 (
    .a(argY[31:16]), .b(argZ[31:16]), .out(multiplier_7_out[31:16]), .cout(multiplier_7_cout[31:16]));  // open: cin
  Multiplier #(.mode("twosComplement"), .width(16)) multiplier_7 (
    .a(argY[15:0]), .b(argZ[15:0]), .out(multiplier_7_out[15:0]), .cout(multiplier_7_cout[15:0]));  // open: cin
  Multiplexer #(.width(16)) multiplexer_77 (
    .in0({16{1'b0}}), .in1(16'h1), .out(multiplexer_80_out[47:32]), .sel(fpcomparator_8_p4));
  Multiplexer #(.width(16)) multiplexer_78 (
    .in0({16{1'b0}}), .in1(16'h1), .out(multiplexer_78_out[15:0]), .sel(fpcomparator_14_p3));
  not not_9 (not_9_out, comparator_30_eq);
  Comparator #(.mode("unsigned")) comparator_30 (
    .a(argZ[63:56]), .b({8{1'b0}}), .eq(comparator_30_eq));  // open: gt, lt
  not not_10 (not_10_out, comparator_31_eq);
  Comparator #(.mode("unsigned")) comparator_31 (
    .a(argZ[55:48]), .b({8{1'b0}}), .eq(comparator_31_eq));  // open: gt, lt
  not not_11 (not_11_out, comparator_32_eq);
  Comparator #(.mode("unsigned")) comparator_32 (
    .a(argZ[47:40]), .b({8{1'b0}}), .eq(comparator_32_eq));  // open: gt, lt
  not not_12 (not_12_out, comparator_33_eq);
  Comparator #(.mode("unsigned")) comparator_33 (
    .a(argZ[39:32]), .b({8{1'b0}}), .eq(comparator_33_eq));  // open: gt, lt
  not not_13 (not_13_out, comparator_34_eq);
  Comparator #(.mode("unsigned")) comparator_34 (
    .a(argZ[31:24]), .b({8{1'b0}}), .eq(comparator_34_eq));  // open: gt, lt
  not not_14 (not_14_out, comparator_35_eq);
  Comparator #(.mode("unsigned")) comparator_35 (
    .a(argZ[23:16]), .b({8{1'b0}}), .eq(comparator_35_eq));  // open: gt, lt
  not not_15 (not_15_out, comparator_36_eq);
  Comparator #(.mode("unsigned")) comparator_36 (.a(argZ[15:8]), .b({8{1'b0}}), .eq(comparator_36_eq));  // open: gt, lt
  not not_16 (not_16_out, comparator_37_eq);
  Comparator #(.mode("unsigned")) comparator_37 (.a(argZ[7:0]), .b({8{1'b0}}), .eq(comparator_37_eq));  // open: gt, lt
  assign bit_extender_47_out[63:48] = {{11{1'b0}}, bitadder_4_out};  // Bit_Extender bit_extender_44
  assign bit_extender_47_out[47:32] = {{11{1'b0}}, bitadder_5_out};  // Bit_Extender bit_extender_45
  assign bit_extender_47_out[31:16] = {{11{1'b0}}, bitadder_6_out};  // Bit_Extender bit_extender_46
  assign bit_extender_47_out[15:0] = {{11{1'b0}}, bitadder_7_out};  // Bit_Extender bit_extender_47
  Multiplexer #(.width(16)) multiplexer_79 (
    .in0({16{1'b0}}), .in1(16'h1), .out(multiplexer_80_out[31:16]), .sel(fpcomparator_9_p4));
  Multiplexer #(.width(16)) multiplexer_80 (
    .in0({16{1'b0}}), .in1(16'h1), .out(multiplexer_80_out[15:0]), .sel(fpcomparator_10_p4));
  Multiplexer #(.width(16)) multiplexer_81 (
    .in0({16{1'b0}}), .in1(16'h1), .out(multiplexer_87_out[63:48]), .sel(fpcomparator_11_p4));
  Multiplexer #(.width(16)) multiplexer_82 (
    .in0({16{1'b0}}), .in1(16'h1), .out(multiplexer_87_out[47:32]), .sel(fpcomparator_12_p4));
  Multiplexer #(.width(8)) multiplexer_83 (
    .in0(argX[63:56]), .in1(buffer_9_out), .out(multiplexer_99_out[63:56]), .sel(not_9_out));
  Multiplexer #(.width(8)) multiplexer_84 (
    .in0(argX[55:48]), .in1(buffer_10_out), .out(multiplexer_99_out[55:48]), .sel(not_10_out));
  assign buffer_9_out = argY[63:56];  // Buffer buffer_9, 8 bits wide
  Multiplexer #(.width(16)) multiplexer_85 (
    .in0({16{1'b0}}), .in1(16'h1), .out(multiplexer_87_out[31:16]), .sel(fpcomparator_13_p4));
  Multiplexer #(.width(8)) multiplexer_86 (
    .in0(argX[47:40]), .in1(buffer_11_out), .out(multiplexer_99_out[47:40]), .sel(not_11_out));
  assign buffer_10_out = argY[55:48];  // Buffer buffer_10, 8 bits wide
  assign buffer_11_out = argY[47:40];  // Buffer buffer_11, 8 bits wide
  Shifter #(.shift("lr")) shifter_44 (.in(argY[63:56]), .\dist (bitselector_22_out), .out(shifter_51_out[63:56]));
  Shifter #(.shift("lr")) shifter_45 (.in(argY[55:48]), .\dist (bitselector_21_out), .out(shifter_51_out[55:48]));
  Shifter #(.shift("lr")) shifter_46 (.in(argY[47:40]), .\dist (bitselector_20_out), .out(shifter_51_out[47:40]));
  Shifter #(.shift("lr")) shifter_47 (.in(argY[39:32]), .\dist (bitselector_19_out), .out(shifter_51_out[39:32]));
  Shifter #(.shift("lr")) shifter_48 (.in(argY[31:24]), .\dist (bitselector_18_out), .out(shifter_51_out[31:24]));
  Shifter #(.shift("lr")) shifter_49 (.in(argY[23:16]), .\dist (bitselector_17_out), .out(shifter_51_out[23:16]));
  Shifter #(.shift("lr")) shifter_50 (.in(argY[15:8]), .\dist (bitselector_16_out), .out(shifter_51_out[15:8]));
  Shifter #(.shift("lr")) shifter_51 (.in(argY[7:0]), .\dist (bitselector_15_out), .out(shifter_51_out[7:0]));
  Divider #(.mode("twosComplement"), .width(16)) divider_4 (
    .a(argY[63:48]), .b(argZ[63:48]), .out(divider_7_out[63:48]), .rem(divider_7_rem[63:48]));  // open: upper
  Divider #(.mode("twosComplement"), .width(16)) divider_5 (
    .a(argY[47:32]), .b(argZ[47:32]), .out(divider_7_out[47:32]), .rem(divider_7_rem[47:32]));  // open: upper
  Divider #(.mode("twosComplement"), .width(16)) divider_6 (
    .a(argY[31:16]), .b(argZ[31:16]), .out(divider_7_out[31:16]), .rem(divider_7_rem[31:16]));  // open: upper
  Divider #(.mode("twosComplement"), .width(16)) divider_7 (
    .a(argY[15:0]), .b(argZ[15:0]), .out(divider_7_out[15:0]), .rem(divider_7_rem[15:0]));  // open: upper
  Multiplexer #(.width(16)) multiplexer_87 (
    .in0({16{1'b0}}), .in1(16'h1), .out(multiplexer_87_out[15:0]), .sel(fpcomparator_14_p4));
  Multiplexer #(.width(8)) multiplexer_88 (
    .in0(argX[39:32]), .in1(buffer_12_out), .out(multiplexer_99_out[39:32]), .sel(not_12_out));
  assign buffer_12_out = argY[39:32];  // Buffer buffer_12, 8 bits wide
  BitSelector #(.group(3)) bitselector_23 (.in(argZ[7:0]), .out(bitselector_23_out), .sel(2'b00));
  BitSelector #(.group(3)) bitselector_24 (.in(argZ[15:8]), .out(bitselector_24_out), .sel(2'b00));
  BitSelector #(.group(3)) bitselector_25 (.in(argZ[23:16]), .out(bitselector_25_out), .sel(2'b00));
  BitSelector #(.group(3)) bitselector_26 (.in(argZ[31:24]), .out(bitselector_26_out), .sel(2'b00));
  BitSelector #(.group(3)) bitselector_27 (.in(argZ[39:32]), .out(bitselector_27_out), .sel(2'b00));
  BitSelector #(.group(3)) bitselector_28 (.in(argZ[47:40]), .out(bitselector_28_out), .sel(2'b00));
  BitSelector #(.group(3)) bitselector_29 (.in(argZ[55:48]), .out(bitselector_29_out), .sel(2'b00));
  BitSelector #(.group(3)) bitselector_30 (.in(argZ[63:56]), .out(bitselector_30_out), .sel(2'b00));
  BitFinder #(.width(16)) bitfinder_13 (.in(argY[63:48]), .index(bitfinder_13_index), .found(bitfinder_13_found));
  BitFinder #(.width(16)) bitfinder_14 (.in(argY[47:32]), .index(bitfinder_14_index), .found(bitfinder_14_found));
  BitFinder #(.width(16)) bitfinder_15 (.in(argY[31:16]), .index(bitfinder_15_index), .found(bitfinder_15_found));
  BitFinder #(.width(16)) bitfinder_16 (.in(argY[15:0]), .index(bitfinder_16_index), .found(bitfinder_16_found));
  Comparator comparator_38 (.a(argY[63:56]), .b({8{1'b0}}), .eq(comparator_38_eq), .lt(comparator_38_lt));  // open: gt
  Comparator comparator_39 (.a(argY[55:48]), .b({8{1'b0}}), .eq(comparator_39_eq), .lt(comparator_39_lt));  // open: gt
  Comparator comparator_40 (.a(argY[47:40]), .b({8{1'b0}}), .eq(comparator_40_eq), .lt(comparator_40_lt));  // open: gt
  Comparator comparator_41 (.a(argY[39:32]), .b({8{1'b0}}), .eq(comparator_41_eq), .lt(comparator_41_lt));  // open: gt
  Comparator comparator_42 (.a(argY[31:24]), .b({8{1'b0}}), .eq(comparator_42_eq), .lt(comparator_42_lt));  // open: gt
  Comparator comparator_43 (.a(argY[23:16]), .b({8{1'b0}}), .eq(comparator_43_eq), .lt(comparator_43_lt));  // open: gt
  Comparator comparator_44 (.a(argY[15:8]), .b({8{1'b0}}), .eq(comparator_44_eq), .lt(comparator_44_lt));  // open: gt
  Comparator comparator_45 (.a(argY[7:0]), .b({8{1'b0}}), .eq(comparator_45_eq), .lt(comparator_45_lt));  // open: gt
  Multiplexer #(.width(8)) multiplexer_89 (
    .in0(argX[31:24]), .in1(buffer_13_out), .out(multiplexer_99_out[31:24]), .sel(not_13_out));
  Multiplexer #(.width(8)) multiplexer_90 (
    .in0(argX[23:16]), .in1(buffer_14_out), .out(multiplexer_99_out[23:16]), .sel(not_14_out));
  assign buffer_13_out = argY[31:24];  // Buffer buffer_13, 8 bits wide
  assign bit_extender_48_out = {{12{1'b0}}, bitfinder_13_index};  // Bit_Extender bit_extender_48
  Multiplexer #(.width(16)) multiplexer_91 (
    .in0({16{1'b1}}), .in1(bit_extender_48_out), .out(multiplexer_94_out[63:48]), .sel(bitfinder_13_found));
  assign bit_extender_49_out = {{12{1'b0}}, bitfinder_14_index};  // Bit_Extender bit_extender_49
  Multiplexer #(.width(16)) multiplexer_92 (
    .in0({16{1'b1}}), .in1(bit_extender_49_out), .out(multiplexer_94_out[47:32]), .sel(bitfinder_14_found));
  assign bit_extender_50_out = {{12{1'b0}}, bitfinder_15_index};  // Bit_Extender bit_extender_50
  Multiplexer #(.width(16)) multiplexer_93 (
    .in0({16{1'b1}}), .in1(bit_extender_50_out), .out(multiplexer_94_out[31:16]), .sel(bitfinder_15_found));
  assign bit_extender_51_out = {{12{1'b0}}, bitfinder_16_index};  // Bit_Extender bit_extender_51
  Multiplexer #(.width(16)) multiplexer_94 (
    .in0({16{1'b1}}), .in1(bit_extender_51_out), .out(multiplexer_94_out[15:0]), .sel(bitfinder_16_found));
  Multiplexer #(.width(8)) multiplexer_95 (
    .in0({8{1'b0}}), .in1(8'h1), .out(multiplexer_112_out[63:56]), .sel(comparator_38_eq));
  Multiplexer #(.width(8)) multiplexer_96 (
    .in0({8{1'b0}}), .in1(8'h1), .out(multiplexer_112_out[55:48]), .sel(comparator_39_eq));
  Multiplexer #(.width(8)) multiplexer_97 (
    .in0(argX[15:8]), .in1(buffer_15_out), .out(multiplexer_99_out[15:8]), .sel(not_15_out));
  assign buffer_14_out = argY[23:16];  // Buffer buffer_14, 8 bits wide
  assign buffer_15_out = argY[15:8];  // Buffer buffer_15, 8 bits wide
  Multiplexer #(.width(8)) multiplexer_98 (
    .in0({8{1'b0}}), .in1(8'h1), .out(multiplexer_112_out[47:40]), .sel(comparator_40_eq));
  Multiplexer #(.width(8)) multiplexer_99 (
    .in0(argX[7:0]), .in1(buffer_16_out), .out(multiplexer_99_out[7:0]), .sel(not_16_out));
  assign buffer_16_out = argY[7:0];  // Buffer buffer_16, 8 bits wide
  Shifter #(.shift("ar")) shifter_52 (.in(argY[63:56]), .\dist (bitselector_30_out), .out(shifter_59_out[63:56]));
  Shifter #(.shift("ar")) shifter_53 (.in(argY[55:48]), .\dist (bitselector_29_out), .out(shifter_59_out[55:48]));
  Shifter #(.shift("ar")) shifter_54 (.in(argY[47:40]), .\dist (bitselector_28_out), .out(shifter_59_out[47:40]));
  Shifter #(.shift("ar")) shifter_55 (.in(argY[39:32]), .\dist (bitselector_27_out), .out(shifter_59_out[39:32]));
  Shifter #(.shift("ar")) shifter_56 (.in(argY[31:24]), .\dist (bitselector_26_out), .out(shifter_59_out[31:24]));
  Shifter #(.shift("ar")) shifter_57 (.in(argY[23:16]), .\dist (bitselector_25_out), .out(shifter_59_out[23:16]));
  Shifter #(.shift("ar")) shifter_58 (.in(argY[15:8]), .\dist (bitselector_24_out), .out(shifter_59_out[15:8]));
  Shifter #(.shift("ar")) shifter_59 (.in(argY[7:0]), .\dist (bitselector_23_out), .out(shifter_59_out[7:0]));
  BitFinder #(.\type ("high1"), .width(16)) bitfinder_17 (
    .in(argY[63:48]), .index(bitfinder_17_index), .found(bitfinder_17_found));
  BitFinder #(.\type ("high1"), .width(16)) bitfinder_18 (
    .in(argY[47:32]), .index(bitfinder_18_index), .found(bitfinder_18_found));
  BitFinder #(.\type ("high1"), .width(16)) bitfinder_19 (
    .in(argY[31:16]), .index(bitfinder_19_index), .found(bitfinder_19_found));
  BitFinder #(.\type ("high1"), .width(16)) bitfinder_20 (
    .in(argY[15:0]), .index(bitfinder_20_index), .found(bitfinder_20_found));
  Multiplexer #(.width(8)) multiplexer_100 (
    .in0({8{1'b0}}), .in1(8'h1), .out(multiplexer_112_out[39:32]), .sel(comparator_41_eq));
  Multiplexer #(.width(8)) multiplexer_101 (
    .in0({8{1'b0}}), .in1(8'h1), .out(multiplexer_123_out[63:56]), .sel(comparator_46_eq));
  Comparator comparator_46 (
    .a(argY[63:56]), .b(argZ[63:56]), .eq(comparator_46_eq), .lt(comparator_46_lt));  // open: gt
  Comparator comparator_47 (
    .a(argY[55:48]), .b(argZ[55:48]), .eq(comparator_47_eq), .lt(comparator_47_lt));  // open: gt
  Comparator comparator_48 (
    .a(argY[47:40]), .b(argZ[47:40]), .eq(comparator_48_eq), .lt(comparator_48_lt));  // open: gt
  Comparator comparator_49 (
    .a(argY[39:32]), .b(argZ[39:32]), .eq(comparator_49_eq), .lt(comparator_49_lt));  // open: gt
  Comparator comparator_50 (
    .a(argY[31:24]), .b(argZ[31:24]), .eq(comparator_50_eq), .lt(comparator_50_lt));  // open: gt
  Comparator comparator_51 (
    .a(argY[23:16]), .b(argZ[23:16]), .eq(comparator_51_eq), .lt(comparator_51_lt));  // open: gt
  Comparator comparator_52 (.a(argY[15:8]), .b(argZ[15:8]), .eq(comparator_52_eq), .lt(comparator_52_lt));  // open: gt
  Comparator comparator_53 (.a(argY[7:0]), .b(argZ[7:0]), .eq(comparator_53_eq), .lt(comparator_53_lt));  // open: gt
  assign bit_extender_52_out = {{12{1'b0}}, bitfinder_17_index};  // Bit_Extender bit_extender_52
  Multiplexer #(.width(16)) multiplexer_102 (
    .in0({16{1'b1}}), .in1(bit_extender_52_out), .out(multiplexer_105_out[63:48]), .sel(bitfinder_17_found));
  assign bit_extender_53_out = {{12{1'b0}}, bitfinder_18_index};  // Bit_Extender bit_extender_53
  Multiplexer #(.width(16)) multiplexer_103 (
    .in0({16{1'b1}}), .in1(bit_extender_53_out), .out(multiplexer_105_out[47:32]), .sel(bitfinder_18_found));
  assign bit_extender_54_out = {{12{1'b0}}, bitfinder_19_index};  // Bit_Extender bit_extender_54
  Multiplexer #(.width(16)) multiplexer_104 (
    .in0({16{1'b1}}), .in1(bit_extender_54_out), .out(multiplexer_105_out[31:16]), .sel(bitfinder_19_found));
  assign bit_extender_55_out = {{12{1'b0}}, bitfinder_20_index};  // Bit_Extender bit_extender_55
  Multiplexer #(.width(16)) multiplexer_105 (
    .in0({16{1'b1}}), .in1(bit_extender_55_out), .out(multiplexer_105_out[15:0]), .sel(bitfinder_20_found));
  Multiplexer #(.width(8)) multiplexer_106 (
    .in0({8{1'b0}}), .in1(8'h1), .out(multiplexer_112_out[31:24]), .sel(comparator_42_eq));
  Multiplexer #(.width(8)) multiplexer_107 (
    .in0({8{1'b0}}), .in1(8'h1), .out(multiplexer_112_out[23:16]));  // open: sel
  Multiplexer #(.width(8)) multiplexer_108 (
    .in0({8{1'b0}}), .in1(8'h1), .out(multiplexer_123_out[55:48]), .sel(comparator_47_eq));
  Adder adder_8 (.a(argY[63:56]), .b(argZ[63:56]), .out(adder_15_out[63:56]), .cout(adder_8_cout));  // open: cin
  assign bit_extender_63_out[63:56] = {{7{1'b0}}, adder_8_cout};  // Bit_Extender bit_extender_56
  Adder adder_9 (.a(argY[55:48]), .b(argZ[55:48]), .out(adder_15_out[55:48]), .cout(adder_9_cout));  // open: cin
  assign bit_extender_63_out[55:48] = {{7{1'b0}}, adder_9_cout};  // Bit_Extender bit_extender_57
  Adder adder_10 (.a(argY[47:40]), .b(argZ[47:40]), .out(adder_15_out[47:40]), .cout(adder_10_cout));  // open: cin
  assign bit_extender_63_out[47:40] = {{7{1'b0}}, adder_10_cout};  // Bit_Extender bit_extender_58
  Adder adder_11 (.a(argY[39:32]), .b(argZ[39:32]), .out(adder_15_out[39:32]), .cout(adder_11_cout));  // open: cin
  assign bit_extender_63_out[39:32] = {{7{1'b0}}, adder_11_cout};  // Bit_Extender bit_extender_59
  Adder adder_12 (.a(argY[31:24]), .b(argZ[31:24]), .out(adder_15_out[31:24]), .cout(adder_12_cout));  // open: cin
  assign bit_extender_63_out[31:24] = {{7{1'b0}}, adder_12_cout};  // Bit_Extender bit_extender_60
  Adder adder_13 (.a(argY[23:16]), .b(argZ[23:16]), .out(adder_15_out[23:16]), .cout(adder_13_cout));  // open: cin
  assign bit_extender_63_out[23:16] = {{7{1'b0}}, adder_13_cout};  // Bit_Extender bit_extender_61
  Adder adder_14 (.a(argY[15:8]), .b(argZ[15:8]), .out(adder_15_out[15:8]), .cout(adder_14_cout));  // open: cin
  assign bit_extender_63_out[15:8] = {{7{1'b0}}, adder_14_cout};  // Bit_Extender bit_extender_62
  Adder adder_15 (.a(argY[7:0]), .b(argZ[7:0]), .out(adder_15_out[7:0]), .cout(adder_15_cout));  // open: cin
  assign bit_extender_63_out[7:0] = {{7{1'b0}}, adder_15_cout};  // Bit_Extender bit_extender_63
  Multiplexer #(.width(8)) multiplexer_109 (
    .in0({8{1'b0}}), .in1(8'h1), .out(multiplexer_112_out[15:8]), .sel(comparator_44_eq));
  Multiplexer #(.width(8)) multiplexer_110 (
    .in0({8{1'b0}}), .in1(8'h1), .out(multiplexer_123_out[47:40]), .sel(comparator_48_eq));
  Multiplexer #(.width(8)) multiplexer_111 (
    .in0({8{1'b0}}), .in1(8'h1), .out(multiplexer_123_out[39:32]), .sel(comparator_49_eq));
  // FPClassificator #(.fpwidth(8)) fpclassificator_8: pin names not known; wires that end beside it: argY[63:56], fpclassificator_8_p2, fpclassificator_8_p3
  // FPClassificator #(.fpwidth(8)) fpclassificator_9: pin names not known; wires that end beside it: argY[55:48], fpclassificator_9_p2, fpclassificator_9_p3
  // FPClassificator #(.fpwidth(8)) fpclassificator_10: pin names not known; wires that end beside it: argY[47:40], fpclassificator_10_p2, fpclassificator_10_p3
  // FPClassificator #(.fpwidth(8)) fpclassificator_11: pin names not known; wires that end beside it: argY[39:32], fpclassificator_11_p2, fpclassificator_11_p3
  // FPClassificator #(.fpwidth(8)) fpclassificator_12: pin names not known; wires that end beside it: argY[31:24], fpclassificator_12_p2, fpclassificator_12_p3
  // FPClassificator #(.fpwidth(8)) fpclassificator_13: pin names not known; wires that end beside it: argY[23:16], fpclassificator_13_p2, fpclassificator_13_p3
  // FPClassificator #(.fpwidth(8)) fpclassificator_14: pin names not known; wires that end beside it: argY[15:8], fpclassificator_14_p2, fpclassificator_14_p3
  // FPClassificator #(.fpwidth(8)) fpclassificator_15: pin names not known; wires that end beside it: argY[7:0], fpclassificator_15_p2, fpclassificator_15_p3
  BitFinder #(.\type ("low0"), .width(16)) bitfinder_21 (
    .in(argY[63:48]), .index(bitfinder_21_index), .found(bitfinder_21_found));
  BitFinder #(.\type ("low0"), .width(16)) bitfinder_22 (
    .in(argY[47:32]), .index(bitfinder_22_index), .found(bitfinder_22_found));
  BitFinder #(.\type ("low0"), .width(16)) bitfinder_23 (
    .in(argY[31:16]), .index(bitfinder_23_index), .found(bitfinder_23_found));
  BitFinder #(.\type ("low0"), .width(16)) bitfinder_24 (
    .in(argY[15:0]), .index(bitfinder_24_index), .found(bitfinder_24_found));
  Multiplexer #(.width(8)) multiplexer_112 (
    .in0({8{1'b0}}), .in1(8'h1), .out(multiplexer_112_out[7:0]), .sel(comparator_45_eq));
  Multiplexer #(.width(8)) multiplexer_113 (
    .in0({8{1'b0}}), .in1(8'h1), .out(multiplexer_123_out[31:24]), .sel(comparator_50_eq));
  assign bit_extender_78_out[63:56] = {{7{1'b0}}, fpclassificator_8_p2};  // Bit_Extender bit_extender_64
  assign bit_extender_79_out[63:56] = {{7{1'b0}}, fpclassificator_8_p3};  // Bit_Extender bit_extender_65
  assign bit_extender_78_out[55:48] = {{7{1'b0}}, fpclassificator_9_p2};  // Bit_Extender bit_extender_66
  assign bit_extender_79_out[55:48] = {{7{1'b0}}, fpclassificator_9_p3};  // Bit_Extender bit_extender_67
  assign bit_extender_78_out[47:40] = {{7{1'b0}}, fpclassificator_10_p2};  // Bit_Extender bit_extender_68
  assign bit_extender_79_out[47:40] = {{7{1'b0}}, fpclassificator_10_p3};  // Bit_Extender bit_extender_69
  assign bit_extender_78_out[39:32] = {{7{1'b0}}, fpclassificator_11_p2};  // Bit_Extender bit_extender_70
  assign bit_extender_79_out[39:32] = {{7{1'b0}}, fpclassificator_11_p3};  // Bit_Extender bit_extender_71
  assign bit_extender_78_out[31:24] = {{7{1'b0}}, fpclassificator_12_p2};  // Bit_Extender bit_extender_72
  assign bit_extender_79_out[31:24] = {{7{1'b0}}, fpclassificator_12_p3};  // Bit_Extender bit_extender_73
  assign bit_extender_78_out[23:16] = {{7{1'b0}}, fpclassificator_13_p2};  // Bit_Extender bit_extender_74
  assign bit_extender_79_out[23:16] = {{7{1'b0}}, fpclassificator_13_p3};  // Bit_Extender bit_extender_75
  assign bit_extender_78_out[15:8] = {{7{1'b0}}, fpclassificator_14_p2};  // Bit_Extender bit_extender_76
  assign bit_extender_79_out[15:8] = {{7{1'b0}}, fpclassificator_14_p3};  // Bit_Extender bit_extender_77
  assign bit_extender_78_out[7:0] = {{7{1'b0}}, fpclassificator_15_p2};  // Bit_Extender bit_extender_78
  assign bit_extender_79_out[7:0] = {{7{1'b0}}, fpclassificator_15_p3};  // Bit_Extender bit_extender_79
  Shifter #(.shift("rl")) shifter_60 (.in(argY[63:56]), .\dist (bitselector_30_out), .out(shifter_67_out[63:56]));
  Shifter #(.shift("rl")) shifter_61 (.in(argY[55:48]), .\dist (bitselector_29_out), .out(shifter_67_out[55:48]));
  Shifter #(.shift("rl")) shifter_62 (.in(argY[47:40]), .\dist (bitselector_28_out), .out(shifter_67_out[47:40]));
  Shifter #(.shift("rl")) shifter_63 (.in(argY[39:32]), .\dist (bitselector_27_out), .out(shifter_67_out[39:32]));
  Shifter #(.shift("rl")) shifter_64 (.in(argY[31:24]), .\dist (bitselector_26_out), .out(shifter_67_out[31:24]));
  Shifter #(.shift("rl")) shifter_65 (.in(argY[23:16]), .\dist (bitselector_25_out), .out(shifter_67_out[23:16]));
  Shifter #(.shift("rl")) shifter_66 (.in(argY[15:8]), .\dist (bitselector_24_out), .out(shifter_67_out[15:8]));
  Shifter #(.shift("rl")) shifter_67 (.in(argY[7:0]), .\dist (bitselector_23_out), .out(shifter_67_out[7:0]));
  assign bit_extender_80_out = {{12{1'b0}}, bitfinder_21_index};  // Bit_Extender bit_extender_80
  Multiplexer #(.width(16)) multiplexer_114 (
    .in0({16{1'b1}}), .in1(bit_extender_80_out), .out(multiplexer_117_out[63:48]), .sel(bitfinder_21_found));
  assign bit_extender_81_out = {{12{1'b0}}, bitfinder_22_index};  // Bit_Extender bit_extender_81
  Multiplexer #(.width(16)) multiplexer_115 (
    .in0({16{1'b1}}), .in1(bit_extender_81_out), .out(multiplexer_117_out[47:32]), .sel(bitfinder_22_found));
  assign bit_extender_82_out = {{12{1'b0}}, bitfinder_23_index};  // Bit_Extender bit_extender_82
  Multiplexer #(.width(16)) multiplexer_116 (
    .in0({16{1'b1}}), .in1(bit_extender_82_out), .out(multiplexer_117_out[31:16]), .sel(bitfinder_23_found));
  assign bit_extender_83_out = {{12{1'b0}}, bitfinder_24_index};  // Bit_Extender bit_extender_83
  Multiplexer #(.width(16)) multiplexer_117 (
    .in0({16{1'b1}}), .in1(bit_extender_83_out), .out(multiplexer_117_out[15:0]), .sel(bitfinder_24_found));
  Multiplexer #(.width(8)) multiplexer_118 (
    .in0({8{1'b0}}), .in1(8'h1), .out(multiplexer_135_out[63:56]), .sel(comparator_38_lt));
  Multiplexer #(.width(8)) multiplexer_119 (
    .in0({8{1'b0}}), .in1(8'h1), .out(multiplexer_123_out[23:16]), .sel(comparator_51_eq));
  Multiplexer #(.width(8)) multiplexer_120 (
    .in0({8{1'b0}}), .in1(8'h1), .out(multiplexer_135_out[55:48]), .sel(comparator_39_lt));
  Multiplexer #(.width(8)) multiplexer_121 (
    .in0({8{1'b0}}), .in1(8'h1), .out(multiplexer_135_out[47:40]), .sel(comparator_40_lt));
  Multiplexer #(.width(8)) multiplexer_122 (
    .in0({8{1'b0}}), .in1(8'h1), .out(multiplexer_123_out[15:8]), .sel(comparator_52_eq));
  Multiplexer #(.width(8)) multiplexer_123 (
    .in0({8{1'b0}}), .in1(8'h1), .out(multiplexer_123_out[7:0]), .sel(comparator_53_eq));
  BitFinder #(.\type ("high0"), .width(16)) bitfinder_25 (
    .in(argY[63:48]), .index(bitfinder_25_index), .found(bitfinder_25_found));
  BitFinder #(.\type ("high0"), .width(16)) bitfinder_26 (
    .in(argY[47:32]), .index(bitfinder_26_index), .found(bitfinder_26_found));
  BitFinder #(.\type ("high0"), .width(16)) bitfinder_27 (
    .in(argY[31:16]), .index(bitfinder_27_index), .found(bitfinder_27_found));
  BitFinder #(.\type ("high0"), .width(16)) bitfinder_28 (
    .in(argY[15:0]), .index(bitfinder_28_index), .found(bitfinder_28_found));
  Multiplexer #(.width(8)) multiplexer_124 (
    .in0({8{1'b0}}), .in1(8'h1), .out(multiplexer_135_out[39:32]), .sel(comparator_41_lt));
  assign bit_extender_84_out = {{12{1'b0}}, bitfinder_25_index};  // Bit_Extender bit_extender_84
  Multiplexer #(.width(16)) multiplexer_125 (
    .in0({16{1'b1}}), .in1(bit_extender_84_out), .out(multiplexer_128_out[63:48]), .sel(bitfinder_25_found));
  assign bit_extender_85_out = {{12{1'b0}}, bitfinder_26_index};  // Bit_Extender bit_extender_85
  Multiplexer #(.width(16)) multiplexer_126 (
    .in0({16{1'b1}}), .in1(bit_extender_85_out), .out(multiplexer_128_out[47:32]), .sel(bitfinder_26_found));
  assign bit_extender_86_out = {{12{1'b0}}, bitfinder_27_index};  // Bit_Extender bit_extender_86
  Multiplexer #(.width(16)) multiplexer_127 (
    .in0({16{1'b1}}), .in1(bit_extender_86_out), .out(multiplexer_128_out[31:16]), .sel(bitfinder_27_found));
  assign bit_extender_87_out = {{12{1'b0}}, bitfinder_28_index};  // Bit_Extender bit_extender_87
  Multiplexer #(.width(16)) multiplexer_128 (
    .in0({16{1'b1}}), .in1(bit_extender_87_out), .out(multiplexer_128_out[15:0]), .sel(bitfinder_28_found));
  Subtractor subtractor_8 (
    .a(argY[63:56]), .b(argZ[63:56]), .out(subtractor_15_out[63:56]), .bout(subtractor_8_bout));  // open: bin
  assign bit_extender_95_out[63:56] = {{7{1'b0}}, subtractor_8_bout};  // Bit_Extender bit_extender_88
  Subtractor subtractor_9 (
    .a(argY[55:48]), .b(argZ[55:48]), .out(subtractor_15_out[55:48]), .bout(subtractor_9_bout));  // open: bin
  assign bit_extender_95_out[55:48] = {{7{1'b0}}, subtractor_9_bout};  // Bit_Extender bit_extender_89
  Subtractor subtractor_10 (
    .a(argY[47:40]), .b(argZ[47:40]), .out(subtractor_15_out[47:40]), .bout(subtractor_10_bout));  // open: bin
  assign bit_extender_95_out[47:40] = {{7{1'b0}}, subtractor_10_bout};  // Bit_Extender bit_extender_90
  Subtractor subtractor_11 (
    .a(argY[39:32]), .b(argZ[39:32]), .out(subtractor_15_out[39:32]), .bout(subtractor_11_bout));  // open: bin
  assign bit_extender_95_out[39:32] = {{7{1'b0}}, subtractor_11_bout};  // Bit_Extender bit_extender_91
  Subtractor subtractor_12 (
    .a(argY[31:24]), .b(argZ[31:24]), .out(subtractor_15_out[31:24]), .bout(subtractor_12_bout));  // open: bin
  assign bit_extender_95_out[31:24] = {{7{1'b0}}, subtractor_12_bout};  // Bit_Extender bit_extender_92
  Subtractor subtractor_13 (
    .a(argY[23:16]), .b(argZ[23:16]), .out(subtractor_15_out[23:16]), .bout(subtractor_13_bout));  // open: bin
  assign bit_extender_95_out[23:16] = {{7{1'b0}}, subtractor_13_bout};  // Bit_Extender bit_extender_93
  Subtractor subtractor_14 (
    .a(argY[15:8]), .b(argZ[15:8]), .out(subtractor_15_out[15:8]), .bout(subtractor_14_bout));  // open: bin
  assign bit_extender_95_out[15:8] = {{7{1'b0}}, subtractor_14_bout};  // Bit_Extender bit_extender_94
  Subtractor subtractor_15 (
    .a(argY[7:0]), .b(argZ[7:0]), .out(subtractor_15_out[7:0]), .bout(subtractor_15_bout));  // open: bin
  assign bit_extender_95_out[7:0] = {{7{1'b0}}, subtractor_15_bout};  // Bit_Extender bit_extender_95
  Multiplexer #(.width(8)) multiplexer_129 (
    .in0({8{1'b0}}), .in1(8'h1), .out(multiplexer_135_out[31:24]), .sel(comparator_42_lt));
  Multiplexer #(.width(8)) multiplexer_130 (
    .in0({8{1'b0}}), .in1(8'h1), .out(multiplexer_142_out[63:56]), .sel(comparator_46_lt));
  Multiplexer #(.width(8)) multiplexer_131 (
    .in0({8{1'b0}}), .in1(8'h1), .out(multiplexer_142_out[55:48]), .sel(comparator_47_lt));
  Shifter #(.shift("rr")) shifter_68 (.in(argY[63:56]), .\dist (bitselector_30_out), .out(shifter_75_out[63:56]));
  Shifter #(.shift("rr")) shifter_69 (.in(argY[55:48]), .\dist (bitselector_29_out), .out(shifter_75_out[55:48]));
  Shifter #(.shift("rr")) shifter_70 (.in(argY[47:40]), .\dist (bitselector_28_out), .out(shifter_75_out[47:40]));
  Shifter #(.shift("rr")) shifter_71 (.in(argY[39:32]), .\dist (bitselector_27_out), .out(shifter_75_out[39:32]));
  Shifter #(.shift("rr")) shifter_72 (.in(argY[31:24]), .\dist (bitselector_26_out), .out(shifter_75_out[31:24]));
  Shifter #(.shift("rr")) shifter_73 (.in(argY[23:16]), .\dist (bitselector_25_out), .out(shifter_75_out[23:16]));
  Shifter #(.shift("rr")) shifter_74 (.in(argY[15:8]), .\dist (bitselector_24_out), .out(shifter_75_out[15:8]));
  Shifter #(.shift("rr")) shifter_75 (.in(argY[7:0]), .\dist (bitselector_23_out), .out(shifter_75_out[7:0]));
  Multiplexer #(.width(8)) multiplexer_132 (
    .in0({8{1'b0}}), .in1(8'h1), .out(multiplexer_135_out[23:16]), .sel(comparator_43_lt));
  Multiplexer #(.width(8)) multiplexer_133 (
    .in0({8{1'b0}}), .in1(8'h1), .out(multiplexer_135_out[15:8]), .sel(comparator_44_lt));
  Multiplexer #(.width(8)) multiplexer_134 (
    .in0({8{1'b0}}), .in1(8'h1), .out(multiplexer_142_out[47:40]), .sel(comparator_48_lt));
  Multiplexer #(.width(8)) multiplexer_135 (
    .in0({8{1'b0}}), .in1(8'h1), .out(multiplexer_135_out[7:0]), .sel(comparator_45_lt));
  Multiplexer #(.width(8)) multiplexer_136 (
    .in0({8{1'b0}}), .in1(8'h1), .out(multiplexer_142_out[39:32]), .sel(comparator_49_lt));
  BitAdder bitadder_8 (.in0(argY[63:56]), .out(bitadder_8_out));
  BitAdder bitadder_9 (.in0(argY[55:48]), .out(bitadder_9_out));
  BitAdder bitadder_10 (.in0(argY[47:40]), .out(bitadder_10_out));
  BitAdder bitadder_11 (.in0(argY[39:32]), .out(bitadder_11_out));
  BitAdder bitadder_12 (.in0(argY[31:24]), .out(bitadder_12_out));
  BitAdder bitadder_13 (.in0(argY[23:16]), .out(bitadder_13_out));
  BitAdder bitadder_14 (.in0(argY[15:8]), .out(bitadder_14_out));
  BitAdder bitadder_15 (.in0(argY[7:0]), .out(bitadder_15_out));
  Multiplexer #(.width(8)) multiplexer_137 (
    .in0({8{1'b0}}), .in1(8'h1), .out(multiplexer_142_out[31:24]), .sel(comparator_50_lt));
  Multiplexer #(.width(8)) multiplexer_138 (
    .in0({8{1'b0}}), .in1(8'h1), .out(multiplexer_142_out[23:16]), .sel(comparator_51_lt));
  assign bit_extender_103_out[63:56] = {{4{1'b0}}, bitadder_8_out};  // Bit_Extender bit_extender_96
  assign bit_extender_103_out[55:48] = {{4{1'b0}}, bitadder_9_out};  // Bit_Extender bit_extender_97
  assign bit_extender_103_out[47:40] = {{4{1'b0}}, bitadder_10_out};  // Bit_Extender bit_extender_98
  assign bit_extender_103_out[39:32] = {{4{1'b0}}, bitadder_11_out};  // Bit_Extender bit_extender_99
  assign bit_extender_103_out[31:24] = {{4{1'b0}}, bitadder_12_out};  // Bit_Extender bit_extender_100
  assign bit_extender_103_out[23:16] = {{4{1'b0}}, bitadder_13_out};  // Bit_Extender bit_extender_101
  assign bit_extender_103_out[15:8] = {{4{1'b0}}, bitadder_14_out};  // Bit_Extender bit_extender_102
  assign bit_extender_103_out[7:0] = {{4{1'b0}}, bitadder_15_out};  // Bit_Extender bit_extender_103
  Multiplexer #(.width(8)) multiplexer_139 (
    .in0({8{1'b0}}), .in1(8'h1), .out(multiplexer_158_out[63:56]), .sel(fpcomparator_15_p3));
  // FPComparator #(.fpwidth(8)) fpcomparator_15: pin names not known; wires that end beside it: argY[63:56], {8{1'b0}}, fpcomparator_15_p3, fpcomparator_15_p4
  // FPComparator #(.fpwidth(8)) fpcomparator_16: pin names not known; wires that end beside it: argY[55:48], {8{1'b0}}, fpcomparator_16_p3, fpcomparator_16_p4
  // FPComparator #(.fpwidth(8)) fpcomparator_17: pin names not known; wires that end beside it: argY[47:40], {8{1'b0}}, fpcomparator_17_p3, fpcomparator_17_p4
  // FPComparator #(.fpwidth(8)) fpcomparator_18: pin names not known; wires that end beside it: argY[39:32], {8{1'b0}}, fpcomparator_18_p3, fpcomparator_18_p4
  // FPComparator #(.fpwidth(8)) fpcomparator_19: pin names not known; wires that end beside it: argY[31:24], {8{1'b0}}, fpcomparator_19_p3, fpcomparator_19_p4
  // FPComparator #(.fpwidth(8)) fpcomparator_20: pin names not known; wires that end beside it: argY[23:16], {8{1'b0}}, fpcomparator_20_p3, fpcomparator_20_p4
  // FPComparator #(.fpwidth(8)) fpcomparator_21: pin names not known; wires that end beside it: argY[15:8], {8{1'b0}}, fpcomparator_21_p3, fpcomparator_21_p4
  // FPComparator #(.fpwidth(8)) fpcomparator_22: pin names not known; wires that end beside it: argY[7:0], {8{1'b0}}, fpcomparator_22_p3, fpcomparator_22_p4
  Multiplexer #(.width(8)) multiplexer_140 (
    .in0({8{1'b0}}), .in1(8'h1), .out(multiplexer_142_out[15:8]), .sel(comparator_52_lt));
  Multiplier #(.mode("twosComplement")) multiplier_8 (
    .a(argY[63:56]), .b(argZ[63:56]), .out(multiplier_15_out[63:56]), .cout(multiplier_15_cout[63:56]));  // open: cin
  Multiplier #(.mode("twosComplement")) multiplier_9 (
    .a(argY[55:48]), .b(argZ[55:48]), .out(multiplier_15_out[55:48]), .cout(multiplier_15_cout[55:48]));  // open: cin
  Multiplier #(.mode("twosComplement")) multiplier_10 (
    .a(argY[47:40]), .b(argZ[47:40]), .out(multiplier_15_out[47:40]), .cout(multiplier_15_cout[47:40]));  // open: cin
  Multiplier #(.mode("twosComplement")) multiplier_11 (
    .a(argY[39:32]), .b(argZ[39:32]), .out(multiplier_15_out[39:32]), .cout(multiplier_15_cout[39:32]));  // open: cin
  Multiplier #(.mode("twosComplement")) multiplier_12 (
    .a(argY[31:24]), .b(argZ[31:24]), .out(multiplier_15_out[31:24]), .cout(multiplier_15_cout[31:24]));  // open: cin
  Multiplier #(.mode("twosComplement")) multiplier_13 (
    .a(argY[23:16]), .b(argZ[23:16]), .out(multiplier_15_out[23:16]), .cout(multiplier_15_cout[23:16]));  // open: cin
  Multiplier #(.mode("twosComplement")) multiplier_14 (
    .a(argY[15:8]), .b(argZ[15:8]), .out(multiplier_15_out[15:8]), .cout(multiplier_15_cout[15:8]));  // open: cin
  Multiplier #(.mode("twosComplement")) multiplier_15 (
    .a(argY[7:0]), .b(argZ[7:0]), .out(multiplier_15_out[7:0]), .cout(multiplier_15_cout[7:0]));  // open: cin
  Multiplexer #(.width(8)) multiplexer_141 (
    .in0({8{1'b0}}), .in1(8'h1), .out(multiplexer_158_out[55:48]), .sel(fpcomparator_16_p3));
  Multiplexer #(.width(8)) multiplexer_142 (
    .in0({8{1'b0}}), .in1(8'h1), .out(multiplexer_142_out[7:0]), .sel(comparator_53_lt));
  BitFinder bitfinder_29 (.in(argY[63:56]), .index(bitfinder_29_index), .found(bitfinder_29_found));
  BitFinder bitfinder_30 (.in(argY[55:48]), .index(bitfinder_30_index), .found(bitfinder_30_found));
  BitFinder bitfinder_31 (.in(argY[47:40]), .index(bitfinder_31_index), .found(bitfinder_31_found));
  BitFinder bitfinder_32 (.in(argY[39:32]), .index(bitfinder_32_index), .found(bitfinder_32_found));
  BitFinder bitfinder_33 (.in(argY[31:24]), .index(bitfinder_33_index), .found(bitfinder_33_found));
  BitFinder bitfinder_34 (.in(argY[23:16]), .index(bitfinder_34_index), .found(bitfinder_34_found));
  BitFinder bitfinder_35 (.in(argY[15:8]), .index(bitfinder_35_index), .found(bitfinder_35_found));
  BitFinder bitfinder_36 (.in(argY[7:0]), .index(bitfinder_36_index), .found(bitfinder_36_found));
  Multiplexer #(.width(8)) multiplexer_143 (
    .in0({8{1'b0}}), .in1(8'h1), .out(multiplexer_158_out[47:40]), .sel(fpcomparator_17_p3));
  Multiplexer #(.width(8)) multiplexer_144 (
    .in0({8{1'b0}}), .in1(8'h1), .out(multiplexer_158_out[39:32]), .sel(fpcomparator_18_p3));
  assign bit_extender_104_out = {{5{1'b0}}, bitfinder_29_index};  // Bit_Extender bit_extender_104
  assign bit_extender_105_out = {{5{1'b0}}, bitfinder_30_index};  // Bit_Extender bit_extender_105
  assign bit_extender_106_out = {{5{1'b0}}, bitfinder_31_index};  // Bit_Extender bit_extender_106
  assign bit_extender_107_out = {{5{1'b0}}, bitfinder_32_index};  // Bit_Extender bit_extender_107
  assign bit_extender_108_out = {{5{1'b0}}, bitfinder_33_index};  // Bit_Extender bit_extender_108
  assign bit_extender_109_out = {{5{1'b0}}, bitfinder_34_index};  // Bit_Extender bit_extender_109
  assign bit_extender_110_out = {{5{1'b0}}, bitfinder_35_index};  // Bit_Extender bit_extender_110
  assign bit_extender_111_out = {{5{1'b0}}, bitfinder_36_index};  // Bit_Extender bit_extender_111
  Multiplexer #(.width(8)) multiplexer_145 (
    .in0({8{1'b0}}), .in1(8'h1), .out(multiplexer_158_out[31:24]), .sel(fpcomparator_19_p3));
  // FPComparator #(.fpwidth(8)) fpcomparator_23: pin names not known; wires that end beside it: argY[63:56], argZ[63:56], fpcomparator_23_p3, fpcomparator_23_p4
  // FPComparator #(.fpwidth(8)) fpcomparator_24: pin names not known; wires that end beside it: argY[55:48], argZ[55:48], fpcomparator_24_p3, fpcomparator_24_p4
  // FPComparator #(.fpwidth(8)) fpcomparator_25: pin names not known; wires that end beside it: argY[47:40], argZ[47:40], fpcomparator_25_p3, fpcomparator_25_p4
  // FPComparator #(.fpwidth(8)) fpcomparator_26: pin names not known; wires that end beside it: argY[39:32], argZ[39:32], fpcomparator_26_p3, fpcomparator_26_p4
  // FPComparator #(.fpwidth(8)) fpcomparator_27: pin names not known; wires that end beside it: argY[31:24], argZ[31:24], fpcomparator_27_p3, fpcomparator_27_p4
  // FPComparator #(.fpwidth(8)) fpcomparator_28: pin names not known; wires that end beside it: argY[23:16], argZ[23:16], fpcomparator_28_p3, fpcomparator_28_p4
  // FPComparator #(.fpwidth(8)) fpcomparator_29: pin names not known; wires that end beside it: argY[15:8], argZ[15:8], fpcomparator_29_p3, fpcomparator_29_p4
  // FPComparator #(.fpwidth(8)) fpcomparator_30: pin names not known; wires that end beside it: argY[7:0], argZ[7:0], fpcomparator_30_p3, fpcomparator_30_p4
  Multiplexer #(.width(8)) multiplexer_146 (
    .in0({8{1'b1}}), .in1(bit_extender_104_out), .out(multiplexer_153_out[63:56]), .sel(bitfinder_29_found));
  Multiplexer #(.width(8)) multiplexer_147 (
    .in0({8{1'b1}}), .in1(bit_extender_105_out), .out(multiplexer_153_out[55:48]), .sel(bitfinder_30_found));
  Multiplexer #(.width(8)) multiplexer_148 (
    .in0({8{1'b1}}), .in1(bit_extender_106_out), .out(multiplexer_153_out[47:40]), .sel(bitfinder_31_found));
  Multiplexer #(.width(8)) multiplexer_149 (
    .in0({8{1'b1}}), .in1(bit_extender_107_out), .out(multiplexer_153_out[39:32]), .sel(bitfinder_32_found));
  Multiplexer #(.width(8)) multiplexer_150 (
    .in0({8{1'b1}}), .in1(bit_extender_108_out), .out(multiplexer_153_out[31:24]), .sel(bitfinder_33_found));
  Multiplexer #(.width(8)) multiplexer_151 (
    .in0({8{1'b1}}), .in1(bit_extender_109_out), .out(multiplexer_153_out[23:16]), .sel(bitfinder_34_found));
  Multiplexer #(.width(8)) multiplexer_152 (
    .in0({8{1'b1}}), .in1(bit_extender_110_out), .out(multiplexer_153_out[15:8]), .sel(bitfinder_35_found));
  Multiplexer #(.width(8)) multiplexer_153 (
    .in0({8{1'b1}}), .in1(bit_extender_111_out), .out(multiplexer_153_out[7:0]), .sel(bitfinder_36_found));
  Multiplexer #(.width(8)) multiplexer_154 (
    .in0({8{1'b0}}), .in1(8'h1), .out(multiplexer_158_out[23:16]), .sel(fpcomparator_20_p3));
  Multiplexer #(.width(8)) multiplexer_155 (
    .in0({8{1'b0}}), .in1(8'h1), .out(multiplexer_176_out[63:56]), .sel(fpcomparator_23_p3));
  Multiplexer #(.width(8)) multiplexer_156 (
    .in0({8{1'b0}}), .in1(8'h1), .out(multiplexer_176_out[55:48]), .sel(fpcomparator_24_p3));
  Multiplexer #(.width(8)) multiplexer_157 (
    .in0({8{1'b0}}), .in1(8'h1), .out(multiplexer_158_out[15:8]), .sel(fpcomparator_21_p3));
  Multiplexer #(.width(8)) multiplexer_158 (.in0({8{1'b0}}), .in1(8'h1), .out(multiplexer_158_out[7:0]));  // open: sel
  Multiplexer #(.width(8)) multiplexer_159 (
    .in0({8{1'b0}}), .in1(8'h1), .out(multiplexer_176_out[47:40]), .sel(fpcomparator_25_p3));
  BitFinder #(.\type ("high1")) bitfinder_37 (.in(argY[63:56]), .index(bitfinder_37_index), .found(bitfinder_37_found));
  BitFinder #(.\type ("high1")) bitfinder_38 (.in(argY[55:48]), .index(bitfinder_38_index), .found(bitfinder_38_found));
  BitFinder #(.\type ("high1")) bitfinder_39 (.in(argY[47:40]), .index(bitfinder_39_index), .found(bitfinder_39_found));
  BitFinder #(.\type ("high1")) bitfinder_40 (.in(argY[39:32]), .index(bitfinder_40_index), .found(bitfinder_40_found));
  BitFinder #(.\type ("high1")) bitfinder_41 (.in(argY[31:24]), .index(bitfinder_41_index), .found(bitfinder_41_found));
  BitFinder #(.\type ("high1")) bitfinder_42 (.in(argY[23:16]), .index(bitfinder_42_index), .found(bitfinder_42_found));
  BitFinder #(.\type ("high1")) bitfinder_43 (.in(argY[15:8]), .index(bitfinder_43_index), .found(bitfinder_43_found));
  BitFinder #(.\type ("high1")) bitfinder_44 (.in(argY[7:0]), .index(bitfinder_44_index), .found(bitfinder_44_found));
  Divider #(.mode("twosComplement")) divider_8 (
    .a(argY[63:56]), .b(argZ[63:56]), .out(divider_15_out[63:56]), .rem(divider_15_rem[63:56]));  // open: upper
  Divider #(.mode("twosComplement")) divider_9 (
    .a(argY[55:48]), .b(argZ[55:48]), .out(divider_15_out[55:48]), .rem(divider_15_rem[55:48]));  // open: upper
  Divider #(.mode("twosComplement")) divider_10 (
    .a(argY[47:40]), .b(argZ[47:40]), .out(divider_15_out[47:40]), .rem(divider_15_rem[47:40]));  // open: upper
  Divider #(.mode("twosComplement")) divider_11 (
    .a(argY[39:32]), .b(argZ[39:32]), .out(divider_15_out[39:32]), .rem(divider_15_rem[39:32]));  // open: upper
  Divider #(.mode("twosComplement")) divider_12 (
    .a(argY[31:24]), .b(argZ[31:24]), .out(divider_15_out[31:24]), .rem(divider_15_rem[31:24]));  // open: upper
  Divider #(.mode("twosComplement")) divider_13 (
    .a(argY[23:16]), .b(argZ[23:16]), .out(divider_15_out[23:16]), .rem(divider_15_rem[23:16]));  // open: upper
  Divider #(.mode("twosComplement")) divider_14 (
    .a(argY[15:8]), .b(argZ[15:8]), .out(divider_15_out[15:8]), .rem(divider_15_rem[15:8]));  // open: upper
  Divider #(.mode("twosComplement")) divider_15 (
    .a(argY[7:0]), .b(argZ[7:0]), .out(divider_15_out[7:0]), .rem(divider_15_rem[7:0]));  // open: upper
  Multiplexer #(.width(8)) multiplexer_160 (
    .in0({8{1'b0}}), .in1(8'h1), .out(multiplexer_176_out[39:32]), .sel(fpcomparator_26_p3));
  assign bit_extender_112_out = {{5{1'b0}}, bitfinder_37_index};  // Bit_Extender bit_extender_112
  assign bit_extender_113_out = {{5{1'b0}}, bitfinder_38_index};  // Bit_Extender bit_extender_113
  assign bit_extender_114_out = {{5{1'b0}}, bitfinder_39_index};  // Bit_Extender bit_extender_114
  assign bit_extender_115_out = {{5{1'b0}}, bitfinder_40_index};  // Bit_Extender bit_extender_115
  assign bit_extender_116_out = {{5{1'b0}}, bitfinder_41_index};  // Bit_Extender bit_extender_116
  assign bit_extender_117_out = {{5{1'b0}}, bitfinder_42_index};  // Bit_Extender bit_extender_117
  assign bit_extender_118_out = {{5{1'b0}}, bitfinder_43_index};  // Bit_Extender bit_extender_118
  assign bit_extender_119_out = {{5{1'b0}}, bitfinder_44_index};  // Bit_Extender bit_extender_119
  Multiplexer #(.width(8)) multiplexer_161 (
    .in0({8{1'b0}}), .in1(8'h1), .out(multiplexer_190_out[63:56]), .sel(fpcomparator_15_p4));
  Multiplexer #(.width(8)) multiplexer_162 (
    .in0({8{1'b0}}), .in1(8'h1), .out(multiplexer_190_out[55:48]), .sel(fpcomparator_16_p4));
  Multiplexer #(.width(8)) multiplexer_163 (
    .in0({8{1'b0}}), .in1(8'h1), .out(multiplexer_176_out[31:24]), .sel(fpcomparator_27_p3));
  Multiplexer #(.width(8)) multiplexer_164 (
    .in0({8{1'b0}}), .in1(8'h1), .out(multiplexer_176_out[23:16]), .sel(fpcomparator_28_p3));
  Multiplexer #(.width(8)) multiplexer_165 (
    .in0({8{1'b1}}), .in1(bit_extender_112_out), .out(multiplexer_172_out[63:56]), .sel(bitfinder_37_found));
  Multiplexer #(.width(8)) multiplexer_166 (
    .in0({8{1'b1}}), .in1(bit_extender_113_out), .out(multiplexer_172_out[55:48]), .sel(bitfinder_38_found));
  Multiplexer #(.width(8)) multiplexer_167 (
    .in0({8{1'b1}}), .in1(bit_extender_114_out), .out(multiplexer_172_out[47:40]), .sel(bitfinder_39_found));
  Multiplexer #(.width(8)) multiplexer_168 (
    .in0({8{1'b1}}), .in1(bit_extender_115_out), .out(multiplexer_172_out[39:32]), .sel(bitfinder_40_found));
  Multiplexer #(.width(8)) multiplexer_169 (
    .in0({8{1'b1}}), .in1(bit_extender_116_out), .out(multiplexer_172_out[31:24]), .sel(bitfinder_41_found));
  Multiplexer #(.width(8)) multiplexer_170 (
    .in0({8{1'b1}}), .in1(bit_extender_117_out), .out(multiplexer_172_out[23:16]), .sel(bitfinder_42_found));
  Multiplexer #(.width(8)) multiplexer_171 (
    .in0({8{1'b1}}), .in1(bit_extender_118_out), .out(multiplexer_172_out[15:8]), .sel(bitfinder_43_found));
  Multiplexer #(.width(8)) multiplexer_172 (
    .in0({8{1'b1}}), .in1(bit_extender_119_out), .out(multiplexer_172_out[7:0]), .sel(bitfinder_44_found));
  Multiplexer #(.width(8)) multiplexer_173 (
    .in0({8{1'b0}}), .in1(8'h1), .out(multiplexer_190_out[47:40]), .sel(fpcomparator_17_p4));
  Multiplexer #(.width(8)) multiplexer_174 (
    .in0({8{1'b0}}), .in1(8'h1), .out(multiplexer_176_out[15:8]), .sel(fpcomparator_29_p3));
  Multiplexer #(.width(8)) multiplexer_175 (
    .in0({8{1'b0}}), .in1(8'h1), .out(multiplexer_190_out[39:32]), .sel(fpcomparator_18_p4));
  Multiplexer #(.width(8)) multiplexer_176 (
    .in0({8{1'b0}}), .in1(8'h1), .out(multiplexer_176_out[7:0]), .sel(fpcomparator_30_p3));
  BitFinder #(.\type ("low0")) bitfinder_45 (.in(argY[63:56]), .index(bitfinder_45_index), .found(bitfinder_45_found));
  BitFinder #(.\type ("low0")) bitfinder_46 (.in(argY[55:48]), .index(bitfinder_46_index), .found(bitfinder_46_found));
  BitFinder #(.\type ("low0")) bitfinder_47 (.in(argY[47:40]), .index(bitfinder_47_index), .found(bitfinder_47_found));
  BitFinder #(.\type ("low0")) bitfinder_48 (.in(argY[39:32]), .index(bitfinder_48_index), .found(bitfinder_48_found));
  BitFinder #(.\type ("low0")) bitfinder_49 (.in(argY[31:24]), .index(bitfinder_49_index), .found(bitfinder_49_found));
  BitFinder #(.\type ("low0")) bitfinder_50 (.in(argY[23:16]), .index(bitfinder_50_index), .found(bitfinder_50_found));
  BitFinder #(.\type ("low0")) bitfinder_51 (.in(argY[15:8]), .index(bitfinder_51_index), .found(bitfinder_51_found));
  BitFinder #(.\type ("low0")) bitfinder_52 (.in(argY[7:0]), .index(bitfinder_52_index), .found(bitfinder_52_found));
  Multiplexer #(.width(8)) multiplexer_177 (
    .in0({8{1'b0}}), .in1(8'h1), .out(multiplexer_190_out[31:24]), .sel(fpcomparator_19_p4));
  Multiplexer #(.width(8)) multiplexer_178 (
    .in0({8{1'b0}}), .in1(8'h1), .out(multiplexer_190_out[23:16]), .sel(fpcomparator_20_p4));
  Multiplexer #(.width(8)) multiplexer_179 (
    .in0({8{1'b0}}), .in1(8'h1), .out(multiplexer_196_out[63:56]), .sel(fpcomparator_23_p4));
  assign bit_extender_120_out = {{5{1'b0}}, bitfinder_45_index};  // Bit_Extender bit_extender_120
  assign bit_extender_121_out = {{5{1'b0}}, bitfinder_46_index};  // Bit_Extender bit_extender_121
  assign bit_extender_122_out = {{5{1'b0}}, bitfinder_47_index};  // Bit_Extender bit_extender_122
  assign bit_extender_123_out = {{5{1'b0}}, bitfinder_48_index};  // Bit_Extender bit_extender_123
  assign bit_extender_124_out = {{5{1'b0}}, bitfinder_49_index};  // Bit_Extender bit_extender_124
  assign bit_extender_125_out = {{5{1'b0}}, bitfinder_50_index};  // Bit_Extender bit_extender_125
  assign bit_extender_126_out = {{5{1'b0}}, bitfinder_51_index};  // Bit_Extender bit_extender_126
  assign bit_extender_127_out = {{5{1'b0}}, bitfinder_52_index};  // Bit_Extender bit_extender_127
  Multiplexer #(.width(8)) multiplexer_180 (
    .in0({8{1'b0}}), .in1(8'h1), .out(multiplexer_190_out[15:8]), .sel(fpcomparator_21_p4));
  Multiplexer #(.width(8)) multiplexer_181 (
    .in0({8{1'b0}}), .in1(8'h1), .out(multiplexer_196_out[55:48]), .sel(fpcomparator_24_p4));
  Multiplexer #(.width(8)) multiplexer_182 (
    .in0({8{1'b1}}), .in1(bit_extender_120_out), .out(multiplexer_189_out[63:56]), .sel(bitfinder_45_found));
  Multiplexer #(.width(8)) multiplexer_183 (
    .in0({8{1'b1}}), .in1(bit_extender_121_out), .out(multiplexer_189_out[55:48]), .sel(bitfinder_46_found));
  Multiplexer #(.width(8)) multiplexer_184 (
    .in0({8{1'b1}}), .in1(bit_extender_122_out), .out(multiplexer_189_out[47:40]), .sel(bitfinder_47_found));
  Multiplexer #(.width(8)) multiplexer_185 (
    .in0({8{1'b1}}), .in1(bit_extender_123_out), .out(multiplexer_189_out[39:32]), .sel(bitfinder_48_found));
  Multiplexer #(.width(8)) multiplexer_186 (
    .in0({8{1'b1}}), .in1(bit_extender_124_out), .out(multiplexer_189_out[31:24]), .sel(bitfinder_49_found));
  Multiplexer #(.width(8)) multiplexer_187 (
    .in0({8{1'b1}}), .in1(bit_extender_125_out), .out(multiplexer_189_out[23:16]), .sel(bitfinder_50_found));
  Multiplexer #(.width(8)) multiplexer_188 (
    .in0({8{1'b1}}), .in1(bit_extender_126_out), .out(multiplexer_189_out[15:8]), .sel(bitfinder_51_found));
  Multiplexer #(.width(8)) multiplexer_189 (
    .in0({8{1'b1}}), .in1(bit_extender_127_out), .out(multiplexer_189_out[7:0]), .sel(bitfinder_52_found));
  Multiplexer #(.width(8)) multiplexer_190 (
    .in0({8{1'b0}}), .in1(8'h1), .out(multiplexer_190_out[7:0]), .sel(fpcomparator_22_p4));
  Multiplexer #(.width(8)) multiplexer_191 (
    .in0({8{1'b0}}), .in1(8'h1), .out(multiplexer_196_out[47:40]), .sel(fpcomparator_25_p4));
  Multiplexer #(.width(8)) multiplexer_192 (
    .in0({8{1'b0}}), .in1(8'h1), .out(multiplexer_196_out[39:32]), .sel(fpcomparator_26_p4));
  Multiplexer #(.width(8)) multiplexer_193 (
    .in0({8{1'b0}}), .in1(8'h1), .out(multiplexer_196_out[31:24]), .sel(fpcomparator_27_p4));
  BitFinder #(.\type ("high0")) bitfinder_53 (.in(argY[63:56]), .index(bitfinder_53_index), .found(bitfinder_53_found));
  BitFinder #(.\type ("high0")) bitfinder_54 (.in(argY[55:48]), .index(bitfinder_54_index), .found(bitfinder_54_found));
  BitFinder #(.\type ("high0")) bitfinder_55 (.in(argY[47:40]), .index(bitfinder_55_index), .found(bitfinder_55_found));
  BitFinder #(.\type ("high0")) bitfinder_56 (.in(argY[39:32]), .index(bitfinder_56_index), .found(bitfinder_56_found));
  BitFinder #(.\type ("high0")) bitfinder_57 (.in(argY[31:24]), .index(bitfinder_57_index), .found(bitfinder_57_found));
  BitFinder #(.\type ("high0")) bitfinder_58 (.in(argY[23:16]), .index(bitfinder_58_index), .found(bitfinder_58_found));
  BitFinder #(.\type ("high0")) bitfinder_59 (.in(argY[15:8]), .index(bitfinder_59_index), .found(bitfinder_59_found));
  BitFinder #(.\type ("high0")) bitfinder_60 (.in(argY[7:0]), .index(bitfinder_60_index), .found(bitfinder_60_found));
  Multiplexer #(.width(8)) multiplexer_194 (
    .in0({8{1'b0}}), .in1(8'h1), .out(multiplexer_196_out[23:16]), .sel(fpcomparator_28_p4));
  assign bit_extender_128_out = {{5{1'b0}}, bitfinder_53_index};  // Bit_Extender bit_extender_128
  assign bit_extender_129_out = {{5{1'b0}}, bitfinder_54_index};  // Bit_Extender bit_extender_129
  assign bit_extender_130_out = {{5{1'b0}}, bitfinder_55_index};  // Bit_Extender bit_extender_130
  assign bit_extender_131_out = {{5{1'b0}}, bitfinder_56_index};  // Bit_Extender bit_extender_131
  assign bit_extender_132_out = {{5{1'b0}}, bitfinder_57_index};  // Bit_Extender bit_extender_132
  assign bit_extender_133_out = {{5{1'b0}}, bitfinder_58_index};  // Bit_Extender bit_extender_133
  assign bit_extender_134_out = {{5{1'b0}}, bitfinder_59_index};  // Bit_Extender bit_extender_134
  assign bit_extender_135_out = {{5{1'b0}}, bitfinder_60_index};  // Bit_Extender bit_extender_135
  Multiplexer #(.width(8)) multiplexer_195 (
    .in0({8{1'b0}}), .in1(8'h1), .out(multiplexer_196_out[15:8]), .sel(fpcomparator_29_p4));
  Multiplexer #(.width(8)) multiplexer_196 (
    .in0({8{1'b0}}), .in1(8'h1), .out(multiplexer_196_out[7:0]), .sel(fpcomparator_30_p4));
  Multiplexer #(.width(8)) multiplexer_197 (
    .in0({8{1'b1}}), .in1(bit_extender_128_out), .out(multiplexer_204_out[63:56]), .sel(bitfinder_53_found));
  Multiplexer #(.width(8)) multiplexer_198 (
    .in0({8{1'b1}}), .in1(bit_extender_129_out), .out(multiplexer_204_out[55:48]), .sel(bitfinder_54_found));
  Multiplexer #(.width(8)) multiplexer_199 (
    .in0({8{1'b1}}), .in1(bit_extender_130_out), .out(multiplexer_204_out[47:40]), .sel(bitfinder_55_found));
  Multiplexer #(.width(8)) multiplexer_200 (
    .in0({8{1'b1}}), .in1(bit_extender_131_out), .out(multiplexer_204_out[39:32]), .sel(bitfinder_56_found));
  Multiplexer #(.width(8)) multiplexer_201 (
    .in0({8{1'b1}}), .in1(bit_extender_132_out), .out(multiplexer_204_out[31:24]), .sel(bitfinder_57_found));
  Multiplexer #(.width(8)) multiplexer_202 (
    .in0({8{1'b1}}), .in1(bit_extender_133_out), .out(multiplexer_204_out[23:16]), .sel(bitfinder_58_found));
  Multiplexer #(.width(8)) multiplexer_203 (
    .in0({8{1'b1}}), .in1(bit_extender_134_out), .out(multiplexer_204_out[15:8]), .sel(bitfinder_59_found));
  Multiplexer #(.width(8)) multiplexer_204 (
    .in0({8{1'b1}}), .in1(bit_extender_135_out), .out(multiplexer_204_out[7:0]), .sel(bitfinder_60_found));
  Comparator #(.mode("unsigned"), .width(4)) comparator_54 (
    .a(op), .b(4'b1001), .eq(comparator_54_eq));  // open: gt, lt
  Comparator #(.mode("unsigned"), .width(4)) comparator_55 (
    .a(op), .b(4'b1010), .eq(comparator_55_eq));  // open: gt, lt
  Comparator #(.mode("unsigned"), .width(4)) comparator_56 (
    .a(op), .b(4'b1011), .eq(comparator_56_eq));  // open: gt, lt
  Comparator #(.mode("unsigned"), .width(4)) comparator_57 (
    .a(op), .b(4'b1100), .eq(comparator_57_eq));  // open: gt, lt
  Comparator #(.mode("unsigned"), .width(4)) comparator_58 (
    .a(op), .b(4'b1101), .eq(comparator_58_eq));  // open: gt, lt
  Comparator #(.mode("unsigned"), .width(4)) comparator_59 (
    .a(op), .b(4'b1110), .eq(comparator_59_eq));  // open: gt, lt
  Comparator #(.mode("unsigned"), .width(4)) comparator_60 (
    .a(op), .b(4'b1111), .eq(comparator_60_eq));  // open: gt, lt
  Multiplexer #(.select(4), .width(64)) multiplexer_205 (
    .in0(fpadder_1_out), .in1(fpadder_3_out), .in2(fpadder_7_out), .in3(fpadder_15_out),
    .in4(fpsubtractor_1_out), .in5(fpsubtractor_3_out), .in6(fpsubtractor_7_out), .in7(fpsubtractor_15_out),
    .in8(fpmultiplier_1_out), .in9(fpmultiplier_3_out), .in10(fpmultiplier_7_out),
    .in11(fpmultiplier_15_out), .in12(fpdivider_1_out), .in13(fpdivider_3_out), .in14(fpdivider_7_out),
    .in15(fpdivider_15_out), .out(multiplexer_205_out), .sel(\var ));
  FPAdder #(.fpwidth(64)) fpadder_1 (.a(argY), .b(argZ), .out(fpadder_1_out));
  Multiplexer #(.select(4), .width(64)) multiplexer_206 (
    .in0(fpnegator_1_p2), .in1(fpnegator_3_p2), .in2(fpnegator_7_p2), .in3(fpnegator_15_p2),
    .in4(fplogarithm_2_p1), .in5(fplogarithm_6_p3), .in6(fplogarithm_14_p3), .in7(fplogarithm_30_p3),
    .in8(fpexponentiator_2_p1), .in9(fpexponentiator_6_p3), .in10(fpexponentiator_14_p3),
    .in11(fpexponentiator_30_p3), .in12(fpsquareroot_1_p1), .in13(fpsquareroot_3_p2),
    .in14(fpsquareroot_7_p2), .in15(fpsquareroot_15_p2), .out(multiplexer_206_out), .sel(\var ));
  // FPNegator #(.fpwidth(64)) fpnegator_1: pin names not known; wires that end beside it: argY, fpnegator_1_p2, argY, argZ
  Multiplexer #(.select(4), .width(64)) multiplexer_207 (
    .in0(fptrigonometry_1_p2), .in1(fptrigonometry_4_p2), .in2(fptrigonometry_10_p2),
    .in3(fptrigonometry_22_p2), .in4(fptrigonometry_1_p3), .in5(fptrigonometry_4_p3),
    .in6(fptrigonometry_10_p3), .in7(fptrigonometry_22_p3), .in8(fptrigonometry_1_p4),
    .in9(fptrigonometry_4_p4), .in10(fptrigonometry_10_p4), .in11(fptrigonometry_22_p4),
    .in12(fpminmax_1_p3), .in13(fpminmax_4_p3), .in14(fpminmax_10_p3), .in15(fpminmax_22_p3),
    .out(multiplexer_207_out), .sel(\var ));
  // FPTrigonometry #(.fpwidth(64)) fptrigonometry_1: pin names not known; wires that end beside it: argY, fptrigonometry_1_p2, fptrigonometry_1_p3, fptrigonometry_1_p4
  Multiplexer #(.select(4), .width(64)) multiplexer_208 (
    .in0(fptrigonometry_2_p2), .in1(fptrigonometry_6_p2), .in2(fptrigonometry_14_p2),
    .in3(fptrigonometry_30_p2), .in4(fptrigonometry_2_p3), .in5(fptrigonometry_6_p3),
    .in6(fptrigonometry_14_p3), .in7(fptrigonometry_30_p3), .in8(fptrigonometry_2_p4),
    .in9(fptrigonometry_6_p4), .in10(fptrigonometry_14_p4), .in11(fptrigonometry_30_p4),
    .in12(fpminmax_2_p3), .in13(fpminmax_6_p3), .in14(fpminmax_14_p3), .in15(fpminmax_30_p3),
    .out(multiplexer_208_out), .sel(\var ));
  // FPTrigonometry #(.fpwidth(64), .\type ("arc")) fptrigonometry_2: pin names not known; wires that end beside it: argY, fptrigonometry_2_p2, fptrigonometry_2_p3, fptrigonometry_2_p4
  Multiplexer #(.select(4), .width(64)) multiplexer_209 (
    .in0(fplogarithm_1_p2), .in1(fplogarithm_4_p2), .in2(fplogarithm_10_p2), .in3(fplogarithm_22_p2),
    .in4(fpexponentiator_1_p1), .in5(fpexponentiator_4_p2), .in6(fpexponentiator_10_p2),
    .in7(fpexponentiator_22_p2), .in8(fpabsolute_1_p1), .in9(fpabsolute_3_p2), .in10(fpabsolute_7_p2),
    .in11(fpabsolute_15_p2), .in12(fgam_1_outval), .in13(fptofp_4_p1), .in14(fptofp_12_p1),
    .in15(fptofp_31_p1), .out(multiplexer_209_out), .sel(\var ));
  // FPLogarithm #(.fpwidth(64), .mode("log")) fplogarithm_1: pin names not known; wires that end beside it: argY, fplogarithm_1_p2, argY
  Multiplexer #(.select(4), .width(64)) multiplexer_210 (
    .in0(fptoint_1_p2), .in1(fptoint_6_p2), .in2(fptoint_16_p2), .in3(fptoint_36_p2), .in4(fptoint_2_p1),
    .in5(fptoint_8_p2), .in6(fptoint_20_p2), .in7(fptoint_44_p2), .in8(fptoint_3_p1), .in9(fptoint_10_p2),
    .in10(fptoint_24_p2), .in11(fptoint_52_p2), .in12(fptoint_4_p1), .in13(fptoint_12_p2),
    .in14(fptoint_28_p2), .in15(fptoint_60_p2), .out(multiplexer_210_out), .sel(\var ));
  Multiplexer #(.select(4), .width(64)) multiplexer_211 (
    .in0(inttofp_1_p2), .in1(inttofp_3_p2), .in2(inttofp_7_p2), .in3(inttofp_15_p2),
    .in4({argY[31:0], argY[31:0]}), .in5({argY[47:32], argY[47:32], argY[15:0], argY[15:0]}),
    .in6({argY[55:48], argY[55:48], argY[39:32], argY[39:32], argY[23:16], argY[23:16], argY[7:0], argY[7:0]}),
    .in7(bit_extender_136_out), .in8(bit_extender_137_out), .in9(bit_extender_139_out),
    .in10({fptofp_21_p2, fptofp_21_p2}),
    .in11({fptofp_22_p2[63:48], fptofp_22_p2[63:48], fptofp_22_p2[31:16], fptofp_22_p2[31:16]}),
    .in12({fptofp_32_p2[63:56], fptofp_32_p2[63:56], fptofp_32_p2[47:40], fptofp_32_p2[47:40], fptofp_32_p2[31:24], fptofp_32_p2[31:24], fptofp_32_p2[15:8], fptofp_32_p2[15:8]}),
    .in13(fptofp_36_p2), .in14(fptofp_37_p2), .in15(fptofp_39_p2), .out(multiplexer_211_out), .sel(\var ));
  FPSubtractor #(.fpwidth(64)) fpsubtractor_1 (.a(argY), .b(argZ), .out(fpsubtractor_1_out));
  // FPLogarithm #(.fpwidth(64)) fplogarithm_2: pin names not known; wires that end beside it: fplogarithm_2_p1, argY, argZ
  // FPMinMax #(.fpwidth(64)) fpminmax_1: pin names not known; wires that end beside it: argY, argZ, fpminmax_1_p3
  // FPMinMax #(.fpwidth(64)) fpminmax_2: pin names not known; wires that end beside it: argY, argZ, fpminmax_2_p3
  // FPExponentiator #(.fpwidth(64), .mode("exp")) fpexponentiator_1: pin names not known; wires that end beside it: fpexponentiator_1_p1, argY
  // FPToInt #(.fpwidth(64), .width(64)) fptoint_1: pin names not known; wires that end beside it: argY, fptoint_1_p2, argY
  // IntToFP #(.fpwidth(64), .width(64)) inttofp_1: pin names not known; wires that end beside it: argY, inttofp_1_p2
  FPMultiplier #(.fpwidth(64)) fpmultiplier_1 (.a(argY), .b(argZ), .out(fpmultiplier_1_out));
  // FPExponentiator #(.fpwidth(64)) fpexponentiator_2: pin names not known; wires that end beside it: fpexponentiator_2_p1, argY
  // FPAbsolute #(.fpwidth(64)) fpabsolute_1: pin names not known; wires that end beside it: fpabsolute_1_p1
  // FPToInt #(.fpwidth(64), .mode("floor"), .width(64)) fptoint_2: pin names not known; wires that end beside it: fptoint_2_p1, argY
  FPDivider #(.fpwidth(64)) fpdivider_1 (.a(argY), .b(argZ), .out(fpdivider_1_out));
  // FPSquareRoot #(.fpwidth(64)) fpsquareroot_1: pin names not known; wires that end beside it: fpsquareroot_1_p1
  fgam fgam_1 (.inval(argY), .outval(fgam_1_outval));
  // FPToInt #(.fpwidth(64), .mode("ceil"), .width(64)) fptoint_3: pin names not known; wires that end beside it: fptoint_3_p1, argY
  // IntToFP #(.width(32)) inttofp_2: pin names not known; wires that end beside it: argY[63:32], inttofp_3_p2[63:32]
  // IntToFP #(.width(32)) inttofp_3: pin names not known; wires that end beside it: argY[31:0], inttofp_3_p2[31:0]
  // FPTrigonometry fptrigonometry_3: pin names not known; wires that end beside it: argY[63:32], fptrigonometry_4_p2[63:32], fptrigonometry_4_p3[63:32], fptrigonometry_4_p4[63:32]
  // FPTrigonometry fptrigonometry_4: pin names not known; wires that end beside it: argY[31:0], fptrigonometry_4_p2[31:0], fptrigonometry_4_p3[31:0], fptrigonometry_4_p4[31:0]
  // FPTrigonometry #(.\type ("arc")) fptrigonometry_5: pin names not known; wires that end beside it: argY[63:32], fptrigonometry_6_p2[63:32], fptrigonometry_6_p3[63:32], fptrigonometry_6_p4[63:32]
  // FPTrigonometry #(.\type ("arc")) fptrigonometry_6: pin names not known; wires that end beside it: argY[31:0], fptrigonometry_6_p2[31:0], fptrigonometry_6_p3[31:0], fptrigonometry_6_p4[31:0]
  // FPToInt #(.fpwidth(64), .mode("truncate"), .width(64)) fptoint_4: pin names not known; wires that end beside it: fptoint_4_p1
  // IntToFP #(.fpwidth(16), .width(16)) inttofp_4: pin names not known; wires that end beside it: argY[63:48], inttofp_7_p2[63:48]
  // IntToFP #(.fpwidth(16), .width(16)) inttofp_5: pin names not known; wires that end beside it: argY[47:32], inttofp_7_p2[47:32]
  // IntToFP #(.fpwidth(16), .width(16)) inttofp_6: pin names not known; wires that end beside it: argY[31:16], inttofp_7_p2[31:16]
  // IntToFP #(.fpwidth(16), .width(16)) inttofp_7: pin names not known; wires that end beside it: argY[15:0], inttofp_7_p2[15:0]
  FPAdder fpadder_2 (.a(argY[63:32]), .b(argZ[63:32]), .out(fpadder_3_out[63:32]));
  FPAdder fpadder_3 (.a(argY[31:0]), .b(argZ[31:0]), .out(fpadder_3_out[31:0]));
  // FPNegator fpnegator_2: pin names not known; wires that end beside it: argY[63:32], fpnegator_3_p2[63:32]
  // FPNegator fpnegator_3: pin names not known; wires that end beside it: argY[31:0], fpnegator_3_p2[31:0]
  // FPMinMax fpminmax_3: pin names not known; wires that end beside it: argY[63:32], argZ[63:32], fpminmax_4_p3[63:32]
  // FPMinMax fpminmax_4: pin names not known; wires that end beside it: argY[31:0], argZ[31:0], fpminmax_4_p3[31:0]
  // FPMinMax fpminmax_5: pin names not known; wires that end beside it: argY[63:32], argZ[63:32], fpminmax_6_p3[63:32]
  // FPMinMax fpminmax_6: pin names not known; wires that end beside it: argY[31:0], argZ[31:0], fpminmax_6_p3[31:0]
  // FPLogarithm #(.mode("log")) fplogarithm_3: pin names not known; wires that end beside it: argY[63:32], fplogarithm_4_p2[63:32]
  // FPLogarithm #(.mode("log")) fplogarithm_4: pin names not known; wires that end beside it: argY[31:0], fplogarithm_4_p2[31:0]
  // FPToFP #(.fpwidthout(64)) fptofp_1: pin names not known; wires that end beside it: argY[63:32]
  // FPToFP #(.fpwidthout(64)) fptofp_2: pin names not known; wires that end beside it: argY[31:0]
  FPSubtractor fpsubtractor_2 (.a(argY[63:32]), .b(argZ[63:32]), .out(fpsubtractor_3_out[63:32]));
  FPSubtractor fpsubtractor_3 (.a(argY[31:0]), .b(argZ[31:0]), .out(fpsubtractor_3_out[31:0]));
  // FPLogarithm fplogarithm_5: pin names not known; wires that end beside it: argY[63:32], argZ[63:32], fplogarithm_6_p3[63:32]
  // FPLogarithm fplogarithm_6: pin names not known; wires that end beside it: argY[31:0], argZ[31:0], fplogarithm_6_p3[31:0]
  // FPExponentiator #(.mode("exp")) fpexponentiator_3: pin names not known; wires that end beside it: argY[63:32], fpexponentiator_4_p2[63:32]
  // FPExponentiator #(.mode("exp")) fpexponentiator_4: pin names not known; wires that end beside it: argY[31:0], fpexponentiator_4_p2[31:0]
  // FPToInt #(.width(32)) fptoint_5: pin names not known; wires that end beside it: argY[63:32], fptoint_6_p2[63:32]
  // FPToInt #(.width(32)) fptoint_6: pin names not known; wires that end beside it: argY[31:0], fptoint_6_p2[31:0]
  // FPToInt #(.mode("floor"), .width(32)) fptoint_7: pin names not known; wires that end beside it: argY[63:32], fptoint_8_p2[63:32]
  // FPToInt #(.mode("floor"), .width(32)) fptoint_8: pin names not known; wires that end beside it: argY[31:0], fptoint_8_p2[31:0]
  FPMultiplier fpmultiplier_2 (.a(argY[63:32]), .b(argZ[63:32]), .out(fpmultiplier_3_out[63:32]));
  FPMultiplier fpmultiplier_3 (.a(argY[31:0]), .b(argZ[31:0]), .out(fpmultiplier_3_out[31:0]));
  // FPExponentiator fpexponentiator_5: pin names not known; wires that end beside it: argY[63:32], argZ[63:32], fpexponentiator_6_p3[63:32]
  // FPExponentiator fpexponentiator_6: pin names not known; wires that end beside it: argY[31:0], argZ[31:0], fpexponentiator_6_p3[31:0]
  // FPAbsolute fpabsolute_2: pin names not known; wires that end beside it: argY[63:32], fpabsolute_3_p2[63:32]
  // FPAbsolute fpabsolute_3: pin names not known; wires that end beside it: argY[31:0], fpabsolute_3_p2[31:0]
  fgam fgam_2 ();  // open: inval, outval
  fgam fgam_3 ();  // open: inval, outval
  // FPToInt #(.mode("ceil"), .width(32)) fptoint_9: pin names not known; wires that end beside it: argY[63:32], fptoint_10_p2[63:32]
  // FPToInt #(.mode("ceil"), .width(32)) fptoint_10: pin names not known; wires that end beside it: argY[31:0], fptoint_10_p2[31:0]
  // IntToFP #(.fpwidth(8)) inttofp_8: pin names not known; wires that end beside it: argY[63:56], inttofp_15_p2[63:56]
  // IntToFP #(.fpwidth(8)) inttofp_9: pin names not known; wires that end beside it: argY[55:48], inttofp_15_p2[55:48]
  // IntToFP #(.fpwidth(8)) inttofp_10: pin names not known; wires that end beside it: argY[47:40], inttofp_15_p2[47:40]
  // IntToFP #(.fpwidth(8)) inttofp_11: pin names not known; wires that end beside it: argY[39:32], inttofp_15_p2[39:32]
  // IntToFP #(.fpwidth(8)) inttofp_12: pin names not known; wires that end beside it: argY[31:24], inttofp_15_p2[31:24]
  // IntToFP #(.fpwidth(8)) inttofp_13: pin names not known; wires that end beside it: argY[23:16], inttofp_15_p2[23:16]
  // IntToFP #(.fpwidth(8)) inttofp_14: pin names not known; wires that end beside it: argY[15:8], inttofp_15_p2[15:8]
  // IntToFP #(.fpwidth(8)) inttofp_15: pin names not known; wires that end beside it: argY[7:0], inttofp_15_p2[7:0]
  FPDivider fpdivider_2 (.a(argY[63:32]), .b(argZ[63:32]), .out(fpdivider_3_out[63:32]));
  FPDivider fpdivider_3 (.a(argY[31:0]), .b(argZ[31:0]), .out(fpdivider_3_out[31:0]));
  // FPSquareRoot fpsquareroot_2: pin names not known; wires that end beside it: argY[63:32], fpsquareroot_3_p2[63:32]
  // FPSquareRoot fpsquareroot_3: pin names not known; wires that end beside it: argY[31:0], fpsquareroot_3_p2[31:0]
  // FPTrigonometry #(.fpwidth(16)) fptrigonometry_7: pin names not known; wires that end beside it: argY[63:48], fptrigonometry_10_p2[63:48], fptrigonometry_10_p3[63:48], fptrigonometry_10_p4[63:48]
  // FPTrigonometry #(.fpwidth(16)) fptrigonometry_8: pin names not known; wires that end beside it: argY[47:32], fptrigonometry_10_p2[47:32], fptrigonometry_10_p3[47:32], fptrigonometry_10_p4[47:32]
  // FPTrigonometry #(.fpwidth(16)) fptrigonometry_9: pin names not known; wires that end beside it: argY[31:16], fptrigonometry_10_p2[31:16], fptrigonometry_10_p3[31:16], fptrigonometry_10_p4[31:16]
  // FPTrigonometry #(.fpwidth(16)) fptrigonometry_10: pin names not known; wires that end beside it: argY[15:0], fptrigonometry_10_p2[15:0], fptrigonometry_10_p3[15:0], fptrigonometry_10_p4[15:0]
  // FPTrigonometry #(.fpwidth(16), .\type ("arc")) fptrigonometry_11: pin names not known; wires that end beside it: argY[63:48], fptrigonometry_14_p2[63:48], fptrigonometry_14_p3[63:48], fptrigonometry_14_p4[63:48]
  // FPTrigonometry #(.fpwidth(16), .\type ("arc")) fptrigonometry_12: pin names not known; wires that end beside it: argY[47:32], fptrigonometry_14_p2[47:32], fptrigonometry_14_p3[47:32], fptrigonometry_14_p4[47:32]
  // FPTrigonometry #(.fpwidth(16), .\type ("arc")) fptrigonometry_13: pin names not known; wires that end beside it: argY[31:16], fptrigonometry_14_p2[31:16], fptrigonometry_14_p3[31:16], fptrigonometry_14_p4[31:16]
  // FPTrigonometry #(.fpwidth(16), .\type ("arc")) fptrigonometry_14: pin names not known; wires that end beside it: argY[15:0], fptrigonometry_14_p2[15:0], fptrigonometry_14_p3[15:0], fptrigonometry_14_p4[15:0]
  // FPToFP #(.fpwidthin(64)) fptofp_3: pin names not known; wires that end beside it: fptofp_4_p1[63:32]
  // FPToFP #(.fpwidthin(64)) fptofp_4: pin names not known; wires that end beside it: fptofp_4_p1[31:0]
  // FPToInt #(.mode("truncate"), .width(32)) fptoint_11: pin names not known; wires that end beside it: argY[63:32], fptoint_12_p2[63:32]
  // FPToInt #(.mode("truncate"), .width(32)) fptoint_12: pin names not known; wires that end beside it: argY[31:0], fptoint_12_p2[31:0]
  FPAdder #(.fpwidth(16)) fpadder_4 (.a(argY[63:48]), .b(argZ[63:48]), .out(fpadder_7_out[63:48]));
  FPAdder #(.fpwidth(16)) fpadder_5 (.a(argY[47:32]), .b(argZ[47:32]), .out(fpadder_7_out[47:32]));
  FPAdder #(.fpwidth(16)) fpadder_6 (.a(argY[31:16]), .b(argZ[31:16]), .out(fpadder_7_out[31:16]));
  FPAdder #(.fpwidth(16)) fpadder_7 (.a(argY[15:0]), .b(argZ[15:0]), .out(fpadder_7_out[15:0]));
  // FPNegator #(.fpwidth(16)) fpnegator_4: pin names not known; wires that end beside it: argY[63:48], fpnegator_7_p2[63:48]
  // FPNegator #(.fpwidth(16)) fpnegator_5: pin names not known; wires that end beside it: argY[47:32], fpnegator_7_p2[47:32]
  // FPNegator #(.fpwidth(16)) fpnegator_6: pin names not known; wires that end beside it: argY[31:16], fpnegator_7_p2[31:16]
  // FPNegator #(.fpwidth(16)) fpnegator_7: pin names not known; wires that end beside it: argY[15:0], fpnegator_7_p2[15:0]
  // FPLogarithm #(.fpwidth(16), .mode("log")) fplogarithm_7: pin names not known; wires that end beside it: argY[63:48], fplogarithm_10_p2[63:48]
  // FPLogarithm #(.fpwidth(16), .mode("log")) fplogarithm_8: pin names not known; wires that end beside it: argY[47:32], fplogarithm_10_p2[47:32]
  // FPLogarithm #(.fpwidth(16), .mode("log")) fplogarithm_9: pin names not known; wires that end beside it: argY[31:16], fplogarithm_10_p2[31:16]
  // FPLogarithm #(.fpwidth(16), .mode("log")) fplogarithm_10: pin names not known; wires that end beside it: argY[15:0], fplogarithm_10_p2[15:0]
  // FPMinMax #(.fpwidth(16)) fpminmax_7: pin names not known; wires that end beside it: argY[63:48], argZ[63:48], fpminmax_10_p3[63:48]
  // FPMinMax #(.fpwidth(16)) fpminmax_8: pin names not known; wires that end beside it: argY[47:32], argZ[47:32], fpminmax_10_p3[47:32]
  // FPMinMax #(.fpwidth(16)) fpminmax_9: pin names not known; wires that end beside it: argY[31:16], argZ[31:16], fpminmax_10_p3[31:16]
  // FPMinMax #(.fpwidth(16)) fpminmax_10: pin names not known; wires that end beside it: argY[15:0], argZ[15:0], fpminmax_10_p3[15:0]
  // FPMinMax #(.fpwidth(16)) fpminmax_11: pin names not known; wires that end beside it: argY[63:48], argZ[63:48], fpminmax_14_p3[63:48]
  // FPMinMax #(.fpwidth(16)) fpminmax_12: pin names not known; wires that end beside it: argY[47:32], argZ[47:32], fpminmax_14_p3[47:32]
  // FPMinMax #(.fpwidth(16)) fpminmax_13: pin names not known; wires that end beside it: argY[31:16], argZ[31:16], fpminmax_14_p3[31:16]
  // FPMinMax #(.fpwidth(16)) fpminmax_14: pin names not known; wires that end beside it: argY[15:0], argZ[15:0], fpminmax_14_p3[15:0]
  // FPToInt #(.fpwidth(16), .width(16)) fptoint_13: pin names not known; wires that end beside it: argY[63:48], fptoint_16_p2[63:48]
  // FPToInt #(.fpwidth(16), .width(16)) fptoint_14: pin names not known; wires that end beside it: argY[47:32], fptoint_16_p2[47:32]
  // FPToInt #(.fpwidth(16), .width(16)) fptoint_15: pin names not known; wires that end beside it: argY[31:16], fptoint_16_p2[31:16]
  // FPToInt #(.fpwidth(16), .width(16)) fptoint_16: pin names not known; wires that end beside it: argY[15:0], fptoint_16_p2[15:0]
  FPSubtractor #(.fpwidth(16)) fpsubtractor_4 (.a(argY[63:48]), .b(argZ[63:48]), .out(fpsubtractor_7_out[63:48]));
  FPSubtractor #(.fpwidth(16)) fpsubtractor_5 (.a(argY[47:32]), .b(argZ[47:32]), .out(fpsubtractor_7_out[47:32]));
  FPSubtractor #(.fpwidth(16)) fpsubtractor_6 (.a(argY[31:16]), .b(argZ[31:16]), .out(fpsubtractor_7_out[31:16]));
  FPSubtractor #(.fpwidth(16)) fpsubtractor_7 (.a(argY[15:0]), .b(argZ[15:0]), .out(fpsubtractor_7_out[15:0]));
  // FPLogarithm #(.fpwidth(16)) fplogarithm_11: pin names not known; wires that end beside it: argY[63:48], argZ[63:48], fplogarithm_14_p3[63:48]
  // FPLogarithm #(.fpwidth(16)) fplogarithm_12: pin names not known; wires that end beside it: argY[47:32], argZ[47:32], fplogarithm_14_p3[47:32]
  // FPLogarithm #(.fpwidth(16)) fplogarithm_13: pin names not known; wires that end beside it: argY[31:16], argZ[31:16], fplogarithm_14_p3[31:16]
  // FPLogarithm #(.fpwidth(16)) fplogarithm_14: pin names not known; wires that end beside it: argY[15:0], argZ[15:0], fplogarithm_14_p3[15:0]
  // FPExponentiator #(.fpwidth(16), .mode("exp")) fpexponentiator_7: pin names not known; wires that end beside it: argY[63:48], fpexponentiator_10_p2[63:48]
  // FPExponentiator #(.fpwidth(16), .mode("exp")) fpexponentiator_8: pin names not known; wires that end beside it: argY[47:32], fpexponentiator_10_p2[47:32]
  // FPExponentiator #(.fpwidth(16), .mode("exp")) fpexponentiator_9: pin names not known; wires that end beside it: argY[31:16], fpexponentiator_10_p2[31:16]
  // FPExponentiator #(.fpwidth(16), .mode("exp")) fpexponentiator_10: pin names not known; wires that end beside it: argY[15:0], fpexponentiator_10_p2[15:0]
  // FPToFP #(.fpwidthin(16), .fpwidthout(64)) fptofp_5: pin names not known; wires that end beside it: argY[63:48]
  // FPToFP #(.fpwidthin(16), .fpwidthout(64)) fptofp_6: pin names not known; wires that end beside it: argY[47:32]
  // FPToFP #(.fpwidthin(16), .fpwidthout(64)) fptofp_7: pin names not known; wires that end beside it: argY[31:16]
  // FPToFP #(.fpwidthin(16), .fpwidthout(64)) fptofp_8: pin names not known; wires that end beside it: argY[15:0]
  // FPToInt #(.fpwidth(16), .mode("floor"), .width(16)) fptoint_17: pin names not known; wires that end beside it: argY[63:48], fptoint_20_p2[63:48]
  // FPToInt #(.fpwidth(16), .mode("floor"), .width(16)) fptoint_18: pin names not known; wires that end beside it: argY[47:32], fptoint_20_p2[47:32]
  // FPToInt #(.fpwidth(16), .mode("floor"), .width(16)) fptoint_19: pin names not known; wires that end beside it: argY[31:16], fptoint_20_p2[31:16]
  // FPToInt #(.fpwidth(16), .mode("floor"), .width(16)) fptoint_20: pin names not known; wires that end beside it: argY[15:0], fptoint_20_p2[15:0]
  fgam fgam_4 ();  // open: inval, outval
  fgam fgam_5 ();  // open: inval, outval
  fgam fgam_6 ();  // open: inval, outval
  fgam fgam_7 ();  // open: inval, outval
  FPMultiplier #(.fpwidth(16)) fpmultiplier_4 (.a(argY[63:48]), .b(argZ[63:48]), .out(fpmultiplier_7_out[63:48]));
  FPMultiplier #(.fpwidth(16)) fpmultiplier_5 (.a(argY[47:32]), .b(argZ[47:32]), .out(fpmultiplier_7_out[47:32]));
  FPMultiplier #(.fpwidth(16)) fpmultiplier_6 (.a(argY[31:16]), .b(argZ[31:16]), .out(fpmultiplier_7_out[31:16]));
  FPMultiplier #(.fpwidth(16)) fpmultiplier_7 (.a(argY[15:0]), .b(argZ[15:0]), .out(fpmultiplier_7_out[15:0]));
  // FPExponentiator #(.fpwidth(16)) fpexponentiator_11: pin names not known; wires that end beside it: argY[63:48], argZ[63:48], fpexponentiator_14_p3[63:48]
  // FPExponentiator #(.fpwidth(16)) fpexponentiator_12: pin names not known; wires that end beside it: argY[47:32], argZ[47:32], fpexponentiator_14_p3[47:32]
  // FPExponentiator #(.fpwidth(16)) fpexponentiator_13: pin names not known; wires that end beside it: argY[31:16], argZ[31:16], fpexponentiator_14_p3[31:16]
  // FPExponentiator #(.fpwidth(16)) fpexponentiator_14: pin names not known; wires that end beside it: argY[15:0], argZ[15:0], fpexponentiator_14_p3[15:0]
  // FPAbsolute #(.fpwidth(16)) fpabsolute_4: pin names not known; wires that end beside it: argY[63:48], fpabsolute_7_p2[63:48]
  // FPAbsolute #(.fpwidth(16)) fpabsolute_5: pin names not known; wires that end beside it: argY[47:32], fpabsolute_7_p2[47:32]
  // FPAbsolute #(.fpwidth(16)) fpabsolute_6: pin names not known; wires that end beside it: argY[31:16], fpabsolute_7_p2[31:16]
  // FPAbsolute #(.fpwidth(16)) fpabsolute_7: pin names not known; wires that end beside it: argY[15:0], fpabsolute_7_p2[15:0]
  // FPToFP #(.fpwidthin(64), .fpwidthout(16)) fptofp_9: pin names not known; wires that end beside it: fptofp_12_p1[63:48]
  // FPToFP #(.fpwidthin(64), .fpwidthout(16)) fptofp_10: pin names not known; wires that end beside it: fptofp_12_p1[47:32]
  // FPToFP #(.fpwidthin(64), .fpwidthout(16)) fptofp_11: pin names not known; wires that end beside it: fptofp_12_p1[31:16]
  // FPToFP #(.fpwidthin(64), .fpwidthout(16)) fptofp_12: pin names not known; wires that end beside it: fptofp_12_p1[15:0]
  // FPToInt #(.fpwidth(16), .mode("ceil"), .width(16)) fptoint_21: pin names not known; wires that end beside it: argY[63:48], fptoint_24_p2[63:48]
  // FPToInt #(.fpwidth(16), .mode("ceil"), .width(16)) fptoint_22: pin names not known; wires that end beside it: argY[47:32], fptoint_24_p2[47:32]
  // FPToInt #(.fpwidth(16), .mode("ceil"), .width(16)) fptoint_23: pin names not known; wires that end beside it: argY[31:16], fptoint_24_p2[31:16]
  // FPToInt #(.fpwidth(16), .mode("ceil"), .width(16)) fptoint_24: pin names not known; wires that end beside it: argY[15:0], fptoint_24_p2[15:0]
  // FPTrigonometry #(.fpwidth(8)) fptrigonometry_15: pin names not known; wires that end beside it: argY[63:56], fptrigonometry_22_p2[63:56], fptrigonometry_22_p3[63:56], fptrigonometry_22_p4[63:56]
  // FPTrigonometry #(.fpwidth(8)) fptrigonometry_16: pin names not known; wires that end beside it: argY[55:48], fptrigonometry_22_p2[55:48], fptrigonometry_22_p3[55:48], fptrigonometry_22_p4[55:48]
  // FPTrigonometry #(.fpwidth(8)) fptrigonometry_17: pin names not known; wires that end beside it: argY[47:40], fptrigonometry_22_p2[47:40], fptrigonometry_22_p3[47:40], fptrigonometry_22_p4[47:40]
  // FPTrigonometry #(.fpwidth(8)) fptrigonometry_18: pin names not known; wires that end beside it: argY[39:32], fptrigonometry_22_p2[39:32], fptrigonometry_22_p3[39:32], fptrigonometry_22_p4[39:32]
  // FPTrigonometry #(.fpwidth(8)) fptrigonometry_19: pin names not known; wires that end beside it: argY[31:24], fptrigonometry_22_p2[31:24], fptrigonometry_22_p3[31:24], fptrigonometry_22_p4[31:24]
  // FPTrigonometry #(.fpwidth(8)) fptrigonometry_20: pin names not known; wires that end beside it: argY[23:16], fptrigonometry_22_p2[23:16], fptrigonometry_22_p3[23:16], fptrigonometry_22_p4[23:16]
  // FPTrigonometry #(.fpwidth(8)) fptrigonometry_21: pin names not known; wires that end beside it: argY[15:8], fptrigonometry_22_p2[15:8], fptrigonometry_22_p3[15:8], fptrigonometry_22_p4[15:8]
  // FPTrigonometry #(.fpwidth(8)) fptrigonometry_22: pin names not known; wires that end beside it: argY[7:0], fptrigonometry_22_p2[7:0], fptrigonometry_22_p3[7:0], fptrigonometry_22_p4[7:0]
  // FPTrigonometry #(.fpwidth(8), .\type ("arc")) fptrigonometry_23: pin names not known; wires that end beside it: argY[63:56], fptrigonometry_30_p2[63:56], fptrigonometry_30_p3[63:56], fptrigonometry_30_p4[63:56]
  // FPTrigonometry #(.fpwidth(8), .\type ("arc")) fptrigonometry_24: pin names not known; wires that end beside it: argY[55:48], fptrigonometry_30_p2[55:48], fptrigonometry_30_p3[55:48], fptrigonometry_30_p4[55:48]
  // FPTrigonometry #(.fpwidth(8), .\type ("arc")) fptrigonometry_25: pin names not known; wires that end beside it: argY[47:40], fptrigonometry_30_p2[47:40], fptrigonometry_30_p3[47:40], fptrigonometry_30_p4[47:40]
  // FPTrigonometry #(.fpwidth(8), .\type ("arc")) fptrigonometry_26: pin names not known; wires that end beside it: argY[39:32], fptrigonometry_30_p2[39:32], fptrigonometry_30_p3[39:32], fptrigonometry_30_p4[39:32]
  // FPTrigonometry #(.fpwidth(8), .\type ("arc")) fptrigonometry_27: pin names not known; wires that end beside it: argY[31:24], fptrigonometry_30_p2[31:24], fptrigonometry_30_p3[31:24], fptrigonometry_30_p4[31:24]
  // FPTrigonometry #(.fpwidth(8), .\type ("arc")) fptrigonometry_28: pin names not known; wires that end beside it: argY[23:16], fptrigonometry_30_p2[23:16], fptrigonometry_30_p3[23:16], fptrigonometry_30_p4[23:16]
  // FPTrigonometry #(.fpwidth(8), .\type ("arc")) fptrigonometry_29: pin names not known; wires that end beside it: argY[15:8], fptrigonometry_30_p2[15:8], fptrigonometry_30_p3[15:8], fptrigonometry_30_p4[15:8]
  // FPTrigonometry #(.fpwidth(8), .\type ("arc")) fptrigonometry_30: pin names not known; wires that end beside it: argY[7:0], fptrigonometry_30_p2[7:0], fptrigonometry_30_p3[7:0], fptrigonometry_30_p4[7:0]
  FPDivider #(.fpwidth(16)) fpdivider_4 (.a(argY[63:48]), .b(argZ[63:48]), .out(fpdivider_7_out[63:48]));
  FPDivider #(.fpwidth(16)) fpdivider_5 (.a(argY[47:32]), .b(argZ[47:32]), .out(fpdivider_7_out[47:32]));
  FPDivider #(.fpwidth(16)) fpdivider_6 (.a(argY[31:16]), .b(argZ[31:16]), .out(fpdivider_7_out[31:16]));
  FPDivider #(.fpwidth(16)) fpdivider_7 (.a(argY[15:0]), .b(argZ[15:0]), .out(fpdivider_7_out[15:0]));
  // FPSquareRoot #(.fpwidth(16)) fpsquareroot_4: pin names not known; wires that end beside it: argY[63:48], fpsquareroot_7_p2[63:48]
  // FPSquareRoot #(.fpwidth(16)) fpsquareroot_5: pin names not known; wires that end beside it: argY[47:32], fpsquareroot_7_p2[47:32]
  // FPSquareRoot #(.fpwidth(16)) fpsquareroot_6: pin names not known; wires that end beside it: argY[31:16], fpsquareroot_7_p2[31:16]
  // FPSquareRoot #(.fpwidth(16)) fpsquareroot_7: pin names not known; wires that end beside it: argY[15:0], fpsquareroot_7_p2[15:0]
  // FPToInt #(.fpwidth(16), .mode("truncate"), .width(16)) fptoint_25: pin names not known; wires that end beside it: argY[63:48], fptoint_28_p2[63:48]
  // FPToInt #(.fpwidth(16), .mode("truncate"), .width(16)) fptoint_26: pin names not known; wires that end beside it: argY[47:32], fptoint_28_p2[47:32]
  // FPToInt #(.fpwidth(16), .mode("truncate"), .width(16)) fptoint_27: pin names not known; wires that end beside it: argY[31:16], fptoint_28_p2[31:16]
  // FPToInt #(.fpwidth(16), .mode("truncate"), .width(16)) fptoint_28: pin names not known; wires that end beside it: argY[15:0], fptoint_28_p2[15:0]
  assign bit_extender_136_out = {{32{argY[31]}}, argY[31:0]};  // Bit_Extender bit_extender_136
  assign bit_extender_137_out[31:0] = {{16{argY[15]}}, argY[15:0]};  // Bit_Extender bit_extender_137
  assign bit_extender_137_out[63:32] = {{16{argY[47]}}, argY[47:32]};  // Bit_Extender bit_extender_138
  FPAdder #(.fpwidth(8)) fpadder_8 (.a(argY[63:56]), .b(argZ[63:56]), .out(fpadder_15_out[63:56]));
  FPAdder #(.fpwidth(8)) fpadder_9 (.a(argY[55:48]), .b(argZ[55:48]), .out(fpadder_15_out[55:48]));
  FPAdder #(.fpwidth(8)) fpadder_10 (.a(argY[47:40]), .b(argZ[47:40]), .out(fpadder_15_out[47:40]));
  FPAdder #(.fpwidth(8)) fpadder_11 (.a(argY[39:32]), .b(argZ[39:32]), .out(fpadder_15_out[39:32]));
  FPAdder #(.fpwidth(8)) fpadder_12 (.a(argY[31:24]), .b(argZ[31:24]), .out(fpadder_15_out[31:24]));
  FPAdder #(.fpwidth(8)) fpadder_13 (.a(argY[23:16]), .b(argZ[23:16]), .out(fpadder_15_out[23:16]));
  FPAdder #(.fpwidth(8)) fpadder_14 (.a(argY[15:8]), .b(argZ[15:8]), .out(fpadder_15_out[15:8]));
  FPAdder #(.fpwidth(8)) fpadder_15 (.a(argY[7:0]), .b(argZ[7:0]), .out(fpadder_15_out[7:0]));
  // FPNegator #(.fpwidth(8)) fpnegator_8: pin names not known; wires that end beside it: argY[63:56], fpnegator_15_p2[63:56]
  // FPNegator #(.fpwidth(8)) fpnegator_9: pin names not known; wires that end beside it: argY[55:48], fpnegator_15_p2[55:48]
  // FPNegator #(.fpwidth(8)) fpnegator_10: pin names not known; wires that end beside it: argY[47:40], fpnegator_15_p2[47:40]
  // FPNegator #(.fpwidth(8)) fpnegator_11: pin names not known; wires that end beside it: argY[39:32], fpnegator_15_p2[39:32]
  // FPNegator #(.fpwidth(8)) fpnegator_12: pin names not known; wires that end beside it: argY[31:24], fpnegator_15_p2[31:24]
  // FPNegator #(.fpwidth(8)) fpnegator_13: pin names not known; wires that end beside it: argY[23:16], fpnegator_15_p2[23:16]
  // FPNegator #(.fpwidth(8)) fpnegator_14: pin names not known; wires that end beside it: argY[15:8], fpnegator_15_p2[15:8]
  // FPNegator #(.fpwidth(8)) fpnegator_15: pin names not known; wires that end beside it: argY[7:0], fpnegator_15_p2[7:0]
  // FPMinMax #(.fpwidth(8)) fpminmax_15: pin names not known; wires that end beside it: argY[63:56], argZ[63:56], fpminmax_22_p3[63:56]
  // FPMinMax #(.fpwidth(8)) fpminmax_16: pin names not known; wires that end beside it: argY[55:48], argZ[55:48], fpminmax_22_p3[55:48]
  // FPMinMax #(.fpwidth(8)) fpminmax_17: pin names not known; wires that end beside it: argY[47:40], argZ[47:40], fpminmax_22_p3[47:40]
  // FPMinMax #(.fpwidth(8)) fpminmax_18: pin names not known; wires that end beside it: argY[39:32], argZ[39:32], fpminmax_22_p3[39:32]
  // FPMinMax #(.fpwidth(8)) fpminmax_19: pin names not known; wires that end beside it: argY[31:24], argZ[31:24], fpminmax_22_p3[31:24]
  // FPMinMax #(.fpwidth(8)) fpminmax_20: pin names not known; wires that end beside it: argY[23:16], argZ[23:16], fpminmax_22_p3[23:16]
  // FPMinMax #(.fpwidth(8)) fpminmax_21: pin names not known; wires that end beside it: argY[15:8], argZ[15:8], fpminmax_22_p3[15:8]
  // FPMinMax #(.fpwidth(8)) fpminmax_22: pin names not known; wires that end beside it: argY[7:0], argZ[7:0], fpminmax_22_p3[7:0]
  // FPMinMax #(.fpwidth(8)) fpminmax_23: pin names not known; wires that end beside it: argY[63:56], argZ[63:56], fpminmax_30_p3[63:56]
  // FPMinMax #(.fpwidth(8)) fpminmax_24: pin names not known; wires that end beside it: argY[55:48], argZ[55:48], fpminmax_30_p3[55:48]
  // FPMinMax #(.fpwidth(8)) fpminmax_25: pin names not known; wires that end beside it: argY[47:40], argZ[47:40], fpminmax_30_p3[47:40]
  // FPMinMax #(.fpwidth(8)) fpminmax_26: pin names not known; wires that end beside it: argY[39:32], argZ[39:32], fpminmax_30_p3[39:32]
  // FPMinMax #(.fpwidth(8)) fpminmax_27: pin names not known; wires that end beside it: argY[31:24], argZ[31:24], fpminmax_30_p3[31:24]
  // FPMinMax #(.fpwidth(8)) fpminmax_28: pin names not known; wires that end beside it: argY[23:16], argZ[23:16], fpminmax_30_p3[23:16]
  // FPMinMax #(.fpwidth(8)) fpminmax_29: pin names not known; wires that end beside it: argY[15:8], argZ[15:8], fpminmax_30_p3[15:8]
  // FPMinMax #(.fpwidth(8)) fpminmax_30: pin names not known; wires that end beside it: argY[7:0], argZ[7:0], fpminmax_30_p3[7:0]
  // FPLogarithm #(.fpwidth(8), .mode("log")) fplogarithm_15: pin names not known; wires that end beside it: argY[63:56], fplogarithm_22_p2[63:56]
  // FPLogarithm #(.fpwidth(8), .mode("log")) fplogarithm_16: pin names not known; wires that end beside it: argY[55:48], fplogarithm_22_p2[55:48]
  // FPLogarithm #(.fpwidth(8), .mode("log")) fplogarithm_17: pin names not known; wires that end beside it: argY[47:40], fplogarithm_22_p2[47:40]
  // FPLogarithm #(.fpwidth(8), .mode("log")) fplogarithm_18: pin names not known; wires that end beside it: argY[39:32], fplogarithm_22_p2[39:32]
  // FPLogarithm #(.fpwidth(8), .mode("log")) fplogarithm_19: pin names not known; wires that end beside it: argY[31:24], fplogarithm_22_p2[31:24]
  // FPLogarithm #(.fpwidth(8), .mode("log")) fplogarithm_20: pin names not known; wires that end beside it: argY[23:16], fplogarithm_22_p2[23:16]
  // FPLogarithm #(.fpwidth(8), .mode("log")) fplogarithm_21: pin names not known; wires that end beside it: argY[15:8], fplogarithm_22_p2[15:8]
  // FPLogarithm #(.fpwidth(8), .mode("log")) fplogarithm_22: pin names not known; wires that end beside it: argY[7:0], fplogarithm_22_p2[7:0]
  // FPToInt #(.fpwidth(8)) fptoint_29: pin names not known; wires that end beside it: argY[63:56], fptoint_36_p2[63:56]
  // FPToInt #(.fpwidth(8)) fptoint_30: pin names not known; wires that end beside it: argY[55:48], fptoint_36_p2[55:48]
  // FPToInt #(.fpwidth(8)) fptoint_31: pin names not known; wires that end beside it: argY[47:40], fptoint_36_p2[47:40]
  // FPToInt #(.fpwidth(8)) fptoint_32: pin names not known; wires that end beside it: argY[39:32], fptoint_36_p2[39:32]
  // FPToInt #(.fpwidth(8)) fptoint_33: pin names not known; wires that end beside it: argY[31:24], fptoint_36_p2[31:24]
  // FPToInt #(.fpwidth(8)) fptoint_34: pin names not known; wires that end beside it: argY[23:16], fptoint_36_p2[23:16]
  // FPToInt #(.fpwidth(8)) fptoint_35: pin names not known; wires that end beside it: argY[15:8], fptoint_36_p2[15:8]
  // FPToInt #(.fpwidth(8)) fptoint_36: pin names not known; wires that end beside it: argY[7:0], fptoint_36_p2[7:0]
  assign bit_extender_139_out[15:0] = {{8{argY[7]}}, argY[7:0]};  // Bit_Extender bit_extender_139
  assign bit_extender_139_out[31:16] = {{8{argY[23]}}, argY[23:16]};  // Bit_Extender bit_extender_140
  assign bit_extender_139_out[47:32] = {{8{argY[39]}}, argY[39:32]};  // Bit_Extender bit_extender_141
  assign bit_extender_139_out[63:48] = {{8{argY[55]}}, argY[55:48]};  // Bit_Extender bit_extender_142
  // FPToFP #(.fpwidthin(8), .fpwidthout(64)) fptofp_13: pin names not known; wires that end beside it: argY[63:56]
  // FPToFP #(.fpwidthin(8), .fpwidthout(64)) fptofp_14: pin names not known; wires that end beside it: argY[55:48]
  // FPToFP #(.fpwidthin(8), .fpwidthout(64)) fptofp_15: pin names not known; wires that end beside it: argY[47:40]
  // FPToFP #(.fpwidthin(8), .fpwidthout(64)) fptofp_16: pin names not known; wires that end beside it: argY[39:32]
  // FPToFP #(.fpwidthin(8), .fpwidthout(64)) fptofp_17: pin names not known; wires that end beside it: argY[31:24]
  // FPToFP #(.fpwidthin(8), .fpwidthout(64)) fptofp_18: pin names not known; wires that end beside it: argY[23:16]
  // FPToFP #(.fpwidthin(8), .fpwidthout(64)) fptofp_19: pin names not known; wires that end beside it: argY[15:8]
  // FPToFP #(.fpwidthin(8), .fpwidthout(64)) fptofp_20: pin names not known; wires that end beside it: argY[7:0]
  // FPToFP #(.fpwidthin(64)) fptofp_21: pin names not known; wires that end beside it: argY, fptofp_21_p2
  // FPToInt #(.fpwidth(8), .mode("floor")) fptoint_37: pin names not known; wires that end beside it: argY[63:56], fptoint_44_p2[63:56]
  // FPToInt #(.fpwidth(8), .mode("floor")) fptoint_38: pin names not known; wires that end beside it: argY[55:48], fptoint_44_p2[55:48]
  // FPToInt #(.fpwidth(8), .mode("floor")) fptoint_39: pin names not known; wires that end beside it: argY[47:40], fptoint_44_p2[47:40]
  // FPToInt #(.fpwidth(8), .mode("floor")) fptoint_40: pin names not known; wires that end beside it: argY[39:32], fptoint_44_p2[39:32]
  // FPToInt #(.fpwidth(8), .mode("floor")) fptoint_41: pin names not known; wires that end beside it: argY[31:24], fptoint_44_p2[31:24]
  // FPToInt #(.fpwidth(8), .mode("floor")) fptoint_42: pin names not known; wires that end beside it: argY[23:16], fptoint_44_p2[23:16]
  // FPToInt #(.fpwidth(8), .mode("floor")) fptoint_43: pin names not known; wires that end beside it: argY[15:8], fptoint_44_p2[15:8]
  // FPToInt #(.fpwidth(8), .mode("floor")) fptoint_44: pin names not known; wires that end beside it: argY[7:0], fptoint_44_p2[7:0]
  // FPToFP #(.fpwidthout(16)) fptofp_22: pin names not known; wires that end beside it: argY[31:0], fptofp_22_p2[31:16]
  // FPToFP #(.fpwidthout(16)) fptofp_23: pin names not known; wires that end beside it: argY[63:32], fptofp_22_p2[63:48]
  FPSubtractor #(.fpwidth(8)) fpsubtractor_8 (.a(argY[63:56]), .b(argZ[63:56]), .out(fpsubtractor_15_out[63:56]));
  FPSubtractor #(.fpwidth(8)) fpsubtractor_9 (.a(argY[55:48]), .b(argZ[55:48]), .out(fpsubtractor_15_out[55:48]));
  FPSubtractor #(.fpwidth(8)) fpsubtractor_10 (.a(argY[47:40]), .b(argZ[47:40]), .out(fpsubtractor_15_out[47:40]));
  FPSubtractor #(.fpwidth(8)) fpsubtractor_11 (.a(argY[39:32]), .b(argZ[39:32]), .out(fpsubtractor_15_out[39:32]));
  FPSubtractor #(.fpwidth(8)) fpsubtractor_12 (.a(argY[31:24]), .b(argZ[31:24]), .out(fpsubtractor_15_out[31:24]));
  FPSubtractor #(.fpwidth(8)) fpsubtractor_13 (.a(argY[23:16]), .b(argZ[23:16]), .out(fpsubtractor_15_out[23:16]));
  FPSubtractor #(.fpwidth(8)) fpsubtractor_14 (.a(argY[15:8]), .b(argZ[15:8]), .out(fpsubtractor_15_out[15:8]));
  FPSubtractor #(.fpwidth(8)) fpsubtractor_15 (.a(argY[7:0]), .b(argZ[7:0]), .out(fpsubtractor_15_out[7:0]));
  // FPLogarithm #(.fpwidth(8)) fplogarithm_23: pin names not known; wires that end beside it: argY[63:56], argZ[63:56], fplogarithm_30_p3[63:56]
  // FPLogarithm #(.fpwidth(8)) fplogarithm_24: pin names not known; wires that end beside it: argY[55:48], argZ[55:48], fplogarithm_30_p3[55:48]
  // FPLogarithm #(.fpwidth(8)) fplogarithm_25: pin names not known; wires that end beside it: argY[47:40], argZ[47:40], fplogarithm_30_p3[47:40]
  // FPLogarithm #(.fpwidth(8)) fplogarithm_26: pin names not known; wires that end beside it: argY[39:32], argZ[39:32], fplogarithm_30_p3[39:32]
  // FPLogarithm #(.fpwidth(8)) fplogarithm_27: pin names not known; wires that end beside it: argY[31:24], argZ[31:24], fplogarithm_30_p3[31:24]
  // FPLogarithm #(.fpwidth(8)) fplogarithm_28: pin names not known; wires that end beside it: argY[23:16], argZ[23:16], fplogarithm_30_p3[23:16]
  // FPLogarithm #(.fpwidth(8)) fplogarithm_29: pin names not known; wires that end beside it: argY[15:8], argZ[15:8], fplogarithm_30_p3[15:8]
  // FPLogarithm #(.fpwidth(8)) fplogarithm_30: pin names not known; wires that end beside it: argY[7:0], argZ[7:0], fplogarithm_30_p3[7:0]
  // FPExponentiator #(.fpwidth(8), .mode("exp")) fpexponentiator_15: pin names not known; wires that end beside it: argY[63:56], fpexponentiator_22_p2[63:56]
  // FPExponentiator #(.fpwidth(8), .mode("exp")) fpexponentiator_16: pin names not known; wires that end beside it: argY[55:48], fpexponentiator_22_p2[55:48]
  // FPExponentiator #(.fpwidth(8), .mode("exp")) fpexponentiator_17: pin names not known; wires that end beside it: argY[47:40], fpexponentiator_22_p2[47:40]
  // FPExponentiator #(.fpwidth(8), .mode("exp")) fpexponentiator_18: pin names not known; wires that end beside it: argY[39:32], fpexponentiator_22_p2[39:32]
  // FPExponentiator #(.fpwidth(8), .mode("exp")) fpexponentiator_19: pin names not known; wires that end beside it: argY[31:24], fpexponentiator_22_p2[31:24]
  // FPExponentiator #(.fpwidth(8), .mode("exp")) fpexponentiator_20: pin names not known; wires that end beside it: argY[23:16], fpexponentiator_22_p2[23:16]
  // FPExponentiator #(.fpwidth(8), .mode("exp")) fpexponentiator_21: pin names not known; wires that end beside it: argY[15:8], fpexponentiator_22_p2[15:8]
  // FPExponentiator #(.fpwidth(8), .mode("exp")) fpexponentiator_22: pin names not known; wires that end beside it: argY[7:0], fpexponentiator_22_p2[7:0]
  // FPToFP #(.fpwidthin(64), .fpwidthout(8)) fptofp_24: pin names not known; wires that end beside it: fptofp_31_p1[63:56]
  fgam fgam_8 ();  // open: inval, outval
  // FPToFP #(.fpwidthin(64), .fpwidthout(8)) fptofp_25: pin names not known; wires that end beside it: fptofp_31_p1[55:48]
  fgam fgam_9 ();  // open: inval, outval
  // FPToFP #(.fpwidthin(64), .fpwidthout(8)) fptofp_26: pin names not known; wires that end beside it: fptofp_31_p1[47:40]
  fgam fgam_10 ();  // open: inval, outval
  // FPToFP #(.fpwidthin(64), .fpwidthout(8)) fptofp_27: pin names not known; wires that end beside it: fptofp_31_p1[39:32]
  fgam fgam_11 ();  // open: inval, outval
  // FPToFP #(.fpwidthin(64), .fpwidthout(8)) fptofp_28: pin names not known; wires that end beside it: fptofp_31_p1[31:24]
  fgam fgam_12 ();  // open: inval, outval
  // FPToFP #(.fpwidthin(64), .fpwidthout(8)) fptofp_29: pin names not known; wires that end beside it: fptofp_31_p1[23:16]
  fgam fgam_13 ();  // open: inval, outval
  // FPToFP #(.fpwidthin(64), .fpwidthout(8)) fptofp_30: pin names not known; wires that end beside it: fptofp_31_p1[15:8]
  fgam fgam_14 ();  // open: inval, outval
  // FPToFP #(.fpwidthin(64), .fpwidthout(8)) fptofp_31: pin names not known; wires that end beside it: fptofp_31_p1[7:0]
  fgam fgam_15 ();  // open: inval, outval
  // FPToFP #(.fpwidthin(16), .fpwidthout(8)) fptofp_32: pin names not known; wires that end beside it: argY[15:0], fptofp_32_p2[15:8]
  // FPToFP #(.fpwidthin(16), .fpwidthout(8)) fptofp_33: pin names not known; wires that end beside it: argY[31:16], fptofp_32_p2[31:24]
  // FPToFP #(.fpwidthin(16), .fpwidthout(8)) fptofp_34: pin names not known; wires that end beside it: argY[47:32], fptofp_32_p2[47:40]
  // FPToFP #(.fpwidthin(16), .fpwidthout(8)) fptofp_35: pin names not known; wires that end beside it: argY[63:48], fptofp_32_p2[63:56]
  FPMultiplier #(.fpwidth(8)) fpmultiplier_8 (.a(argY[63:56]), .b(argZ[63:56]), .out(fpmultiplier_15_out[63:56]));
  FPMultiplier #(.fpwidth(8)) fpmultiplier_9 (.a(argY[55:48]), .b(argZ[55:48]), .out(fpmultiplier_15_out[55:48]));
  FPMultiplier #(.fpwidth(8)) fpmultiplier_10 (.a(argY[47:40]), .b(argZ[47:40]), .out(fpmultiplier_15_out[47:40]));
  FPMultiplier #(.fpwidth(8)) fpmultiplier_11 (.a(argY[39:32]), .b(argZ[39:32]), .out(fpmultiplier_15_out[39:32]));
  FPMultiplier #(.fpwidth(8)) fpmultiplier_12 (.a(argY[31:24]), .b(argZ[31:24]), .out(fpmultiplier_15_out[31:24]));
  FPMultiplier #(.fpwidth(8)) fpmultiplier_13 (.a(argY[23:16]), .b(argZ[23:16]), .out(fpmultiplier_15_out[23:16]));
  FPMultiplier #(.fpwidth(8)) fpmultiplier_14 (.a(argY[15:8]), .b(argZ[15:8]), .out(fpmultiplier_15_out[15:8]));
  FPMultiplier #(.fpwidth(8)) fpmultiplier_15 (.a(argY[7:0]), .b(argZ[7:0]), .out(fpmultiplier_15_out[7:0]));
  // FPExponentiator #(.fpwidth(8)) fpexponentiator_23: pin names not known; wires that end beside it: argY[63:56], argZ[63:56], fpexponentiator_30_p3[63:56]
  // FPExponentiator #(.fpwidth(8)) fpexponentiator_24: pin names not known; wires that end beside it: argY[55:48], argZ[55:48], fpexponentiator_30_p3[55:48]
  // FPExponentiator #(.fpwidth(8)) fpexponentiator_25: pin names not known; wires that end beside it: argY[47:40], argZ[47:40], fpexponentiator_30_p3[47:40]
  // FPExponentiator #(.fpwidth(8)) fpexponentiator_26: pin names not known; wires that end beside it: argY[39:32], argZ[39:32], fpexponentiator_30_p3[39:32]
  // FPExponentiator #(.fpwidth(8)) fpexponentiator_27: pin names not known; wires that end beside it: argY[31:24], argZ[31:24], fpexponentiator_30_p3[31:24]
  // FPExponentiator #(.fpwidth(8)) fpexponentiator_28: pin names not known; wires that end beside it: argY[23:16], argZ[23:16], fpexponentiator_30_p3[23:16]
  // FPExponentiator #(.fpwidth(8)) fpexponentiator_29: pin names not known; wires that end beside it: argY[15:8], argZ[15:8], fpexponentiator_30_p3[15:8]
  // FPExponentiator #(.fpwidth(8)) fpexponentiator_30: pin names not known; wires that end beside it: argY[7:0], argZ[7:0], fpexponentiator_30_p3[7:0]
  // FPAbsolute #(.fpwidth(8)) fpabsolute_8: pin names not known; wires that end beside it: argY[63:56], fpabsolute_15_p2[63:56]
  // FPAbsolute #(.fpwidth(8)) fpabsolute_9: pin names not known; wires that end beside it: argY[55:48], fpabsolute_15_p2[55:48]
  // FPAbsolute #(.fpwidth(8)) fpabsolute_10: pin names not known; wires that end beside it: argY[47:40], fpabsolute_15_p2[47:40]
  // FPAbsolute #(.fpwidth(8)) fpabsolute_11: pin names not known; wires that end beside it: argY[39:32], fpabsolute_15_p2[39:32]
  // FPAbsolute #(.fpwidth(8)) fpabsolute_12: pin names not known; wires that end beside it: argY[31:24], fpabsolute_15_p2[31:24]
  // FPAbsolute #(.fpwidth(8)) fpabsolute_13: pin names not known; wires that end beside it: argY[23:16], fpabsolute_15_p2[23:16]
  // FPAbsolute #(.fpwidth(8)) fpabsolute_14: pin names not known; wires that end beside it: argY[15:8], fpabsolute_15_p2[15:8]
  // FPAbsolute #(.fpwidth(8)) fpabsolute_15: pin names not known; wires that end beside it: argY[7:0], fpabsolute_15_p2[7:0]
  // FPToInt #(.fpwidth(8), .mode("ceil")) fptoint_45: pin names not known; wires that end beside it: argY[63:56], fptoint_52_p2[63:56]
  // FPToInt #(.fpwidth(8), .mode("ceil")) fptoint_46: pin names not known; wires that end beside it: argY[55:48], fptoint_52_p2[55:48]
  // FPToInt #(.fpwidth(8), .mode("ceil")) fptoint_47: pin names not known; wires that end beside it: argY[47:40], fptoint_52_p2[47:40]
  // FPToInt #(.fpwidth(8), .mode("ceil")) fptoint_48: pin names not known; wires that end beside it: argY[39:32], fptoint_52_p2[39:32]
  // FPToInt #(.fpwidth(8), .mode("ceil")) fptoint_49: pin names not known; wires that end beside it: argY[31:24], fptoint_52_p2[31:24]
  // FPToInt #(.fpwidth(8), .mode("ceil")) fptoint_50: pin names not known; wires that end beside it: argY[23:16], fptoint_52_p2[23:16]
  // FPToInt #(.fpwidth(8), .mode("ceil")) fptoint_51: pin names not known; wires that end beside it: argY[15:8], fptoint_52_p2[15:8]
  // FPToInt #(.fpwidth(8), .mode("ceil")) fptoint_52: pin names not known; wires that end beside it: argY[7:0], fptoint_52_p2[7:0]
  // FPToFP #(.fpwidthout(64)) fptofp_36: pin names not known; wires that end beside it: argY[31:0], fptofp_36_p2
  // FPToFP #(.fpwidthin(16)) fptofp_37: pin names not known; wires that end beside it: argY[15:0], fptofp_37_p2[31:0]
  // FPToFP #(.fpwidthin(16)) fptofp_38: pin names not known; wires that end beside it: argY[47:32], fptofp_37_p2[63:32]
  // FPToFP #(.fpwidthin(8), .fpwidthout(16)) fptofp_39: pin names not known; wires that end beside it: argY[7:0], fptofp_39_p2[15:0]
  // FPToFP #(.fpwidthin(8), .fpwidthout(16)) fptofp_40: pin names not known; wires that end beside it: argY[23:16], fptofp_39_p2[31:16]
  // FPToFP #(.fpwidthin(8), .fpwidthout(16)) fptofp_41: pin names not known; wires that end beside it: argY[39:32], fptofp_39_p2[47:32]
  // FPToFP #(.fpwidthin(8), .fpwidthout(16)) fptofp_42: pin names not known; wires that end beside it: argY[55:48], fptofp_39_p2[63:48]
  FPDivider #(.fpwidth(8)) fpdivider_8 (.a(argY[63:56]), .b(argZ[63:56]), .out(fpdivider_15_out[63:56]));
  FPDivider #(.fpwidth(8)) fpdivider_9 (.a(argY[55:48]), .b(argZ[55:48]), .out(fpdivider_15_out[55:48]));
  FPDivider #(.fpwidth(8)) fpdivider_10 (.a(argY[47:40]), .b(argZ[47:40]), .out(fpdivider_15_out[47:40]));
  FPDivider #(.fpwidth(8)) fpdivider_11 (.a(argY[39:32]), .b(argZ[39:32]), .out(fpdivider_15_out[39:32]));
  FPDivider #(.fpwidth(8)) fpdivider_12 (.a(argY[31:24]), .b(argZ[31:24]), .out(fpdivider_15_out[31:24]));
  FPDivider #(.fpwidth(8)) fpdivider_13 (.a(argY[23:16]), .b(argZ[23:16]), .out(fpdivider_15_out[23:16]));
  FPDivider #(.fpwidth(8)) fpdivider_14 (.a(argY[15:8]), .b(argZ[15:8]), .out(fpdivider_15_out[15:8]));
  FPDivider #(.fpwidth(8)) fpdivider_15 (.a(argY[7:0]), .b(argZ[7:0]), .out(fpdivider_15_out[7:0]));
  // FPSquareRoot #(.fpwidth(8)) fpsquareroot_8: pin names not known; wires that end beside it: argY[63:56], fpsquareroot_15_p2[63:56]
  // FPSquareRoot #(.fpwidth(8)) fpsquareroot_9: pin names not known; wires that end beside it: argY[55:48], fpsquareroot_15_p2[55:48]
  // FPSquareRoot #(.fpwidth(8)) fpsquareroot_10: pin names not known; wires that end beside it: argY[47:40], fpsquareroot_15_p2[47:40]
  // FPSquareRoot #(.fpwidth(8)) fpsquareroot_11: pin names not known; wires that end beside it: argY[39:32], fpsquareroot_15_p2[39:32]
  // FPSquareRoot #(.fpwidth(8)) fpsquareroot_12: pin names not known; wires that end beside it: argY[31:24], fpsquareroot_15_p2[31:24]
  // FPSquareRoot #(.fpwidth(8)) fpsquareroot_13: pin names not known; wires that end beside it: argY[23:16], fpsquareroot_15_p2[23:16]
  // FPSquareRoot #(.fpwidth(8)) fpsquareroot_14: pin names not known; wires that end beside it: argY[15:8], fpsquareroot_15_p2[15:8]
  // FPSquareRoot #(.fpwidth(8)) fpsquareroot_15: pin names not known; wires that end beside it: argY[7:0], fpsquareroot_15_p2[7:0]
  // FPToInt #(.fpwidth(8), .mode("truncate")) fptoint_53: pin names not known; wires that end beside it: argY[63:56], fptoint_60_p2[63:56]
  // FPToInt #(.fpwidth(8), .mode("truncate")) fptoint_54: pin names not known; wires that end beside it: argY[55:48], fptoint_60_p2[55:48]
  // FPToInt #(.fpwidth(8), .mode("truncate")) fptoint_55: pin names not known; wires that end beside it: argY[47:40], fptoint_60_p2[47:40]
  // FPToInt #(.fpwidth(8), .mode("truncate")) fptoint_56: pin names not known; wires that end beside it: argY[39:32], fptoint_60_p2[39:32]
  // FPToInt #(.fpwidth(8), .mode("truncate")) fptoint_57: pin names not known; wires that end beside it: argY[31:24], fptoint_60_p2[31:24]
  // FPToInt #(.fpwidth(8), .mode("truncate")) fptoint_58: pin names not known; wires that end beside it: argY[23:16], fptoint_60_p2[23:16]
  // FPToInt #(.fpwidth(8), .mode("truncate")) fptoint_59: pin names not known; wires that end beside it: argY[15:8], fptoint_60_p2[15:8]
  // FPToInt #(.fpwidth(8), .mode("truncate")) fptoint_60: pin names not known; wires that end beside it: argY[7:0], fptoint_60_p2[7:0]
endmodule

module fgam (
  input  [63:0] inval,
  output [63:0] outval
);

  wire [63:0] fpadder_1_out, fpadder_2_out, fpadder_3_out, fpadder_4_out, fpadder_5_out, fpadder_6_out,
       fpadder_7_out, fpadder_8_out, fpadder_9_out, fpadder_10_out, fpadder_11_out, fpadder_12_out,
       fpadder_13_out, fpdivider_1_out, fpdivider_2_out, fpdivider_3_out, fpdivider_4_out, fpdivider_5_out,
       fpdivider_6_out, fplogarithm_1_p2, fplogarithm_2_p2, fpmultiplier_1_out, fpmultiplier_2_out,
       fpmultiplier_3_out, fpmultiplier_4_out, fpmultiplier_5_out, fpmultiplier_6_out, fpmultiplier_7_out,
       fpmultiplier_8_out, fpmultiplier_9_out, fpmultiplier_10_out, fpmultiplier_11_out, fpnegator_1_p2;

  FPAdder #(.fpwidth(64)) fpadder_1 (.a(64'h3ff0000000000000), .b(fpadder_6_out), .out(fpadder_1_out));
  FPAdder #(.fpwidth(64)) fpadder_2 (.a(64'h4000000000000000), .b(fpadder_6_out), .out(fpadder_2_out));
  FPAdder #(.fpwidth(64)) fpadder_3 (.a(64'h4008000000000000), .b(fpadder_6_out), .out(fpadder_3_out));
  FPAdder #(.fpwidth(64)) fpadder_4 (.a(64'h4010000000000000), .b(fpadder_6_out), .out(fpadder_4_out));
  FPAdder #(.fpwidth(64)) fpadder_5 (.a(64'h4014000000000000), .b(fpadder_6_out), .out(fpadder_5_out));
  FPDivider #(.fpwidth(64)) fpdivider_1 (.a(64'h3ff0000000000000), .b(fpadder_1_out), .out(fpdivider_1_out));
  FPDivider #(.fpwidth(64)) fpdivider_2 (.a(64'h3ff0000000000000), .b(fpadder_2_out), .out(fpdivider_2_out));
  FPMultiplier #(.fpwidth(64)) fpmultiplier_1 (.a(fpdivider_1_out), .b(fpdivider_2_out), .out(fpmultiplier_1_out));
  FPDivider #(.fpwidth(64)) fpdivider_3 (.a(64'h3ff0000000000000), .b(fpadder_3_out), .out(fpdivider_3_out));
  FPMultiplier #(.fpwidth(64)) fpmultiplier_2 (.a(fpmultiplier_1_out), .b(fpdivider_3_out), .out(fpmultiplier_2_out));
  FPDivider #(.fpwidth(64)) fpdivider_4 (.a(64'h3ff0000000000000), .b(fpadder_4_out), .out(fpdivider_4_out));
  FPMultiplier #(.fpwidth(64)) fpmultiplier_3 (.a(fpmultiplier_2_out), .b(fpdivider_4_out), .out(fpmultiplier_3_out));
  FPDivider #(.fpwidth(64)) fpdivider_5 (.a(64'h3ff0000000000000), .b(fpadder_5_out), .out(fpdivider_5_out));
  FPMultiplier #(.fpwidth(64)) fpmultiplier_4 (.a(fpmultiplier_3_out), .b(fpdivider_5_out), .out(fpmultiplier_4_out));
  // Probe on inval
  FPMultiplier #(.fpwidth(64)) fpmultiplier_5 (.a(64'h3fb5555555555555), .b(fpdivider_1_out), .out(fpmultiplier_5_out));
  FPMultiplier #(.fpwidth(64)) fpmultiplier_6 (
    .a(64'h3fb5555555555555), .b(fpmultiplier_1_out), .out(fpmultiplier_6_out));
  FPMultiplier #(.fpwidth(64)) fpmultiplier_7 (
    .a(64'h3fc4fa4fa4fa4fa5), .b(fpmultiplier_2_out), .out(fpmultiplier_7_out));
  FPMultiplier #(.fpwidth(64)) fpmultiplier_8 (
    .a(64'h3fdeeeeeeeeeeeef), .b(fpmultiplier_3_out), .out(fpmultiplier_8_out));
  FPMultiplier #(.fpwidth(64)) fpmultiplier_9 (
    .a(64'h3ffe750750750750), .b(fpmultiplier_4_out), .out(fpmultiplier_9_out));
  FPAdder #(.fpwidth(64)) fpadder_6 (.a(inval), .b(64'h3ff0000000000000), .out(fpadder_6_out));
  // FPLogarithm #(.fpwidth(64), .mode("log")) fplogarithm_1: pin names not known; wires that end beside it: fpadder_6_out, fplogarithm_1_p2
  // FPNegator #(.fpwidth(64)) fpnegator_1: pin names not known; wires that end beside it: fpadder_6_out, fpnegator_1_p2
  FPDivider #(.fpwidth(64)) fpdivider_6 (.a(64'h401921fb54442d18), .b(fpadder_6_out), .out(fpdivider_6_out));
  FPMultiplier #(.fpwidth(64)) fpmultiplier_10 (.a(fplogarithm_1_p2), .b(fpadder_6_out), .out(fpmultiplier_10_out));
  // FPLogarithm #(.fpwidth(64), .mode("log")) fplogarithm_2: pin names not known; wires that end beside it: fpdivider_6_out, fplogarithm_2_p2
  FPMultiplier #(.fpwidth(64)) fpmultiplier_11 (
    .a(fplogarithm_2_p2), .b(64'h3fe0000000000000), .out(fpmultiplier_11_out));
  // Probe on fpmultiplier_10_out
  // Probe on fpnegator_1_p2
  // Probe on fpmultiplier_11_out
  // Probe on fpmultiplier_5_out
  // Probe on fpmultiplier_6_out
  // Probe on fpmultiplier_7_out
  // Probe on fpmultiplier_8_out
  // Probe on fpmultiplier_9_out
  FPAdder #(.fpwidth(64)) fpadder_7 (.a(fpmultiplier_10_out), .b(fpnegator_1_p2), .out(fpadder_7_out));
  FPAdder #(.fpwidth(64)) fpadder_8 (.a(fpmultiplier_11_out), .b(fpmultiplier_5_out), .out(fpadder_8_out));
  FPAdder #(.fpwidth(64)) fpadder_9 (.a(fpadder_7_out), .b(fpadder_8_out), .out(fpadder_9_out));
  FPAdder #(.fpwidth(64)) fpadder_10 (.a(fpmultiplier_6_out), .b(fpmultiplier_7_out), .out(fpadder_10_out));
  FPAdder #(.fpwidth(64)) fpadder_11 (.a(fpadder_10_out), .b(fpadder_12_out), .out(fpadder_11_out));
  FPAdder #(.fpwidth(64)) fpadder_12 (.a(fpmultiplier_8_out), .b(fpmultiplier_9_out), .out(fpadder_12_out));
  FPAdder #(.fpwidth(64)) fpadder_13 (.a(fpadder_9_out), .b(fpadder_11_out), .out(fpadder_13_out));
  // Probe on fpadder_13_out
  // Probe on outval
  // FPExponentiator #(.fpwidth(64), .mode("exp")) fpexponentiator_1: pin names not known; wires that end beside it: fpadder_13_out, outval

  // Notes on the sheet:
  //   inval: initial=0x4014000000000000
endmodule
